// Logisim project dunk.circ as structural Verilog: 78 circuits, main circuit main
module main (
  input  [31:0] in_1
);

  wire alu_control_1_enable, clock_1_out, gru_1_out_2, hard_reset_out, memory_ctrl_1_done,
       memory_ctrl_1_write, or_1_out, or_4_out, registers_controller_1_to_addr_bus,
       registers_controller_1_to_alu, registers_controller_1_to_data_bus, registers_controller_1_write,
       reset_pk_out, soft_reset_out;
  wire [3:0] registers_controller_1_alu_1, registers_controller_1_alu_2, registers_controller_1_bus_output,
       registers_controller_1_write_target;
  wire [7:0] alu_control_1_operation, memory_ctrl_1_data_send, ram_1_dout;
  wire [15:0] control_unit_1_control_bus_out, memory_ctrl_1_addr_out;
  wire [31:0] alu_1_out_6, alu_control_1_outp1, alu_control_1_outp2, cave_1_out_6, cave_1_out_7,
       control_unit_1_addr_bus_out, control_unit_1_data_bus_out, control_unit_1_to_special_registers,
       memory_ctrl_1_data_out, new_register_unit_1_out_12, new_register_unit_1_out_13,
       new_register_unit_1_out_14, new_register_unit_1_out_15, or_2_out, or_3_out,
       special_registers_1_addr_out, special_registers_1_data_bus_out, special_registers_1_offs_out,
       special_registers_1_pk_out, special_registers_1_sp_out;

  Clock clock_1 (.out(clock_1_out));
  Button reset_pk (.out(reset_pk_out));
  Button hard_reset (.out(hard_reset_out));
  Button soft_reset (.out(soft_reset_out));
  GRU gru_1 (.in_1(clock_1_out), .out_2(gru_1_out_2));
  or or_1 (or_1_out, hard_reset_out, gru_1_out_2);
  assign or_2_out = new_register_unit_1_out_12 | alu_1_out_6 | special_registers_1_data_bus_out | control_unit_1_data_bus_out | in_1 | cave_1_out_6 | memory_ctrl_1_data_out;  // OR_Gate or_2, 32 bits wide
  assign or_3_out = cave_1_out_7 | special_registers_1_addr_out | control_unit_1_addr_bus_out | new_register_unit_1_out_13;  // OR_Gate or_3, 32 bits wide
  or or_4 (or_4_out, or_1_out, soft_reset_out);
  special_registers special_registers_1 (
    .clock(clock_1_out), .reset(or_4_out), .reset_pk(reset_pk_out),
    .from_control_unit(control_unit_1_to_special_registers), .data_bus_in(or_2_out),
    .control_bus_in(control_unit_1_control_bus_out), .offs_out(special_registers_1_offs_out),
    .sp_out(special_registers_1_sp_out), .pk_out(special_registers_1_pk_out),
    .data_bus_out(special_registers_1_data_bus_out), .addr_out(special_registers_1_addr_out));
  control_unit control_unit_1 (
    .addr_bus_in(or_3_out), .pk_in(special_registers_1_pk_out), .sp_in(special_registers_1_sp_out),
    .reset(or_1_out), .force_running(or_4_out), .done(memory_ctrl_1_done), .clock(clock_1_out),
    .data_bus_in(or_2_out), .control_bus_out(control_unit_1_control_bus_out),
    .addr_bus_out(control_unit_1_addr_bus_out), .to_special_registers(control_unit_1_to_special_registers),
    .data_bus_out(control_unit_1_data_bus_out));  // open: in_10, single_instr_mode
  registers_controller registers_controller_1 (
    .control_in(control_unit_1_control_bus_out), .bus_output(registers_controller_1_bus_output),
    .ALU_1(registers_controller_1_alu_1), .ALU_2(registers_controller_1_alu_2),
    .write_target(registers_controller_1_write_target), .write(registers_controller_1_write),
    .to_data_bus(registers_controller_1_to_data_bus), .to_addr_bus(registers_controller_1_to_addr_bus),
    .to_ALU(registers_controller_1_to_alu));
  cave cave_1 (
    .Clock(clock_1_out), .Reset(or_4_out), .in_2(or_2_out), .in_3(or_3_out),
    .in_1(control_unit_1_control_bus_out), .out_6(cave_1_out_6), .out_7(cave_1_out_7));
  new_register_unit new_register_unit_1 (
    .in_10(clock_1_out), .in_11(or_4_out), .data_in(or_2_out), .Write(registers_controller_1_write),
    .Data_out(registers_controller_1_to_data_bus), .Addr_out(registers_controller_1_to_addr_bus),
    .ALU_Out(registers_controller_1_to_alu), .in_5(registers_controller_1_bus_output),
    .in_6(registers_controller_1_alu_1), .in_7(registers_controller_1_alu_2),
    .in_8(registers_controller_1_write_target), .out_12(new_register_unit_1_out_12),
    .out_13(new_register_unit_1_out_13), .out_14(new_register_unit_1_out_14),
    .out_15(new_register_unit_1_out_15));
  ALU_control alu_control_1 (
    .inp2(new_register_unit_1_out_15), .inp1(new_register_unit_1_out_14),
    .control_in(control_unit_1_control_bus_out), .clock_in(clock_1_out), .reset(or_4_out),
    .operation(alu_control_1_operation), .outp2(alu_control_1_outp2), .outp1(alu_control_1_outp1),
    .enable(alu_control_1_enable));
  ALU alu_1 (
    .operation(alu_control_1_operation), .inp1(alu_control_1_outp1), .inp2(alu_control_1_outp2),
    .enable(alu_control_1_enable), .reset(or_4_out), .out_6(alu_1_out_6));  // open: out_7
  // Probe on special_registers_1_pk_out
  // Probe on special_registers_1_pk_out
  // Probe on special_registers_1_sp_out
  // Probe on special_registers_1_sp_out
  memory_ctrl memory_ctrl_1 (
    .data_in(or_2_out), .ram_in(ram_1_dout), .addr_in(or_3_out), .offset_in(special_registers_1_offs_out),
    .control_in(control_unit_1_control_bus_out), .clock_in(clock_1_out), .reset(or_4_out),
    .data_out(memory_ctrl_1_data_out), .done(memory_ctrl_1_done), .addr_out(memory_ctrl_1_addr_out),
    .write(memory_ctrl_1_write), .data_send(memory_ctrl_1_data_send));
  RAM #(.addrWidth(16), .enables("line")) ram_1 (
    .addr(memory_ctrl_1_addr_out), .we(memory_ctrl_1_write), .clk(clock_1_out),
    .din(memory_ctrl_1_data_send), .dout(ram_1_dout));
  // Probe on control_unit_1_control_bus_out
  // Probe on control_unit_1_control_bus_out
  // Probe on or_2_out
  // Probe on or_2_out
  // Probe on or_3_out
  // Probe on or_3_out

  // Notes on the sheet:
  //   program kounter
  //   stack pointer
  //   Control
  //   Data
  //   Address
endmodule

module half_adder (
  input  in_1,
  input  in_2,
  output out_3,
  output out_4
);

  xor xor_1 (out_3, in_1, in_2);
  and and_1 (out_4, in_1, in_2);
endmodule

module full_adder (
  input  in_1,
  input  in_2,
  input  in_3,
  output out_4,
  output out_5
);

  wire and_1_out, and_2_out, xor_1_out;

  xor xor_1 (xor_1_out, in_2, in_3);
  and and_1 (and_1_out, in_2, in_3);
  xor xor_2 (out_4, xor_1_out, in_1);
  xor xor_3 (out_5, and_1_out, and_2_out);
  and and_2 (and_2_out, xor_1_out, in_1);
endmodule

module eight_bit_adder (
  input  in_1,
  input  [7:0] in_2,
  input  [7:0] in_3,
  output [7:0] out_4,
  output out_5
);

  wire full_adder_1_out_5, full_adder_2_out_5, full_adder_3_out_5, full_adder_4_out_5, full_adder_5_out_5,
       full_adder_6_out_5, full_adder_7_out_5;

  full_adder full_adder_1 (.in_1(in_1), .in_2(in_2[0]), .in_3(in_3[0]), .out_5(full_adder_1_out_5), .out_4(out_4[0]));
  full_adder full_adder_2 (
    .in_1(full_adder_1_out_5), .in_2(in_2[1]), .in_3(in_3[1]), .out_5(full_adder_2_out_5), .out_4(out_4[1]));
  full_adder full_adder_3 (
    .in_1(full_adder_2_out_5), .in_2(in_2[2]), .in_3(in_3[2]), .out_5(full_adder_3_out_5), .out_4(out_4[2]));
  full_adder full_adder_4 (
    .in_1(full_adder_3_out_5), .in_2(in_2[3]), .in_3(in_3[3]), .out_5(full_adder_4_out_5), .out_4(out_4[3]));
  full_adder full_adder_5 (
    .in_1(full_adder_4_out_5), .in_2(in_2[4]), .in_3(in_3[4]), .out_5(full_adder_5_out_5), .out_4(out_4[4]));
  full_adder full_adder_6 (
    .in_1(full_adder_5_out_5), .in_2(in_2[5]), .in_3(in_3[5]), .out_5(full_adder_6_out_5), .out_4(out_4[5]));
  full_adder full_adder_7 (
    .in_1(full_adder_6_out_5), .in_2(in_2[6]), .in_3(in_3[6]), .out_5(full_adder_7_out_5), .out_4(out_4[6]));
  full_adder full_adder_8 (.in_1(full_adder_7_out_5), .in_2(in_2[7]), .in_3(in_3[7]), .out_5(out_5), .out_4(out_4[7]));
endmodule

module four_bit_incrementer (
  input  [3:0] in_1,
  output [3:0] out_2
);

  wire and_1_out, and_2_out, and_3_out, and_4_out, and_5_out, xor_2_out, xor_3_out, xor_4_out, xor_8_out,
       xor_9_out;

  xor xor_1 (out_2[0], in_1[0], 1'b1);
  and and_1 (and_1_out, in_1[0], 1'b1);
  xor xor_2 (xor_2_out, in_1[1], 1'b0);
  and and_2 (and_2_out, in_1[1], 1'b0);
  xor xor_3 (xor_3_out, in_1[2], 1'b0);
  and and_3 (and_3_out, in_1[2], 1'b0);
  xor xor_4 (xor_4_out, in_1[3], 1'b0);
  xor xor_5 (out_2[1], xor_2_out, and_1_out);
  and and_4 (and_4_out, xor_2_out, and_1_out);
  xor xor_6 (out_2[2], xor_3_out, xor_8_out);
  and and_5 (and_5_out, xor_3_out, xor_8_out);
  xor xor_7 (out_2[3], xor_4_out, xor_9_out);
  xor xor_8 (xor_8_out, and_2_out, and_4_out);
  xor xor_9 (xor_9_out, and_3_out, and_5_out);
endmodule

module sixt_bit_adder (
  input  [15:0] in_1,
  input  [15:0] in_2,
  output [15:0] out_3,
  output out_4
);

  wire and_1_out, and_2_out, and_3_out, and_4_out, and_5_out, and_6_out, and_7_out, and_8_out, and_9_out,
       and_10_out, and_11_out, and_12_out, and_13_out, and_14_out, and_15_out, and_16_out, and_17_out,
       and_18_out, and_19_out, and_20_out, and_21_out, and_22_out, and_23_out, and_24_out, and_25_out,
       and_26_out, and_27_out, and_28_out, and_29_out, and_30_out, and_31_out, xor_2_out, xor_3_out,
       xor_4_out, xor_5_out, xor_6_out, xor_7_out, xor_8_out, xor_9_out, xor_10_out, xor_11_out, xor_12_out,
       xor_13_out, xor_14_out, xor_15_out, xor_16_out, xor_32_out, xor_33_out, xor_34_out, xor_35_out,
       xor_36_out, xor_37_out, xor_38_out, xor_39_out, xor_40_out, xor_41_out, xor_42_out, xor_43_out,
       xor_44_out, xor_45_out;

  xor xor_1 (out_3[0], in_1[0], in_2[0]);
  and and_1 (and_1_out, in_1[0], in_2[0]);
  xor xor_2 (xor_2_out, in_1[1], in_2[1]);
  and and_2 (and_2_out, in_1[1], in_2[1]);
  xor xor_3 (xor_3_out, in_1[2], in_2[2]);
  and and_3 (and_3_out, in_1[2], in_2[2]);
  xor xor_4 (xor_4_out, in_1[3], in_2[3]);
  and and_4 (and_4_out, in_1[3], in_2[3]);
  xor xor_5 (xor_5_out, in_1[4], in_2[4]);
  and and_5 (and_5_out, in_1[4], in_2[4]);
  xor xor_6 (xor_6_out, in_1[5], in_2[5]);
  and and_6 (and_6_out, in_1[5], in_2[5]);
  xor xor_7 (xor_7_out, in_1[6], in_2[6]);
  and and_7 (and_7_out, in_1[6], in_2[6]);
  xor xor_8 (xor_8_out, in_1[7], in_2[7]);
  and and_8 (and_8_out, in_1[7], in_2[7]);
  xor xor_9 (xor_9_out, in_1[8], in_2[8]);
  and and_9 (and_9_out, in_1[8], in_2[8]);
  xor xor_10 (xor_10_out, in_1[9], in_2[9]);
  and and_10 (and_10_out, in_1[9], in_2[9]);
  xor xor_11 (xor_11_out, in_1[10], in_2[10]);
  and and_11 (and_11_out, in_1[10], in_2[10]);
  xor xor_12 (xor_12_out, in_1[11], in_2[11]);
  and and_12 (and_12_out, in_1[11], in_2[11]);
  xor xor_13 (xor_13_out, in_1[12], in_2[12]);
  and and_13 (and_13_out, in_1[12], in_2[12]);
  xor xor_14 (xor_14_out, in_1[13], in_2[13]);
  and and_14 (and_14_out, in_1[13], in_2[13]);
  xor xor_15 (xor_15_out, in_1[14], in_2[14]);
  and and_15 (and_15_out, in_1[14], in_2[14]);
  xor xor_16 (xor_16_out, in_1[15], in_2[15]);
  and and_16 (and_16_out, in_1[15], in_2[15]);
  xor xor_17 (out_3[1], xor_2_out, and_1_out);
  and and_17 (and_17_out, xor_2_out, and_1_out);
  xor xor_18 (out_3[2], xor_3_out, xor_32_out);
  and and_18 (and_18_out, xor_3_out, xor_32_out);
  xor xor_19 (out_3[3], xor_4_out, xor_33_out);
  and and_19 (and_19_out, xor_4_out, xor_33_out);
  xor xor_20 (out_3[4], xor_5_out, xor_34_out);
  and and_20 (and_20_out, xor_5_out, xor_34_out);
  xor xor_21 (out_3[5], xor_6_out, xor_35_out);
  and and_21 (and_21_out, xor_6_out, xor_35_out);
  xor xor_22 (out_3[6], xor_7_out, xor_36_out);
  and and_22 (and_22_out, xor_7_out, xor_36_out);
  xor xor_23 (out_3[7], xor_8_out, xor_37_out);
  and and_23 (and_23_out, xor_8_out, xor_37_out);
  xor xor_24 (out_3[8], xor_9_out, xor_38_out);
  and and_24 (and_24_out, xor_9_out, xor_38_out);
  xor xor_25 (out_3[9], xor_10_out, xor_39_out);
  and and_25 (and_25_out, xor_10_out, xor_39_out);
  xor xor_26 (out_3[10], xor_11_out, xor_40_out);
  and and_26 (and_26_out, xor_11_out, xor_40_out);
  xor xor_27 (out_3[11], xor_12_out, xor_41_out);
  and and_27 (and_27_out, xor_12_out, xor_41_out);
  xor xor_28 (out_3[12], xor_13_out, xor_42_out);
  and and_28 (and_28_out, xor_13_out, xor_42_out);
  xor xor_29 (out_3[13], xor_14_out, xor_43_out);
  and and_29 (and_29_out, xor_14_out, xor_43_out);
  xor xor_30 (out_3[14], xor_15_out, xor_44_out);
  and and_30 (and_30_out, xor_15_out, xor_44_out);
  xor xor_31 (out_3[15], xor_16_out, xor_45_out);
  and and_31 (and_31_out, xor_16_out, xor_45_out);
  xor xor_32 (xor_32_out, and_2_out, and_17_out);
  xor xor_33 (xor_33_out, and_3_out, and_18_out);
  xor xor_34 (xor_34_out, and_4_out, and_19_out);
  xor xor_35 (xor_35_out, and_5_out, and_20_out);
  xor xor_36 (xor_36_out, and_6_out, and_21_out);
  xor xor_37 (xor_37_out, and_7_out, and_22_out);
  xor xor_38 (xor_38_out, and_8_out, and_23_out);
  xor xor_39 (xor_39_out, and_9_out, and_24_out);
  xor xor_40 (xor_40_out, and_10_out, and_25_out);
  xor xor_41 (xor_41_out, and_11_out, and_26_out);
  xor xor_42 (xor_42_out, and_12_out, and_27_out);
  xor xor_43 (xor_43_out, and_13_out, and_28_out);
  xor xor_44 (xor_44_out, and_14_out, and_29_out);
  xor xor_45 (xor_45_out, and_15_out, and_30_out);
  xor xor_46 (out_4, and_16_out, and_31_out);
endmodule

module sixt_bit_adder_c (
  input  in_1,
  input  [15:0] in_2,
  input  [15:0] in_3,
  output [15:0] out_4,
  output out_5
);

  wire and_1_out, and_2_out, and_3_out, and_4_out, and_5_out, and_6_out, and_7_out, and_8_out, and_9_out,
       and_10_out, and_11_out, and_12_out, and_13_out, and_14_out, and_15_out, and_16_out, and_17_out,
       and_18_out, and_19_out, and_20_out, and_21_out, and_22_out, and_23_out, and_24_out, and_25_out,
       and_26_out, and_27_out, and_28_out, and_29_out, and_30_out, and_31_out, and_32_out, xor_1_out,
       xor_2_out, xor_3_out, xor_4_out, xor_5_out, xor_6_out, xor_7_out, xor_8_out, xor_9_out, xor_10_out,
       xor_11_out, xor_12_out, xor_13_out, xor_14_out, xor_15_out, xor_16_out, xor_33_out, xor_34_out,
       xor_35_out, xor_36_out, xor_37_out, xor_38_out, xor_39_out, xor_40_out, xor_41_out, xor_42_out,
       xor_43_out, xor_44_out, xor_45_out, xor_46_out, xor_47_out;

  xor xor_1 (xor_1_out, in_2[0], in_3[0]);
  and and_1 (and_1_out, in_2[0], in_3[0]);
  xor xor_2 (xor_2_out, in_2[1], in_3[1]);
  and and_2 (and_2_out, in_2[1], in_3[1]);
  xor xor_3 (xor_3_out, in_2[2], in_3[2]);
  and and_3 (and_3_out, in_2[2], in_3[2]);
  xor xor_4 (xor_4_out, in_2[3], in_3[3]);
  and and_4 (and_4_out, in_2[3], in_3[3]);
  xor xor_5 (xor_5_out, in_2[4], in_3[4]);
  and and_5 (and_5_out, in_2[4], in_3[4]);
  xor xor_6 (xor_6_out, in_2[5], in_3[5]);
  and and_6 (and_6_out, in_2[5], in_3[5]);
  xor xor_7 (xor_7_out, in_2[6], in_3[6]);
  and and_7 (and_7_out, in_2[6], in_3[6]);
  xor xor_8 (xor_8_out, in_2[7], in_3[7]);
  and and_8 (and_8_out, in_2[7], in_3[7]);
  xor xor_9 (xor_9_out, in_2[8], in_3[8]);
  and and_9 (and_9_out, in_2[8], in_3[8]);
  xor xor_10 (xor_10_out, in_2[9], in_3[9]);
  and and_10 (and_10_out, in_2[9], in_3[9]);
  xor xor_11 (xor_11_out, in_2[10], in_3[10]);
  and and_11 (and_11_out, in_2[10], in_3[10]);
  xor xor_12 (xor_12_out, in_2[11], in_3[11]);
  and and_12 (and_12_out, in_2[11], in_3[11]);
  xor xor_13 (xor_13_out, in_2[12], in_3[12]);
  and and_13 (and_13_out, in_2[12], in_3[12]);
  xor xor_14 (xor_14_out, in_2[13], in_3[13]);
  and and_14 (and_14_out, in_2[13], in_3[13]);
  xor xor_15 (xor_15_out, in_2[14], in_3[14]);
  and and_15 (and_15_out, in_2[14], in_3[14]);
  xor xor_16 (xor_16_out, in_2[15], in_3[15]);
  and and_16 (and_16_out, in_2[15], in_3[15]);
  xor xor_17 (out_4[0], xor_1_out, in_1);
  and and_17 (and_17_out, xor_1_out, in_1);
  xor xor_18 (out_4[1], xor_2_out, xor_33_out);
  and and_18 (and_18_out, xor_2_out, xor_33_out);
  xor xor_19 (out_4[2], xor_3_out, xor_34_out);
  and and_19 (and_19_out, xor_3_out, xor_34_out);
  xor xor_20 (out_4[3], xor_4_out, xor_35_out);
  and and_20 (and_20_out, xor_4_out, xor_35_out);
  xor xor_21 (out_4[4], xor_5_out, xor_36_out);
  and and_21 (and_21_out, xor_5_out, xor_36_out);
  xor xor_22 (out_4[5], xor_6_out, xor_37_out);
  and and_22 (and_22_out, xor_6_out, xor_37_out);
  xor xor_23 (out_4[6], xor_7_out, xor_38_out);
  and and_23 (and_23_out, xor_7_out, xor_38_out);
  xor xor_24 (out_4[7], xor_8_out, xor_39_out);
  and and_24 (and_24_out, xor_8_out, xor_39_out);
  xor xor_25 (out_4[8], xor_9_out, xor_40_out);
  and and_25 (and_25_out, xor_9_out, xor_40_out);
  xor xor_26 (out_4[9], xor_10_out, xor_41_out);
  and and_26 (and_26_out, xor_10_out, xor_41_out);
  xor xor_27 (out_4[10], xor_11_out, xor_42_out);
  and and_27 (and_27_out, xor_11_out, xor_42_out);
  xor xor_28 (out_4[11], xor_12_out, xor_43_out);
  and and_28 (and_28_out, xor_12_out, xor_43_out);
  xor xor_29 (out_4[12], xor_13_out, xor_44_out);
  and and_29 (and_29_out, xor_13_out, xor_44_out);
  xor xor_30 (out_4[13], xor_14_out, xor_45_out);
  and and_30 (and_30_out, xor_14_out, xor_45_out);
  xor xor_31 (out_4[14], xor_15_out, xor_46_out);
  and and_31 (and_31_out, xor_15_out, xor_46_out);
  xor xor_32 (out_4[15], xor_16_out, xor_47_out);
  and and_32 (and_32_out, xor_16_out, xor_47_out);
  xor xor_33 (xor_33_out, and_1_out, and_17_out);
  xor xor_34 (xor_34_out, and_2_out, and_18_out);
  xor xor_35 (xor_35_out, and_3_out, and_19_out);
  xor xor_36 (xor_36_out, and_4_out, and_20_out);
  xor xor_37 (xor_37_out, and_5_out, and_21_out);
  xor xor_38 (xor_38_out, and_6_out, and_22_out);
  xor xor_39 (xor_39_out, and_7_out, and_23_out);
  xor xor_40 (xor_40_out, and_8_out, and_24_out);
  xor xor_41 (xor_41_out, and_9_out, and_25_out);
  xor xor_42 (xor_42_out, and_10_out, and_26_out);
  xor xor_43 (xor_43_out, and_11_out, and_27_out);
  xor xor_44 (xor_44_out, and_12_out, and_28_out);
  xor xor_45 (xor_45_out, and_13_out, and_29_out);
  xor xor_46 (xor_46_out, and_14_out, and_30_out);
  xor xor_47 (xor_47_out, and_15_out, and_31_out);
  xor xor_48 (out_5, and_16_out, and_32_out);
endmodule

module sixt_bit_subtractor (
  input  [15:0] in_1,
  input  [15:0] in_2,
  output [15:0] out_3,
  output out_4
);

  wire and_1_out, and_2_out, and_3_out, and_4_out, and_5_out, and_6_out, and_7_out, and_8_out, and_9_out,
       and_10_out, and_11_out, and_12_out, and_13_out, and_14_out, and_15_out, and_16_out, and_17_out,
       and_18_out, and_19_out, and_20_out, and_21_out, and_22_out, and_23_out, and_24_out, and_25_out,
       and_26_out, and_27_out, and_28_out, and_29_out, and_30_out, and_31_out, xor_2_out, xor_4_out,
       xor_6_out, xor_8_out, xor_10_out, xor_12_out, xor_14_out, xor_16_out, xor_18_out, xor_20_out,
       xor_22_out, xor_24_out, xor_26_out, xor_28_out, xor_30_out, xor_32_out, xor_33_out, xor_34_out,
       xor_35_out, xor_36_out, xor_37_out, xor_38_out, xor_39_out, xor_40_out, xor_41_out, xor_42_out,
       xor_43_out, xor_44_out, xor_45_out;
  wire [15:0] not_1_out, sixt_bit_incrementer_1_out_2;

  assign not_1_out = ~in_2;  // NOT_Gate not_1, 16 bits wide
  sixt_bit_incrementer sixt_bit_incrementer_1 (.in_1(not_1_out), .out_2(sixt_bit_incrementer_1_out_2));
  xor xor_1 (out_3[0], in_1[0], sixt_bit_incrementer_1_out_2[0]);
  and and_1 (and_1_out, in_1[0], sixt_bit_incrementer_1_out_2[0]);
  xor xor_2 (xor_2_out, in_1[1], sixt_bit_incrementer_1_out_2[1]);
  xor xor_3 (out_3[1], xor_2_out, and_1_out);
  and and_2 (and_2_out, in_1[1], sixt_bit_incrementer_1_out_2[1]);
  and and_3 (and_3_out, xor_2_out, and_1_out);
  xor xor_4 (xor_4_out, in_1[2], sixt_bit_incrementer_1_out_2[2]);
  xor xor_5 (out_3[2], xor_4_out, xor_32_out);
  and and_4 (and_4_out, in_1[2], sixt_bit_incrementer_1_out_2[2]);
  and and_5 (and_5_out, xor_4_out, xor_32_out);
  xor xor_6 (xor_6_out, in_1[3], sixt_bit_incrementer_1_out_2[3]);
  xor xor_7 (out_3[3], xor_6_out, xor_33_out);
  and and_6 (and_6_out, in_1[3], sixt_bit_incrementer_1_out_2[3]);
  and and_7 (and_7_out, xor_6_out, xor_33_out);
  xor xor_8 (xor_8_out, in_1[4], sixt_bit_incrementer_1_out_2[4]);
  xor xor_9 (out_3[4], xor_8_out, xor_34_out);
  and and_8 (and_8_out, in_1[4], sixt_bit_incrementer_1_out_2[4]);
  and and_9 (and_9_out, xor_8_out, xor_34_out);
  xor xor_10 (xor_10_out, in_1[5], sixt_bit_incrementer_1_out_2[5]);
  xor xor_11 (out_3[5], xor_10_out, xor_35_out);
  and and_10 (and_10_out, in_1[5], sixt_bit_incrementer_1_out_2[5]);
  and and_11 (and_11_out, xor_10_out, xor_35_out);
  xor xor_12 (xor_12_out, in_1[6], sixt_bit_incrementer_1_out_2[6]);
  xor xor_13 (out_3[6], xor_12_out, xor_36_out);
  and and_12 (and_12_out, in_1[6], sixt_bit_incrementer_1_out_2[6]);
  and and_13 (and_13_out, xor_12_out, xor_36_out);
  xor xor_14 (xor_14_out, in_1[7], sixt_bit_incrementer_1_out_2[7]);
  xor xor_15 (out_3[7], xor_14_out, xor_37_out);
  and and_14 (and_14_out, in_1[7], sixt_bit_incrementer_1_out_2[7]);
  and and_15 (and_15_out, xor_14_out, xor_37_out);
  xor xor_16 (xor_16_out, in_1[8], sixt_bit_incrementer_1_out_2[8]);
  xor xor_17 (out_3[8], xor_16_out, xor_38_out);
  and and_16 (and_16_out, in_1[8], sixt_bit_incrementer_1_out_2[8]);
  and and_17 (and_17_out, xor_16_out, xor_38_out);
  xor xor_18 (xor_18_out, in_1[9], sixt_bit_incrementer_1_out_2[9]);
  xor xor_19 (out_3[9], xor_18_out, xor_39_out);
  and and_18 (and_18_out, in_1[9], sixt_bit_incrementer_1_out_2[9]);
  and and_19 (and_19_out, xor_18_out, xor_39_out);
  xor xor_20 (xor_20_out, in_1[10], sixt_bit_incrementer_1_out_2[10]);
  xor xor_21 (out_3[10], xor_20_out, xor_40_out);
  and and_20 (and_20_out, in_1[10], sixt_bit_incrementer_1_out_2[10]);
  and and_21 (and_21_out, xor_20_out, xor_40_out);
  xor xor_22 (xor_22_out, in_1[11], sixt_bit_incrementer_1_out_2[11]);
  xor xor_23 (out_3[11], xor_22_out, xor_41_out);
  and and_22 (and_22_out, in_1[11], sixt_bit_incrementer_1_out_2[11]);
  and and_23 (and_23_out, xor_22_out, xor_41_out);
  xor xor_24 (xor_24_out, in_1[12], sixt_bit_incrementer_1_out_2[12]);
  xor xor_25 (out_3[12], xor_24_out, xor_42_out);
  and and_24 (and_24_out, in_1[12], sixt_bit_incrementer_1_out_2[12]);
  and and_25 (and_25_out, xor_24_out, xor_42_out);
  xor xor_26 (xor_26_out, in_1[13], sixt_bit_incrementer_1_out_2[13]);
  xor xor_27 (out_3[13], xor_26_out, xor_43_out);
  and and_26 (and_26_out, in_1[13], sixt_bit_incrementer_1_out_2[13]);
  and and_27 (and_27_out, xor_26_out, xor_43_out);
  xor xor_28 (xor_28_out, in_1[14], sixt_bit_incrementer_1_out_2[14]);
  xor xor_29 (out_3[14], xor_28_out, xor_44_out);
  and and_28 (and_28_out, in_1[14], sixt_bit_incrementer_1_out_2[14]);
  and and_29 (and_29_out, xor_28_out, xor_44_out);
  xor xor_30 (xor_30_out, in_1[15], sixt_bit_incrementer_1_out_2[15]);
  xor xor_31 (out_3[15], xor_30_out, xor_45_out);
  and and_30 (and_30_out, in_1[15], sixt_bit_incrementer_1_out_2[15]);
  and and_31 (and_31_out, xor_30_out, xor_45_out);
  xor xor_32 (xor_32_out, and_2_out, and_3_out);
  xor xor_33 (xor_33_out, and_4_out, and_5_out);
  xor xor_34 (xor_34_out, and_6_out, and_7_out);
  xor xor_35 (xor_35_out, and_8_out, and_9_out);
  xor xor_36 (xor_36_out, and_10_out, and_11_out);
  xor xor_37 (xor_37_out, and_12_out, and_13_out);
  xor xor_38 (xor_38_out, and_14_out, and_15_out);
  xor xor_39 (xor_39_out, and_16_out, and_17_out);
  xor xor_40 (xor_40_out, and_18_out, and_19_out);
  xor xor_41 (xor_41_out, and_20_out, and_21_out);
  xor xor_42 (xor_42_out, and_22_out, and_23_out);
  xor xor_43 (xor_43_out, and_24_out, and_25_out);
  xor xor_44 (xor_44_out, and_26_out, and_27_out);
  xor xor_45 (xor_45_out, and_28_out, and_29_out);
  xor xor_46 (out_4, and_30_out, and_31_out);
endmodule

module sixt_bit_adder_subtractor (
  input  [15:0] in_1,
  input  [15:0] in_2,
  input  in_3,
  output [15:0] out_4,
  output out_5
);

  wire and_1_out, and_2_out, and_3_out, and_4_out, and_5_out, and_6_out, and_7_out, and_8_out, and_9_out,
       and_10_out, and_11_out, and_12_out, and_13_out, and_14_out, and_15_out, and_16_out, and_17_out,
       and_18_out, and_19_out, and_20_out, and_21_out, and_22_out, and_23_out, and_24_out, and_25_out,
       and_26_out, and_27_out, and_28_out, and_29_out, and_30_out, and_31_out, sixt_bit_selector_1_p3,
       xor_2_out, xor_4_out, xor_6_out, xor_8_out, xor_10_out, xor_12_out, xor_14_out, xor_16_out,
       xor_18_out, xor_20_out, xor_22_out, xor_24_out, xor_26_out, xor_28_out, xor_30_out, xor_32_out,
       xor_33_out, xor_34_out, xor_35_out, xor_36_out, xor_37_out, xor_38_out, xor_39_out, xor_40_out,
       xor_41_out, xor_42_out, xor_43_out, xor_44_out, xor_45_out;
  wire [15:0] not_1_out, sixt_bit_selector_1_p4;

  assign not_1_out = ~in_2;  // NOT_Gate not_1, 16 bits wide
  // sixt_bit_selector sixt_bit_selector_1: pin names not known; wires that end beside it: in_3, in_2, sixt_bit_selector_1_p3, sixt_bit_selector_1_p4
  // sixt_bit_incrementer sixt_bit_incrementer_1: pin names not known; wires that end beside it: not_1_out, sixt_bit_selector_1_p3, sixt_bit_selector_1_p4
  xor xor_1 (out_4[0], in_1[0], sixt_bit_selector_1_p4[0]);
  and and_1 (and_1_out, in_1[0], sixt_bit_selector_1_p4[0]);
  xor xor_2 (xor_2_out, in_1[1], sixt_bit_selector_1_p4[1]);
  xor xor_3 (out_4[1], xor_2_out, and_1_out);
  and and_2 (and_2_out, in_1[1], sixt_bit_selector_1_p4[1]);
  and and_3 (and_3_out, xor_2_out, and_1_out);
  xor xor_4 (xor_4_out, in_1[2], sixt_bit_selector_1_p4[2]);
  xor xor_5 (out_4[2], xor_4_out, xor_32_out);
  and and_4 (and_4_out, in_1[2], sixt_bit_selector_1_p4[2]);
  and and_5 (and_5_out, xor_4_out, xor_32_out);
  xor xor_6 (xor_6_out, in_1[3], sixt_bit_selector_1_p4[3]);
  xor xor_7 (out_4[3], xor_6_out, xor_33_out);
  and and_6 (and_6_out, in_1[3], sixt_bit_selector_1_p4[3]);
  and and_7 (and_7_out, xor_6_out, xor_33_out);
  xor xor_8 (xor_8_out, in_1[4], sixt_bit_selector_1_p4[4]);
  xor xor_9 (out_4[4], xor_8_out, xor_34_out);
  and and_8 (and_8_out, in_1[4], sixt_bit_selector_1_p4[4]);
  and and_9 (and_9_out, xor_8_out, xor_34_out);
  xor xor_10 (xor_10_out, in_1[5], sixt_bit_selector_1_p4[5]);
  xor xor_11 (out_4[5], xor_10_out, xor_35_out);
  and and_10 (and_10_out, in_1[5], sixt_bit_selector_1_p4[5]);
  and and_11 (and_11_out, xor_10_out, xor_35_out);
  xor xor_12 (xor_12_out, in_1[6], sixt_bit_selector_1_p4[6]);
  xor xor_13 (out_4[6], xor_12_out, xor_36_out);
  and and_12 (and_12_out, in_1[6], sixt_bit_selector_1_p4[6]);
  and and_13 (and_13_out, xor_12_out, xor_36_out);
  xor xor_14 (xor_14_out, in_1[7], sixt_bit_selector_1_p4[7]);
  xor xor_15 (out_4[7], xor_14_out, xor_37_out);
  and and_14 (and_14_out, in_1[7], sixt_bit_selector_1_p4[7]);
  and and_15 (and_15_out, xor_14_out, xor_37_out);
  xor xor_16 (xor_16_out, in_1[8], sixt_bit_selector_1_p4[8]);
  xor xor_17 (out_4[8], xor_16_out, xor_38_out);
  and and_16 (and_16_out, in_1[8], sixt_bit_selector_1_p4[8]);
  and and_17 (and_17_out, xor_16_out, xor_38_out);
  xor xor_18 (xor_18_out, in_1[9], sixt_bit_selector_1_p4[9]);
  xor xor_19 (out_4[9], xor_18_out, xor_39_out);
  and and_18 (and_18_out, in_1[9], sixt_bit_selector_1_p4[9]);
  and and_19 (and_19_out, xor_18_out, xor_39_out);
  xor xor_20 (xor_20_out, in_1[10], sixt_bit_selector_1_p4[10]);
  xor xor_21 (out_4[10], xor_20_out, xor_40_out);
  and and_20 (and_20_out, in_1[10], sixt_bit_selector_1_p4[10]);
  and and_21 (and_21_out, xor_20_out, xor_40_out);
  xor xor_22 (xor_22_out, in_1[11], sixt_bit_selector_1_p4[11]);
  xor xor_23 (out_4[11], xor_22_out, xor_41_out);
  and and_22 (and_22_out, in_1[11], sixt_bit_selector_1_p4[11]);
  and and_23 (and_23_out, xor_22_out, xor_41_out);
  xor xor_24 (xor_24_out, in_1[12], sixt_bit_selector_1_p4[12]);
  xor xor_25 (out_4[12], xor_24_out, xor_42_out);
  and and_24 (and_24_out, in_1[12], sixt_bit_selector_1_p4[12]);
  and and_25 (and_25_out, xor_24_out, xor_42_out);
  xor xor_26 (xor_26_out, in_1[13], sixt_bit_selector_1_p4[13]);
  xor xor_27 (out_4[13], xor_26_out, xor_43_out);
  and and_26 (and_26_out, in_1[13], sixt_bit_selector_1_p4[13]);
  and and_27 (and_27_out, xor_26_out, xor_43_out);
  xor xor_28 (xor_28_out, in_1[14], sixt_bit_selector_1_p4[14]);
  xor xor_29 (out_4[14], xor_28_out, xor_44_out);
  and and_28 (and_28_out, in_1[14], sixt_bit_selector_1_p4[14]);
  and and_29 (and_29_out, xor_28_out, xor_44_out);
  xor xor_30 (xor_30_out, in_1[15], sixt_bit_selector_1_p4[15]);
  xor xor_31 (out_4[15], xor_30_out, xor_45_out);
  and and_30 (and_30_out, in_1[15], sixt_bit_selector_1_p4[15]);
  and and_31 (and_31_out, xor_30_out, xor_45_out);
  xor xor_32 (xor_32_out, and_2_out, and_3_out);
  xor xor_33 (xor_33_out, and_4_out, and_5_out);
  xor xor_34 (xor_34_out, and_6_out, and_7_out);
  xor xor_35 (xor_35_out, and_8_out, and_9_out);
  xor xor_36 (xor_36_out, and_10_out, and_11_out);
  xor xor_37 (xor_37_out, and_12_out, and_13_out);
  xor xor_38 (xor_38_out, and_14_out, and_15_out);
  xor xor_39 (xor_39_out, and_16_out, and_17_out);
  xor xor_40 (xor_40_out, and_18_out, and_19_out);
  xor xor_41 (xor_41_out, and_20_out, and_21_out);
  xor xor_42 (xor_42_out, and_22_out, and_23_out);
  xor xor_43 (xor_43_out, and_24_out, and_25_out);
  xor xor_44 (xor_44_out, and_26_out, and_27_out);
  xor xor_45 (xor_45_out, and_28_out, and_29_out);
  xor xor_46 (out_5, and_30_out, and_31_out);
endmodule

module sixt_bit_incrementer (
  input  [15:0] in_1,
  output [15:0] out_2
);

  sixt_bit_adder sixt_bit_adder_1 (.in_1(16'h1), .in_2(in_1), .out_3(out_2));  // open: out_4
endmodule

module sixt_bit_decrementer (
  input  [15:0] in_1,
  output [15:0] out_2
);

  sixt_bit_adder sixt_bit_adder_1 (.in_1({16{1'b1}}), .in_2(in_1), .out_3(out_2));  // open: out_4
endmodule

module eight_bit_selector (
  input  in_1,
  input  [7:0] in_2,
  input  [7:0] in_3,
  output [7:0] out_4
);

  wire [7:0] and_1_out, and_2_out;

  assign and_1_out = ~{8{in_1}} & in_2;  // AND_Gate and_1, 8 bits wide
  assign and_2_out = {8{in_1}} & in_3;  // AND_Gate and_2, 8 bits wide
  assign out_4 = and_1_out | and_2_out;  // OR_Gate or_1, 8 bits wide
endmodule

module sixt_bit_selector (
  input  enable,
  input  [31:0] data0,
  input  [31:0] data1,
  output [31:0] out_put
);

  Multiplexer #(.width(32)) multiplexer_1 (.in0(data0), .in1(data1), .out(out_put));  // open: sel
endmodule

module sixt_bit_multiplier_old (
  input  [15:0] in_1,
  input  [15:0] in_2,
  output [15:0] out_3
);

  wire gatekeeper_1_p2, gatekeeper_3_p2, gatekeeper_4_p2, gatekeeper_5_p2, gatekeeper_6_p2, gatekeeper_8_p2,
       gatekeeper_9_p2, gatekeeper_10_p2, gatekeeper_11_p2, gatekeeper_12_p2, gatekeeper_13_p2,
       gatekeeper_14_p2, gatekeeper_15_p2, sixt_bit_adder_c_3_p3;
  wire [15:0] sixt_bit_adder_c_1_p2, sixt_bit_adder_c_2_p2, sixt_bit_adder_c_3_p2, sixt_bit_adder_c_4_out_4,
       sixt_bit_adder_c_5_p2, sixt_bit_adder_c_6_out_4, sixt_bit_adder_c_7_out_4, sixt_bit_adder_c_8_p2,
       sixt_bit_adder_c_9_out_4, sixt_bit_adder_c_10_out_4, sixt_bit_adder_c_12_p2,
       sixt_bit_adder_c_13_out_4, sixt_bit_adder_c_14_p2, sixt_bit_adder_c_15_p2,
       sixt_bit_shift_by_one_1_out_2, sixt_bit_shift_by_one_2_out_2, sixt_bit_shift_by_one_3_out_2,
       sixt_bit_shift_by_one_4_out_2, sixt_bit_shift_by_one_5_out_2, sixt_bit_shift_by_one_6_out_2,
       sixt_bit_shift_by_one_7_out_2, sixt_bit_shift_by_one_8_out_2, sixt_bit_shift_by_one_9_out_2,
       sixt_bit_shift_by_one_10_out_2, sixt_bit_shift_by_one_11_out_2, sixt_bit_shift_by_one_12_out_2,
       sixt_bit_shift_by_one_13_out_2, sixt_bit_shift_by_one_14_out_2;
  wire [31:0] gatekeeper_2_out_3, gatekeeper_16_out_3, sixt_bit_shift_by_one_15_out_2;

  sixt_bit_shift_by_one sixt_bit_shift_by_one_1 (.in_1(in_1), .out_2(sixt_bit_shift_by_one_1_out_2));
  sixt_bit_shift_by_one sixt_bit_shift_by_one_2 (
    .in_1(sixt_bit_shift_by_one_15_out_2[15:0]), .out_2(sixt_bit_shift_by_one_2_out_2));
  // gatekeeper gatekeeper_1: pin names not known; wires that end beside it: in_1, gatekeeper_1_p2, in_2[0]
  gatekeeper gatekeeper_2 (.in_1(in_2[8]), .in_2(sixt_bit_shift_by_one_15_out_2), .out_3(gatekeeper_2_out_3));
  // sixt_bit_adder_c sixt_bit_adder_c_1: pin names not known; wires that end beside it: gatekeeper_1_p2, sixt_bit_adder_c_1_p2, gatekeeper_2_out_3, 1'b0
  sixt_bit_shift_by_one sixt_bit_shift_by_one_3 (
    .in_1(sixt_bit_shift_by_one_1_out_2), .out_2(sixt_bit_shift_by_one_3_out_2));
  sixt_bit_shift_by_one sixt_bit_shift_by_one_4 (
    .in_1(sixt_bit_shift_by_one_2_out_2), .out_2(sixt_bit_shift_by_one_4_out_2));
  // gatekeeper gatekeeper_3: pin names not known; wires that end beside it: sixt_bit_shift_by_one_2_out_2, gatekeeper_3_p2, in_2[1]
  // gatekeeper gatekeeper_4: pin names not known; wires that end beside it: sixt_bit_shift_by_one_4_out_2, gatekeeper_4_p2, in_2[2]
  // gatekeeper gatekeeper_5: pin names not known; wires that end beside it: sixt_bit_shift_by_one_1_out_2, gatekeeper_5_p2, in_2[9]
  // sixt_bit_adder_c sixt_bit_adder_c_2: pin names not known; wires that end beside it: gatekeeper_3_p2, sixt_bit_adder_c_2_p2, gatekeeper_5_p2, 1'b0
  // sixt_bit_adder_c sixt_bit_adder_c_3: pin names not known; wires that end beside it: gatekeeper_4_p2, sixt_bit_adder_c_3_p2, sixt_bit_adder_c_3_p3, 1'b0
  sixt_bit_adder_c sixt_bit_adder_c_4 (
    .in_1(1'b0), .in_2(sixt_bit_adder_c_2_p2), .in_3(sixt_bit_adder_c_1_p2), .out_4(sixt_bit_adder_c_4_out_4));  // open: out_5
  sixt_bit_shift_by_one sixt_bit_shift_by_one_5 (
    .in_1(sixt_bit_shift_by_one_3_out_2), .out_2(sixt_bit_shift_by_one_5_out_2));
  sixt_bit_shift_by_one sixt_bit_shift_by_one_6 (
    .in_1(sixt_bit_shift_by_one_4_out_2), .out_2(sixt_bit_shift_by_one_6_out_2));
  // gatekeeper gatekeeper_6: pin names not known; wires that end beside it: sixt_bit_shift_by_one_6_out_2, gatekeeper_6_p2, in_2[3]
  // gatekeeper gatekeeper_7: pin names not known; wires that end beside it: sixt_bit_shift_by_one_3_out_2, sixt_bit_adder_c_3_p3, in_2[10]
  // gatekeeper gatekeeper_8: pin names not known; wires that end beside it: sixt_bit_shift_by_one_5_out_2, gatekeeper_8_p2, in_2[11]
  // sixt_bit_adder_c sixt_bit_adder_c_5: pin names not known; wires that end beside it: gatekeeper_6_p2, sixt_bit_adder_c_5_p2, gatekeeper_8_p2, 1'b0
  sixt_bit_adder_c sixt_bit_adder_c_6 (
    .in_1(1'b0), .in_2(sixt_bit_adder_c_5_p2), .in_3(sixt_bit_adder_c_3_p2), .out_4(sixt_bit_adder_c_6_out_4));  // open: out_5
  sixt_bit_adder_c sixt_bit_adder_c_7 (
    .in_1(1'b0), .in_2(sixt_bit_adder_c_6_out_4), .in_3(sixt_bit_adder_c_4_out_4),
    .out_4(sixt_bit_adder_c_7_out_4));  // open: out_5
  sixt_bit_shift_by_one sixt_bit_shift_by_one_7 (
    .in_1(sixt_bit_shift_by_one_5_out_2), .out_2(sixt_bit_shift_by_one_7_out_2));
  sixt_bit_shift_by_one sixt_bit_shift_by_one_8 (
    .in_1(sixt_bit_shift_by_one_7_out_2), .out_2(sixt_bit_shift_by_one_8_out_2));
  sixt_bit_shift_by_one sixt_bit_shift_by_one_9 (
    .in_1(sixt_bit_shift_by_one_6_out_2), .out_2(sixt_bit_shift_by_one_9_out_2));
  sixt_bit_shift_by_one sixt_bit_shift_by_one_10 (
    .in_1(sixt_bit_shift_by_one_9_out_2), .out_2(sixt_bit_shift_by_one_10_out_2));
  // gatekeeper gatekeeper_9: pin names not known; wires that end beside it: sixt_bit_shift_by_one_9_out_2, gatekeeper_9_p2, in_2[4]
  // gatekeeper gatekeeper_10: pin names not known; wires that end beside it: sixt_bit_shift_by_one_7_out_2, gatekeeper_10_p2, in_2[12]
  // sixt_bit_adder_c sixt_bit_adder_c_8: pin names not known; wires that end beside it: gatekeeper_9_p2, sixt_bit_adder_c_8_p2, gatekeeper_10_p2, 1'b0
  sixt_bit_adder_c sixt_bit_adder_c_9 (
    .in_1(1'b0), .in_2(sixt_bit_adder_c_12_p2), .in_3(sixt_bit_adder_c_8_p2), .out_4(sixt_bit_adder_c_9_out_4));  // open: out_5
  sixt_bit_adder_c sixt_bit_adder_c_10 (
    .in_1(1'b0), .in_2(sixt_bit_adder_c_13_out_4), .in_3(sixt_bit_adder_c_9_out_4),
    .out_4(sixt_bit_adder_c_10_out_4));  // open: out_5
  sixt_bit_adder_c sixt_bit_adder_c_11 (
    .in_1(1'b0), .in_2(sixt_bit_adder_c_10_out_4), .in_3(sixt_bit_adder_c_7_out_4), .out_4(out_3));  // open: out_5
  sixt_bit_shift_by_one sixt_bit_shift_by_one_11 (
    .in_1(sixt_bit_shift_by_one_8_out_2), .out_2(sixt_bit_shift_by_one_11_out_2));
  sixt_bit_shift_by_one sixt_bit_shift_by_one_12 (
    .in_1(sixt_bit_shift_by_one_10_out_2), .out_2(sixt_bit_shift_by_one_12_out_2));
  // gatekeeper gatekeeper_11: pin names not known; wires that end beside it: sixt_bit_shift_by_one_10_out_2, gatekeeper_11_p2, in_2[5]
  // gatekeeper gatekeeper_12: pin names not known; wires that end beside it: sixt_bit_shift_by_one_8_out_2, gatekeeper_12_p2, in_2[13]
  // sixt_bit_adder_c sixt_bit_adder_c_12: pin names not known; wires that end beside it: gatekeeper_11_p2, sixt_bit_adder_c_12_p2, gatekeeper_12_p2, 1'b0
  sixt_bit_adder_c sixt_bit_adder_c_13 (
    .in_1(1'b0), .in_2(sixt_bit_adder_c_15_p2), .in_3(sixt_bit_adder_c_14_p2),
    .out_4(sixt_bit_adder_c_13_out_4));  // open: out_5
  sixt_bit_shift_by_one sixt_bit_shift_by_one_13 (
    .in_1(sixt_bit_shift_by_one_11_out_2), .out_2(sixt_bit_shift_by_one_13_out_2));
  sixt_bit_shift_by_one sixt_bit_shift_by_one_14 (
    .in_1(sixt_bit_shift_by_one_12_out_2), .out_2(sixt_bit_shift_by_one_14_out_2));
  // gatekeeper gatekeeper_13: pin names not known; wires that end beside it: sixt_bit_shift_by_one_12_out_2, gatekeeper_13_p2, in_2[6]
  // gatekeeper gatekeeper_14: pin names not known; wires that end beside it: sixt_bit_shift_by_one_14_out_2, gatekeeper_14_p2, in_2[7]
  // gatekeeper gatekeeper_15: pin names not known; wires that end beside it: sixt_bit_shift_by_one_11_out_2, gatekeeper_15_p2, in_2[14]
  // sixt_bit_adder_c sixt_bit_adder_c_14: pin names not known; wires that end beside it: gatekeeper_13_p2, sixt_bit_adder_c_14_p2, gatekeeper_15_p2, 1'b0
  sixt_bit_shift_by_one sixt_bit_shift_by_one_15 (
    .in_1(sixt_bit_shift_by_one_13_out_2), .out_2(sixt_bit_shift_by_one_15_out_2[15:0]));
  gatekeeper gatekeeper_16 (.in_1(in_2[15]), .in_2(sixt_bit_shift_by_one_15_out_2), .out_3(gatekeeper_16_out_3));
  // sixt_bit_adder_c sixt_bit_adder_c_15: pin names not known; wires that end beside it: gatekeeper_14_p2, sixt_bit_adder_c_15_p2, gatekeeper_16_out_3, 1'b0
  // Pins of 16 and 32 bits meet at sixt_bit_shift_by_one_15_out_2
endmodule

module sixt_bit_shift_by_one (
  input  [15:0] in_1,
  output [15:0] out_2
);


  assign out_2 = {in_1[14:0], 1'b0};
endmodule

module gatekeeper (
  input  in_1,
  input  [31:0] in_2,
  output [31:0] out_3
);

  assign out_3 = {32{in_1}} & in_2;  // AND_Gate and_1, 32 bits wide
endmodule

module sixt_bit_gatekeeper_vert (
  input  in_1,
  input  [15:0] in_2,
  output [15:0] out_3
);

  assign out_3 = {16{in_1}} & in_2;  // AND_Gate and_1, 16 bits wide
endmodule

module sixt_bit_multuiplier (
  input  [15:0] in_1,
  input  [15:0] in_2,
  output [15:0] out_3
);

  wire [15:0] sixt_bit_adder_1_out_3, sixt_bit_adder_2_out_3, sixt_bit_adder_3_out_3, sixt_bit_adder_4_out_3,
       sixt_bit_adder_5_out_3, sixt_bit_adder_6_out_3, sixt_bit_adder_7_out_3, sixt_bit_adder_8_out_3,
       sixt_bit_adder_9_out_3, sixt_bit_adder_10_out_3, sixt_bit_adder_11_out_3, sixt_bit_adder_12_out_3,
       sixt_bit_adder_13_out_3, sixt_bit_adder_14_out_3, sixt_bit_gatekeeper_vert_1_out_3,
       sixt_bit_gatekeeper_vert_2_out_3, sixt_bit_gatekeeper_vert_3_out_3, sixt_bit_gatekeeper_vert_4_out_3,
       sixt_bit_gatekeeper_vert_5_out_3, sixt_bit_gatekeeper_vert_6_out_3, sixt_bit_gatekeeper_vert_7_out_3,
       sixt_bit_gatekeeper_vert_8_out_3, sixt_bit_gatekeeper_vert_9_out_3, sixt_bit_gatekeeper_vert_10_out_3,
       sixt_bit_gatekeeper_vert_11_out_3, sixt_bit_gatekeeper_vert_12_out_3,
       sixt_bit_gatekeeper_vert_13_out_3, sixt_bit_gatekeeper_vert_14_out_3,
       sixt_bit_gatekeeper_vert_15_out_3, sixt_bit_gatekeeper_vert_16_out_3, sixt_bit_shift_by_one_1_out_2,
       sixt_bit_shift_by_one_2_out_2, sixt_bit_shift_by_one_3_out_2, sixt_bit_shift_by_one_4_out_2,
       sixt_bit_shift_by_one_5_out_2, sixt_bit_shift_by_one_6_out_2, sixt_bit_shift_by_one_7_out_2,
       sixt_bit_shift_by_one_8_out_2, sixt_bit_shift_by_one_9_out_2, sixt_bit_shift_by_one_10_out_2,
       sixt_bit_shift_by_one_11_out_2, sixt_bit_shift_by_one_12_out_2, sixt_bit_shift_by_one_13_out_2,
       sixt_bit_shift_by_one_14_out_2, sixt_bit_shift_by_one_15_out_2;

  sixt_bit_gatekeeper_vert sixt_bit_gatekeeper_vert_1 (
    .in_1(in_1[0]), .in_2(in_2), .out_3(sixt_bit_gatekeeper_vert_1_out_3));
  sixt_bit_shift_by_one sixt_bit_shift_by_one_1 (.in_1(in_2), .out_2(sixt_bit_shift_by_one_1_out_2));
  sixt_bit_shift_by_one sixt_bit_shift_by_one_2 (
    .in_1(sixt_bit_shift_by_one_1_out_2), .out_2(sixt_bit_shift_by_one_2_out_2));
  sixt_bit_gatekeeper_vert sixt_bit_gatekeeper_vert_2 (
    .in_1(in_1[1]), .in_2(sixt_bit_shift_by_one_1_out_2), .out_3(sixt_bit_gatekeeper_vert_2_out_3));
  sixt_bit_gatekeeper_vert sixt_bit_gatekeeper_vert_3 (
    .in_1(in_1[2]), .in_2(sixt_bit_shift_by_one_2_out_2), .out_3(sixt_bit_gatekeeper_vert_3_out_3));
  sixt_bit_adder sixt_bit_adder_1 (
    .in_1(sixt_bit_gatekeeper_vert_2_out_3), .in_2(sixt_bit_gatekeeper_vert_1_out_3),
    .out_3(sixt_bit_adder_1_out_3));  // open: out_4
  sixt_bit_shift_by_one sixt_bit_shift_by_one_3 (
    .in_1(sixt_bit_shift_by_one_2_out_2), .out_2(sixt_bit_shift_by_one_3_out_2));
  sixt_bit_gatekeeper_vert sixt_bit_gatekeeper_vert_4 (
    .in_1(in_1[3]), .in_2(sixt_bit_shift_by_one_3_out_2), .out_3(sixt_bit_gatekeeper_vert_4_out_3));
  sixt_bit_adder sixt_bit_adder_2 (
    .in_1(sixt_bit_gatekeeper_vert_3_out_3), .in_2(sixt_bit_adder_1_out_3), .out_3(sixt_bit_adder_2_out_3));  // open: out_4
  sixt_bit_adder sixt_bit_adder_3 (
    .in_1(sixt_bit_gatekeeper_vert_4_out_3), .in_2(sixt_bit_adder_2_out_3), .out_3(sixt_bit_adder_3_out_3));  // open: out_4
  sixt_bit_shift_by_one sixt_bit_shift_by_one_4 (
    .in_1(sixt_bit_shift_by_one_3_out_2), .out_2(sixt_bit_shift_by_one_4_out_2));
  sixt_bit_shift_by_one sixt_bit_shift_by_one_5 (
    .in_1(sixt_bit_shift_by_one_4_out_2), .out_2(sixt_bit_shift_by_one_5_out_2));
  sixt_bit_gatekeeper_vert sixt_bit_gatekeeper_vert_5 (
    .in_1(in_1[4]), .in_2(sixt_bit_shift_by_one_4_out_2), .out_3(sixt_bit_gatekeeper_vert_5_out_3));
  sixt_bit_gatekeeper_vert sixt_bit_gatekeeper_vert_6 (
    .in_1(in_1[5]), .in_2(sixt_bit_shift_by_one_5_out_2), .out_3(sixt_bit_gatekeeper_vert_6_out_3));
  sixt_bit_adder sixt_bit_adder_4 (
    .in_1(sixt_bit_gatekeeper_vert_5_out_3), .in_2(sixt_bit_adder_3_out_3), .out_3(sixt_bit_adder_4_out_3));  // open: out_4
  sixt_bit_shift_by_one sixt_bit_shift_by_one_6 (
    .in_1(sixt_bit_shift_by_one_5_out_2), .out_2(sixt_bit_shift_by_one_6_out_2));
  sixt_bit_gatekeeper_vert sixt_bit_gatekeeper_vert_7 (
    .in_1(in_1[6]), .in_2(sixt_bit_shift_by_one_6_out_2), .out_3(sixt_bit_gatekeeper_vert_7_out_3));
  sixt_bit_gatekeeper_vert sixt_bit_gatekeeper_vert_8 (
    .in_1(in_1[7]), .in_2(sixt_bit_shift_by_one_7_out_2), .out_3(sixt_bit_gatekeeper_vert_8_out_3));
  sixt_bit_adder sixt_bit_adder_5 (
    .in_1(sixt_bit_gatekeeper_vert_6_out_3), .in_2(sixt_bit_adder_4_out_3), .out_3(sixt_bit_adder_5_out_3));  // open: out_4
  sixt_bit_adder sixt_bit_adder_6 (
    .in_1(sixt_bit_gatekeeper_vert_7_out_3), .in_2(sixt_bit_adder_5_out_3), .out_3(sixt_bit_adder_6_out_3));  // open: out_4
  sixt_bit_shift_by_one sixt_bit_shift_by_one_7 (
    .in_1(sixt_bit_shift_by_one_6_out_2), .out_2(sixt_bit_shift_by_one_7_out_2));
  sixt_bit_shift_by_one sixt_bit_shift_by_one_8 (
    .in_1(sixt_bit_shift_by_one_7_out_2), .out_2(sixt_bit_shift_by_one_8_out_2));
  sixt_bit_gatekeeper_vert sixt_bit_gatekeeper_vert_9 (
    .in_1(in_1[8]), .in_2(sixt_bit_shift_by_one_8_out_2), .out_3(sixt_bit_gatekeeper_vert_9_out_3));
  sixt_bit_adder sixt_bit_adder_7 (
    .in_1(sixt_bit_gatekeeper_vert_8_out_3), .in_2(sixt_bit_adder_6_out_3), .out_3(sixt_bit_adder_7_out_3));  // open: out_4
  sixt_bit_adder sixt_bit_adder_8 (
    .in_1(sixt_bit_gatekeeper_vert_9_out_3), .in_2(sixt_bit_adder_7_out_3), .out_3(sixt_bit_adder_8_out_3));  // open: out_4
  sixt_bit_shift_by_one sixt_bit_shift_by_one_9 (
    .in_1(sixt_bit_shift_by_one_8_out_2), .out_2(sixt_bit_shift_by_one_9_out_2));
  sixt_bit_shift_by_one sixt_bit_shift_by_one_10 (
    .in_1(sixt_bit_shift_by_one_9_out_2), .out_2(sixt_bit_shift_by_one_10_out_2));
  sixt_bit_gatekeeper_vert sixt_bit_gatekeeper_vert_10 (
    .in_1(in_1[9]), .in_2(sixt_bit_shift_by_one_9_out_2), .out_3(sixt_bit_gatekeeper_vert_10_out_3));
  sixt_bit_gatekeeper_vert sixt_bit_gatekeeper_vert_11 (
    .in_1(in_1[10]), .in_2(sixt_bit_shift_by_one_10_out_2), .out_3(sixt_bit_gatekeeper_vert_11_out_3));
  sixt_bit_adder sixt_bit_adder_9 (
    .in_1(sixt_bit_gatekeeper_vert_10_out_3), .in_2(sixt_bit_adder_8_out_3), .out_3(sixt_bit_adder_9_out_3));  // open: out_4
  sixt_bit_shift_by_one sixt_bit_shift_by_one_11 (
    .in_1(sixt_bit_shift_by_one_10_out_2), .out_2(sixt_bit_shift_by_one_11_out_2));
  sixt_bit_gatekeeper_vert sixt_bit_gatekeeper_vert_12 (
    .in_1(in_1[11]), .in_2(sixt_bit_shift_by_one_11_out_2), .out_3(sixt_bit_gatekeeper_vert_12_out_3));
  sixt_bit_adder sixt_bit_adder_10 (
    .in_1(sixt_bit_gatekeeper_vert_11_out_3), .in_2(sixt_bit_adder_9_out_3), .out_3(sixt_bit_adder_10_out_3));  // open: out_4
  sixt_bit_adder sixt_bit_adder_11 (
    .in_1(sixt_bit_gatekeeper_vert_12_out_3), .in_2(sixt_bit_adder_10_out_3), .out_3(sixt_bit_adder_11_out_3));  // open: out_4
  sixt_bit_shift_by_one sixt_bit_shift_by_one_12 (
    .in_1(sixt_bit_shift_by_one_11_out_2), .out_2(sixt_bit_shift_by_one_12_out_2));
  sixt_bit_shift_by_one sixt_bit_shift_by_one_13 (
    .in_1(sixt_bit_shift_by_one_12_out_2), .out_2(sixt_bit_shift_by_one_13_out_2));
  sixt_bit_gatekeeper_vert sixt_bit_gatekeeper_vert_13 (
    .in_1(in_1[12]), .in_2(sixt_bit_shift_by_one_12_out_2), .out_3(sixt_bit_gatekeeper_vert_13_out_3));
  sixt_bit_gatekeeper_vert sixt_bit_gatekeeper_vert_14 (
    .in_1(in_1[13]), .in_2(sixt_bit_shift_by_one_13_out_2), .out_3(sixt_bit_gatekeeper_vert_14_out_3));
  sixt_bit_adder sixt_bit_adder_12 (
    .in_1(sixt_bit_gatekeeper_vert_13_out_3), .in_2(sixt_bit_adder_11_out_3), .out_3(sixt_bit_adder_12_out_3));  // open: out_4
  sixt_bit_shift_by_one sixt_bit_shift_by_one_14 (
    .in_1(sixt_bit_shift_by_one_13_out_2), .out_2(sixt_bit_shift_by_one_14_out_2));
  sixt_bit_gatekeeper_vert sixt_bit_gatekeeper_vert_15 (
    .in_1(in_1[14]), .in_2(sixt_bit_shift_by_one_14_out_2), .out_3(sixt_bit_gatekeeper_vert_15_out_3));
  sixt_bit_gatekeeper_vert sixt_bit_gatekeeper_vert_16 (
    .in_1(in_1[15]), .in_2(sixt_bit_shift_by_one_15_out_2), .out_3(sixt_bit_gatekeeper_vert_16_out_3));
  sixt_bit_adder sixt_bit_adder_13 (
    .in_1(sixt_bit_gatekeeper_vert_14_out_3), .in_2(sixt_bit_adder_12_out_3), .out_3(sixt_bit_adder_13_out_3));  // open: out_4
  sixt_bit_adder sixt_bit_adder_14 (
    .in_1(sixt_bit_gatekeeper_vert_15_out_3), .in_2(sixt_bit_adder_13_out_3), .out_3(sixt_bit_adder_14_out_3));  // open: out_4
  sixt_bit_shift_by_one sixt_bit_shift_by_one_15 (
    .in_1(sixt_bit_shift_by_one_14_out_2), .out_2(sixt_bit_shift_by_one_15_out_2));
  sixt_bit_adder sixt_bit_adder_15 (
    .in_1(sixt_bit_gatekeeper_vert_16_out_3), .in_2(sixt_bit_adder_14_out_3), .out_3(out_3));  // open: out_4
endmodule

module sixt_bit_eq_cmp (
  input  [15:0] in_1,
  input  [15:0] in_2,
  output out_3
);

  wire or_1_out;
  wire [15:0] xor_1_out;

  xor xor_1 (xor_1_out[0], in_1[0], in_2[0]);
  xor xor_2 (xor_1_out[1], in_1[1], in_2[1]);
  xor xor_3 (xor_1_out[2], in_1[2], in_2[2]);
  xor xor_4 (xor_1_out[3], in_1[3], in_2[3]);
  xor xor_5 (xor_1_out[4], in_1[4], in_2[4]);
  xor xor_6 (xor_1_out[5], in_1[5], in_2[5]);
  xor xor_7 (xor_1_out[6], in_1[6], in_2[6]);
  xor xor_8 (xor_1_out[7], in_1[7], in_2[7]);
  xor xor_9 (xor_1_out[8], in_1[8], in_2[8]);
  xor xor_10 (xor_1_out[9], in_1[9], in_2[9]);
  xor xor_11 (xor_1_out[10], in_1[10], in_2[10]);
  xor xor_12 (xor_1_out[11], in_1[11], in_2[11]);
  xor xor_13 (xor_1_out[12], in_1[12], in_2[12]);
  xor xor_14 (xor_1_out[13], in_1[13], in_2[13]);
  xor xor_15 (xor_1_out[14], in_1[14], in_2[14]);
  xor xor_16 (xor_1_out[15], in_1[15], in_2[15]);
  or or_1 (or_1_out, xor_1_out[0], xor_1_out[1], xor_1_out[2], xor_1_out[3], xor_1_out[4], xor_1_out[5], xor_1_out[6], xor_1_out[7], xor_1_out[8], xor_1_out[9], xor_1_out[10], xor_1_out[11], xor_1_out[12], xor_1_out[13], xor_1_out[14], xor_1_out[15]);
  not not_1 (out_3, or_1_out);
endmodule

module eight_bit_eq_cmp (
  input  [7:0] in_1,
  input  [7:0] in_2,
  output out_3
);

  wire xor_1_out, xor_2_out, xor_3_out, xor_4_out, xor_5_out, xor_6_out, xor_7_out, xor_8_out;

  xor xor_1 (xor_1_out, in_1[0], in_2[0]);
  xor xor_2 (xor_2_out, in_1[1], in_2[1]);
  xor xor_3 (xor_3_out, in_1[2], in_2[2]);
  xor xor_4 (xor_4_out, in_1[3], in_2[3]);
  xor xor_5 (xor_5_out, in_1[4], in_2[4]);
  xor xor_6 (xor_6_out, in_1[5], in_2[5]);
  xor xor_7 (xor_7_out, in_1[6], in_2[6]);
  xor xor_8 (xor_8_out, in_1[7], in_2[7]);
  nor nor_1 (out_3, xor_1_out, xor_2_out, xor_3_out, xor_4_out, xor_5_out, xor_6_out, xor_7_out, xor_8_out);
endmodule

module four_bit_eq_cmp (
  input  [3:0] in_1,
  input  [3:0] in_2,
  output out_3
);

  wire xor_1_out, xor_2_out, xor_3_out, xor_4_out;

  xor xor_1 (xor_1_out, in_1[0], in_2[0]);
  xor xor_2 (xor_2_out, in_1[1], in_2[1]);
  xor xor_3 (xor_3_out, in_1[2], in_2[2]);
  xor xor_4 (xor_4_out, in_1[3], in_2[3]);
  nor nor_1 (out_3, xor_1_out, xor_2_out, xor_3_out, xor_4_out);
endmodule

module four_bit_x_or_y (
  input  [3:0] in_1,
  input  [3:0] in_2,
  input  [3:0] in_3,
  output out_4
);

  wire four_bit_eq_cmp_1_out_3, four_bit_eq_cmp_2_out_3;

  four_bit_eq_cmp four_bit_eq_cmp_1 (.in_1(in_1), .in_2(in_2), .out_3(four_bit_eq_cmp_1_out_3));
  or or_1 (out_4, four_bit_eq_cmp_1_out_3, four_bit_eq_cmp_2_out_3);
  four_bit_eq_cmp four_bit_eq_cmp_2 (.in_1(in_1), .in_2(in_3), .out_3(four_bit_eq_cmp_2_out_3));
endmodule

module sixt_bit_controlled_swapper (
  input  [15:0] in_1,
  input  [15:0] in_2,
  input  in_3,
  output [15:0] out_4,
  output [15:0] out_5
);

  // sixt_bit_selector sixt_bit_selector_1: pin names not known; wires that end beside it: in_3, in_1, in_2, out_4, out_5
  // sixt_bit_selector sixt_bit_selector_2: pin names not known; wires that end beside it: in_3, in_2, in_1, out_4, out_5
endmodule

module sixt_bit_comparator (
  input  [15:0] in_1,
  input  [15:0] in_2,
  output out_3,
  output out_4
);

  wire and_1_out, and_2_out, and_3_out, and_4_out, and_5_out, and_6_out, and_7_out, and_8_out, and_9_out,
       and_10_out, and_11_out, and_12_out, and_13_out, and_14_out, and_15_out, and_16_out, and_17_out,
       and_18_out, and_19_out, and_20_out, and_21_out, and_22_out, and_23_out, and_24_out, and_25_out,
       and_26_out, and_27_out, and_28_out, and_29_out, and_30_out, or_1_out, or_2_out, or_3_out, or_4_out,
       or_5_out, or_6_out, or_7_out, or_8_out, or_9_out, or_10_out, or_11_out, or_12_out, or_13_out,
       or_14_out, or_15_out, or_17_out, or_18_out, or_19_out, or_20_out, or_21_out, or_22_out, or_23_out,
       or_24_out, or_25_out, or_26_out, or_27_out, or_28_out, or_29_out, or_30_out, xor_1_out, xor_2_out,
       xor_3_out, xor_4_out, xor_5_out, xor_6_out, xor_7_out, xor_8_out, xor_9_out, xor_10_out, xor_11_out,
       xor_12_out, xor_13_out, xor_14_out, xor_15_out, xor_16_out;

  xor xor_1 (xor_1_out, in_1[0], in_2[0]);
  xor xor_2 (xor_2_out, in_1[1], in_2[1]);
  xor xor_3 (xor_3_out, in_1[2], in_2[2]);
  xor xor_4 (xor_4_out, in_1[3], in_2[3]);
  xor xor_5 (xor_5_out, in_1[4], in_2[4]);
  xor xor_6 (xor_6_out, in_1[5], in_2[5]);
  xor xor_7 (xor_7_out, in_1[6], in_2[6]);
  xor xor_8 (xor_8_out, in_1[7], in_2[7]);
  xor xor_9 (xor_9_out, in_1[8], in_2[8]);
  xor xor_10 (xor_10_out, in_1[9], in_2[9]);
  xor xor_11 (xor_11_out, in_1[10], in_2[10]);
  xor xor_12 (xor_12_out, in_1[11], in_2[11]);
  xor xor_13 (xor_13_out, in_1[12], in_2[12]);
  xor xor_14 (xor_14_out, in_1[13], in_2[13]);
  xor xor_15 (xor_15_out, in_1[14], in_2[14]);
  xor xor_16 (xor_16_out, in_1[15], in_2[15]);
  or or_1 (or_1_out, or_2_out, xor_1_out);
  and and_1 (and_1_out, xor_1_out, ~or_2_out);  // AND_Gate
  or or_2 (or_2_out, or_3_out, xor_2_out);
  and and_2 (and_2_out, xor_2_out, ~or_3_out);  // AND_Gate
  or or_3 (or_3_out, or_4_out, xor_3_out);
  and and_3 (and_3_out, xor_3_out, ~or_4_out);  // AND_Gate
  or or_4 (or_4_out, or_5_out, xor_4_out);
  and and_4 (and_4_out, xor_4_out, ~or_5_out);  // AND_Gate
  or or_5 (or_5_out, or_6_out, xor_5_out);
  and and_5 (and_5_out, xor_5_out, ~or_6_out);  // AND_Gate
  or or_6 (or_6_out, or_7_out, xor_6_out);
  and and_6 (and_6_out, xor_6_out, ~or_7_out);  // AND_Gate
  or or_7 (or_7_out, or_8_out, xor_7_out);
  and and_7 (and_7_out, xor_7_out, ~or_8_out);  // AND_Gate
  or or_8 (or_8_out, or_9_out, xor_8_out);
  and and_8 (and_8_out, xor_8_out, ~or_9_out);  // AND_Gate
  or or_9 (or_9_out, or_10_out, xor_9_out);
  and and_9 (and_9_out, xor_9_out, ~or_10_out);  // AND_Gate
  or or_10 (or_10_out, or_11_out, xor_10_out);
  and and_10 (and_10_out, xor_10_out, ~or_11_out);  // AND_Gate
  or or_11 (or_11_out, or_12_out, xor_11_out);
  and and_11 (and_11_out, xor_11_out, ~or_12_out);  // AND_Gate
  or or_12 (or_12_out, or_13_out, xor_12_out);
  and and_12 (and_12_out, xor_12_out, ~or_13_out);  // AND_Gate
  or or_13 (or_13_out, or_14_out, xor_13_out);
  and and_13 (and_13_out, xor_13_out, ~or_14_out);  // AND_Gate
  or or_14 (or_14_out, or_15_out, xor_14_out);
  and and_14 (and_14_out, xor_14_out, ~or_15_out);  // AND_Gate
  or or_15 (or_15_out, xor_16_out, xor_15_out);
  and and_15 (and_15_out, xor_15_out, ~xor_16_out);  // AND_Gate
  and and_16 (and_16_out, and_1_out, in_1[0]);
  or or_16 (out_3, and_16_out, or_17_out);
  and and_17 (and_17_out, and_2_out, in_1[1]);
  or or_17 (or_17_out, and_17_out, or_18_out);
  and and_18 (and_18_out, and_3_out, in_1[2]);
  or or_18 (or_18_out, and_18_out, or_19_out);
  and and_19 (and_19_out, and_4_out, in_1[3]);
  or or_19 (or_19_out, and_19_out, or_20_out);
  and and_20 (and_20_out, and_5_out, in_1[4]);
  or or_20 (or_20_out, and_20_out, or_21_out);
  and and_21 (and_21_out, and_6_out, in_1[5]);
  or or_21 (or_21_out, and_21_out, or_22_out);
  and and_22 (and_22_out, and_7_out, in_1[6]);
  or or_22 (or_22_out, and_22_out, or_23_out);
  and and_23 (and_23_out, and_8_out, in_1[7]);
  or or_23 (or_23_out, and_23_out, or_24_out);
  and and_24 (and_24_out, and_9_out, in_1[8]);
  or or_24 (or_24_out, and_24_out, or_25_out);
  and and_25 (and_25_out, and_10_out, in_1[9]);
  or or_25 (or_25_out, and_25_out, or_26_out);
  and and_26 (and_26_out, and_11_out, in_1[10]);
  or or_26 (or_26_out, and_26_out, or_27_out);
  and and_27 (and_27_out, and_12_out, in_1[11]);
  or or_27 (or_27_out, and_27_out, or_28_out);
  and and_28 (and_28_out, and_13_out, in_1[12]);
  or or_28 (or_28_out, and_28_out, or_29_out);
  and and_29 (and_29_out, and_14_out, in_1[13]);
  or or_29 (or_29_out, and_29_out, or_30_out);
  and and_30 (and_30_out, and_15_out, in_1[14]);
  or or_30 (or_30_out, and_30_out, xor_16_out);
  and and_31 (out_4, ~out_3, or_1_out);  // AND_Gate
endmodule

module sixt_bit_eq_zero (
  input  [15:0] in_1,
  output out_2
);

  wire [15:0] not_1_out;

  assign not_1_out = ~in_1;  // NOT_Gate not_1, 16 bits wide
  and and_1 (out_2, not_1_out[0], not_1_out[1], not_1_out[2], not_1_out[3], not_1_out[4], not_1_out[5], not_1_out[6], not_1_out[7], not_1_out[8], not_1_out[9], not_1_out[10], not_1_out[11], not_1_out[12], not_1_out[13], not_1_out[14], not_1_out[15]);
endmodule

module long_eq_zero (
  input  [31:0] in_1,
  output out_2
);

  wire [31:0] not_1_out;

  assign not_1_out = ~in_1;  // NOT_Gate not_1, 32 bits wide
  and and_1 (out_2, not_1_out[0], not_1_out[1], not_1_out[2], not_1_out[3], not_1_out[4], not_1_out[5], not_1_out[6], not_1_out[7], not_1_out[8], not_1_out[9], not_1_out[10], not_1_out[11], not_1_out[12], not_1_out[13], not_1_out[14], not_1_out[15], not_1_out[16], not_1_out[17], not_1_out[18], not_1_out[19], not_1_out[20], not_1_out[21], not_1_out[22], not_1_out[23], not_1_out[24], not_1_out[25], not_1_out[26], not_1_out[27], not_1_out[28], not_1_out[29], not_1_out[30], not_1_out[31]);
endmodule

module sixt_bit_looping_incrementer (
  input  [15:0] in_1,
  input  [15:0] in_2,
  output [15:0] out_3
);

  wire and_1_out, sixt_bit_comparator_1_out_3, sixt_bit_comparator_1_out_4;
  wire [15:0] sixt_bit_incrementer_1_out_2;

  sixt_bit_incrementer sixt_bit_incrementer_1 (.in_1(in_1), .out_2(sixt_bit_incrementer_1_out_2));
  sixt_bit_comparator sixt_bit_comparator_1 (
    .in_1(sixt_bit_incrementer_1_out_2), .in_2(in_2), .out_3(sixt_bit_comparator_1_out_3),
    .out_4(sixt_bit_comparator_1_out_4));
  sixt_bit_gatekeeper_vert sixt_bit_gatekeeper_vert_1 (
    .in_1(and_1_out), .in_2(sixt_bit_incrementer_1_out_2), .out_3(out_3));
  and and_1 (and_1_out, ~sixt_bit_comparator_1_out_3, sixt_bit_comparator_1_out_4);  // AND_Gate
endmodule

module sixt_bit_looping_counter (
  input  [15:0] in_1,
  input  in_2,
  input  in_3,
  output [15:0] out_4
);

  wire and_1_out, sixt_bit_comparator_1_out_3, sixt_bit_comparator_1_out_4;
  wire [15:0] gatekeeper_1_p3, sixt_bit_incrementer_1_out_2;

  Register #(.width(16)) register_1 (.D(gatekeeper_1_p3), .en(1'b1), .clk(in_2), .Q(out_4), .clr(in_3));
  sixt_bit_incrementer sixt_bit_incrementer_1 (.in_1(out_4), .out_2(sixt_bit_incrementer_1_out_2));
  sixt_bit_comparator sixt_bit_comparator_1 (
    .in_1(sixt_bit_incrementer_1_out_2), .in_2(in_1), .out_3(sixt_bit_comparator_1_out_3),
    .out_4(sixt_bit_comparator_1_out_4));
  and and_1 (and_1_out, sixt_bit_comparator_1_out_4, ~sixt_bit_comparator_1_out_3);  // AND_Gate
  // gatekeeper gatekeeper_1: pin names not known; wires that end beside it: sixt_bit_incrementer_1_out_2, and_1_out, gatekeeper_1_p3
endmodule

module sixt_bit_counter (
  input  in_1,
  input  in_2,
  output [15:0] out_3
);

  wire [15:0] sixt_bit_incrementer_1_out_2;

  Register #(.width(16)) register_1 (.D(sixt_bit_incrementer_1_out_2), .en(1'b1), .clk(in_1), .Q(out_3), .clr(in_2));
  sixt_bit_incrementer sixt_bit_incrementer_1 (.in_1(out_3), .out_2(sixt_bit_incrementer_1_out_2));
endmodule

module register_unit (
  input  Write,
  input  Data_out,
  input  Addr_out,
  input  ALU_Out,
  input  [3:0] in_5,
  input  [3:0] in_6,
  input  [3:0] in_7,
  input  [15:0] in_8,
  input  in_9,
  input  in_10,
  output [15:0] out_11,
  output [15:0] out_12,
  output [15:0] out_13,
  output [15:0] out_14
);

  wire and_1_out, and_2_out, and_3_out, and_4_out, and_5_out, and_6_out, and_7_out, and_8_out, and_9_out,
       and_10_out, and_11_out, and_12_out, and_13_out, and_14_out, and_15_out, and_16_out,
       four_bit_eq_cmp_1_out_3, four_bit_eq_cmp_2_out_3, four_bit_eq_cmp_3_out_3, four_bit_eq_cmp_4_out_3,
       four_bit_eq_cmp_5_out_3, four_bit_eq_cmp_6_out_3, four_bit_eq_cmp_7_out_3, four_bit_eq_cmp_8_out_3,
       four_bit_eq_cmp_9_out_3, four_bit_eq_cmp_10_out_3, four_bit_eq_cmp_11_out_3, four_bit_eq_cmp_12_out_3,
       four_bit_eq_cmp_13_out_3, four_bit_eq_cmp_14_out_3, four_bit_eq_cmp_15_out_3,
       four_bit_eq_cmp_16_out_3, four_bit_eq_cmp_17_out_3, four_bit_eq_cmp_18_out_3,
       four_bit_eq_cmp_19_out_3, four_bit_eq_cmp_20_out_3, four_bit_eq_cmp_21_out_3,
       four_bit_eq_cmp_22_out_3, four_bit_eq_cmp_23_out_3, four_bit_eq_cmp_24_out_3,
       four_bit_eq_cmp_25_out_3, four_bit_eq_cmp_26_out_3, four_bit_eq_cmp_27_out_3,
       four_bit_eq_cmp_28_out_3, four_bit_eq_cmp_29_out_3, four_bit_eq_cmp_30_out_3,
       four_bit_eq_cmp_31_out_3, four_bit_eq_cmp_32_out_3, four_bit_eq_cmp_33_out_3,
       four_bit_eq_cmp_34_out_3, four_bit_eq_cmp_35_out_3, four_bit_eq_cmp_36_out_3,
       four_bit_eq_cmp_37_out_3, four_bit_eq_cmp_38_out_3, four_bit_eq_cmp_39_out_3,
       four_bit_eq_cmp_40_out_3, four_bit_eq_cmp_41_out_3, four_bit_eq_cmp_42_out_3,
       four_bit_eq_cmp_43_out_3, four_bit_eq_cmp_44_out_3, four_bit_eq_cmp_45_out_3,
       four_bit_eq_cmp_46_out_3, four_bit_eq_cmp_47_out_3, four_bit_eq_cmp_48_out_3;
  wire [3:0] four_bit_incrementer_1_out_2, four_bit_incrementer_2_out_2, four_bit_incrementer_3_out_2,
       four_bit_incrementer_4_out_2, four_bit_incrementer_5_out_2, four_bit_incrementer_6_out_2,
       four_bit_incrementer_7_out_2, four_bit_incrementer_8_out_2, four_bit_incrementer_9_out_2,
       four_bit_incrementer_10_out_2, four_bit_incrementer_11_out_2, four_bit_incrementer_12_out_2,
       four_bit_incrementer_13_out_2, four_bit_incrementer_14_out_2, four_bit_incrementer_15_out_2;
  wire [15:0] gatekeeper_1_p3, gatekeeper_2_p3, gatekeeper_3_p3, gatekeeper_4_p3, gatekeeper_5_p3,
       gatekeeper_6_p3, gatekeeper_7_p3, gatekeeper_8_p3, gatekeeper_11_p1, gatekeeper_12_p3,
       gatekeeper_13_p3, gatekeeper_14_p3, gatekeeper_15_p3, gatekeeper_16_p3, gatekeeper_17_p3,
       gatekeeper_18_p3, gatekeeper_19_p3, gatekeeper_21_p3, gatekeeper_22_p3, gatekeeper_23_p3,
       gatekeeper_24_p3, gatekeeper_25_p3, gatekeeper_26_p3, gatekeeper_27_p3, gatekeeper_28_p3, or_1_out,
       or_2_out, or_3_out, or_4_out, or_5_out, or_6_out, or_7_out, or_8_out, or_9_out, or_10_out, or_11_out,
       or_12_out, or_13_out, or_14_out, or_15_out, or_16_out, or_17_out, or_18_out, or_19_out, or_20_out,
       or_21_out, or_22_out, or_23_out, or_24_out, or_25_out, or_26_out, or_27_out, or_28_out, or_29_out,
       or_31_out, or_32_out, or_33_out, or_34_out, or_35_out, or_36_out, or_37_out, or_38_out, or_39_out,
       or_40_out, or_41_out, or_42_out, or_43_out, or_44_out, or_45_out, register_1_q, register_2_q,
       register_3_q, register_4_q, register_5_q, register_6_q, register_7_q, register_8_q, register_9_q,
       register_10_q, register_11_q, register_12_q, register_13_q, register_14_q, register_15_q,
       register_16_q, sixt_bit_gatekeeper_vert_1_out_3, sixt_bit_gatekeeper_vert_2_out_3,
       sixt_bit_gatekeeper_vert_3_out_3, sixt_bit_gatekeeper_vert_4_out_3, sixt_bit_gatekeeper_vert_5_out_3,
       sixt_bit_gatekeeper_vert_6_out_3, sixt_bit_gatekeeper_vert_7_out_3, sixt_bit_gatekeeper_vert_8_out_3,
       sixt_bit_gatekeeper_vert_9_out_3, sixt_bit_gatekeeper_vert_10_out_3,
       sixt_bit_gatekeeper_vert_11_out_3, sixt_bit_gatekeeper_vert_12_out_3,
       sixt_bit_gatekeeper_vert_13_out_3, sixt_bit_gatekeeper_vert_14_out_3,
       sixt_bit_gatekeeper_vert_15_out_3, sixt_bit_gatekeeper_vert_16_out_3,
       sixt_bit_gatekeeper_vert_17_out_3, sixt_bit_gatekeeper_vert_18_out_3,
       sixt_bit_gatekeeper_vert_19_out_3, sixt_bit_gatekeeper_vert_20_out_3,
       sixt_bit_gatekeeper_vert_21_out_3, sixt_bit_gatekeeper_vert_22_out_3,
       sixt_bit_gatekeeper_vert_23_out_3, sixt_bit_gatekeeper_vert_24_out_3;

  four_bit_incrementer four_bit_incrementer_1 (.in_1(4'b0000), .out_2(four_bit_incrementer_1_out_2));
  four_bit_incrementer four_bit_incrementer_2 (
    .in_1(four_bit_incrementer_1_out_2), .out_2(four_bit_incrementer_2_out_2));
  four_bit_incrementer four_bit_incrementer_3 (
    .in_1(four_bit_incrementer_2_out_2), .out_2(four_bit_incrementer_3_out_2));
  four_bit_incrementer four_bit_incrementer_4 (
    .in_1(four_bit_incrementer_3_out_2), .out_2(four_bit_incrementer_4_out_2));
  four_bit_incrementer four_bit_incrementer_5 (
    .in_1(four_bit_incrementer_4_out_2), .out_2(four_bit_incrementer_5_out_2));
  four_bit_incrementer four_bit_incrementer_6 (
    .in_1(four_bit_incrementer_5_out_2), .out_2(four_bit_incrementer_6_out_2));
  four_bit_incrementer four_bit_incrementer_7 (
    .in_1(four_bit_incrementer_6_out_2), .out_2(four_bit_incrementer_7_out_2));
  four_bit_eq_cmp four_bit_eq_cmp_1 (.in_1(in_5), .in_2(4'b0000), .out_3(four_bit_eq_cmp_1_out_3));
  four_bit_eq_cmp four_bit_eq_cmp_2 (.in_1(in_5), .in_2(four_bit_incrementer_1_out_2), .out_3(four_bit_eq_cmp_2_out_3));
  four_bit_eq_cmp four_bit_eq_cmp_3 (.in_1(in_5), .in_2(four_bit_incrementer_2_out_2), .out_3(four_bit_eq_cmp_3_out_3));
  four_bit_eq_cmp four_bit_eq_cmp_4 (.in_1(in_5), .in_2(four_bit_incrementer_3_out_2), .out_3(four_bit_eq_cmp_4_out_3));
  four_bit_eq_cmp four_bit_eq_cmp_5 (.in_1(in_5), .in_2(four_bit_incrementer_4_out_2), .out_3(four_bit_eq_cmp_5_out_3));
  four_bit_eq_cmp four_bit_eq_cmp_6 (.in_1(in_5), .in_2(four_bit_incrementer_5_out_2), .out_3(four_bit_eq_cmp_6_out_3));
  four_bit_eq_cmp four_bit_eq_cmp_7 (.in_1(in_5), .in_2(four_bit_incrementer_6_out_2), .out_3(four_bit_eq_cmp_7_out_3));
  four_bit_eq_cmp four_bit_eq_cmp_8 (.in_1(in_5), .in_2(four_bit_incrementer_7_out_2), .out_3(four_bit_eq_cmp_8_out_3));
  four_bit_incrementer four_bit_incrementer_8 (
    .in_1(four_bit_incrementer_7_out_2), .out_2(four_bit_incrementer_8_out_2));
  four_bit_eq_cmp four_bit_eq_cmp_9 (.in_1(in_7), .in_2(4'b0000), .out_3(four_bit_eq_cmp_9_out_3));
  four_bit_eq_cmp four_bit_eq_cmp_10 (.in_1(in_6), .in_2(4'b0000), .out_3(four_bit_eq_cmp_10_out_3));
  four_bit_eq_cmp four_bit_eq_cmp_11 (
    .in_1(in_7), .in_2(four_bit_incrementer_1_out_2), .out_3(four_bit_eq_cmp_11_out_3));
  four_bit_eq_cmp four_bit_eq_cmp_12 (
    .in_1(in_6), .in_2(four_bit_incrementer_1_out_2), .out_3(four_bit_eq_cmp_12_out_3));
  four_bit_eq_cmp four_bit_eq_cmp_13 (
    .in_1(in_7), .in_2(four_bit_incrementer_2_out_2), .out_3(four_bit_eq_cmp_13_out_3));
  four_bit_eq_cmp four_bit_eq_cmp_14 (
    .in_1(in_6), .in_2(four_bit_incrementer_2_out_2), .out_3(four_bit_eq_cmp_14_out_3));
  four_bit_eq_cmp four_bit_eq_cmp_15 (
    .in_1(in_7), .in_2(four_bit_incrementer_3_out_2), .out_3(four_bit_eq_cmp_15_out_3));
  four_bit_eq_cmp four_bit_eq_cmp_16 (
    .in_1(in_6), .in_2(four_bit_incrementer_3_out_2), .out_3(four_bit_eq_cmp_16_out_3));
  four_bit_eq_cmp four_bit_eq_cmp_17 (
    .in_1(in_7), .in_2(four_bit_incrementer_4_out_2), .out_3(four_bit_eq_cmp_17_out_3));
  four_bit_eq_cmp four_bit_eq_cmp_18 (
    .in_1(in_6), .in_2(four_bit_incrementer_4_out_2), .out_3(four_bit_eq_cmp_18_out_3));
  four_bit_eq_cmp four_bit_eq_cmp_19 (
    .in_1(in_7), .in_2(four_bit_incrementer_5_out_2), .out_3(four_bit_eq_cmp_19_out_3));
  four_bit_eq_cmp four_bit_eq_cmp_20 (
    .in_1(in_6), .in_2(four_bit_incrementer_5_out_2), .out_3(four_bit_eq_cmp_20_out_3));
  four_bit_eq_cmp four_bit_eq_cmp_21 (
    .in_1(in_7), .in_2(four_bit_incrementer_6_out_2), .out_3(four_bit_eq_cmp_21_out_3));
  four_bit_eq_cmp four_bit_eq_cmp_22 (
    .in_1(in_6), .in_2(four_bit_incrementer_6_out_2), .out_3(four_bit_eq_cmp_22_out_3));
  four_bit_eq_cmp four_bit_eq_cmp_23 (
    .in_1(in_7), .in_2(four_bit_incrementer_7_out_2), .out_3(four_bit_eq_cmp_23_out_3));
  four_bit_eq_cmp four_bit_eq_cmp_24 (
    .in_1(in_6), .in_2(four_bit_incrementer_7_out_2), .out_3(four_bit_eq_cmp_24_out_3));
  Register #(.width(16)) register_1 (.D(in_8), .en(and_1_out), .clk(in_9), .Q(register_1_q), .clr(in_10));
  and and_1 (and_1_out, Write, four_bit_eq_cmp_1_out_3);
  Register #(.width(16)) register_2 (.D(in_8), .en(and_2_out), .clk(in_9), .Q(register_2_q), .clr(in_10));
  and and_2 (and_2_out, Write, four_bit_eq_cmp_2_out_3);
  Register #(.width(16)) register_3 (.D(in_8), .en(and_3_out), .clk(in_9), .Q(register_3_q), .clr(in_10));
  and and_3 (and_3_out, Write, four_bit_eq_cmp_3_out_3);
  Register #(.width(16)) register_4 (.D(in_8), .en(and_4_out), .clk(in_9), .Q(register_4_q), .clr(in_10));
  and and_4 (and_4_out, Write, four_bit_eq_cmp_4_out_3);
  Register #(.width(16)) register_5 (.D(in_8), .en(and_5_out), .clk(in_9), .Q(register_5_q), .clr(in_10));
  and and_5 (and_5_out, Write, four_bit_eq_cmp_5_out_3);
  Register #(.width(16)) register_6 (.D(in_8), .en(and_6_out), .clk(in_9), .Q(register_6_q), .clr(in_10));
  and and_6 (and_6_out, Write, four_bit_eq_cmp_6_out_3);
  Register #(.width(16)) register_7 (.D(in_8), .en(and_7_out), .clk(in_9), .Q(register_7_q), .clr(in_10));
  and and_7 (and_7_out, Write, four_bit_eq_cmp_7_out_3);
  Register #(.width(16)) register_8 (.D(in_8), .en(and_8_out), .clk(in_9), .Q(register_8_q), .clr(in_10));
  and and_8 (and_8_out, Write, four_bit_eq_cmp_8_out_3);
  sixt_bit_gatekeeper_vert sixt_bit_gatekeeper_vert_1 (
    .in_1(four_bit_eq_cmp_2_out_3), .in_2(register_2_q), .out_3(sixt_bit_gatekeeper_vert_1_out_3));
  assign or_1_out = sixt_bit_gatekeeper_vert_1_out_3 | sixt_bit_gatekeeper_vert_8_out_3;  // OR_Gate or_1, 16 bits wide
  sixt_bit_gatekeeper_vert sixt_bit_gatekeeper_vert_2 (
    .in_1(four_bit_eq_cmp_3_out_3), .in_2(register_3_q), .out_3(sixt_bit_gatekeeper_vert_2_out_3));
  assign or_2_out = sixt_bit_gatekeeper_vert_2_out_3 | or_1_out;  // OR_Gate or_2, 16 bits wide
  sixt_bit_gatekeeper_vert sixt_bit_gatekeeper_vert_3 (
    .in_1(four_bit_eq_cmp_4_out_3), .in_2(register_4_q), .out_3(sixt_bit_gatekeeper_vert_3_out_3));
  assign or_3_out = sixt_bit_gatekeeper_vert_3_out_3 | or_2_out;  // OR_Gate or_3, 16 bits wide
  sixt_bit_gatekeeper_vert sixt_bit_gatekeeper_vert_4 (
    .in_1(four_bit_eq_cmp_5_out_3), .in_2(register_5_q), .out_3(sixt_bit_gatekeeper_vert_4_out_3));
  assign or_4_out = sixt_bit_gatekeeper_vert_4_out_3 | or_3_out;  // OR_Gate or_4, 16 bits wide
  sixt_bit_gatekeeper_vert sixt_bit_gatekeeper_vert_5 (
    .in_1(four_bit_eq_cmp_6_out_3), .in_2(register_6_q), .out_3(sixt_bit_gatekeeper_vert_5_out_3));
  assign or_5_out = sixt_bit_gatekeeper_vert_5_out_3 | or_4_out;  // OR_Gate or_5, 16 bits wide
  sixt_bit_gatekeeper_vert sixt_bit_gatekeeper_vert_6 (
    .in_1(four_bit_eq_cmp_7_out_3), .in_2(register_7_q), .out_3(sixt_bit_gatekeeper_vert_6_out_3));
  assign or_6_out = sixt_bit_gatekeeper_vert_6_out_3 | or_5_out;  // OR_Gate or_6, 16 bits wide
  sixt_bit_gatekeeper_vert sixt_bit_gatekeeper_vert_7 (
    .in_1(four_bit_eq_cmp_8_out_3), .in_2(register_8_q), .out_3(sixt_bit_gatekeeper_vert_7_out_3));
  assign or_7_out = sixt_bit_gatekeeper_vert_7_out_3 | or_6_out;  // OR_Gate or_7, 16 bits wide
  sixt_bit_gatekeeper_vert sixt_bit_gatekeeper_vert_8 (
    .in_1(four_bit_eq_cmp_1_out_3), .in_2(register_1_q), .out_3(sixt_bit_gatekeeper_vert_8_out_3));
  sixt_bit_gatekeeper_vert sixt_bit_gatekeeper_vert_9 (
    .in_1(four_bit_eq_cmp_10_out_3), .in_2(register_1_q), .out_3(sixt_bit_gatekeeper_vert_9_out_3));
  sixt_bit_gatekeeper_vert sixt_bit_gatekeeper_vert_10 (
    .in_1(four_bit_eq_cmp_12_out_3), .in_2(register_2_q), .out_3(sixt_bit_gatekeeper_vert_10_out_3));
  assign or_8_out = sixt_bit_gatekeeper_vert_10_out_3 | sixt_bit_gatekeeper_vert_9_out_3;  // OR_Gate or_8, 16 bits wide
  assign or_9_out = sixt_bit_gatekeeper_vert_17_out_3 | sixt_bit_gatekeeper_vert_18_out_3;  // OR_Gate or_9, 16 bits wide
  sixt_bit_gatekeeper_vert sixt_bit_gatekeeper_vert_11 (
    .in_1(four_bit_eq_cmp_14_out_3), .in_2(register_3_q), .out_3(sixt_bit_gatekeeper_vert_11_out_3));
  assign or_10_out = sixt_bit_gatekeeper_vert_11_out_3 | or_8_out;  // OR_Gate or_10, 16 bits wide
  assign or_11_out = or_9_out | sixt_bit_gatekeeper_vert_19_out_3;  // OR_Gate or_11, 16 bits wide
  sixt_bit_gatekeeper_vert sixt_bit_gatekeeper_vert_12 (
    .in_1(four_bit_eq_cmp_16_out_3), .in_2(register_4_q), .out_3(sixt_bit_gatekeeper_vert_12_out_3));
  assign or_12_out = sixt_bit_gatekeeper_vert_12_out_3 | or_10_out;  // OR_Gate or_12, 16 bits wide
  assign or_13_out = or_11_out | sixt_bit_gatekeeper_vert_20_out_3;  // OR_Gate or_13, 16 bits wide
  sixt_bit_gatekeeper_vert sixt_bit_gatekeeper_vert_13 (
    .in_1(four_bit_eq_cmp_18_out_3), .in_2(register_5_q), .out_3(sixt_bit_gatekeeper_vert_13_out_3));
  assign or_14_out = sixt_bit_gatekeeper_vert_13_out_3 | or_12_out;  // OR_Gate or_14, 16 bits wide
  assign or_15_out = or_13_out | sixt_bit_gatekeeper_vert_21_out_3;  // OR_Gate or_15, 16 bits wide
  sixt_bit_gatekeeper_vert sixt_bit_gatekeeper_vert_14 (
    .in_1(four_bit_eq_cmp_20_out_3), .in_2(register_6_q), .out_3(sixt_bit_gatekeeper_vert_14_out_3));
  assign or_16_out = sixt_bit_gatekeeper_vert_14_out_3 | or_14_out;  // OR_Gate or_16, 16 bits wide
  assign or_17_out = or_15_out | sixt_bit_gatekeeper_vert_22_out_3;  // OR_Gate or_17, 16 bits wide
  sixt_bit_gatekeeper_vert sixt_bit_gatekeeper_vert_15 (
    .in_1(four_bit_eq_cmp_22_out_3), .in_2(register_7_q), .out_3(sixt_bit_gatekeeper_vert_15_out_3));
  assign or_18_out = sixt_bit_gatekeeper_vert_15_out_3 | or_16_out;  // OR_Gate or_18, 16 bits wide
  assign or_19_out = or_17_out | sixt_bit_gatekeeper_vert_23_out_3;  // OR_Gate or_19, 16 bits wide
  sixt_bit_gatekeeper_vert sixt_bit_gatekeeper_vert_16 (
    .in_1(four_bit_eq_cmp_24_out_3), .in_2(register_8_q), .out_3(sixt_bit_gatekeeper_vert_16_out_3));
  assign or_20_out = sixt_bit_gatekeeper_vert_16_out_3 | or_18_out;  // OR_Gate or_20, 16 bits wide
  assign or_21_out = or_19_out | sixt_bit_gatekeeper_vert_24_out_3;  // OR_Gate or_21, 16 bits wide
  sixt_bit_gatekeeper_vert sixt_bit_gatekeeper_vert_17 (
    .in_1(four_bit_eq_cmp_9_out_3), .in_2(register_1_q), .out_3(sixt_bit_gatekeeper_vert_17_out_3));
  four_bit_incrementer four_bit_incrementer_9 (
    .in_1(four_bit_incrementer_10_out_2), .out_2(four_bit_incrementer_9_out_2));
  sixt_bit_gatekeeper_vert sixt_bit_gatekeeper_vert_18 (
    .in_1(four_bit_eq_cmp_11_out_3), .in_2(register_2_q), .out_3(sixt_bit_gatekeeper_vert_18_out_3));
  four_bit_incrementer four_bit_incrementer_10 (
    .in_1(four_bit_incrementer_11_out_2), .out_2(four_bit_incrementer_10_out_2));
  sixt_bit_gatekeeper_vert sixt_bit_gatekeeper_vert_19 (
    .in_1(four_bit_eq_cmp_13_out_3), .in_2(register_3_q), .out_3(sixt_bit_gatekeeper_vert_19_out_3));
  four_bit_incrementer four_bit_incrementer_11 (
    .in_1(four_bit_incrementer_12_out_2), .out_2(four_bit_incrementer_11_out_2));
  sixt_bit_gatekeeper_vert sixt_bit_gatekeeper_vert_20 (
    .in_1(four_bit_eq_cmp_15_out_3), .in_2(register_4_q), .out_3(sixt_bit_gatekeeper_vert_20_out_3));
  four_bit_incrementer four_bit_incrementer_12 (
    .in_1(four_bit_incrementer_13_out_2), .out_2(four_bit_incrementer_12_out_2));
  sixt_bit_gatekeeper_vert sixt_bit_gatekeeper_vert_21 (
    .in_1(four_bit_eq_cmp_17_out_3), .in_2(register_5_q), .out_3(sixt_bit_gatekeeper_vert_21_out_3));
  four_bit_incrementer four_bit_incrementer_13 (
    .in_1(four_bit_incrementer_14_out_2), .out_2(four_bit_incrementer_13_out_2));
  sixt_bit_gatekeeper_vert sixt_bit_gatekeeper_vert_22 (
    .in_1(four_bit_eq_cmp_19_out_3), .in_2(register_6_q), .out_3(sixt_bit_gatekeeper_vert_22_out_3));
  four_bit_incrementer four_bit_incrementer_14 (
    .in_1(four_bit_incrementer_15_out_2), .out_2(four_bit_incrementer_14_out_2));
  sixt_bit_gatekeeper_vert sixt_bit_gatekeeper_vert_23 (
    .in_1(four_bit_eq_cmp_21_out_3), .in_2(register_7_q), .out_3(sixt_bit_gatekeeper_vert_23_out_3));
  four_bit_incrementer four_bit_incrementer_15 (
    .in_1(four_bit_incrementer_8_out_2), .out_2(four_bit_incrementer_15_out_2));
  sixt_bit_gatekeeper_vert sixt_bit_gatekeeper_vert_24 (
    .in_1(four_bit_eq_cmp_23_out_3), .in_2(register_8_q), .out_3(sixt_bit_gatekeeper_vert_24_out_3));
  four_bit_eq_cmp four_bit_eq_cmp_25 (
    .in_1(in_6), .in_2(four_bit_incrementer_9_out_2), .out_3(four_bit_eq_cmp_25_out_3));
  four_bit_eq_cmp four_bit_eq_cmp_26 (
    .in_1(in_5), .in_2(four_bit_incrementer_9_out_2), .out_3(four_bit_eq_cmp_26_out_3));
  four_bit_eq_cmp four_bit_eq_cmp_27 (
    .in_1(in_6), .in_2(four_bit_incrementer_10_out_2), .out_3(four_bit_eq_cmp_27_out_3));
  four_bit_eq_cmp four_bit_eq_cmp_28 (
    .in_1(in_5), .in_2(four_bit_incrementer_10_out_2), .out_3(four_bit_eq_cmp_28_out_3));
  four_bit_eq_cmp four_bit_eq_cmp_29 (
    .in_1(in_6), .in_2(four_bit_incrementer_11_out_2), .out_3(four_bit_eq_cmp_29_out_3));
  four_bit_eq_cmp four_bit_eq_cmp_30 (
    .in_1(in_5), .in_2(four_bit_incrementer_11_out_2), .out_3(four_bit_eq_cmp_30_out_3));
  four_bit_eq_cmp four_bit_eq_cmp_31 (
    .in_1(in_6), .in_2(four_bit_incrementer_12_out_2), .out_3(four_bit_eq_cmp_31_out_3));
  four_bit_eq_cmp four_bit_eq_cmp_32 (
    .in_1(in_5), .in_2(four_bit_incrementer_12_out_2), .out_3(four_bit_eq_cmp_32_out_3));
  four_bit_eq_cmp four_bit_eq_cmp_33 (
    .in_1(in_6), .in_2(four_bit_incrementer_13_out_2), .out_3(four_bit_eq_cmp_33_out_3));
  four_bit_eq_cmp four_bit_eq_cmp_34 (
    .in_1(in_5), .in_2(four_bit_incrementer_13_out_2), .out_3(four_bit_eq_cmp_34_out_3));
  four_bit_eq_cmp four_bit_eq_cmp_35 (
    .in_1(in_6), .in_2(four_bit_incrementer_14_out_2), .out_3(four_bit_eq_cmp_35_out_3));
  four_bit_eq_cmp four_bit_eq_cmp_36 (
    .in_1(in_5), .in_2(four_bit_incrementer_14_out_2), .out_3(four_bit_eq_cmp_36_out_3));
  four_bit_eq_cmp four_bit_eq_cmp_37 (
    .in_1(in_6), .in_2(four_bit_incrementer_15_out_2), .out_3(four_bit_eq_cmp_37_out_3));
  four_bit_eq_cmp four_bit_eq_cmp_38 (
    .in_1(in_5), .in_2(four_bit_incrementer_15_out_2), .out_3(four_bit_eq_cmp_38_out_3));
  four_bit_eq_cmp four_bit_eq_cmp_39 (
    .in_1(in_6), .in_2(four_bit_incrementer_8_out_2), .out_3(four_bit_eq_cmp_39_out_3));
  four_bit_eq_cmp four_bit_eq_cmp_40 (
    .in_1(in_5), .in_2(four_bit_incrementer_8_out_2), .out_3(four_bit_eq_cmp_40_out_3));
  four_bit_eq_cmp four_bit_eq_cmp_41 (
    .in_1(in_7), .in_2(four_bit_incrementer_9_out_2), .out_3(four_bit_eq_cmp_41_out_3));
  four_bit_eq_cmp four_bit_eq_cmp_42 (
    .in_1(in_7), .in_2(four_bit_incrementer_10_out_2), .out_3(four_bit_eq_cmp_42_out_3));
  four_bit_eq_cmp four_bit_eq_cmp_43 (
    .in_1(in_7), .in_2(four_bit_incrementer_11_out_2), .out_3(four_bit_eq_cmp_43_out_3));
  four_bit_eq_cmp four_bit_eq_cmp_44 (
    .in_1(in_7), .in_2(four_bit_incrementer_12_out_2), .out_3(four_bit_eq_cmp_44_out_3));
  four_bit_eq_cmp four_bit_eq_cmp_45 (
    .in_1(in_7), .in_2(four_bit_incrementer_13_out_2), .out_3(four_bit_eq_cmp_45_out_3));
  four_bit_eq_cmp four_bit_eq_cmp_46 (
    .in_1(in_7), .in_2(four_bit_incrementer_14_out_2), .out_3(four_bit_eq_cmp_46_out_3));
  four_bit_eq_cmp four_bit_eq_cmp_47 (
    .in_1(in_7), .in_2(four_bit_incrementer_15_out_2), .out_3(four_bit_eq_cmp_47_out_3));
  four_bit_eq_cmp four_bit_eq_cmp_48 (
    .in_1(in_7), .in_2(four_bit_incrementer_8_out_2), .out_3(four_bit_eq_cmp_48_out_3));
  Register #(.width(16)) register_9 (.D(in_8), .en(and_9_out), .clk(in_9), .Q(register_9_q), .clr(in_10));
  and and_9 (and_9_out, Write, four_bit_eq_cmp_26_out_3);
  Register #(.width(16)) register_10 (.D(in_8), .en(and_10_out), .clk(in_9), .Q(register_10_q), .clr(in_10));
  and and_10 (and_10_out, Write, four_bit_eq_cmp_28_out_3);
  Register #(.width(16)) register_11 (.D(in_8), .en(and_11_out), .clk(in_9), .Q(register_11_q), .clr(in_10));
  and and_11 (and_11_out, Write, four_bit_eq_cmp_30_out_3);
  Register #(.width(16)) register_12 (.D(in_8), .en(and_12_out), .clk(in_9), .Q(register_12_q), .clr(in_10));
  and and_12 (and_12_out, Write, four_bit_eq_cmp_32_out_3);
  Register #(.width(16)) register_13 (.D(in_8), .en(and_13_out), .clk(in_9), .Q(register_13_q), .clr(in_10));
  and and_13 (and_13_out, Write, four_bit_eq_cmp_34_out_3);
  Register #(.width(16)) register_14 (.D(in_8), .en(and_14_out), .clk(in_9), .Q(register_14_q), .clr(in_10));
  and and_14 (and_14_out, Write, four_bit_eq_cmp_36_out_3);
  Register #(.width(16)) register_15 (.D(in_8), .en(and_15_out), .clk(in_9), .Q(register_15_q), .clr(in_10));
  and and_15 (and_15_out, Write, four_bit_eq_cmp_38_out_3);
  Register #(.width(16)) register_16 (.D(in_8), .en(and_16_out), .clk(in_9), .Q(register_16_q), .clr(in_10));
  and and_16 (and_16_out, Write, four_bit_eq_cmp_40_out_3);
  assign or_22_out = gatekeeper_1_p3 | or_23_out;  // OR_Gate or_22, 16 bits wide
  // gatekeeper gatekeeper_1: pin names not known; wires that end beside it: register_9_q, four_bit_eq_cmp_26_out_3, gatekeeper_1_p3
  assign or_23_out = gatekeeper_2_p3 | or_24_out;  // OR_Gate or_23, 16 bits wide
  // gatekeeper gatekeeper_2: pin names not known; wires that end beside it: register_10_q, four_bit_eq_cmp_28_out_3, gatekeeper_2_p3
  assign or_24_out = gatekeeper_3_p3 | or_25_out;  // OR_Gate or_24, 16 bits wide
  // gatekeeper gatekeeper_3: pin names not known; wires that end beside it: register_11_q, four_bit_eq_cmp_30_out_3, gatekeeper_3_p3
  assign or_25_out = gatekeeper_4_p3 | or_26_out;  // OR_Gate or_25, 16 bits wide
  // gatekeeper gatekeeper_4: pin names not known; wires that end beside it: register_12_q, four_bit_eq_cmp_32_out_3, gatekeeper_4_p3
  assign or_26_out = gatekeeper_5_p3 | or_27_out;  // OR_Gate or_26, 16 bits wide
  // gatekeeper gatekeeper_5: pin names not known; wires that end beside it: register_13_q, four_bit_eq_cmp_34_out_3, gatekeeper_5_p3
  assign or_27_out = gatekeeper_6_p3 | or_28_out;  // OR_Gate or_27, 16 bits wide
  // gatekeeper gatekeeper_6: pin names not known; wires that end beside it: register_14_q, four_bit_eq_cmp_36_out_3, gatekeeper_6_p3
  assign or_28_out = gatekeeper_7_p3 | or_29_out;  // OR_Gate or_28, 16 bits wide
  // gatekeeper gatekeeper_7: pin names not known; wires that end beside it: register_15_q, four_bit_eq_cmp_38_out_3, gatekeeper_7_p3
  assign or_29_out = gatekeeper_8_p3 | or_7_out;  // OR_Gate or_29, 16 bits wide
  // gatekeeper gatekeeper_8: pin names not known; wires that end beside it: register_16_q, four_bit_eq_cmp_40_out_3, gatekeeper_8_p3
  // gatekeeper gatekeeper_9: pin names not known; wires that end beside it: or_22_out, Data_out, out_11
  // gatekeeper gatekeeper_10: pin names not known; wires that end beside it: or_22_out, Addr_out, out_12
  // gatekeeper gatekeeper_11: pin names not known; wires that end beside it: gatekeeper_11_p1, ALU_Out, out_13
  assign gatekeeper_11_p1 = gatekeeper_12_p3 | or_32_out;  // OR_Gate or_30, 16 bits wide
  assign or_31_out = gatekeeper_21_p3 | or_33_out;  // OR_Gate or_31, 16 bits wide
  // gatekeeper gatekeeper_12: pin names not known; wires that end beside it: register_9_q, four_bit_eq_cmp_41_out_3, gatekeeper_12_p3
  assign or_32_out = gatekeeper_13_p3 | or_34_out;  // OR_Gate or_32, 16 bits wide
  assign or_33_out = gatekeeper_22_p3 | or_35_out;  // OR_Gate or_33, 16 bits wide
  // gatekeeper gatekeeper_13: pin names not known; wires that end beside it: register_10_q, four_bit_eq_cmp_42_out_3, gatekeeper_13_p3
  assign or_34_out = gatekeeper_14_p3 | or_36_out;  // OR_Gate or_34, 16 bits wide
  assign or_35_out = gatekeeper_23_p3 | or_37_out;  // OR_Gate or_35, 16 bits wide
  // gatekeeper gatekeeper_14: pin names not known; wires that end beside it: register_11_q, four_bit_eq_cmp_43_out_3, gatekeeper_14_p3
  assign or_36_out = gatekeeper_15_p3 | or_38_out;  // OR_Gate or_36, 16 bits wide
  assign or_37_out = gatekeeper_24_p3 | or_39_out;  // OR_Gate or_37, 16 bits wide
  // gatekeeper gatekeeper_15: pin names not known; wires that end beside it: register_12_q, four_bit_eq_cmp_44_out_3, gatekeeper_15_p3
  assign or_38_out = gatekeeper_16_p3 | or_40_out;  // OR_Gate or_38, 16 bits wide
  assign or_39_out = gatekeeper_25_p3 | or_41_out;  // OR_Gate or_39, 16 bits wide
  // gatekeeper gatekeeper_16: pin names not known; wires that end beside it: register_13_q, four_bit_eq_cmp_45_out_3, gatekeeper_16_p3
  assign or_40_out = gatekeeper_17_p3 | or_42_out;  // OR_Gate or_40, 16 bits wide
  assign or_41_out = gatekeeper_26_p3 | or_43_out;  // OR_Gate or_41, 16 bits wide
  // gatekeeper gatekeeper_17: pin names not known; wires that end beside it: register_14_q, four_bit_eq_cmp_46_out_3, gatekeeper_17_p3
  assign or_42_out = gatekeeper_18_p3 | or_44_out;  // OR_Gate or_42, 16 bits wide
  assign or_43_out = gatekeeper_27_p3 | or_45_out;  // OR_Gate or_43, 16 bits wide
  // gatekeeper gatekeeper_18: pin names not known; wires that end beside it: register_15_q, four_bit_eq_cmp_47_out_3, gatekeeper_18_p3
  assign or_44_out = gatekeeper_19_p3 | or_20_out;  // OR_Gate or_44, 16 bits wide
  assign or_45_out = gatekeeper_28_p3 | or_21_out;  // OR_Gate or_45, 16 bits wide
  // gatekeeper gatekeeper_19: pin names not known; wires that end beside it: register_16_q, four_bit_eq_cmp_48_out_3, gatekeeper_19_p3
  // gatekeeper gatekeeper_20: pin names not known; wires that end beside it: or_31_out, ALU_Out, out_14
  // gatekeeper gatekeeper_21: pin names not known; wires that end beside it: register_9_q, four_bit_eq_cmp_25_out_3, gatekeeper_21_p3
  // gatekeeper gatekeeper_22: pin names not known; wires that end beside it: register_10_q, four_bit_eq_cmp_27_out_3, gatekeeper_22_p3
  // gatekeeper gatekeeper_23: pin names not known; wires that end beside it: register_11_q, four_bit_eq_cmp_29_out_3, gatekeeper_23_p3
  // gatekeeper gatekeeper_24: pin names not known; wires that end beside it: register_12_q, four_bit_eq_cmp_31_out_3, gatekeeper_24_p3
  // gatekeeper gatekeeper_25: pin names not known; wires that end beside it: register_13_q, four_bit_eq_cmp_33_out_3, gatekeeper_25_p3
  // gatekeeper gatekeeper_26: pin names not known; wires that end beside it: register_14_q, four_bit_eq_cmp_35_out_3, gatekeeper_26_p3
  // gatekeeper gatekeeper_27: pin names not known; wires that end beside it: register_15_q, four_bit_eq_cmp_37_out_3, gatekeeper_27_p3
  // gatekeeper gatekeeper_28: pin names not known; wires that end beside it: register_16_q, four_bit_eq_cmp_39_out_3, gatekeeper_28_p3

  // Notes on the sheet:
  //   bus output
  //   ALU out 1
  //   ALU out 2
  //   Data
  //   Data Out
  //   Addr Out
  //   r1 out
  //   r2 out
endmodule

module registers_controller (
  input  [15:0] control_in,
  output write,
  output to_data_bus,
  output to_addr_bus,
  output to_ALU,
  output [3:0] bus_output,
  output [3:0] ALU_1,
  output [3:0] ALU_2,
  output [3:0] write_target
);

  wire comparator_2_eq, comparator_3_eq, comparator_4_eq, or_1_out;
  wire [3:3] or_3_out;

  four_bit_eq_cmp four_bit_eq_cmp_1 (.in_1(control_in[7:4]), .in_2(4'b0001), .out_3(to_ALU));
  Comparator #(.width(12)) comparator_1 (.a(control_in[11:0]), .b(12'h3), .eq(to_data_bus));  // open: gt, lt
  Comparator #(.width(12)) comparator_2 (.a(control_in[11:0]), .b(12'h103), .eq(comparator_2_eq));  // open: gt, lt
  Comparator #(.width(12)) comparator_3 (.a(control_in[11:0]), .b(12'h203), .eq(comparator_3_eq));  // open: gt, lt
  Comparator #(.width(12)) comparator_4 (.a(control_in[11:0]), .b(12'h303), .eq(comparator_4_eq));  // open: gt, lt
  Comparator #(.width(12)) comparator_5 (.a(control_in[11:0]), .b(12'h403), .eq(write));  // open: gt, lt
  or or_1 (or_1_out, comparator_3_eq, comparator_4_eq);
  or or_2 (to_addr_bus, comparator_2_eq, or_1_out);
  assign bus_output = control_in[15:12] & {4{or_3_out[3]}};  // AND_Gate and_1, 4 bits wide
  or or_3 (or_3_out[3], to_data_bus, comparator_2_eq, write, or_1_out);

  assign ALU_1 = control_in[15:12];
  assign ALU_2 = control_in[11:8];
  assign write_target = bus_output;
endmodule
module control_unit (
  input  [31:0] addr_bus_in,
  input  [31:0] data_bus_in,
  input  [31:0] sp_in,
  input  clock,
  input  [31:0] pk_in,
  input  single_instr_mode,
  input  reset,
  input  force_running,
  input  done,
  input  in_10,
  output [15:0] control_bus_out,
  output [31:0] addr_bus_out,
  output [31:0] to_special_registers,
  output [31:0] data_bus_out
);

  wire and_1_out, and_2_out, button_1_out, button_2_out, microcode_address_register_1_set_run_bit_high,
       new_one_ticker_1_signal_out, new_one_ticker_2_signal_out, or_1_out, or_2_out, or_3_out, or_4_out,
       or_5_out, or_6_out, or_8_out, or_9_out, or_10_out, s_r_ff_1_q, s_r_ff_2_q, sixt_bit_eq_cmp_1_out_3,
       sixt_bit_eq_cmp_2_out_3, sixt_bit_eq_cmp_3_out_3, tmp_regs_controller_1_a_to_secret,
       tmp_regs_controller_1_b_to_addr, tmp_regs_controller_1_b_to_data, tmp_regs_controller_1_out_2,
       tmp_regs_controller_1_out_3, tmp_regs_controller_1_out_4, tmp_regs_controller_1_out_5,
       tmp_regs_controller_1_out_8, tmp_regs_controller_1_out_11, tmp_regs_controller_1_write_b,
       wait_inducer_1_start_waiting;
  wire [7:0] BIOS_ROM_data, register_1_q, register_2_q;
  wire [15:0] microcode_address_register_1_mcar_out, rom_1_data;
  wire [31:0] sticky_gate_1_out_put, tmp_regs_unit_1_a_out, tmp_regs_unit_1_b_out,
       tmp_regs_unit_1_data_bus_out;

  Button button_1 (.out(button_1_out));
  Button button_2 (.out(button_2_out));
  or or_1 (or_1_out, button_1_out, reset);
  or or_2 (or_2_out, button_2_out, force_running);
  ROM #(.addrWidth(16)) BIOS_ROM (.addr(addr_bus_in[15:0]), .data(BIOS_ROM_data));
  buf or_3 (or_3_out, ~single_instr_mode);  // OR_Gate OR_Gate
  or or_4 (or_4_out, or_2_out, or_1_out);
  // Probe on data_bus_in
  and and_1 (and_1_out, clock, or_3_out);
  Register register_1 (
    .D(data_bus_in[7:0]), .en(sixt_bit_eq_cmp_1_out_3), .clk(and_1_out), .Q(register_1_q), .clr(or_4_out));
  Register register_2 (
    .D(data_bus_in[15:8]), .en(sixt_bit_eq_cmp_1_out_3), .clk(and_1_out), .Q(register_2_q), .clr(or_4_out));
  sixt_bit_eq_cmp sixt_bit_eq_cmp_1 (
    .in_1(microcode_address_register_1_mcar_out), .in_2(16'h9), .out_3(sixt_bit_eq_cmp_1_out_3));
  tmp_regs_controller tmp_regs_controller_1 (
    .in_1(control_bus_out), .out_2(tmp_regs_controller_1_out_2), .out_3(tmp_regs_controller_1_out_3),
    .out_4(tmp_regs_controller_1_out_4), .out_5(tmp_regs_controller_1_out_5),
    .A_to_secret(tmp_regs_controller_1_a_to_secret), .B_to_data(tmp_regs_controller_1_b_to_data),
    .out_8(tmp_regs_controller_1_out_8), .B_to_addr(tmp_regs_controller_1_b_to_addr),
    .Write_B(tmp_regs_controller_1_write_b), .out_11(tmp_regs_controller_1_out_11));
  sixt_bit_eq_cmp sixt_bit_eq_cmp_2 (.in_1(control_bus_out), .in_2(16'hb0), .out_3(sixt_bit_eq_cmp_2_out_3));
  ROM #(.addrWidth(16), .dataWidth(16)) rom_1 (.addr({register_2_q, register_1_q}), .data(rom_1_data));
  S_R_Flip_Flop s_r_ff_1 (.Q(s_r_ff_1_q), .reset(or_6_out), .preset(or_5_out));  // open: S, R, clk, Qn
  // Probe on tmp_regs_unit_1_a_out
  // Probe on tmp_regs_unit_1_b_out
  tmp_regs_unit tmp_regs_unit_1 (
    .a_to_data(tmp_regs_controller_1_out_2), .data_bus_in(data_bus_in),
    .a_to_addr_long(tmp_regs_controller_1_out_3), .a_to_addr(tmp_regs_controller_1_out_4),
    .write_a(tmp_regs_controller_1_out_5), .a_to_special_regs(tmp_regs_controller_1_a_to_secret),
    .b_to_data(tmp_regs_controller_1_b_to_data), .b_to_addr_long(tmp_regs_controller_1_out_8),
    .b_to_addr(tmp_regs_controller_1_b_to_addr), .write_b(tmp_regs_controller_1_write_b),
    .b_to_special_regs(tmp_regs_controller_1_out_11), .clock(and_1_out), .reset(or_4_out),
    .b_out(tmp_regs_unit_1_b_out), .a_out(tmp_regs_unit_1_a_out),
    .data_bus_out(tmp_regs_unit_1_data_bus_out), .addr_bus_out(addr_bus_out),
    .to_special_regs(to_special_registers));
  sticky_gate sticky_gate_1 (
    .clock(clock), .enable(sixt_bit_eq_cmp_2_out_3), .data({{24{1'b0}}, BIOS_ROM_data}),
    .out_put(sticky_gate_1_out_put));  // open: reset, propagate_reset
  or or_5 (or_5_out, or_2_out, microcode_address_register_1_set_run_bit_high);
  or or_6 (or_6_out, or_4_out, sixt_bit_eq_cmp_3_out_3);
  sixt_bit_eq_cmp sixt_bit_eq_cmp_3 (.in_1(control_bus_out), .in_2(16'hff00), .out_3(sixt_bit_eq_cmp_3_out_3));
  assign data_bus_out = tmp_regs_unit_1_data_bus_out | sticky_gate_1_out_put;  // OR_Gate or_7, 32 bits wide
  and and_2 (and_2_out, and_1_out, ~s_r_ff_2_q);  // AND_Gate
  microcode_address_register microcode_address_register_1 (
    .running_bit(s_r_ff_1_q), .clock(and_2_out), .restart_instr(or_8_out), .reload_bios(or_1_out),
    .control_bus_in(control_bus_out), .dbus(data_bus_in), .instr_decoder(rom_1_data),
    .mcar_out(microcode_address_register_1_mcar_out),
    .set_run_bit_high(microcode_address_register_1_set_run_bit_high));
  or or_8 (or_8_out, or_2_out, or_4_out);
  // Probe on rom_1_data
  ROM #(.addrWidth(16), .dataWidth(16)) rom_2 (.addr(microcode_address_register_1_mcar_out), .data(control_bus_out));
  // Probe on microcode_address_register_1_mcar_out
  // Probe on addr_bus_in
  // Probe on pk_in
  // Probe on sp_in
  // Probe on control_bus_out
  wait_inducer wait_inducer_1 (.opcode(control_bus_out), .start_waiting(wait_inducer_1_start_waiting));
  new_one_ticker new_one_ticker_1 (
    .clock_in(and_1_out), .reset(or_4_out), .signal_in(in_10), .signal_out(new_one_ticker_1_signal_out));
  new_one_ticker new_one_ticker_2 (
    .clock_in(and_1_out), .reset(or_4_out), .signal_in(wait_inducer_1_start_waiting),
    .signal_out(new_one_ticker_2_signal_out));
  S_R_Flip_Flop #(.trigger("falling")) s_r_ff_2 (
    .S(1'b0), .R(1'b0), .clk(and_1_out), .Q(s_r_ff_2_q), .reset(or_9_out), .preset(or_10_out));  // open: Qn
  or or_9 (or_9_out, or_4_out, done);
  or or_10 (or_10_out, new_one_ticker_1_signal_out, new_one_ticker_2_signal_out);

  // Other names for the same wires on the sheet: addr[31:0] = addr_bus_in

  // Notes on the sheet:
  //   contents of BIOS_ROM (hex, n*v repeats v):
  //   4 4*0 6 5
  //   Data bus
  //   contents of rom_1 (hex, n*v repeats v):
  //   d 0 13 19 12*0 253 256 259 25c 25f 262 265 268 8*0 3d3 3d6 3d9 3dc 3df 3e2 3e5 3e8 8*0 553 556 559
  //   55c 55f 562 565 568 8*0 1a53 6d6 6d9 6dc 6df 6e2 6e5 6e8 8*0 1a6b 856 859 85c 85f 862 865 868 8*0
  //   1a77 1a79 1a80 1bc9 1bce 1bd4 9e5 9e8 8*0 1c2d b56 1c2f 1c38 1c3c 1c42 1d68 1d6c 1d72 7*0 cd3 cd6
  //   cd9 1c4b 1c4f 1c55 1d7b 1d7f 1d85 7*0 e53 e56 e59 1c5e 1c62 1c68 1d8e 1d92 1d98 7*0 fd3 fd6 fd9 1c71
  //   1c75 1c7b 1da1 1da5 1dab 7*0 1153 1156 1159 1c84 1c88 1c8e 1db4 1db8 1dbe 7*0 12d3 12d6 12d9 1c97
  //   1c9b 1ca1 1dc7 1dcb 1dd1 7*0 1453 1456 1459 1caa 1cae 1cb4 1dda 1dde 1de4 7*0 15d3 15d6 15d9 1cbd
  //   1cc1 1cc7 1ded 1df1 1df7 7*0 1753 1756 1759 1cd0 1cd4 1cda 1e00 1e04 1e0a 7*0 18d3 18d6 18d9 1ce3
  //   1ce7 1ced 1e13 1e17 1e1d 7*0 18eb 18ee 18f1 1cf6 1cfa 1d00 1e26 1e2a 1e30 7*0 1903 1906 1909 1d09
  //   1d0d 1d13 1e39 1e3d 1e43 7*0 191b 191e 1921 1d1c 1d20 1d26 1e4c 1e50 1e56 7*0 1933 1936 1939 1d2f
  //   1d33 1d39 1e5f 1e63 1e69 7*0 194b 194e 1951 1d42 1d46 1d4c 1e72 1e76 1e7c 7*0 1963 1966 1969 1d55
  //   1d59 1d5f 1e85 1e89 1e8f 7*0 197b 197e 1981 1984 1987 198a 198d 1990 8*0 1993 1996 1999 199c 199f
  //   19a2 19a5 19a8 8*0 19ab 19ae 19b1 19b4 19b7 19ba 19bd 19c0 8*0 19c3 19c6 19c9 19cc 19cf 19d2 19d5
  //   19d8 8*0 19db 19de 19e1 19e4 19e7 19ea 19ed 19f0 8*0 19f3 19f6 19f9 19fc 19ff 1a02 1a05 1a08 8*0
  //   1a0b 1a0e 1a11 1a14 1a17 1a1a 1a1d 1a20 8*0 1a23 1a26 1a29 1a2c 1a2f 1a32 1a35 1a38 8*0 1a3b 1a3e
  //   1a41 1a44 1a47 1a4a 1a4d 1a50 264*0 1e98 1ea1 14*0 1eab 1eb1 1eb8 1f7b 1f81 1f88 10*0 1eb8 1ebe 1ec5
  //   1f88 1f8e 1f95 10*0 1fbc 1ecb 1ed2 1f95 1f9b 1fa2 10*0 224a 1ed8 1edf 1fa2 1fa8 1faf 10*0 24d8 1ff2
  //   2010 202e 204c 206a 2088 20a6 20c4 20e2 2100 211e 213c 215a 2178 2196 2766 2280 229e 22bc 22da 22f8
  //   2316 2334 2352 2370 238e 23ac 23ca 23e8 2406 2424 29f4 250e 252c 254a 2568 2586 25a4 25c2 25e0 25fe
  //   261c 263a 2658 2676 2694 26b2 2c82 279c 27ba 27d8 27f6 2814 2832 2850 286e 288c 28aa 28c8 28e6 2904
  //   2922 2940 2f10 2a2a 2a48 2a66 2a84 2aa2 2ac0 2ade 2afc 2b1a 2b38 2b56 2b74 2b92 2bb0 2bce 319e 2cb8
  //   2cd6 2cf4 2d12 2d30 2d4e 2d6c 2d8a 2da8 2dc6 2de4 2e02 2e20 2e3e 2e5c 342c 2f46 2f64 2f82 2fa0 2fbe
  //   2fdc 2ffa 3018 3036 3054 3072 3090 30ae 30cc 30ea 36ba 31d4 31f2 3210 322e 324c 326a 3288 32a6 32c4
  //   32e2 3300 331e 333c 335a 3378 3948 3462 3480 349e 34bc 34da 34f8 3516 3534 3552 3570 358e 35ac 35ca
  //   35e8 3606 3bd6 36f0 370e 372c 374a 3768 3786 37a4 37c2 37e0 37fe 381c 383a 3858 3876 3894 3e64 397e
  //   399c 39ba 39d8 39f6 3a14 3a32 3a50 3a6e 3a8c 3aaa 3ac8 3ae6 3b04 3b22 40f2 3c0c 3c2a 3c48 3c66 3c84
  //   3ca2 3cc0 3cde 3cfc 3d1a 3d38 3d56 3d74 3d92 3db0 4380 3e9a 3eb8 3ed6 3ef4 3f12 3f30 3f4e 3f6c 3f8a
  //   3fa8 3fc6 3fe4 4002 4020 403e 460e 4128 4146 4164 4182 41a0 41be 41dc 41fa 4218 4236 4254 4272 4290
  //   42ae 42cc 4612 4626 43d4 43f2 4410 442e 444c 446a 4488 44a6 44c4 44e2 4500 451e 453c 455a 4626 4644
  //   4662 4680 469e 46bc 46da 46f8 4716 4734 4752 4770 478e 47ac 47ca 47e8 4629 4647 4665 4683 46a1 46bf
  //   46dd 46fb 4719 4737 4755 4773 4791 47af 47cd 47eb 462c 464a 4668 4686 46a4 46c2 46e0 46fe 471c 473a
  //   4758 4776 4794 47b2 47d0 47ee 4806 4824 4842 4860 487e 3a02 3a20 3a3e 3a5c 3a7a 3a98 3ab6 3ad4 3af2
  //   3b10 3b2e 4809 4827 4845 4863 4881 3c90 3cae 3ccc 3cea 3d08 3d26 3d44 3d62 3d80 3d9e 3dbc 480c 482a
  //   4848 4866 4884 3f1e 3f3c 3f5a 3f78 3f96 3fb4 3fd2 3ff0 400e 402c 404a 489c 489c 4152 4170 418e 41ac
  //   41ca 41e8 4206 4224 4242 4260 427e 429c 42ba 42d8 4920 4920 48be 48c5 48cc 48d3 48da 48e1 48e8 48ef
  //   48f6 48fd 4904 490b 4912 4919 49a4 49a4 4942 4949 4950 4957 495e 4965 496c 4973 497a 4981 4988 498f
  //   4996 499d 4a28 4a28 49c6 49cd 49d4 49db 49e2 49e9 49f0 49f7 49fe 4a05 4a0c 4a13 4a1a 4a21 4aac 4aac
  //   4a4a 4a51 4a58 4a5f 4a66 4a6d 4a74 4a7b 4a82 4a89 4a90 4a97 4a9e 4aa5 4ac0 4ac7 4ace 4ad5 4adc 4ae3
  //   4aea 4af1 4af8 4aff 4b06 4b0d 4b14 4b1b 4b22 4b29 4ac0 4ac7 4ace 4ad5 4adc 4ae3 4aea 4af1 4af8 4aff
  //   4b06 4b0d 4b14 4b1b 4b22 4b29 4ac0 4ac7 4ace 4ad5 4adc 4ae3 4aea 4af1 4af8 4aff 4b06 4b0d 4b14 4b1b
  //   4b22 4b29 5*4b30 48d3 48da 48e1 48e8 48ef 48f6 48fd 4904 490b 4912 4919 5*4b30 4957 495e 4965 496c
  //   4973 497a 4981 4988 498f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
  //   contents of rom_2 (hex, n*v repeats v):
  //   11 403 ff00 103 b0 4 13 403 fffe ff0f 502 0 1 0 fffe 102 4005 402 fffe 102 4005 2402 3 602 fffe 102
  //   4005 2402 3 702 fffe 102 4005 2402 3 802 fffe 102 4005 2402 3 902 fffe 102 4005 2402 3 a02 fffe 102
  //   4005 2402 3 b02 fffe 102 4005 2402 1003 602 fffe 102 4005 2402 1003 702 fffe 102 4005 2402 1003 802
  //   fffe 102 4005 2402 1003 902 fffe 102 4005 2402 1003 a02 fffe 102 4005 2402 1003 b02 fffe 102 4005
  //   2402 2003 602 fffe 102 4005 2402 2003 702 fffe 102 4005 2402 2003 802 fffe 102 4005 2402 2003 902
  //   fffe 102 4005 2402 2003 a02 fffe 102 4005 2402 2003 b02 fffe 102 4005 2402 3003 602 fffe 102 4005
  //   2402 3003 702 fffe 102 4005 2402 3003 802 fffe 102 4005 2402 3003 902 fffe 102 4005 2402 3003 a02
  //   fffe 102 4005 2402 3003 b02 fffe 102 4005 2402 4003 602 fffe 102 4005 2402 4003 702 fffe 102 4005
  //   2402 4003 802 fffe 102 4005 2402 4003 902 fffe 102 4005 2402 4003 a02 fffe 102 4005 2402 4003 b02
  //   fffe 102 4005 2402 5003 602 fffe 102 4005 2402 5003 702 fffe 102 4005 2402 5003 802 fffe 102 4005
  //   2402 5003 902 fffe 102 4005 2402 5003 a02 fffe 102 4005 2402 5003 b02 fffe 102 4005 2402 6003 602
  //   fffe 102 4005 2402 6003 702 fffe 102 4005 2402 6003 802 fffe 102 4005 2402 6003 902 fffe 102 4005
  //   2402 6003 a02 fffe 102 4005 2402 6003 b02 fffe 102 4005 2402 7003 602 fffe 102 4005 2402 7003 702
  //   fffe 102 4005 2402 7003 802 fffe 102 4005 2402 7003 902 fffe 102 4005 2402 7003 a02 fffe 102 4005
  //   2402 7003 b02 fffe 102 4005 2402 8003 602 fffe 102 4005 2402 8003 702 fffe 102 4005 2402 8003 802
  //   fffe 102 4005 2402 8003 902 fffe 102 4005 2402 8003 a02 fffe 102 4005 2402 8003 b02 fffe 102 4005
  //   2402 9003 602 fffe 102 4005 2402 9003 702 fffe 102 4005 2402 9003 802 fffe 102 4005 2402 9003 902
  //   fffe 102 4005 2402 9003 a02 fffe 102 4005 2402 9003 b02 fffe 102 4005 2402 a003 602 fffe 102 4005
  //   2402 a003 702 fffe 102 4005 2402 a003 802 fffe 102 4005 2402 a003 902 fffe 102 4005 2402 a003 a02
  //   fffe 102 4005 2402 a003 b02 fffe 102 4005 2402 b003 602 fffe 102 4005 2402 b003 702 fffe 102 4005
  //   2402 b003 802 fffe 102 4005 2402 b003 902 fffe 102 4005 2402 b003 a02 fffe 102 4005 2402 b003 b02
  //   fffe 102 4005 2402 c003 602 fffe 102 4005 2402 c003 702 fffe 102 4005 2402 c003 802 fffe 102 4005
  //   2402 c003 902 fffe 102 4005 2402 c003 a02 fffe 102 4005 2402 c003 b02 fffe 102 4005 2402 d003 602
  //   fffe 102 4005 2402 d003 702 fffe 102 4005 2402 d003 802 fffe 102 4005 2402 d003 902 fffe 102 4005
  //   2402 d003 a02 fffe 102 4005 2402 d003 b02 fffe 102 4005 2402 e003 602 fffe 102 4005 2402 e003 702
  //   fffe 102 4005 2402 e003 802 fffe 102 4005 2402 e003 902 fffe 102 4005 2402 e003 a02 fffe 102 4005
  //   2402 e003 b02 fffe 102 4005 2402 f003 602 fffe 102 4005 2402 f003 702 fffe 102 4005 2402 f003 802
  //   fffe 102 4005 2402 f003 902 fffe 102 4005 2402 f003 a02 fffe 102 4005 2402 f003 b02 fffe 10 403 fffe
  //   11 403 fffe 12 403 fffe 13 403 fffe 14 403 fffe 15 403 fffe 16 403 fffe 17 403 fffe 110 403 fffe 111
  //   403 fffe 112 403 fffe 113 403 fffe 114 403 fffe 115 403 fffe 116 403 fffe 117 403 fffe 210 403 fffe
  //   211 403 fffe 212 403 fffe 213 403 fffe 214 403 fffe 215 403 fffe 216 403 fffe 217 403 fffe 310 403
  //   fffe 311 403 fffe 312 403 fffe 313 403 fffe 314 403 fffe 315 403 fffe 316 403 fffe 317 403 fffe 410
  //   403 fffe 411 403 fffe 412 403 fffe 413 403 fffe 414 403 fffe 415 403 fffe 416 403 fffe 417 403 fffe
  //   510 403 fffe 511 403 fffe 512 403 fffe 513 403 fffe 514 403 fffe 515 403 fffe 516 403 fffe 517 403
  //   fffe 610 403 fffe 611 403 fffe 612 403 fffe 613 403 fffe 614 403 fffe 615 403 fffe 616 403 fffe 617
  //   403 fffe 710 403 fffe 711 403 fffe 712 403 fffe 713 403 fffe 714 403 fffe 715 403 fffe 716 403 fffe
  //   717 403 fffe 810 403 fffe 811 403 fffe 812 403 fffe 813 403 fffe 814 403 fffe 815 403 fffe 816 403
  //   fffe 817 403 fffe 910 403 fffe 911 403 fffe 912 403 fffe 913 403 fffe 914 403 fffe 915 403 fffe 916
  //   403 fffe 917 403 fffe a10 403 fffe a11 403 fffe a12 403 fffe a13 403 fffe a14 403 fffe a15 403 fffe
  //   a16 403 fffe a17 403 fffe b10 403 fffe b11 403 fffe b12 403 fffe b13 403 fffe b14 403 fffe b15 403
  //   fffe b16 403 fffe b17 403 fffe c10 403 fffe c11 40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
endmodule

module counting_register (
  input  [31:0] data_in,
  input  clock,
  input  increment,
  input  decrement,
  input  write,
  input  reset,
  output [31:0] out_7
);

  wire button_1_out, new_one_ticker_1_signal_out, new_one_ticker_2_signal_out, or_1_out, or_2_out;
  wire [31:0] adder_1_out, multiplexer_1_out, multiplexer_2_out;

  Button button_1 (.out(button_1_out));
  new_one_ticker new_one_ticker_1 (
    .clock_in(clock), .reset(or_1_out), .signal_in(increment), .signal_out(new_one_ticker_1_signal_out));
  new_one_ticker new_one_ticker_2 (
    .clock_in(clock), .reset(or_1_out), .signal_in(decrement), .signal_out(new_one_ticker_2_signal_out));
  or or_1 (or_1_out, reset, button_1_out);
  Multiplexer #(.width(32)) multiplexer_1 (.in0(adder_1_out), .in1(data_in), .out(multiplexer_1_out));  // open: sel
  Register #(.width(32)) register_1 (.D(multiplexer_1_out), .en(or_2_out), .clk(clock), .Q(out_7), .clr(or_1_out));
  or or_2 (or_2_out, new_one_ticker_1_signal_out, new_one_ticker_2_signal_out, write);
  Multiplexer #(.width(32)) multiplexer_2 (.in0(32'h1), .in1({32{1'b1}}), .out(multiplexer_2_out));  // open: sel
  Adder #(.width(32)) adder_1 (.a(multiplexer_2_out), .b(out_7), .out(adder_1_out));  // open: cin, cout
endmodule

module PK_control (
  input  [15:0] in_1,
  input  in_2,
  input  Restart,
  input  [15:0] in_4,
  input  [15:0] in_5,
  output [15:0] out_6,
  output out_7,
  output out_8,
  output out_9,
  output out_10,
  output out_11
);

  wire and_1_out, and_2_out, and_3_out, and_4_out, or_1_out, or_2_out, or_3_out, pulse_extender_1_out_put,
       sixt_bit_eq_cmp_1_out_3, sixt_bit_eq_cmp_2_out_3, sixt_bit_eq_cmp_3_out_3, sixt_bit_eq_cmp_4_out_3,
       sixt_bit_eq_zero_1_out_2;
  wire [5:0] rom_1_data;

  ROM #(.addrWidth(16), .dataWidth(6)) rom_1 (.addr(in_1), .data({rom_1_data[5:4], out_10, rom_1_data[2:0]}));
  sixt_bit_eq_zero sixt_bit_eq_zero_1 (.in_1(in_4), .out_2(sixt_bit_eq_zero_1_out_2));
  sixt_bit_eq_cmp sixt_bit_eq_cmp_1 (.in_1(in_1), .in_2(16'h20), .out_3(sixt_bit_eq_cmp_1_out_3));
  sixt_bit_eq_cmp sixt_bit_eq_cmp_2 (.in_1(in_1), .in_2(16'h21), .out_3(sixt_bit_eq_cmp_2_out_3));
  sixt_bit_eq_cmp sixt_bit_eq_cmp_3 (.in_1(in_1), .in_2(16'h22), .out_3(sixt_bit_eq_cmp_3_out_3));
  sixt_bit_eq_cmp sixt_bit_eq_cmp_4 (.in_1(in_1), .in_2(16'h23), .out_3(sixt_bit_eq_cmp_4_out_3));
  and and_1 (and_1_out, sixt_bit_eq_zero_1_out_2, sixt_bit_eq_cmp_1_out_3);
  or or_1 (or_1_out, and_1_out, and_2_out);
  and and_2 (and_2_out, ~sixt_bit_eq_zero_1_out_2, sixt_bit_eq_cmp_2_out_3);  // AND_Gate
  and and_3 (and_3_out, sixt_bit_eq_zero_1_out_2, sixt_bit_eq_cmp_3_out_3);
  or or_2 (or_2_out, and_3_out, and_4_out);
  and and_4 (and_4_out, ~sixt_bit_eq_zero_1_out_2, sixt_bit_eq_cmp_4_out_3);  // AND_Gate
  // sixt_bit_selector sixt_bit_selector_1: pin names not known; wires that end beside it: or_1_out, in_4, in_5, out_6
  or or_3 (or_3_out, rom_1_data[4], pulse_extender_1_out_put);
  pulse_extender pulse_extender_1 (
    .inp(rom_1_data[5]), .clock(in_2), .out_put(pulse_extender_1_out_put));  // open: reset, reset_out, clock_out
  pulse_extender pulse_extender_2 (
    .inp(or_3_out), .clock(in_2), .out_put(out_11));  // open: reset, reset_out, clock_out
  or or_4 (out_8, rom_1_data[1], or_1_out);
  or or_5 (out_9, rom_1_data[2], Restart);
  or or_6 (out_7, rom_1_data[0], or_2_out);

  // Notes on the sheet:
  //   contents of rom_1 (hex, n*v repeats v):
  //   0 10 0 0 1 2 65528*0 1
  //   data input
  //   Increment
  //   Write
  //   Reset
  //   Data bus
  //   Addr Bus
endmodule

module memory_ctrl (
  input  [31:0] data_in,
  input  [7:0] ram_in,
  input  [31:0] addr_in,
  input  [31:0] offset_in,
  input  [15:0] control_in,
  input  clock_in,
  input  reset,
  output [31:0] data_out,
  output done,
  output [15:0] addr_out,
  output write,
  output [7:0] data_send
);

  wire and_1_out, and_2_out, and_3_out, and_4_out, and_5_out, and_6_out, and_7_out, and_8_out, and_9_out,
       and_10_out, and_11_out, and_12_out, and_13_out, and_14_out, and_15_out, and_16_out, and_17_out,
       and_18_out, and_19_out, and_20_out, button_1_out, comparator_1_eq, comparator_2_eq, comparator_3_eq,
       comparator_4_eq, d_ff_1_q, d_ff_2_q, eight_bit_eq_cmp_1_out_3, eight_bit_eq_cmp_2_out_3,
       four_bit_eq_cmp_1_out_3, four_bit_eq_cmp_2_out_3, four_bit_eq_cmp_3_out_3, four_bit_eq_cmp_4_out_3,
       is_long_instruction_1_out_2, multiplexer_4_out, new_one_ticker_1_signal_out,
       new_one_ticker_2_signal_out, nor_1_out, not_1_out, not_2_out, not_3_out, or_1_out, or_2_out, or_3_out,
       or_4_out, or_5_out, or_6_out, or_7_out, or_8_out, or_9_out, or_11_out, or_12_out, or_13_out,
       or_15_out, or_16_out, or_17_out, or_18_out, or_19_out, or_20_out, or_21_out, or_22_out, or_23_out,
       or_24_out, or_25_out, or_26_out, or_28_out, s_r_ff_1_q, s_r_ff_2_q, s_r_ff_3_q, s_r_ff_4_q,
       s_r_ff_5_q, s_r_ff_6_q, s_r_ff_7_q, s_r_ff_8_q, s_r_ff_9_q, s_r_ff_10_q, s_r_ff_11_q, s_r_ff_12_q,
       s_r_ff_13_q, s_r_ff_14_q, s_r_ff_15_q, sixt_bit_eq_cmp_1_out_3, sixt_bit_eq_cmp_2_out_3,
       sixt_bit_eq_cmp_3_out_3;
  wire [3:0] adder_2_out, multiplexer_2_out, register_3_q;
  wire [4:0] multiplier_1_out, subtractor_1_out, subtractor_2_out;
  wire [7:0] and_21_out, and_22_out, and_23_out, and_24_out, continuous_byte_reader_1_byte1,
       continuous_byte_reader_1_byte2, continuous_byte_reader_1_byte3, continuous_byte_reader_1_byte4,
       register_4_q, register_4_q_2, register_4_q_3, register_4_q_4;
  wire [7:7] d_ff_3_q, d_ff_4_q, d_ff_5_q, or_27_out;
  wire [31:0] adder_1_out, adder_3_out, adder_4_out, adder_5_out, adder_6_out, adder_7_out, adder_8_out,
       adder_9_out, adder_10_out, buffer_1_out, buffer_2_out, buffer_3_out, buffer_4_out,
       continuous_byte_reader_1_address_out, continuous_byte_reader_1_bytes_read,
       continuous_byte_reader_1_data_out, gatekeeper_1_out_3, gatekeeper_2_out_3, gatekeeper_3_out_3,
       gatekeeper_4_out_3, multiplexer_1_out, multiplexer_3_out, multiplexer_5_out, or_29_out, register_1_q,
       register_2_q, shifter_1_out, sticky_gate_2_out_put;
  wire [31:16] multiplexer_6_out;

  or or_1 (or_1_out, control_in[12], control_in[13], control_in[14], control_in[15]);
  or or_2 (or_2_out, control_in[12], control_in[13], control_in[14], control_in[15]);
  Subtractor #(.width(5)) subtractor_1 (
    .a({1'b0, control_in[15:12]}), .b({1'b0, register_3_q}), .out(subtractor_1_out));  // open: bin, bout
  Subtractor #(.width(5)) subtractor_2 (.a(subtractor_1_out), .b(5'b00001), .out(subtractor_2_out));  // open: bin, bout
  Button button_1 (.out(button_1_out));
  and and_1 (and_1_out, control_in[0], ~control_in[1], control_in[2], ~control_in[3], ~control_in[4], ~control_in[5], ~control_in[6], ~control_in[7], ~control_in[9], ~control_in[10], ~control_in[11], or_1_out);  // AND_Gate
  and and_2 (and_2_out, ~control_in[0], ~control_in[1], control_in[2], ~control_in[3], ~control_in[4], ~control_in[5], ~control_in[6], ~control_in[7], ~control_in[9], ~control_in[10], ~control_in[11], or_2_out);  // AND_Gate
  Multiplier #(.width(5)) multiplier_1 (.a(5'b01000), .b(subtractor_2_out), .out(multiplier_1_out));  // open: cin, cout
  or or_3 (or_3_out, button_1_out, s_r_ff_14_q, reset);
  sixt_bit_eq_cmp sixt_bit_eq_cmp_1 (.in_1(control_in), .in_2(16'hff0f), .out_3(sixt_bit_eq_cmp_1_out_3));
  sixt_bit_eq_cmp sixt_bit_eq_cmp_2 (.in_1(control_in), .in_2(16'h4), .out_3(sixt_bit_eq_cmp_2_out_3));
  sixt_bit_eq_cmp sixt_bit_eq_cmp_3 (.in_1(control_in), .in_2(16'h104), .out_3(sixt_bit_eq_cmp_3_out_3));
  eight_bit_eq_cmp eight_bit_eq_cmp_1 (.in_1(control_in[7:0]), .in_2(8'h2), .out_3(eight_bit_eq_cmp_1_out_3));
  four_bit_eq_cmp four_bit_eq_cmp_1 (.in_1(control_in[11:8]), .in_2(4'b0010), .out_3(four_bit_eq_cmp_1_out_3));
  four_bit_eq_cmp four_bit_eq_cmp_2 (.in_1(control_in[11:8]), .in_2(4'b0011), .out_3(four_bit_eq_cmp_2_out_3));
  eight_bit_eq_cmp eight_bit_eq_cmp_2 (.in_1(control_in[7:0]), .in_2(8'h3), .out_3(eight_bit_eq_cmp_2_out_3));
  four_bit_eq_cmp four_bit_eq_cmp_3 (.in_1(control_in[11:8]), .in_2(4'b0010), .out_3(four_bit_eq_cmp_3_out_3));
  four_bit_eq_cmp four_bit_eq_cmp_4 (.in_1(control_in[11:8]), .in_2(4'b0011), .out_3(four_bit_eq_cmp_4_out_3));
  or or_4 (or_4_out, sixt_bit_eq_cmp_1_out_3, and_1_out);
  new_one_ticker new_one_ticker_1 (
    .clock_in(clock_in), .reset(or_3_out), .signal_in(and_1_out), .signal_out(new_one_ticker_1_signal_out));
  S_R_Flip_Flop s_r_ff_1 (
    .Q(s_r_ff_1_q), .reset(or_6_out), .preset(new_one_ticker_1_signal_out));  // open: S, R, clk, Qn
  new_one_ticker new_one_ticker_2 (
    .clock_in(clock_in), .reset(or_3_out), .signal_in(and_2_out), .signal_out(new_one_ticker_2_signal_out));
  Shifter #(.width(32)) shifter_1 (.in({{24{1'b0}}, ram_in}), .\dist (multiplier_1_out), .out(shifter_1_out));
  Comparator #(.width(4)) comparator_1 (.a(register_3_q), .b(control_in[15:12]), .eq(comparator_1_eq));  // open: gt, lt
  Register #(.width(32)) register_1 (.D(addr_in), .en(1'b1), .clk(or_5_out), .Q(register_1_q), .clr(or_3_out));
  or or_5 (or_5_out, s_r_ff_1_q, new_one_ticker_2_signal_out, s_r_ff_2_q, sixt_bit_eq_cmp_2_out_3, sixt_bit_eq_cmp_3_out_3);
  or or_6 (or_6_out, or_3_out, d_ff_1_q);
  S_R_Flip_Flop s_r_ff_2 (
    .S(1'b0), .R(1'b0), .clk(clock_in), .Q(s_r_ff_2_q), .reset(or_7_out), .preset(new_one_ticker_2_signal_out));  // open: Qn
  or or_7 (or_7_out, and_4_out, or_3_out);
  and and_3 (and_3_out, comparator_1_eq, s_r_ff_1_q);
  and and_4 (and_4_out, s_r_ff_2_q, s_r_ff_13_q);
  and and_5 (and_5_out, eight_bit_eq_cmp_1_out_3, four_bit_eq_cmp_1_out_3);
  or or_8 (or_8_out, and_5_out, and_6_out);
  and and_6 (and_6_out, eight_bit_eq_cmp_1_out_3, four_bit_eq_cmp_2_out_3);
  and and_7 (and_7_out, eight_bit_eq_cmp_2_out_3, four_bit_eq_cmp_3_out_3);
  or or_9 (or_9_out, and_7_out, and_8_out);
  and and_8 (and_8_out, eight_bit_eq_cmp_2_out_3, four_bit_eq_cmp_4_out_3);
  Adder #(.width(32)) adder_1 (.a(register_2_q), .b(shifter_1_out), .out(adder_1_out));  // open: cin, cout
  D_Flip_Flop #(.trigger("falling")) d_ff_1 (.D(and_3_out), .clk(clock_in), .Q(d_ff_1_q));  // open: Qn, preset, reset
  // Probe on continuous_byte_reader_1_byte1
  continuous_byte_reader continuous_byte_reader_1 (
    .byte_in(ram_in), .address_in(addr_in), .read(or_4_out), .offs(offset_in), .use_offset(or_25_out),
    .output_enable(or_4_out), .clock(clock_in), .reset(or_3_out), .byte1(continuous_byte_reader_1_byte1),
    .byte2(continuous_byte_reader_1_byte2), .byte3(continuous_byte_reader_1_byte3),
    .byte4(continuous_byte_reader_1_byte4), .data_out(continuous_byte_reader_1_data_out),
    .bytes_read(continuous_byte_reader_1_bytes_read), .address_out(continuous_byte_reader_1_address_out));  // open: remember_between_reads
  // Probe on continuous_byte_reader_1_byte2
  // Probe on continuous_byte_reader_1_byte3
  // Probe on continuous_byte_reader_1_byte4
  // Probe on continuous_byte_reader_1_bytes_read
  Register #(.trigger("falling"), .width(32)) register_2 (
    .D(multiplexer_1_out), .en(not_1_out), .clk(clock_in), .Q(register_2_q), .clr(or_3_out));
  Multiplexer #(.width(32)) multiplexer_1 (
    .in0({32{1'b0}}), .in1(adder_1_out), .out(multiplexer_1_out), .sel(s_r_ff_1_q));
  not not_1 (not_1_out, d_ff_1_q);
  Multiplexer #(.width(4)) multiplexer_2 (.in0(4'b0000), .in1(adder_2_out), .out(multiplexer_2_out), .sel(s_r_ff_1_q));
  // OR_Gate or_10 has open pins: in0=or_8_out, in1=or_9_out, out=open
  Register #(.trigger("falling"), .width(4)) register_3 (
    .D(multiplexer_2_out), .en(or_11_out), .clk(clock_in), .Q(register_3_q), .clr(or_3_out));
  or or_11 (or_11_out, s_r_ff_1_q, or_16_out);
  or or_12 (or_12_out, sixt_bit_eq_cmp_3_out_3, or_13_out);
  or or_13 (or_13_out, and_6_out, and_8_out);
  sticky_gate sticky_gate_1 (
    .clock(clock_in), .reset(and_9_out), .enable(or_4_out), .data(continuous_byte_reader_1_data_out),
    .out_put(data_out));  // open: propagate_reset
  and and_9 (and_9_out, ~or_28_out, or_3_out);  // AND_Gate
  assign buffer_1_out = register_2_q;  // Buffer buffer_1, 32 bits wide
  assign buffer_2_out = buffer_1_out;  // Buffer buffer_2, 32 bits wide
  sticky_gate sticky_gate_2 (
    .clock(clock_in), .reset(or_3_out), .enable(or_12_out), .data(offset_in), .out_put(sticky_gate_2_out_put));  // open: propagate_reset
  or or_14 (write, sixt_bit_eq_cmp_2_out_3, or_15_out);
  or or_15 (or_15_out, sixt_bit_eq_cmp_3_out_3, s_r_ff_2_q);
  nor nor_1 (nor_1_out, control_in[12], control_in[13], control_in[14], control_in[15]);
  is_long_instruction is_long_instruction_1 (
    .first_byte(continuous_byte_reader_1_byte1), .out_2(is_long_instruction_1_out_2));
  assign buffer_3_out = buffer_2_out;  // Buffer buffer_3, 32 bits wide
  assign buffer_4_out = buffer_3_out;  // Buffer buffer_4, 32 bits wide
  or or_16 (or_16_out, register_3_q[0], register_3_q[1], register_3_q[2], register_3_q[3]);
  S_R_Flip_Flop s_r_ff_3 (
    .S(control_in[12]), .R(1'b0), .clk(s_r_ff_2_q), .Q(s_r_ff_3_q), .reset(or_17_out));  // open: Qn, preset
  S_R_Flip_Flop s_r_ff_4 (
    .S(control_in[13]), .R(1'b0), .clk(s_r_ff_2_q), .Q(s_r_ff_4_q), .reset(or_18_out));  // open: Qn, preset
  S_R_Flip_Flop s_r_ff_5 (
    .S(control_in[14]), .R(1'b0), .clk(s_r_ff_2_q), .Q(s_r_ff_5_q), .reset(or_19_out));  // open: Qn, preset
  S_R_Flip_Flop s_r_ff_6 (
    .S(control_in[15]), .R(1'b0), .clk(s_r_ff_2_q), .Q(s_r_ff_6_q), .reset(or_20_out));  // open: Qn, preset
  S_R_Flip_Flop s_r_ff_7 (
    .S(control_in[12]), .R(1'b0), .clk(s_r_ff_2_q), .Q(s_r_ff_7_q), .reset(or_3_out));  // open: Qn, preset
  S_R_Flip_Flop s_r_ff_8 (
    .S(control_in[13]), .R(1'b0), .clk(s_r_ff_2_q), .Q(s_r_ff_8_q), .reset(or_3_out));  // open: Qn, preset
  S_R_Flip_Flop s_r_ff_9 (
    .S(control_in[14]), .R(1'b0), .clk(s_r_ff_2_q), .Q(s_r_ff_9_q), .reset(or_3_out));  // open: Qn, preset
  and and_10 (and_10_out, sixt_bit_eq_cmp_1_out_3, is_long_instruction_1_out_2);
  and and_11 (and_11_out, sixt_bit_eq_cmp_1_out_3, ~is_long_instruction_1_out_2);  // AND_Gate
  Comparator #(.width(32)) comparator_2 (
    .a(continuous_byte_reader_1_bytes_read), .b(32'h1), .eq(comparator_2_eq));  // open: gt, lt
  Comparator #(.width(32)) comparator_3 (
    .a(continuous_byte_reader_1_bytes_read), .b(32'h2), .eq(comparator_3_eq));  // open: gt, lt
  Adder #(.width(4)) adder_2 (.a(register_3_q), .b(4'b0001), .out(adder_2_out));  // open: cin, cout
  or or_17 (or_17_out, or_3_out, d_ff_2_q);
  or or_18 (or_18_out, or_3_out, d_ff_3_q[7]);
  or or_19 (or_19_out, or_3_out, d_ff_4_q[7]);
  or or_20 (or_20_out, or_3_out, d_ff_5_q[7]);
  S_R_Flip_Flop #(.trigger("falling")) s_r_ff_10 (
    .S(sixt_bit_eq_cmp_1_out_3), .R(not_2_out), .clk(clock_in), .Q(s_r_ff_10_q), .reset(or_3_out));  // open: Qn, preset
  not not_2 (not_2_out, sixt_bit_eq_cmp_1_out_3);
  and and_12 (and_12_out, comparator_2_eq, and_11_out);
  and and_13 (and_13_out, comparator_3_eq, and_10_out);
  Adder #(.width(32)) adder_3 (.a({{28{1'b0}}, register_3_q}), .b(register_1_q), .out(adder_3_out));  // open: cin, cout
  and and_14 (and_14_out, ~s_r_ff_3_q, s_r_ff_4_q);  // AND_Gate
  or or_21 (or_21_out, and_14_out, s_r_ff_3_q);
  and and_15 (and_15_out, ~or_21_out, s_r_ff_5_q);  // AND_Gate
  or or_22 (or_22_out, and_15_out, or_21_out);
  and and_16 (and_16_out, ~or_22_out, s_r_ff_6_q);  // AND_Gate
  or or_23 (or_23_out, and_16_out, or_22_out);
  and and_17 (and_17_out, s_r_ff_2_q, ~or_23_out);  // AND_Gate
  Adder #(.width(32)) adder_4 (.a({32{1'b0}}), .b({32{1'b0}}), .out(adder_4_out), .cin(s_r_ff_7_q));  // open: cout
  Adder #(.width(32)) adder_5 (.a(adder_4_out), .b({32{1'b0}}), .out(adder_5_out), .cin(s_r_ff_8_q));  // open: cout
  Adder #(.width(32)) adder_6 (.a(adder_5_out), .b({32{1'b0}}), .out(adder_6_out), .cin(s_r_ff_9_q));  // open: cout
  not not_3 (not_3_out, and_1_out);
  better_sticky_gate better_sticky_gate_1 (
    .enable(d_ff_1_q), .data(buffer_4_out), .clock(clock_in), .reset(or_3_out));  // open: out_put
  or or_24 (or_24_out, d_ff_1_q, s_r_ff_13_q, and_4_out);
  or or_25 (or_25_out, sixt_bit_eq_cmp_3_out_3, control_in[8]);
  D_Flip_Flop #(.trigger("falling")) d_ff_2 (
    .D(s_r_ff_3_q), .clk(clock_in), .Q(d_ff_2_q), .reset(or_3_out));  // open: Qn, preset
  D_Flip_Flop #(.trigger("falling")) d_ff_3 (
    .D(and_14_out), .clk(clock_in), .Q(d_ff_3_q[7]), .reset(or_3_out));  // open: Qn, preset
  D_Flip_Flop #(.trigger("falling")) d_ff_4 (
    .D(and_15_out), .clk(clock_in), .Q(d_ff_4_q[7]), .reset(or_3_out));  // open: Qn, preset
  D_Flip_Flop #(.trigger("falling")) d_ff_5 (
    .D(and_16_out), .clk(clock_in), .Q(d_ff_5_q[7]), .reset(or_3_out));  // open: Qn, preset
  S_R_Flip_Flop #(.trigger("falling")) s_r_ff_11 (
    .S(and_17_out), .R(1'b0), .clk(clock_in), .Q(s_r_ff_11_q), .reset(s_r_ff_13_q));  // open: Qn, preset
  Comparator #(.width(32)) comparator_4 (
    .a({{28{1'b0}}, control_in[15:12]}), .b(data_out), .eq(comparator_4_eq));  // open: gt, lt
  and and_18 (and_18_out, comparator_4_eq, and_1_out);
  S_R_Flip_Flop #(.trigger("falling")) s_r_ff_12 (
    .S(and_1_out), .R(not_3_out), .clk(clock_in), .Q(s_r_ff_12_q), .reset(or_3_out));  // open: Qn, preset
  and and_19 (and_19_out, and_13_out, s_r_ff_10_q);
  Adder #(.width(32)) adder_7 (.a(adder_3_out), .b(sticky_gate_2_out_put), .out(adder_7_out));  // open: cin, cout
  Multiplexer #(.width(32)) multiplexer_3 (
    .in0(adder_3_out), .in1(adder_7_out), .out(multiplexer_3_out), .sel(or_25_out));
  Register #(.width(32)) register_4 (
    .D(data_in), .en(1'b1), .clk(or_26_out),
    .Q({register_4_q_4, register_4_q_3, register_4_q_2, register_4_q}), .clr(or_3_out));
  or or_26 (or_26_out, sixt_bit_eq_cmp_3_out_3, new_one_ticker_2_signal_out, sixt_bit_eq_cmp_2_out_3);
  or or_27 (or_27_out[7], sixt_bit_eq_cmp_2_out_3, sixt_bit_eq_cmp_3_out_3, d_ff_2_q);
  S_R_Flip_Flop s_r_ff_13 (
    .S(s_r_ff_11_q), .R(1'b0), .clk(clock_in), .Q(s_r_ff_13_q), .reset(s_r_ff_13_q));  // open: Qn, preset
  Multiplexer multiplexer_4 (.in0(s_r_ff_12_q), .in1(and_18_out), .out(multiplexer_4_out));  // open: sel
  Multiplexer #(.width(32)) multiplexer_5 (
    .in0(adder_7_out), .in1(continuous_byte_reader_1_address_out), .out(multiplexer_5_out));  // open: sel
  or or_28 (or_28_out, multiplexer_4_out, and_12_out, and_19_out);
  S_R_Flip_Flop s_r_ff_14 (.Q(s_r_ff_14_q), .reset(or_3_out), .preset(and_20_out));  // open: S, R, clk, Qn
  S_R_Flip_Flop s_r_ff_15 (
    .S(1'b0), .R(1'b1), .clk(clock_in), .Q(s_r_ff_15_q), .preset(s_r_ff_14_q));  // open: reset, Qn
  Multiplexer #(.width(32)) multiplexer_6 (
    .in0(multiplexer_5_out), .in1(or_29_out), .out({multiplexer_6_out, addr_out}), .sel(s_r_ff_2_q));
  gatekeeper gatekeeper_1 (.in_1(d_ff_5_q[7]), .in_2(multiplexer_3_out), .out_3(gatekeeper_1_out_3));
  Adder #(.width(32)) adder_8 (.a(multiplexer_3_out), .b(adder_4_out), .out(adder_8_out));  // open: cin, cout
  Adder #(.width(32)) adder_9 (.a(multiplexer_3_out), .b(adder_5_out), .out(adder_9_out));  // open: cin, cout
  Adder #(.width(32)) adder_10 (.a(multiplexer_3_out), .b(adder_6_out), .out(adder_10_out));  // open: cin, cout
  and and_20 (and_20_out, or_28_out, ~s_r_ff_15_q);  // AND_Gate
  assign and_21_out = {8{or_27_out[7]}} & register_4_q;  // AND_Gate and_21, 8 bits wide
  assign and_22_out = {8{d_ff_3_q[7]}} & register_4_q_2;  // AND_Gate and_22, 8 bits wide
  assign and_23_out = {8{d_ff_4_q[7]}} & register_4_q_3;  // AND_Gate and_23, 8 bits wide
  assign and_24_out = {8{d_ff_5_q[7]}} & register_4_q_4;  // AND_Gate and_24, 8 bits wide
  assign or_29_out = gatekeeper_1_out_3 | gatekeeper_2_out_3 | gatekeeper_3_out_3 | gatekeeper_4_out_3;  // OR_Gate or_29, 32 bits wide
  gatekeeper gatekeeper_2 (.in_1(d_ff_4_q[7]), .in_2(adder_8_out), .out_3(gatekeeper_2_out_3));
  gatekeeper gatekeeper_3 (.in_1(d_ff_3_q[7]), .in_2(adder_9_out), .out_3(gatekeeper_3_out_3));
  gatekeeper gatekeeper_4 (.in_1(d_ff_2_q), .in_2(adder_10_out), .out_3(gatekeeper_4_out_3));
  or or_30 (done, s_r_ff_15_q, or_24_out);
  assign data_send = and_21_out | and_22_out | and_23_out | and_24_out;  // OR_Gate or_31, 8 bits wide
endmodule

module ALU (
  input  [31:0] inp1,
  input  [31:0] inp2,
  input  enable,
  input  reset,
  input  [7:0] operation,
  output [31:0] out_6,
  output out_7
);

  wire and_2_out, comparator_1_gt, comparator_1_lt, comparator_2_gt, comparator_2_lt, comparator_3_eq,
       comparator_3_gt, comparator_3_lt, comparator_4_gt, comparator_4_lt, eight_bit_eq_cmp_1_out_3,
       eight_bit_eq_cmp_2_out_3, eight_bit_eq_cmp_3_out_3, eight_bit_eq_cmp_4_out_3,
       eight_bit_eq_cmp_5_out_3, eight_bit_eq_cmp_6_out_3, eight_bit_eq_cmp_7_out_3,
       eight_bit_eq_cmp_8_out_3, eight_bit_eq_cmp_9_out_3, eight_bit_eq_cmp_10_out_3,
       eight_bit_eq_cmp_11_out_3, eight_bit_eq_cmp_12_out_3, eight_bit_eq_cmp_13_out_3,
       eight_bit_eq_cmp_14_out_3, eight_bit_eq_cmp_15_out_3, eight_bit_eq_cmp_16_out_3, nor_1_out, or_3_out;
  wire [31:0] adder_1_out, adder_2_out, adder_3_out, adder_4_out, adder_5_out, and_1_out, gatekeeper_1_out_3,
       gatekeeper_2_out_3, gatekeeper_3_out_3, gatekeeper_4_out_3, gatekeeper_5_out_3, gatekeeper_6_out_3,
       gatekeeper_7_out_3, gatekeeper_8_out_3, gatekeeper_9_out_3, gatekeeper_10_out_3, gatekeeper_11_out_3,
       gatekeeper_12_out_3, gatekeeper_13_out_3, gatekeeper_14_out_3, gatekeeper_15_out_3,
       gatekeeper_16_out_3, gatekeeper_17_out_3, gatekeeper_18_out_3, gatekeeper_19_out_3,
       gatekeeper_20_out_3, gatekeeper_21_out_3, gatekeeper_22_out_3, gatekeeper_23_out_3,
       gatekeeper_24_out_3, multiplexer_1_out, multiplier_1_out, not_1_out, not_2_out, not_3_out, or_1_out,
       or_2_out, or_4_out, or_5_out, or_6_out, or_7_out, or_8_out, or_9_out, or_10_out, or_11_out, or_12_out,
       or_13_out, or_14_out, or_15_out, or_16_out, or_17_out, or_18_out, or_19_out, or_20_out, or_21_out,
       shifter_1_out, shifter_2_out, shifter_3_out, xor_1_out;

  eight_bit_eq_cmp eight_bit_eq_cmp_1 (.in_1(operation), .in_2({8{1'b0}}), .out_3(eight_bit_eq_cmp_1_out_3));
  eight_bit_eq_cmp eight_bit_eq_cmp_2 (.in_1(operation), .in_2(8'h1), .out_3(eight_bit_eq_cmp_2_out_3));
  eight_bit_eq_cmp eight_bit_eq_cmp_3 (.in_1(operation), .in_2(8'h2), .out_3(eight_bit_eq_cmp_3_out_3));
  eight_bit_eq_cmp eight_bit_eq_cmp_4 (.in_1(operation), .in_2(8'h3), .out_3(eight_bit_eq_cmp_4_out_3));
  eight_bit_eq_cmp eight_bit_eq_cmp_5 (.in_1(operation), .in_2(8'h4), .out_3(eight_bit_eq_cmp_5_out_3));
  eight_bit_eq_cmp eight_bit_eq_cmp_6 (.in_1(operation), .in_2(8'h5), .out_3(eight_bit_eq_cmp_6_out_3));
  eight_bit_eq_cmp eight_bit_eq_cmp_7 (.in_1(operation), .in_2(8'h6), .out_3(eight_bit_eq_cmp_7_out_3));
  eight_bit_eq_cmp eight_bit_eq_cmp_8 (.in_1(operation), .in_2(8'h7), .out_3(eight_bit_eq_cmp_8_out_3));
  eight_bit_eq_cmp eight_bit_eq_cmp_9 (.in_1(operation), .in_2(8'h8), .out_3(eight_bit_eq_cmp_9_out_3));
  eight_bit_eq_cmp eight_bit_eq_cmp_10 (.in_1(operation), .in_2(8'h9), .out_3(eight_bit_eq_cmp_10_out_3));
  eight_bit_eq_cmp eight_bit_eq_cmp_11 (.in_1(operation), .in_2(8'ha), .out_3(eight_bit_eq_cmp_11_out_3));
  eight_bit_eq_cmp eight_bit_eq_cmp_12 (.in_1(operation), .in_2(8'hb), .out_3(eight_bit_eq_cmp_12_out_3));
  eight_bit_eq_cmp eight_bit_eq_cmp_13 (.in_1(operation), .in_2(8'hc), .out_3(eight_bit_eq_cmp_13_out_3));
  eight_bit_eq_cmp eight_bit_eq_cmp_14 (.in_1(operation), .in_2(8'hd), .out_3(eight_bit_eq_cmp_14_out_3));
  eight_bit_eq_cmp eight_bit_eq_cmp_15 (.in_1(operation), .in_2(8'he), .out_3(eight_bit_eq_cmp_15_out_3));
  eight_bit_eq_cmp eight_bit_eq_cmp_16 (.in_1(operation), .in_2(8'hf), .out_3(eight_bit_eq_cmp_16_out_3));
  Adder #(.width(32)) adder_1 (.a(inp1), .b(inp2), .out(adder_1_out));  // open: cin, cout
  gatekeeper gatekeeper_1 (.in_1(eight_bit_eq_cmp_1_out_3), .in_2(adder_1_out), .out_3(gatekeeper_1_out_3));
  Adder #(.width(32)) adder_2 (.a(inp1), .b(not_1_out), .out(adder_2_out), .cin(1'b1));  // open: cout
  assign not_1_out = ~inp2;  // NOT_Gate not_1, 32 bits wide
  gatekeeper gatekeeper_2 (.in_1(eight_bit_eq_cmp_2_out_3), .in_2(adder_2_out), .out_3(gatekeeper_2_out_3));
  Multiplier #(.width(32)) multiplier_1 (.a(inp1), .b(inp2), .out(multiplier_1_out));  // open: cin, cout
  Adder #(.width(32)) adder_3 (.a(32'h1), .b(inp1), .out(adder_3_out));  // open: cin, cout
  Adder #(.width(32)) adder_4 (.a(inp1), .b({32{1'b1}}), .out(adder_4_out));  // open: cin, cout
  Comparator #(.width(64)) comparator_1 (
    .a({{32{1'b0}}, inp1}), .b({{32{1'b0}}, inp2}), .gt(comparator_1_gt), .lt(comparator_1_lt));  // open: eq
  assign and_1_out = inp1 & inp2;  // AND_Gate and_1, 32 bits wide
  assign or_1_out = inp1 | inp2;  // OR_Gate or_1, 32 bits wide
  assign xor_1_out = inp1 ^ inp2;  // XOR_Gate xor_1, 32 bits wide
  assign not_2_out = ~inp2;  // NOT_Gate not_2, 32 bits wide
  assign or_2_out = gatekeeper_1_out_3 | gatekeeper_2_out_3;  // OR_Gate or_2, 32 bits wide
  gatekeeper gatekeeper_3 (.in_1(eight_bit_eq_cmp_3_out_3), .in_2(multiplier_1_out), .out_3(gatekeeper_3_out_3));
  gatekeeper gatekeeper_4 (.in_1(eight_bit_eq_cmp_4_out_3), .in_2(adder_3_out), .out_3(gatekeeper_4_out_3));
  gatekeeper gatekeeper_5 (.in_1(eight_bit_eq_cmp_5_out_3), .in_2(adder_4_out), .out_3(gatekeeper_5_out_3));
  Comparator #(.width(32)) comparator_2 (.a(inp1), .b(inp2), .gt(comparator_2_gt), .lt(comparator_2_lt));  // open: eq
  or or_3 (or_3_out, comparator_3_gt, comparator_3_lt);
  Comparator #(.width(32)) comparator_3 (
    .a(inp1), .b({32{1'b0}}), .gt(comparator_3_gt), .eq(comparator_3_eq), .lt(comparator_3_lt));
  Comparator #(.width(32)) comparator_4 (
    .a(inp1), .b({32{1'b0}}), .gt(comparator_4_gt), .lt(comparator_4_lt));  // open: eq
  gatekeeper gatekeeper_6 (.in_1(eight_bit_eq_cmp_10_out_3), .in_2(and_1_out), .out_3(gatekeeper_6_out_3));
  gatekeeper gatekeeper_7 (.in_1(eight_bit_eq_cmp_11_out_3), .in_2(or_1_out), .out_3(gatekeeper_7_out_3));
  gatekeeper gatekeeper_8 (.in_1(eight_bit_eq_cmp_12_out_3), .in_2(xor_1_out), .out_3(gatekeeper_8_out_3));
  gatekeeper gatekeeper_9 (.in_1(eight_bit_eq_cmp_13_out_3), .in_2(not_2_out), .out_3(gatekeeper_9_out_3));
  Shifter #(.width(32)) shifter_1 (.in(inp1), .\dist (5'b00001), .out(shifter_1_out));
  gatekeeper gatekeeper_10 (.in_1(eight_bit_eq_cmp_14_out_3), .in_2(shifter_1_out), .out_3(gatekeeper_10_out_3));
  Shifter #(.shift("lr"), .width(32)) shifter_2 (.in(inp1), .\dist (5'b00001), .out(shifter_2_out));
  gatekeeper gatekeeper_11 (.in_1(eight_bit_eq_cmp_15_out_3), .in_2(shifter_2_out), .out_3(gatekeeper_11_out_3));
  assign not_3_out = ~inp2;  // NOT_Gate not_3, 32 bits wide
  Adder #(.width(32)) adder_5 (.a(not_3_out), .b(32'h1), .out(adder_5_out));  // open: cin, cout
  assign or_4_out = or_2_out | gatekeeper_3_out_3;  // OR_Gate or_4, 32 bits wide
  gatekeeper gatekeeper_12 (.in_1(comparator_1_gt), .in_2(32'h1), .out_3(gatekeeper_12_out_3));
  assign or_5_out = gatekeeper_12_out_3 | gatekeeper_13_out_3;  // OR_Gate or_5, 32 bits wide
  gatekeeper gatekeeper_13 (.in_1(comparator_1_lt), .in_2({32{1'b1}}), .out_3(gatekeeper_13_out_3));
  gatekeeper gatekeeper_14 (.in_1(comparator_2_gt), .in_2(32'h1), .out_3(gatekeeper_14_out_3));
  gatekeeper gatekeeper_15 (.in_1(comparator_2_lt), .in_2({32{1'b1}}), .out_3(gatekeeper_15_out_3));
  gatekeeper gatekeeper_16 (.in_1(or_3_out), .in_2({32{1'b0}}), .out_3(gatekeeper_16_out_3));
  gatekeeper gatekeeper_17 (.in_1(comparator_3_eq), .in_2(32'h1), .out_3(gatekeeper_17_out_3));
  gatekeeper gatekeeper_18 (.in_1(comparator_4_gt), .in_2(32'h1), .out_3(gatekeeper_18_out_3));
  gatekeeper gatekeeper_19 (.in_1(comparator_4_lt), .in_2({32{1'b1}}), .out_3(gatekeeper_19_out_3));
  Multiplexer #(.width(32)) multiplexer_1 (.in0(inp2), .in1(adder_5_out), .out(multiplexer_1_out));  // open: sel
  assign or_6_out = or_4_out | gatekeeper_4_out_3;  // OR_Gate or_6, 32 bits wide
  gatekeeper gatekeeper_20 (.in_1(eight_bit_eq_cmp_6_out_3), .in_2(or_5_out), .out_3(gatekeeper_20_out_3));
  assign or_7_out = gatekeeper_14_out_3 | gatekeeper_15_out_3;  // OR_Gate or_7, 32 bits wide
  gatekeeper gatekeeper_21 (.in_1(eight_bit_eq_cmp_7_out_3), .in_2(or_7_out), .out_3(gatekeeper_21_out_3));
  assign or_8_out = gatekeeper_16_out_3 | gatekeeper_17_out_3;  // OR_Gate or_8, 32 bits wide
  gatekeeper gatekeeper_22 (.in_1(eight_bit_eq_cmp_8_out_3), .in_2(or_8_out), .out_3(gatekeeper_22_out_3));
  assign or_9_out = gatekeeper_18_out_3 | gatekeeper_19_out_3;  // OR_Gate or_9, 32 bits wide
  gatekeeper gatekeeper_23 (.in_1(eight_bit_eq_cmp_9_out_3), .in_2(or_9_out), .out_3(gatekeeper_23_out_3));
  nor nor_1 (nor_1_out, multiplexer_1_out[5], multiplexer_1_out[6], multiplexer_1_out[7], multiplexer_1_out[8], multiplexer_1_out[9], multiplexer_1_out[10], multiplexer_1_out[11], multiplexer_1_out[12], multiplexer_1_out[13], multiplexer_1_out[14], multiplexer_1_out[15], multiplexer_1_out[16], multiplexer_1_out[17], multiplexer_1_out[18], multiplexer_1_out[19], multiplexer_1_out[20], multiplexer_1_out[21], multiplexer_1_out[22], multiplexer_1_out[23], multiplexer_1_out[24], multiplexer_1_out[25], multiplexer_1_out[26], multiplexer_1_out[27], multiplexer_1_out[28], multiplexer_1_out[29], multiplexer_1_out[30], multiplexer_1_out[31]);
  assign or_10_out = or_6_out | gatekeeper_5_out_3;  // OR_Gate or_10, 32 bits wide
  assign or_11_out = or_10_out | gatekeeper_20_out_3;  // OR_Gate or_11, 32 bits wide
  and and_2 (and_2_out, eight_bit_eq_cmp_16_out_3, nor_1_out);
  Shifter #(.width(32)) shifter_3 (.in(inp1), .\dist (multiplexer_1_out[4:0]), .out(shifter_3_out));
  assign or_12_out = or_11_out | gatekeeper_21_out_3;  // OR_Gate or_12, 32 bits wide
  gatekeeper gatekeeper_24 (.in_1(and_2_out), .in_2(shifter_3_out), .out_3(gatekeeper_24_out_3));
  assign or_13_out = or_14_out | gatekeeper_23_out_3;  // OR_Gate or_13, 32 bits wide
  assign or_14_out = or_12_out | gatekeeper_22_out_3;  // OR_Gate or_14, 32 bits wide
  assign or_15_out = or_13_out | gatekeeper_6_out_3;  // OR_Gate or_15, 32 bits wide
  assign or_16_out = or_15_out | gatekeeper_7_out_3;  // OR_Gate or_16, 32 bits wide
  assign or_17_out = or_16_out | gatekeeper_8_out_3;  // OR_Gate or_17, 32 bits wide
  assign or_18_out = or_17_out | gatekeeper_9_out_3;  // OR_Gate or_18, 32 bits wide
  assign or_19_out = or_18_out | gatekeeper_10_out_3;  // OR_Gate or_19, 32 bits wide
  assign or_20_out = or_19_out | gatekeeper_11_out_3;  // OR_Gate or_20, 32 bits wide
  assign or_21_out = or_20_out | gatekeeper_24_out_3;  // OR_Gate or_21, 32 bits wide
  gatekeeper gatekeeper_25 (.in_1(enable), .in_2(or_21_out), .out_3(out_6));

  // Notes on the sheet:
  //   Add
  //   Subtract
  //   Multiply
  //   Increment
  //   Decrement
  //   Unsigned Cmp
  //   Signed Cmp
  //   ucmp0
  //   cmp0
  //   AND
  //   OR
  //   XOR
  //   NOT
  //   <<
  //   >>
  //   Bit shift
endmodule

module ALU_control (
  input  [31:0] inp1,
  input  [31:0] inp2,
  input  [15:0] control_in,
  input  clock_in,
  input  reset,
  output [31:0] outp1,
  output [31:0] outp2,
  output enable,
  output [7:0] operation
);

  wire button_1_out, falling_edge_pe_1_out_6, four_bit_eq_cmp_1_out_3, new_one_ticker_1_signal_out, or_1_out,
       or_2_out, or_3_out, or_4_out, or_5_out, or_6_out, sixt_bit_eq_cmp_1_out_3;
  wire [15:0] undriven;
  wire [31:4] extra_sticky_gate_1_out_put;

  Button button_1 (.out(button_1_out));
  sixt_bit_eq_cmp sixt_bit_eq_cmp_1 (.in_1(control_in), .in_2(16'hfffe), .out_3(sixt_bit_eq_cmp_1_out_3));
  or or_1 (or_1_out, reset, button_1_out);
  four_bit_eq_cmp four_bit_eq_cmp_1 (.in_1(control_in[7:4]), .in_2(4'b0001), .out_3(four_bit_eq_cmp_1_out_3));
  new_one_ticker new_one_ticker_1 (
    .clock_in(clock_in), .reset(or_2_out), .signal_in(four_bit_eq_cmp_1_out_3),
    .signal_out(new_one_ticker_1_signal_out));
  or or_2 (or_2_out, or_1_out, sixt_bit_eq_cmp_1_out_3);
  or or_3 (or_3_out, sixt_bit_eq_cmp_1_out_3, or_1_out);
  extra_sticky_gate extra_sticky_gate_1 (
    .clock(clock_in), .reset(or_4_out), .enable(new_one_ticker_1_signal_out), .data({undriven, control_in}),
    .out_put({extra_sticky_gate_1_out_put, operation[3:0]}));  // open: propagate_reset
  or or_4 (or_4_out, sixt_bit_eq_cmp_1_out_3, or_1_out);
  falling_edge_PE falling_edge_pe_1 (
    .in_1(four_bit_eq_cmp_1_out_3), .in_3(or_3_out), .in_2(clock_in), .out_6(falling_edge_pe_1_out_6));  // open: out_4, out_5
  buf or_5 (or_5_out, falling_edge_pe_1_out_6);  // OR_Gate
  better_sticky_gate better_sticky_gate_1 (
    .enable(new_one_ticker_1_signal_out), .data(inp1), .clock(clock_in), .reset(or_1_out), .out_put(outp1));
  better_sticky_gate better_sticky_gate_2 (
    .enable(new_one_ticker_1_signal_out), .data(inp2), .clock(clock_in), .reset(or_1_out), .out_put(outp2));
  falling_edge_PE falling_edge_pe_2 (
    .in_1(or_5_out), .in_3(or_6_out), .in_2(clock_in), .out_6(enable));  // open: out_4, out_5
  or or_6 (or_6_out, sixt_bit_eq_cmp_1_out_3, or_1_out);

  assign operation[7:4] = 4'b0000;
endmodule

module pulse_extender (
  input  inp,
  input  clock,
  input  reset,
  output reset_out,
  output clock_out,
  output out_put
);

  wire not_1_out;

  S_R_Flip_Flop s_r_ff_1 (.S(1'b0), .R(not_1_out), .clk(clock), .Q(out_put), .reset(reset), .preset(inp));  // open: Qn
  not not_1 (not_1_out, inp);

  assign clock_out = clock;
  assign reset_out = reset;
endmodule

module double_pulse_extender (
  input  in_1,
  input  in_2,
  input  in_3,
  output out_4,
  output out_5,
  output out_6
);

  wire not_1_out, not_2_out, s_r_ff_1_q;

  S_R_Flip_Flop s_r_ff_1 (
    .S(1'b0), .R(not_1_out), .clk(in_2), .Q(s_r_ff_1_q), .reset(in_3), .preset(in_1));  // open: Qn
  not not_1 (not_1_out, in_1);
  S_R_Flip_Flop s_r_ff_2 (.S(1'b0), .R(not_2_out), .clk(in_2), .Q(out_6), .reset(in_3), .preset(in_1));  // open: Qn
  not not_2 (not_2_out, s_r_ff_1_q);

  assign out_4 = in_3;
  assign out_5 = in_2;
endmodule

module VPE_three (
  input  in_1,
  input  [3:0] in_2,
  input  [3:0] in_3,
  input  in_4,
  output out_5
);

  wire and_5_out, and_6_out, and_7_out, and_8_out, and_9_out, and_10_out, and_11_out, and_12_out, j_k_ff_1_q,
       j_k_ff_2_q, j_k_ff_3_q, j_k_ff_4_q, or_3_out;
  wire [3:0] and_1_out, and_2_out, and_3_out, and_4_out, four_bit_incrementer_1_out_2, not_1_out, not_2_out,
       or_1_out, or_2_out;
  wire [3:3] four_bit_eq_cmp_1_out_3, four_bit_eq_cmp_2_out_3;

  four_bit_eq_cmp four_bit_eq_cmp_1 (.in_1(in_2), .in_2(4'b0000), .out_3(four_bit_eq_cmp_1_out_3[3]));
  four_bit_eq_cmp four_bit_eq_cmp_2 (.in_1(in_3), .in_2(4'b0000), .out_3(four_bit_eq_cmp_2_out_3[3]));
  assign and_1_out = 4'b0010 & {4{four_bit_eq_cmp_1_out_3[3]}};  // AND_Gate and_1, 4 bits wide
  assign or_1_out = and_1_out | and_2_out;  // OR_Gate or_1, 4 bits wide
  assign and_2_out = in_2 & ~{4{four_bit_eq_cmp_1_out_3[3]}};  // AND_Gate and_2, 4 bits wide
  assign and_3_out = or_1_out & {4{four_bit_eq_cmp_2_out_3[3]}};  // AND_Gate and_3, 4 bits wide
  assign or_2_out = and_3_out | and_4_out;  // OR_Gate or_2, 4 bits wide
  assign and_4_out = in_3 & ~{4{four_bit_eq_cmp_2_out_3[3]}};  // AND_Gate and_4, 4 bits wide
  assign not_1_out = ~or_2_out;  // NOT_Gate not_1, 4 bits wide
  assign not_2_out = ~four_bit_incrementer_1_out_2;  // NOT_Gate not_2, 4 bits wide
  four_bit_incrementer four_bit_incrementer_1 (.in_1(not_1_out), .out_2(four_bit_incrementer_1_out_2));
  and and_5 (and_5_out, not_2_out[0], in_1);
  J_K_Flip_Flop j_k_ff_1 (
    .J(or_3_out), .K(or_3_out), .clk(in_4), .Q(j_k_ff_1_q), .preset(and_5_out), .reset(and_6_out));  // open: Qn
  and and_6 (and_6_out, ~not_2_out[0], in_1);  // AND_Gate
  and and_7 (and_7_out, not_2_out[1], in_1);
  J_K_Flip_Flop j_k_ff_2 (
    .J(or_3_out), .K(or_3_out), .clk(j_k_ff_1_q), .Q(j_k_ff_2_q), .preset(and_7_out), .reset(and_8_out));  // open: Qn
  and and_8 (and_8_out, ~not_2_out[1], in_1);  // AND_Gate
  J_K_Flip_Flop j_k_ff_3 (
    .J(or_3_out), .K(or_3_out), .clk(j_k_ff_2_q), .Q(j_k_ff_3_q), .preset(and_9_out), .reset(and_10_out));  // open: Qn
  and and_9 (and_9_out, not_2_out[2], in_1);
  and and_10 (and_10_out, ~not_2_out[2], in_1);  // AND_Gate
  and and_11 (and_11_out, not_2_out[3], in_1);
  J_K_Flip_Flop j_k_ff_4 (
    .J(or_3_out), .K(or_3_out), .clk(j_k_ff_3_q), .Q(j_k_ff_4_q), .preset(and_11_out), .reset(and_12_out));  // open: Qn
  and and_12 (and_12_out, ~not_2_out[3], in_1);  // AND_Gate
  or or_3 (or_3_out, j_k_ff_4_q, j_k_ff_3_q, j_k_ff_2_q, j_k_ff_1_q);
  or or_4 (out_5, in_1, or_3_out);
endmodule

module micro_instr_passthrough (
  input  [15:0] in_1,
  output [3:0] out_2,
  output [3:0] out_3,
  output [3:0] out_4
);

  wire and_1_out, and_2_out, and_3_out, and_4_out, and_5_out, and_6_out, and_7_out, undriven, undriven_2,
       undriven_3, undriven_4, undriven_5, undriven_6, undriven_7, undriven_8;
  wire [3:0] and_29_out, and_30_out, and_31_out, and_32_out, and_33_out, and_34_out, and_35_out, and_36_out,
       and_37_out, and_38_out, and_39_out, and_40_out, and_41_out, and_42_out, and_43_out, and_44_out,
       and_45_out, and_46_out, and_47_out, and_48_out, and_49_out, or_2_out, or_3_out, or_4_out, or_5_out,
       or_6_out, or_7_out, or_10_out, or_11_out, or_12_out, or_13_out, or_14_out, or_15_out, or_16_out,
       or_17_out, or_18_out, or_19_out, or_20_out, or_21_out;
  wire [3:3] and_8_out, and_9_out, and_10_out, and_11_out, and_12_out, and_13_out, and_14_out, and_15_out,
       and_16_out, and_17_out, and_18_out, and_19_out, and_20_out, and_21_out, and_22_out, and_23_out,
       and_24_out, and_25_out, and_26_out, and_27_out, and_28_out;

  and and_1 (and_1_out, in_1[0], ~in_1[1], ~in_1[2], ~in_1[3], ~in_1[4], ~in_1[5], ~in_1[6], ~in_1[7], 1'b1, 1'b1, 1'b1, 1'b1, ~in_1[12], ~in_1[13], ~in_1[14], ~in_1[15]);  // AND_Gate
  and and_2 (and_2_out, ~in_1[0], in_1[1], ~in_1[2], ~in_1[3], ~in_1[4], ~in_1[5], ~in_1[6], ~in_1[7], 1'b1, 1'b1, 1'b1, 1'b1, ~in_1[12], ~in_1[13], ~in_1[14], ~in_1[15]);  // AND_Gate
  and and_3 (and_3_out, in_1[0], in_1[1], in_1[2], ~in_1[3], ~in_1[4], ~in_1[5], ~in_1[6], ~in_1[7], 1'b1, 1'b1, 1'b1, 1'b1, 1'b1, 1'b1, 1'b1, 1'b1);  // AND_Gate
  and and_4 (and_4_out, ~in_1[0], ~in_1[1], ~in_1[2], in_1[3], ~in_1[4], ~in_1[5], ~in_1[6], ~in_1[7], 1'b1, 1'b1, 1'b1, 1'b1, 1'b1, 1'b1, 1'b1, 1'b1);  // AND_Gate
  and and_5 (and_5_out, in_1[0], ~in_1[1], ~in_1[2], in_1[3], ~in_1[4], ~in_1[5], ~in_1[6], ~in_1[7], in_1[8], in_1[9], in_1[10], in_1[11], 1'b1, 1'b1, 1'b1, 1'b1);  // AND_Gate
  and and_6 (and_6_out, ~in_1[0], in_1[1], ~in_1[2], in_1[3], ~in_1[4], ~in_1[5], ~in_1[6], ~in_1[7], 1'b1, 1'b1, 1'b1, 1'b1, ~in_1[12], ~in_1[13], ~in_1[14], ~in_1[15]);  // AND_Gate
  and and_7 (and_7_out, in_1[0], in_1[1], ~in_1[2], in_1[3], ~in_1[4], ~in_1[5], ~in_1[6], ~in_1[7], 1'b1, 1'b1, 1'b1, 1'b1, ~in_1[12], ~in_1[13], ~in_1[14], ~in_1[15]);  // AND_Gate
  and and_8 (and_8_out[3], and_1_out, ~1'b1);  // AND_Gate
  and and_9 (and_9_out[3], and_1_out, 1'b1);
  and and_10 (and_10_out[3], and_1_out, ~1'b1);  // AND_Gate
  and and_11 (and_11_out[3], and_2_out, ~1'b1);  // AND_Gate
  and and_12 (and_12_out[3], and_2_out, 1'b1);
  and and_13 (and_13_out[3], and_2_out, ~1'b1);  // AND_Gate
  and and_14 (and_14_out[3], and_3_out, ~1'b1);  // AND_Gate
  and and_15 (and_15_out[3], and_3_out, 1'b1);
  and and_16 (and_16_out[3], and_3_out, 1'b1);
  and and_17 (and_17_out[3], and_4_out, ~1'b1);  // AND_Gate
  and and_18 (and_18_out[3], and_4_out, 1'b1);
  and and_19 (and_19_out[3], and_4_out, 1'b1);
  and and_20 (and_20_out[3], and_5_out, ~1'b1);  // AND_Gate
  and and_21 (and_21_out[3], and_5_out, ~1'b1);  // AND_Gate
  and and_22 (and_22_out[3], and_5_out, 1'b1);
  and and_23 (and_23_out[3], and_6_out, ~1'b1);  // AND_Gate
  and and_24 (and_24_out[3], and_6_out, 1'b1);
  and and_25 (and_25_out[3], and_6_out, ~1'b1);  // AND_Gate
  and and_26 (and_26_out[3], and_7_out, ~1'b1);  // AND_Gate
  and and_27 (and_27_out[3], and_7_out, 1'b1);
  and and_28 (and_28_out[3], and_7_out, ~1'b1);  // AND_Gate
  assign out_2 = and_29_out | or_2_out;  // OR_Gate or_1, 4 bits wide
  assign and_29_out = {4{and_8_out[3]}} & in_1[7:4];  // AND_Gate and_29, 4 bits wide
  assign and_30_out = {4{and_9_out[3]}} & in_1[11:8];  // AND_Gate and_30, 4 bits wide
  assign and_31_out = {4{and_10_out[3]}} & in_1[15:12];  // AND_Gate and_31, 4 bits wide
  assign or_2_out = and_32_out | or_3_out;  // OR_Gate or_2, 4 bits wide
  assign and_32_out = {4{and_11_out[3]}} & in_1[7:4];  // AND_Gate and_32, 4 bits wide
  assign and_33_out = {4{and_12_out[3]}} & in_1[11:8];  // AND_Gate and_33, 4 bits wide
  assign and_34_out = {4{and_13_out[3]}} & in_1[15:12];  // AND_Gate and_34, 4 bits wide
  assign or_3_out = and_35_out | or_4_out;  // OR_Gate or_3, 4 bits wide
  assign and_35_out = {4{and_14_out[3]}} & in_1[7:4];  // AND_Gate and_35, 4 bits wide
  assign and_36_out = {4{and_15_out[3]}} & in_1[11:8];  // AND_Gate and_36, 4 bits wide
  assign and_37_out = {4{and_16_out[3]}} & in_1[15:12];  // AND_Gate and_37, 4 bits wide
  assign or_4_out = and_38_out | or_5_out;  // OR_Gate or_4, 4 bits wide
  assign and_38_out = {4{and_17_out[3]}} & in_1[7:4];  // AND_Gate and_38, 4 bits wide
  assign and_39_out = {4{and_18_out[3]}} & in_1[11:8];  // AND_Gate and_39, 4 bits wide
  assign and_40_out = {4{and_19_out[3]}} & in_1[15:12];  // AND_Gate and_40, 4 bits wide
  assign or_5_out = and_41_out | or_6_out;  // OR_Gate or_5, 4 bits wide
  assign and_41_out = {4{and_20_out[3]}} & in_1[7:4];  // AND_Gate and_41, 4 bits wide
  assign and_42_out = {4{and_21_out[3]}} & in_1[11:8];  // AND_Gate and_42, 4 bits wide
  assign and_43_out = {4{and_22_out[3]}} & in_1[15:12];  // AND_Gate and_43, 4 bits wide
  assign or_6_out = and_44_out | or_7_out;  // OR_Gate or_6, 4 bits wide
  assign and_44_out = {4{and_23_out[3]}} & in_1[7:4];  // AND_Gate and_44, 4 bits wide
  assign and_45_out = {4{and_24_out[3]}} & in_1[11:8];  // AND_Gate and_45, 4 bits wide
  assign and_46_out = {4{and_25_out[3]}} & in_1[15:12];  // AND_Gate and_46, 4 bits wide
  assign or_7_out = and_47_out | and_48_out;  // OR_Gate or_7, 4 bits wide
  assign and_47_out = {4{and_26_out[3]}} & in_1[7:4];  // AND_Gate and_47, 4 bits wide
  assign and_48_out = {4{and_27_out[3]}} & in_1[11:8];  // AND_Gate and_48, 4 bits wide
  assign and_49_out = {4{and_28_out[3]}} & in_1[15:12];  // AND_Gate and_49, 4 bits wide
  assign out_3 = and_30_out | or_10_out;  // OR_Gate or_8, 4 bits wide
  assign out_4 = and_31_out | or_11_out;  // OR_Gate or_9, 4 bits wide
  assign or_10_out = and_33_out | or_12_out;  // OR_Gate or_10, 4 bits wide
  assign or_11_out = and_34_out | or_13_out;  // OR_Gate or_11, 4 bits wide
  assign or_12_out = and_36_out | or_14_out;  // OR_Gate or_12, 4 bits wide
  assign or_13_out = and_37_out | or_15_out;  // OR_Gate or_13, 4 bits wide
  assign or_14_out = and_39_out | or_16_out;  // OR_Gate or_14, 4 bits wide
  assign or_15_out = and_40_out | or_17_out;  // OR_Gate or_15, 4 bits wide
  assign or_16_out = and_42_out | or_18_out;  // OR_Gate or_16, 4 bits wide
  assign or_17_out = and_43_out | or_19_out;  // OR_Gate or_17, 4 bits wide
  assign or_18_out = and_45_out | or_20_out;  // OR_Gate or_18, 4 bits wide
  assign or_19_out = and_46_out | or_21_out;  // OR_Gate or_19, 4 bits wide
  assign or_20_out = and_48_out | 4'b0000;  // OR_Gate or_20, 4 bits wide
  assign or_21_out = and_49_out | 4'b0000;  // OR_Gate or_21, 4 bits wide
  // AND_Gate and_50 has open pins: in0=undriven, in1=undriven_2, out=open
  // AND_Gate and_51 has open pins: in0=undriven, in1=undriven_2, out=open
  // AND_Gate and_52 has open pins: in0=undriven, in1=undriven_2, out=open
  // AND_Gate and_53 has open pins: in0=undriven_3, in1=undriven_4, out=open
  // AND_Gate and_54 has open pins: in0=undriven_3, in1=undriven_4, out=open
  // AND_Gate and_55 has open pins: in0=undriven_3, in1=undriven_4, out=open
  // AND_Gate and_56 has open pins: in0=undriven_5, in1=undriven_6, out=open
  // AND_Gate and_57 has open pins: in0=undriven_5, in1=undriven_6, out=open
  // AND_Gate and_58 has open pins: in0=undriven_5, in1=undriven_6, out=open
  // AND_Gate and_59 has open pins: in0=undriven_7, in1=undriven_8, out=open
  // AND_Gate and_60 has open pins: in0=undriven_7, in1=undriven_8, out=open
  // AND_Gate and_61 has open pins: in0=undriven_7, in1=undriven_8, out=open
  // also tied to GND on the sheet: {and_48_out[0], and_48_out[1], and_48_out[2], and_48_out[3]}

  // Notes on the sheet:
  //   0D01
  //   0D02
  //   ND07
  //   ND08
  //   N009
  //   0D0a
  //   0D0a
endmodule

module tmp_regs_controller (
  input  [15:0] in_1,
  output out_2,
  output out_3,
  output out_4,
  output out_5,
  output A_to_secret,
  output B_to_data,
  output out_8,
  output B_to_addr,
  output Write_B,
  output out_11
);

  wire and_3_out, and_4_out, and_6_out, and_9_out, and_10_out, and_13_out, eight_bit_eq_cmp_1_out_3,
       four_bit_eq_cmp_1_out_3, four_bit_eq_cmp_2_out_3, four_bit_eq_cmp_3_out_3, four_bit_eq_cmp_4_out_3,
       four_bit_eq_cmp_5_out_3, four_bit_eq_cmp_6_out_3, or_1_out;

  and and_1 (out_2, ~in_1[0], in_1[1], ~in_1[2], ~in_1[3], ~in_1[4], ~in_1[5], ~in_1[6], ~in_1[7], ~in_1[8], ~in_1[9], ~in_1[10], ~in_1[11], ~in_1[12], in_1[13], ~in_1[14], ~in_1[15]);  // AND_Gate
  and and_2 (out_3, ~in_1[0], in_1[1], ~in_1[2], ~in_1[3], ~in_1[4], ~in_1[5], ~in_1[6], ~in_1[7], in_1[8], ~in_1[9], ~in_1[10], ~in_1[11], ~in_1[12], in_1[13], ~in_1[14], ~in_1[15]);  // AND_Gate
  and and_3 (and_3_out, ~in_1[0], in_1[1], ~in_1[2], ~in_1[3], ~in_1[4], ~in_1[5], ~in_1[6], ~in_1[7], ~in_1[8], in_1[9], ~in_1[10], ~in_1[11], ~in_1[12], in_1[13], ~in_1[14], ~in_1[15]);  // AND_Gate
  and and_4 (and_4_out, ~in_1[0], in_1[1], ~in_1[2], ~in_1[3], ~in_1[4], ~in_1[5], ~in_1[6], ~in_1[7], in_1[8], in_1[9], ~in_1[10], ~in_1[11], ~in_1[12], in_1[13], ~in_1[14], ~in_1[15]);  // AND_Gate
  and and_5 (out_5, ~in_1[0], in_1[1], ~in_1[2], ~in_1[3], ~in_1[4], ~in_1[5], ~in_1[6], ~in_1[7], ~in_1[8], ~in_1[9], in_1[10], ~in_1[11], ~in_1[12], in_1[13], ~in_1[14], ~in_1[15]);  // AND_Gate
  and and_6 (and_6_out, ~in_1[0], in_1[1], ~in_1[2], ~in_1[3], ~in_1[4], ~in_1[5], ~in_1[6], ~in_1[7], in_1[8], ~in_1[9], in_1[10], ~in_1[11], ~in_1[12], in_1[13], ~in_1[14], ~in_1[15]);  // AND_Gate
  and and_7 (B_to_data, ~in_1[0], in_1[1], ~in_1[2], ~in_1[3], ~in_1[4], ~in_1[5], ~in_1[6], ~in_1[7], ~in_1[8], ~in_1[9], ~in_1[10], ~in_1[11], in_1[12], in_1[13], ~in_1[14], ~in_1[15]);  // AND_Gate
  and and_8 (out_8, ~in_1[0], in_1[1], ~in_1[2], ~in_1[3], ~in_1[4], ~in_1[5], ~in_1[6], ~in_1[7], in_1[8], ~in_1[9], ~in_1[10], ~in_1[11], in_1[12], in_1[13], ~in_1[14], ~in_1[15]);  // AND_Gate
  and and_9 (and_9_out, ~in_1[0], in_1[1], ~in_1[2], ~in_1[3], ~in_1[4], ~in_1[5], ~in_1[6], ~in_1[7], ~in_1[8], in_1[9], ~in_1[10], ~in_1[11], in_1[12], in_1[13], ~in_1[14], ~in_1[15]);  // AND_Gate
  and and_10 (and_10_out, ~in_1[0], in_1[1], ~in_1[2], ~in_1[3], ~in_1[4], ~in_1[5], ~in_1[6], ~in_1[7], in_1[8], in_1[9], ~in_1[10], ~in_1[11], in_1[12], in_1[13], ~in_1[14], ~in_1[15]);  // AND_Gate
  and and_11 (Write_B, ~in_1[0], in_1[1], ~in_1[2], ~in_1[3], ~in_1[4], ~in_1[5], ~in_1[6], ~in_1[7], ~in_1[8], ~in_1[9], in_1[10], ~in_1[11], in_1[12], in_1[13], ~in_1[14], ~in_1[15]);  // AND_Gate
  and and_12 (out_11, ~in_1[0], in_1[1], ~in_1[2], ~in_1[3], ~in_1[4], ~in_1[5], ~in_1[6], ~in_1[7], in_1[8], ~in_1[9], in_1[10], ~in_1[11], in_1[12], in_1[13], ~in_1[14], ~in_1[15]);  // AND_Gate
  eight_bit_eq_cmp eight_bit_eq_cmp_1 (.in_1(in_1[7:0]), .in_2(8'h2), .out_3(eight_bit_eq_cmp_1_out_3));
  four_bit_eq_cmp four_bit_eq_cmp_1 (.in_1(in_1[11:8]), .in_2(4'b0110), .out_3(four_bit_eq_cmp_1_out_3));
  four_bit_eq_cmp four_bit_eq_cmp_2 (.in_1(in_1[11:8]), .in_2(4'b1000), .out_3(four_bit_eq_cmp_2_out_3));
  four_bit_eq_cmp four_bit_eq_cmp_3 (.in_1(in_1[11:8]), .in_2(4'b0111), .out_3(four_bit_eq_cmp_3_out_3));
  four_bit_eq_cmp four_bit_eq_cmp_4 (.in_1(in_1[11:8]), .in_2(4'b1001), .out_3(four_bit_eq_cmp_4_out_3));
  or or_1 (or_1_out, four_bit_eq_cmp_1_out_3, four_bit_eq_cmp_3_out_3, four_bit_eq_cmp_2_out_3, four_bit_eq_cmp_4_out_3, four_bit_eq_cmp_5_out_3, four_bit_eq_cmp_6_out_3);
  and and_13 (and_13_out, or_1_out, eight_bit_eq_cmp_1_out_3);
  four_bit_eq_cmp four_bit_eq_cmp_5 (.in_1(in_1[11:8]), .in_2(4'b1010), .out_3(four_bit_eq_cmp_5_out_3));
  four_bit_eq_cmp four_bit_eq_cmp_6 (.in_1(in_1[11:8]), .in_2(4'b1011), .out_3(four_bit_eq_cmp_6_out_3));
  or or_2 (out_4, and_3_out, and_4_out);
  or or_3 (A_to_secret, and_6_out, and_13_out);
  or or_4 (B_to_addr, and_9_out, and_10_out);

  // Notes on the sheet:
  //   A
  //   B
  //   To data bus
  //   To address bus
  //   ptr val to data bus
  //   ptr val + offs to data
  //   write
  //   to secret bus
  //   To data bus
  //   To address bus
  //   ptr val to data bus
  //   ptr val + offs to data
  //   write
  //   to secret bus
  //   A to data
  //   A to addr (3 ticks)
  //   A to addr
  //   Write A
  //   B to addr (3 ticks)
  //   B to secret
endmodule

module tmp_regs_unit (
  input  [31:0] data_bus_in,
  input  a_to_data,
  input  a_to_addr_long,
  input  a_to_addr,
  input  write_a,
  input  a_to_special_regs,
  input  b_to_data,
  input  b_to_addr_long,
  input  b_to_addr,
  input  write_b,
  input  b_to_special_regs,
  input  clock,
  input  reset,
  output [31:0] a_out,
  output [31:0] b_out,
  output [31:0] data_bus_out,
  output [31:0] addr_bus_out,
  output [31:0] to_special_regs
);

  wire [31:0] extra_sticky_gate_1_out_put, extra_sticky_gate_2_out_put, or_1_out, or_2_out,
       sticky_gate_1_out_put, sticky_gate_2_out_put, sticky_gate_3_out_put, sticky_gate_4_out_put,
       sticky_gate_5_out_put, sticky_gate_6_out_put;

  Register #(.width(32)) register_1 (.D(data_bus_in), .en(write_a), .clk(clock), .Q(a_out), .clr(reset));
  Register #(.width(32)) register_2 (.D(data_bus_in), .en(write_b), .clk(clock), .Q(b_out), .clr(reset));
  sticky_gate sticky_gate_1 (
    .clock(clock), .reset(reset), .enable(a_to_special_regs), .data(a_out), .out_put(sticky_gate_1_out_put));  // open: propagate_reset
  sticky_gate sticky_gate_2 (
    .clock(clock), .reset(reset), .enable(b_to_special_regs), .data(b_out), .out_put(sticky_gate_2_out_put));  // open: propagate_reset
  extra_sticky_gate extra_sticky_gate_1 (
    .clock(clock), .reset(reset), .enable(a_to_addr_long), .data(a_out), .out_put(extra_sticky_gate_1_out_put));  // open: propagate_reset
  sticky_gate sticky_gate_3 (
    .clock(clock), .reset(reset), .enable(a_to_addr), .data(a_out), .out_put(sticky_gate_3_out_put));  // open: propagate_reset
  extra_sticky_gate extra_sticky_gate_2 (
    .clock(clock), .reset(reset), .enable(b_to_addr_long), .data(b_out), .out_put(extra_sticky_gate_2_out_put));  // open: propagate_reset
  sticky_gate sticky_gate_4 (
    .clock(clock), .reset(reset), .enable(b_to_addr), .data(b_out), .out_put(sticky_gate_4_out_put));  // open: propagate_reset
  sticky_gate sticky_gate_5 (
    .clock(clock), .reset(reset), .enable(a_to_data), .data(a_out), .out_put(sticky_gate_5_out_put));  // open: propagate_reset
  assign or_1_out = extra_sticky_gate_1_out_put | sticky_gate_3_out_put;  // OR_Gate or_1, 32 bits wide
  sticky_gate sticky_gate_6 (
    .clock(clock), .reset(reset), .enable(b_to_data), .data(b_out), .out_put(sticky_gate_6_out_put));  // open: propagate_reset
  assign or_2_out = extra_sticky_gate_2_out_put | sticky_gate_4_out_put;  // OR_Gate or_2, 32 bits wide
  assign data_bus_out = sticky_gate_5_out_put | sticky_gate_6_out_put;  // OR_Gate or_3, 32 bits wide
  assign addr_bus_out = or_1_out | or_2_out;  // OR_Gate or_4, 32 bits wide
  assign to_special_regs = sticky_gate_1_out_put | sticky_gate_2_out_put;  // OR_Gate or_5, 32 bits wide
endmodule

module contextualiser (
  input  [15:0] in_1,
  input  [15:0] in_2,
  input  [15:0] in_3,
  output [15:0] out_4
);

  wire and_1_out, and_2_out, and_3_out, and_4_out, and_5_out, and_6_out, and_7_out, and_8_out,
       eight_bit_eq_cmp_1_out_3, eight_bit_eq_cmp_2_out_3, four_bit_eq_cmp_1_out_3, four_bit_eq_cmp_2_out_3,
       four_bit_eq_cmp_3_out_3, four_bit_eq_cmp_4_out_3, four_bit_eq_cmp_5_out_3, four_bit_eq_cmp_6_out_3,
       not_1_out, or_1_out, or_2_out, or_3_out, or_4_out, or_6_out, or_8_out;
  wire [3:0] four_bit_g8_upwards_1_out_3, four_bit_g8_upwards_2_out_3, four_bit_g8_upwards_3_out_3,
       four_bit_g8_upwards_4_out_3, four_bit_g8_upwards_5_out_3, four_bit_g8_upwards_6_out_3,
       four_bit_g8_upwards_7_out_3, four_bit_g8_upwards_8_out_3, four_bit_g8_upwards_9_out_3,
       four_bit_g8_upwards_10_out_3, four_bit_g8_upwards_11_out_3, four_bit_g8_upwards_12_out_3,
       four_bit_g8_upwards_13_out_3, four_bit_g8_upwards_15_out_3, four_bit_g8_upwards_16_out_3;
  wire [15:0] gatekeeper_1_p3, or_5_out, or_7_out, or_9_out;
  wire [15:12] four_bit_g8_upwards_14_out_3;

  eight_bit_eq_cmp eight_bit_eq_cmp_1 (.in_1(in_2[7:0]), .in_2(8'h3), .out_3(eight_bit_eq_cmp_1_out_3));
  eight_bit_eq_cmp eight_bit_eq_cmp_2 (.in_1(in_1[7:0]), .in_2(8'h31), .out_3(eight_bit_eq_cmp_2_out_3));
  four_bit_eq_cmp four_bit_eq_cmp_1 (.in_1(in_2[11:8]), .in_2(4'b0000), .out_3(four_bit_eq_cmp_1_out_3));
  four_bit_g8_upwards four_bit_g8_upwards_1 (.in_1(and_3_out), .in_2(in_1[15:12]), .out_3(four_bit_g8_upwards_1_out_3));
  four_bit_g8_upwards four_bit_g8_upwards_2 (.in_1(and_3_out), .in_2(in_2[11:8]), .out_3(four_bit_g8_upwards_2_out_3));
  and and_1 (and_1_out, eight_bit_eq_cmp_1_out_3, and_4_out);
  and and_2 (and_2_out, ~in_2[8], ~in_2[9]);  // AND_Gate
  four_bit_eq_cmp four_bit_eq_cmp_2 (.in_1(in_1[7:4]), .in_2(4'b0001), .out_3(four_bit_eq_cmp_2_out_3));
  four_bit_eq_cmp four_bit_eq_cmp_3 (.in_1(in_2[7:4]), .in_2(4'b0001), .out_3(four_bit_eq_cmp_3_out_3));
  four_bit_eq_cmp four_bit_eq_cmp_4 (.in_1(in_2[3:0]), .in_2(4'b0011), .out_3(four_bit_eq_cmp_4_out_3));
  four_bit_eq_cmp four_bit_eq_cmp_5 (.in_1(in_2[7:4]), .in_2(4'b0000), .out_3(four_bit_eq_cmp_5_out_3));
  four_bit_eq_cmp four_bit_eq_cmp_6 (.in_1(in_2[11:8]), .in_2(4'b0100), .out_3(four_bit_eq_cmp_6_out_3));
  four_bit_g8_upwards four_bit_g8_upwards_3 (.in_1(and_3_out), .in_2(in_2[7:4]), .out_3(four_bit_g8_upwards_3_out_3));
  four_bit_g8_upwards four_bit_g8_upwards_4 (.in_1(and_3_out), .in_2(in_2[3:0]), .out_3(four_bit_g8_upwards_4_out_3));
  and and_3 (and_3_out, and_1_out, ~or_2_out);  // AND_Gate
  or or_1 (or_1_out, and_2_out, ~in_2[10]);  // OR_Gate
  and and_4 (and_4_out, or_1_out, ~in_2[11]);  // AND_Gate
  or or_2 (or_2_out, and_5_out, and_7_out);
  and and_5 (and_5_out, eight_bit_eq_cmp_1_out_3, eight_bit_eq_cmp_2_out_3, ~four_bit_eq_cmp_1_out_3);  // AND_Gate
  and and_6 (and_6_out, four_bit_eq_cmp_2_out_3, four_bit_eq_cmp_3_out_3);
  and and_7 (and_7_out, four_bit_eq_cmp_2_out_3, and_8_out);
  and and_8 (and_8_out, four_bit_eq_cmp_4_out_3, four_bit_eq_cmp_5_out_3, four_bit_eq_cmp_6_out_3);
  four_bit_g8_upwards four_bit_g8_upwards_5 (.in_1(or_4_out), .in_2(in_1[11:8]), .out_3(four_bit_g8_upwards_5_out_3));
  or or_3 (or_3_out, and_3_out, or_4_out);
  or or_4 (or_4_out, 1'b0, and_5_out);
  four_bit_g8_upwards four_bit_g8_upwards_6 (.in_1(or_4_out), .in_2(in_2[11:8]), .out_3(four_bit_g8_upwards_6_out_3));
  four_bit_g8_upwards four_bit_g8_upwards_7 (.in_1(or_4_out), .in_2(in_2[7:4]), .out_3(four_bit_g8_upwards_7_out_3));
  assign or_5_out = {four_bit_g8_upwards_1_out_3, four_bit_g8_upwards_2_out_3, four_bit_g8_upwards_3_out_3, four_bit_g8_upwards_4_out_3} | {four_bit_g8_upwards_5_out_3, four_bit_g8_upwards_6_out_3, four_bit_g8_upwards_7_out_3, four_bit_g8_upwards_8_out_3};  // OR_Gate or_5, 16 bits wide
  four_bit_g8_upwards four_bit_g8_upwards_8 (.in_1(or_4_out), .in_2(in_2[3:0]), .out_3(four_bit_g8_upwards_8_out_3));
  or or_6 (or_6_out, or_3_out, and_6_out);
  four_bit_g8_upwards four_bit_g8_upwards_9 (.in_1(and_6_out), .in_2(in_1[15:12]), .out_3(four_bit_g8_upwards_9_out_3));
  four_bit_g8_upwards four_bit_g8_upwards_10 (
    .in_1(and_6_out), .in_2(in_1[11:8]), .out_3(four_bit_g8_upwards_10_out_3));
  four_bit_g8_upwards four_bit_g8_upwards_11 (.in_1(and_6_out), .in_2(in_2[7:4]), .out_3(four_bit_g8_upwards_11_out_3));
  four_bit_g8_upwards four_bit_g8_upwards_12 (.in_1(and_6_out), .in_2(in_1[3:0]), .out_3(four_bit_g8_upwards_12_out_3));
  assign or_7_out = or_5_out | {four_bit_g8_upwards_9_out_3, four_bit_g8_upwards_10_out_3, four_bit_g8_upwards_11_out_3, four_bit_g8_upwards_12_out_3};  // OR_Gate or_7, 16 bits wide
  four_bit_g8_upwards four_bit_g8_upwards_13 (
    .in_1(and_7_out), .in_2(in_2[11:8]), .out_3(four_bit_g8_upwards_13_out_3));
  four_bit_g8_upwards four_bit_g8_upwards_14 (
    .in_1(and_7_out), .in_2(in_1[11:8]), .out_3(four_bit_g8_upwards_14_out_3));
  or or_8 (or_8_out, or_6_out, and_7_out);
  four_bit_g8_upwards four_bit_g8_upwards_15 (.in_1(and_7_out), .in_2(in_2[7:4]), .out_3(four_bit_g8_upwards_15_out_3));
  four_bit_g8_upwards four_bit_g8_upwards_16 (.in_1(and_7_out), .in_2(in_2[3:0]), .out_3(four_bit_g8_upwards_16_out_3));
  assign or_9_out = or_7_out | {four_bit_g8_upwards_14_out_3, four_bit_g8_upwards_13_out_3, four_bit_g8_upwards_15_out_3, four_bit_g8_upwards_16_out_3};  // OR_Gate or_9, 16 bits wide
  not not_1 (not_1_out, or_8_out);
  // gatekeeper gatekeeper_1: pin names not known; wires that end beside it: in_2, not_1_out, gatekeeper_1_p3
  assign out_4 = gatekeeper_1_p3 | or_9_out;  // OR_Gate or_10, 16 bits wide

  // Notes on the sheet:
  //   instruction
  //   micro-instruction
  //   tmp
endmodule

module four_bit_g8 (
  input  in_1,
  input  [3:0] in_2,
  output [3:0] out_3
);

  assign out_3 = {4{in_1}} & in_2;  // AND_Gate and_1, 4 bits wide
endmodule

module four_bit_g8_upwards (
  input  in_1,
  input  [3:0] in_2,
  output [3:0] out_3
);

  assign out_3 = {4{in_1}} & in_2;  // AND_Gate and_1, 4 bits wide
endmodule

module instruction_decoder (
  input  [15:0] in_1,
  output [15:0] out_2
);

  wire and_1_out, and_2_out, and_3_out, eight_bit_eq_cmp_1_out_3, four_bit_eq_cmp_1_out_3,
       four_bit_eq_cmp_2_out_3, four_bit_eq_cmp_3_out_3, four_bit_eq_cmp_4_out_3, four_bit_eq_cmp_5_out_3,
       four_bit_eq_cmp_6_out_3, four_bit_eq_cmp_7_out_3;
  wire [3:0] undriven, undriven_2;
  wire [15:0] gatekeeper_1_p3, or_1_out, rom_1_data, rom_2_data, rom_3_data;
  wire [31:0] gatekeeper_2_out_3, gatekeeper_3_out_3, gatekeeper_4_out_3;
  wire [31:16] undriven_3, undriven_4, undriven_5;

  ROM #(.addrWidth(16), .dataWidth(16)) rom_1 (.addr(in_1), .data(rom_1_data));
  ROM #(.addrWidth(12), .dataWidth(16)) rom_2 (.addr(in_1[11:0]), .data(rom_2_data));
  ROM #(.dataWidth(16)) rom_3 (.addr(in_1[7:0]), .data(rom_3_data));
  four_bit_eq_cmp four_bit_eq_cmp_1 (.in_1(in_1[7:4]), .in_2(4'b0001), .out_3(four_bit_eq_cmp_1_out_3));
  four_bit_eq_cmp four_bit_eq_cmp_2 (.in_2(4'b0001), .out_3(four_bit_eq_cmp_2_out_3));  // open: in_1
  eight_bit_eq_cmp eight_bit_eq_cmp_1 (.in_1({undriven_2, undriven}), .in_2(8'h11), .out_3(eight_bit_eq_cmp_1_out_3));
  four_bit_eq_cmp four_bit_eq_cmp_3 (.in_2(4'b0001), .out_3(four_bit_eq_cmp_3_out_3));  // open: in_1
  four_bit_eq_cmp four_bit_eq_cmp_4 (.in_2(4'b0001), .out_3(four_bit_eq_cmp_4_out_3));  // open: in_1
  four_bit_eq_cmp four_bit_eq_cmp_5 (.in_2(4'b0001), .out_3(four_bit_eq_cmp_5_out_3));  // open: in_1
  four_bit_eq_cmp four_bit_eq_cmp_6 (.in_2(4'b0001), .out_3(four_bit_eq_cmp_6_out_3));  // open: in_1
  four_bit_eq_cmp four_bit_eq_cmp_7 (.in_1(4'b0001), .out_3(four_bit_eq_cmp_7_out_3));  // open: in_2
  // gatekeeper gatekeeper_1: pin names not known; wires that end beside it: 16'h100, four_bit_eq_cmp_1_out_3, gatekeeper_1_p3
  and and_1 (and_1_out, four_bit_eq_cmp_2_out_3, eight_bit_eq_cmp_1_out_3);
  gatekeeper gatekeeper_2 (.in_1(and_1_out), .in_2({undriven_3, 16'h2f}), .out_3(gatekeeper_2_out_3));
  and and_2 (and_2_out, four_bit_eq_cmp_3_out_3, four_bit_eq_cmp_4_out_3);
  gatekeeper gatekeeper_3 (.in_1(and_2_out), .in_2({undriven_4, 16'h47}), .out_3(gatekeeper_3_out_3));
  and and_3 (and_3_out, four_bit_eq_cmp_5_out_3, four_bit_eq_cmp_6_out_3, four_bit_eq_cmp_7_out_3);
  gatekeeper gatekeeper_4 (.in_1(and_3_out), .in_2({undriven_5, 16'h47}), .out_3(gatekeeper_4_out_3));
  assign or_1_out = gatekeeper_1_p3;  // OR_Gate or_1, 16 bits wide OR_Gate
  assign out_2 = rom_1_data | rom_2_data | rom_3_data | or_1_out;  // OR_Gate or_2, 16 bits wide
  // Pins of 16 and 32 bits meet at {undriven_3, 16'h2f}
  // Pins of 16 and 32 bits meet at {undriven_4, 16'h47}
  // Pins of 16 and 32 bits meet at {undriven_5, 16'h47}

  // Notes on the sheet:
  //   contents of rom_1 (hex, n*v repeats v):
  //   2 0 0 0 16 1e 32*0 4b 55
  //   contents of rom_2 (hex, n*v repeats v):
  //   0 4 7 c 44*0 a4 8*0 b0 200*0 11 16 254*0 1b 20
  //   contents of rom_3 (hex, n*v repeats v):
  //   49*0 a0
endmodule

module instruction_decdoer_v2 (
  input  [15:0] in_1,
  input  [7:0] in_2,
  output [15:0] out_3
);

  wire comparator_1_eq, comparator_2_eq, comparator_3_eq, comparator_4_eq, comparator_5_eq, comparator_6_eq,
       comparator_7_eq, comparator_8_eq, comparator_9_eq, comparator_10_eq, comparator_11_eq,
       comparator_12_eq, comparator_13_eq;
  wire [15:0] acc1, acc2, gatekeeper_1_p3, gatekeeper_2_p3, gatekeeper_3_p3, gatekeeper_4_p3,
       gatekeeper_5_p3, gatekeeper_7_p3, gatekeeper_8_p3, gatekeeper_9_p3, gatekeeper_10_p3,
       gatekeeper_11_p3, gatekeeper_12_p3, gatekeeper_13_p3, or_1_out, or_2_out, or_3_out, or_4_out,
       or_5_out, or_6_out, or_8_out, or_9_out, or_10_out, rom_1_data, rom_2_data, rom_3_data, rom_4_data,
       rom_5_data, rom_7_data, rom_8_data, rom_9_data, rom_10_data, rom_11_data, rom_12_data, rom_13_data;
  wire [31:0] gatekeeper_6_out_3, undriven;

  Comparator #(.width(16)) comparator_1 (.a(in_1), .b({16{1'b0}}), .eq(comparator_1_eq));  // open: gt, lt
  ROM #(.addrWidth(2), .dataWidth(16)) rom_1 (.addr(in_2[1:0]), .data(rom_1_data));
  Comparator #(.width(16)) comparator_2 (.a(in_1), .b(16'h1), .eq(comparator_2_eq));  // open: gt, lt
  ROM #(.addrWidth(2), .dataWidth(16)) rom_2 (.addr(in_2[1:0]), .data(rom_2_data));
  Comparator #(.width(12)) comparator_3 (.a(in_1[11:0]), .b(12'h2), .eq(comparator_3_eq));  // open: gt, lt
  ROM #(.addrWidth(3), .dataWidth(16)) rom_3 (.addr(in_2[2:0]), .data(rom_3_data));
  Comparator #(.width(12)) comparator_4 (.a(in_1[11:0]), .b(12'h3), .eq(comparator_4_eq));  // open: gt, lt
  ROM #(.addrWidth(3), .dataWidth(16)) rom_4 (.addr(in_2[2:0]), .data(rom_4_data));
  Comparator #(.width(12)) comparator_5 (.a(in_1[11:0]), .b(12'h102), .eq(comparator_5_eq));  // open: gt, lt
  ROM #(.addrWidth(3), .dataWidth(16)) rom_5 (.addr(in_2[2:0]), .data(rom_5_data));
  Comparator #(.width(12)) comparator_6 (.a(in_1[11:0]), .b(12'h103), .eq(comparator_6_eq));  // open: gt, lt
  ROM #(.addrWidth(3), .dataWidth(16)) rom_6 ();  // open: addr, data
  Comparator #(.width(12)) comparator_7 (.a(in_1[11:0]), .b(12'h202), .eq(comparator_7_eq));  // open: gt, lt
  ROM #(.addrWidth(3), .dataWidth(16)) rom_7 (.addr(in_2[2:0]), .data(rom_7_data));
  Comparator #(.width(12)) comparator_8 (.a(in_1[11:0]), .b(12'h202), .eq(comparator_8_eq));  // open: gt, lt
  ROM #(.addrWidth(3), .dataWidth(16)) rom_8 (.addr(in_2[2:0]), .data(rom_8_data));
  // gatekeeper gatekeeper_1: pin names not known; wires that end beside it: rom_1_data, comparator_1_eq, gatekeeper_1_p3
  // gatekeeper gatekeeper_2: pin names not known; wires that end beside it: rom_2_data, comparator_2_eq, gatekeeper_2_p3
  // gatekeeper gatekeeper_3: pin names not known; wires that end beside it: rom_3_data, comparator_3_eq, gatekeeper_3_p3
  // gatekeeper gatekeeper_4: pin names not known; wires that end beside it: rom_4_data, comparator_4_eq, gatekeeper_4_p3
  // gatekeeper gatekeeper_5: pin names not known; wires that end beside it: rom_5_data, comparator_5_eq, gatekeeper_5_p3
  gatekeeper gatekeeper_6 (.in_1(comparator_6_eq), .in_2(undriven), .out_3(gatekeeper_6_out_3));
  // gatekeeper gatekeeper_7: pin names not known; wires that end beside it: rom_7_data, comparator_7_eq, gatekeeper_7_p3
  // gatekeeper gatekeeper_8: pin names not known; wires that end beside it: rom_8_data, comparator_8_eq, gatekeeper_8_p3
  assign or_1_out = gatekeeper_2_p3 | gatekeeper_1_p3;  // OR_Gate or_1, 16 bits wide
  assign or_2_out = gatekeeper_3_p3 | or_1_out;  // OR_Gate or_2, 16 bits wide
  assign or_3_out = gatekeeper_4_p3 | or_2_out;  // OR_Gate or_3, 16 bits wide
  assign or_4_out = gatekeeper_5_p3 | or_3_out;  // OR_Gate or_4, 16 bits wide
  assign or_5_out = gatekeeper_6_out_3[15:0] | or_4_out;  // OR_Gate or_5, 16 bits wide
  assign or_6_out = gatekeeper_7_p3 | or_5_out;  // OR_Gate or_6, 16 bits wide
  assign acc1 = gatekeeper_8_p3 | or_6_out;  // OR_Gate or_7, 16 bits wide
  Comparator #(.width(16)) comparator_9 (.a(in_1), .b(16'h4), .eq(comparator_9_eq));  // open: gt, lt
  Comparator #(.width(16)) comparator_10 (.a(in_1), .b(16'h5), .eq(comparator_10_eq));  // open: gt, lt
  Comparator #(.width(16)) comparator_11 (.a(in_1), .b(16'h6), .eq(comparator_11_eq));  // open: gt, lt
  Comparator #(.width(16)) comparator_12 (.a(in_1), .b(16'h106), .eq(comparator_12_eq));  // open: gt, lt
  ROM #(.addrWidth(4), .dataWidth(16)) rom_9 (.addr(in_2[3:0]), .data(rom_9_data));
  ROM #(.addrWidth(3), .dataWidth(16)) rom_10 (.addr(in_2[2:0]), .data(rom_10_data));
  ROM #(.addrWidth(3), .dataWidth(16)) rom_11 (.addr(in_2[2:0]), .data(rom_11_data));
  ROM #(.addrWidth(4), .dataWidth(16)) rom_12 (.addr(in_2[3:0]), .data(rom_12_data));
  // gatekeeper gatekeeper_9: pin names not known; wires that end beside it: rom_9_data, comparator_9_eq, gatekeeper_9_p3
  assign or_8_out = gatekeeper_9_p3 | acc1;  // OR_Gate or_8, 16 bits wide
  // gatekeeper gatekeeper_10: pin names not known; wires that end beside it: rom_10_data, comparator_10_eq, gatekeeper_10_p3
  assign or_9_out = gatekeeper_10_p3 | or_8_out;  // OR_Gate or_9, 16 bits wide
  // gatekeeper gatekeeper_11: pin names not known; wires that end beside it: rom_11_data, comparator_11_eq, gatekeeper_11_p3
  assign or_10_out = gatekeeper_11_p3 | or_9_out;  // OR_Gate or_10, 16 bits wide
  // gatekeeper gatekeeper_12: pin names not known; wires that end beside it: rom_12_data, comparator_12_eq, gatekeeper_12_p3
  assign acc2 = gatekeeper_12_p3 | or_10_out;  // OR_Gate or_11, 16 bits wide
  Comparator #(.width(4)) comparator_13 (.a(in_1[7:4]), .b(4'b0001), .eq(comparator_13_eq));  // open: gt, lt
  ROM #(.addrWidth(3), .dataWidth(16)) rom_13 (.addr(in_2[2:0]), .data(rom_13_data));
  // gatekeeper gatekeeper_13: pin names not known; wires that end beside it: rom_13_data, comparator_13_eq, gatekeeper_13_p3
  assign out_3 = gatekeeper_13_p3 | acc2;  // OR_Gate or_12, 16 bits wide
  // Pins of 16 and 32 bits meet at gatekeeper_6_out_3

  // Other names for the same wires on the sheet: ctr[7:0] = in_2; instr[15:0] = in_1

  // Notes on the sheet:
  //   contents of rom_1 (hex, n*v repeats v):
  //   202 1 fffe fffe
  //   contents of rom_2 (hex, n*v repeats v):
  //   202 402 fffe fffe
  //   contents of rom_3 (hex, n*v repeats v):
  //   202 2402 3 602 fffe
  //   contents of rom_4 (hex, n*v repeats v):
  //   202 2402 3 702 fffe
  //   contents of rom_5 (hex, n*v repeats v):
  //   202 2402 3 802 fffe
  //   contents of rom_6 (hex, n*v repeats v):
  //   202 2402 3 902 fffe
  //   contents of rom_7 (hex, n*v repeats v):
  //   202 2402 3 a02 fffe
  //   contents of rom_8 (hex, n*v repeats v):
  //   202 2402 3 b02 fffe
  //   Call
  //   Return
  //   Push nothing
  //   Push constant
  //   contents of rom_9 (hex, n*v repeats v):
  //   202 2402 502 1602 1102 2 4 2202 402 fffe
  //   contents of rom_10 (hex, n*v repeats v):
  //   1202 402 1502 fffe
  //   contents of rom_11 (hex, n*v repeats v):
  //   1602 fffe
  //   contents of rom_12 (hex, n*v repeats v):
  //   202 2402 1602 1102 2202 25 1102 4 fffe
  //   ALU
  //   contents of rom_13 (hex, n*v repeats v):
  //   10 403 fffe
endmodule

module one_ticker (
  input  in_1,
  input  in_2,
  input  Reset,
  output out_4
);

  wire and_1_out, d_ff_1_q, not_1_out, or_1_out, s_r_ff_1_q;

  not not_1 (not_1_out, in_1);
  S_R_Flip_Flop s_r_ff_1 (.Q(s_r_ff_1_q), .reset(in_1), .preset(not_1_out));  // open: S, R, clk, Qn
  S_R_Flip_Flop s_r_ff_2 (.Q(out_4), .reset(or_1_out), .preset(and_1_out));  // open: S, R, clk, Qn
  and and_1 (and_1_out, in_1, s_r_ff_1_q, ~d_ff_1_q);  // AND_Gate
  or or_1 (or_1_out, Reset, d_ff_1_q);
  D_Flip_Flop d_ff_1 (.D(out_4), .clk(in_2), .Q(d_ff_1_q));  // open: Qn, preset, reset
endmodule

module special_registers (
  input  [31:0] data_bus_in,
  input  [15:0] control_bus_in,
  input  [31:0] from_control_unit,
  input  reset_pk,
  input  clock,
  input  reset,
  output [31:0] pk_out,
  output [31:0] data_bus_out,
  output [31:0] addr_out,
  output [31:0] sp_out,
  output [31:0] offs_out
);

  wire and_1_out, and_2_out, and_3_out, and_4_out, and_21_out, and_22_out, button_1_out,
       double_pulse_extender_1_out_6, new_one_ticker_1_signal_out, new_one_ticker_2_signal_out,
       new_one_ticker_3_signal_out, not_1_out, not_2_out, not_3_out, one_ticker_1_out_4, or_1_out, or_2_out,
       or_4_out, or_5_out, or_6_out, or_7_out, or_8_out, or_10_out, pk_write_control_1_increment,
       pk_write_control_1_write, pulse_extender_1_out_put, s_r_ff_1_qn, s_r_ff_2_q, s_r_ff_3_q, undriven_2,
       undriven_5, undriven_6;
  wire [4:0] undriven_4;
  wire [9:8] undriven_3;
  wire [11:0] undriven;
  wire [15:0] and_5_out;
  wire [15:15] and_23_out, and_24_out, and_25_out;
  wire [31:0] extra_sticky_gate_1_out_put, extra_sticky_gate_2_out_put, or_9_out, or_11_out,
       pk_write_control_1_data_out, sixt_bit_selector_1_p4, sticky_gate_1_out_put, sticky_gate_2_out_put,
       sticky_gate_3_out_put, sticky_gate_4_out_put, sticky_gate_5_out_put, sticky_gate_6_out_put,
       sticky_gate_7_out_put;

  and and_1 (and_1_out, ~control_bus_in[0], control_bus_in[1], ~control_bus_in[2], ~control_bus_in[3], ~control_bus_in[4], ~control_bus_in[5], ~control_bus_in[6], ~control_bus_in[7]);  // AND_Gate
  and and_2 (and_2_out, ~control_bus_in[8], ~control_bus_in[9], ~control_bus_in[10], ~control_bus_in[11]);  // AND_Gate
  and and_3 (and_3_out, control_bus_in[12], ~control_bus_in[13], ~control_bus_in[14], ~control_bus_in[15]);  // AND_Gate
  and and_4 (and_4_out, ~control_bus_in[12], ~control_bus_in[13], control_bus_in[14], ~control_bus_in[15]);  // AND_Gate
  and and_5 (and_5_out[0], ~control_bus_in[12], ~control_bus_in[13], ~control_bus_in[14], ~control_bus_in[15]);  // AND_Gate
  and and_6 (and_5_out[1], control_bus_in[12], ~control_bus_in[13], ~control_bus_in[14], ~control_bus_in[15]);  // AND_Gate
  and and_7 (and_5_out[2], ~control_bus_in[12], control_bus_in[13], ~control_bus_in[14], ~control_bus_in[15]);  // AND_Gate
  and and_8 (and_5_out[3], control_bus_in[12], control_bus_in[13], ~control_bus_in[14], ~control_bus_in[15]);  // AND_Gate
  and and_9 (and_5_out[4], ~control_bus_in[12], ~control_bus_in[13], control_bus_in[14], ~control_bus_in[15]);  // AND_Gate
  and and_10 (and_5_out[5], control_bus_in[12], ~control_bus_in[13], control_bus_in[14], ~control_bus_in[15]);  // AND_Gate
  and and_11 (and_5_out[6], ~control_bus_in[12], control_bus_in[13], control_bus_in[14], ~control_bus_in[15]);  // AND_Gate
  and and_12 (and_5_out[7], control_bus_in[12], control_bus_in[13], control_bus_in[14], ~control_bus_in[15]);  // AND_Gate
  and and_13 (and_5_out[8], ~control_bus_in[12], ~control_bus_in[13], ~control_bus_in[14], control_bus_in[15]);  // AND_Gate
  and and_14 (and_5_out[9], control_bus_in[12], ~control_bus_in[13], ~control_bus_in[14], control_bus_in[15]);  // AND_Gate
  and and_15 (and_5_out[10], ~control_bus_in[12], control_bus_in[13], ~control_bus_in[14], control_bus_in[15]);  // AND_Gate
  and and_16 (and_5_out[11], control_bus_in[12], control_bus_in[13], ~control_bus_in[14], control_bus_in[15]);  // AND_Gate
  and and_17 (and_5_out[12], ~control_bus_in[12], ~control_bus_in[13], control_bus_in[14], control_bus_in[15]);  // AND_Gate
  and and_18 (and_5_out[13], control_bus_in[12], ~control_bus_in[13], control_bus_in[14], control_bus_in[15]);  // AND_Gate
  and and_19 (and_5_out[14], ~control_bus_in[12], control_bus_in[13], control_bus_in[14], control_bus_in[15]);  // AND_Gate
  and and_20 (and_5_out[15], control_bus_in[12], control_bus_in[13], control_bus_in[14], control_bus_in[15]);
  and and_21 (and_21_out, control_bus_in[0], ~control_bus_in[1], ~control_bus_in[2], ~control_bus_in[3], ~control_bus_in[4], ~control_bus_in[5], ~control_bus_in[6], ~control_bus_in[7], ~control_bus_in[8], ~control_bus_in[9], ~control_bus_in[10], ~control_bus_in[11], ~control_bus_in[12], ~control_bus_in[13], ~control_bus_in[14], ~control_bus_in[15]);  // AND_Gate
  and and_22 (and_22_out, ~control_bus_in[0], control_bus_in[1], control_bus_in[2], control_bus_in[3], control_bus_in[4], control_bus_in[5], control_bus_in[6], control_bus_in[7], control_bus_in[8], control_bus_in[9], control_bus_in[10], control_bus_in[11], control_bus_in[12], control_bus_in[13], control_bus_in[14], control_bus_in[15]);  // AND_Gate
  and and_23 (and_23_out[15], and_1_out, and_2_out);
  and and_24 (and_24_out[15], and_1_out, and_3_out);
  and and_25 (and_25_out[15], and_1_out, and_4_out);
  // AND_Gate and_26 has open pins: in0={16{and_23_out[15]}}, in1=and_5_out, out=open
  // AND_Gate and_27 has open pins: in0={16{and_24_out[15]}}, in1=and_5_out, out=open
  // AND_Gate and_28 has open pins: in0={16{and_25_out[15]}}, in1=and_5_out, out=open
  S_R_Flip_Flop s_r_ff_1 (.Qn(s_r_ff_1_qn), .preset(pulse_extender_1_out_put));  // open: S, R, clk, Q, reset
  Button button_1 (.out(button_1_out));
  or or_1 (or_1_out, reset, s_r_ff_1_qn);
  S_R_Flip_Flop s_r_ff_2 (.Q(s_r_ff_2_q), .reset(pulse_extender_1_out_put), .preset(or_1_out));  // open: S, R, clk, Qn
  or or_2 (or_2_out, button_1_out, reset_pk);
  double_pulse_extender double_pulse_extender_1 (
    .in_1(s_r_ff_2_q), .in_2(clock), .out_6(double_pulse_extender_1_out_6));  // open: in_3, out_4, out_5
  S_R_Flip_Flop #(.trigger("falling")) s_r_ff_3 (
    .S(s_r_ff_2_q), .R(pulse_extender_1_out_put), .clk(clock), .Q(s_r_ff_3_q), .reset(undriven_2));  // open: Qn, preset
  one_ticker one_ticker_1 (.in_1(s_r_ff_3_q), .in_2(clock), .out_4(one_ticker_1_out_4));  // open: Reset
  pulse_extender pulse_extender_1 (
    .inp(one_ticker_1_out_4), .clock(clock), .out_put(pulse_extender_1_out_put));  // open: reset, reset_out, clock_out
  or or_3 (undriven_3[9], undriven_3[9], undriven_3[9]);
  or or_4 (or_4_out, undriven_3[8], double_pulse_extender_1_out_6);
  or or_5 (or_5_out, clock, s_r_ff_3_q);
  new_one_ticker new_one_ticker_1 (
    .clock_in(clock), .signal_in(reset), .signal_out(new_one_ticker_1_signal_out));  // open: reset
  counting_register counting_register_1 (
    .data_in(sixt_bit_selector_1_p4), .clock(or_5_out), .increment(undriven_5), .decrement(undriven_3[9]),
    .write(or_4_out), .reset(reset), .out_7(sp_out));
  Register #(.width(32)) register_1 (.D(data_bus_in), .en(undriven_4[4]), .clk(clock), .Q(offs_out), .clr(reset));
  not not_1 (not_1_out, new_one_ticker_1_signal_out);
  not not_2 (not_2_out, new_one_ticker_2_signal_out);
  new_one_ticker new_one_ticker_2 (
    .clock_in(clock), .signal_in(not_1_out), .signal_out(new_one_ticker_2_signal_out));  // open: reset
  sticky_gate sticky_gate_1 (
    .clock(clock), .reset(or_7_out), .enable(undriven_3[9]), .data(sp_out), .out_put(sticky_gate_1_out_put));  // open: propagate_reset
  // sixt_bit_selector sixt_bit_selector_1: pin names not known; wires that end beside it: double_pulse_extender_1_out_6, data_bus_in, {32{1'b1}}, sixt_bit_selector_1_p4
  or or_6 (or_6_out, and_22_out, reset);
  not not_3 (not_3_out, new_one_ticker_3_signal_out);
  new_one_ticker new_one_ticker_3 (
    .clock_in(clock), .signal_in(not_2_out), .signal_out(new_one_ticker_3_signal_out));  // open: reset
  new_one_ticker new_one_ticker_4 (.clock_in(clock), .signal_in(not_3_out), .signal_out(undriven_3[9]));  // open: reset
  sticky_gate sticky_gate_2 (
    .clock(clock), .reset(or_7_out), .enable(undriven_3[9]), .data(sp_out), .out_put(sticky_gate_2_out_put));  // open: propagate_reset
  sticky_gate sticky_gate_3 (
    .clock(clock), .reset(or_6_out), .enable(undriven_4[0]), .data(offs_out), .out_put(sticky_gate_3_out_put));  // open: propagate_reset
  pk_write_control pk_write_control_1 (
    .begin_instruction(and_21_out), .write_in(undriven[4]), .increment_in(undriven[5]),
    .data_bus_in(data_bus_in), .goto_z(undriven[6]), .goto_nz(undriven[7]), .goto_n(undriven[8]),
    .goto_nn(undriven[9]), .goto_p(undriven[10]), .goto_np(undriven[11]),
    .from_control_bus(from_control_unit), .data_out(pk_write_control_1_data_out),
    .increment(pk_write_control_1_increment), .write(pk_write_control_1_write));
  sticky_gate sticky_gate_4 (
    .clock(clock), .reset(or_7_out), .enable(undriven_6), .data(sp_out), .out_put(sticky_gate_4_out_put));  // open: propagate_reset
  extra_sticky_gate extra_sticky_gate_1 (
    .clock(clock), .reset(or_7_out), .enable(undriven_3[9]), .data(sp_out),
    .out_put(extra_sticky_gate_1_out_put));  // open: propagate_reset
  or or_7 (or_7_out, reset, and_22_out);
  counting_register counting_register_2 (
    .data_in(pk_write_control_1_data_out), .clock(clock), .increment(pk_write_control_1_increment),
    .write(pk_write_control_1_write), .reset(or_8_out), .out_7(pk_out));  // open: decrement
  or or_8 (or_8_out, or_2_out, reset);
  assign or_9_out = extra_sticky_gate_1_out_put | sticky_gate_2_out_put | sticky_gate_1_out_put;  // OR_Gate or_9, 32 bits wide
  // Probe on pk_out
  sticky_gate sticky_gate_5 (
    .clock(clock), .reset(or_10_out), .enable(undriven[3]), .data(pk_out), .out_put(sticky_gate_5_out_put));  // open: propagate_reset
  or or_10 (or_10_out, or_8_out, and_22_out);
  extra_sticky_gate extra_sticky_gate_2 (
    .clock(clock), .reset(or_10_out), .enable(undriven[1]), .data(pk_out),
    .out_put(extra_sticky_gate_2_out_put));  // open: propagate_reset
  sticky_gate sticky_gate_6 (
    .clock(clock), .reset(or_10_out), .enable(undriven[2]), .data(pk_out), .out_put(sticky_gate_6_out_put));  // open: propagate_reset
  sticky_gate sticky_gate_7 (
    .clock(clock), .reset(or_10_out), .enable(undriven[0]), .data(pk_out), .out_put(sticky_gate_7_out_put));  // open: propagate_reset
  assign or_11_out = extra_sticky_gate_2_out_put | sticky_gate_6_out_put | sticky_gate_5_out_put;  // OR_Gate or_11, 32 bits wide
  assign data_bus_out = sticky_gate_7_out_put | sticky_gate_4_out_put | sticky_gate_3_out_put;  // OR_Gate or_12, 32 bits wide
  assign addr_out = or_11_out | or_9_out;  // OR_Gate or_13, 32 bits wide
endmodule

module pk_write_control (
  input  begin_instruction,
  input  write_in,
  input  increment_in,
  input  [31:0] data_bus_in,
  input  goto_z,
  input  goto_nz,
  input  goto_n,
  input  goto_nn,
  input  goto_p,
  input  goto_np,
  input  [31:0] from_control_bus,
  output [31:0] data_out,
  output increment,
  output write
);

  wire and_1_out, and_2_out, and_3_out, and_4_out, and_5_out, and_6_out, and_7_out, and_8_out, and_9_out,
       and_10_out, and_11_out, and_12_out, and_13_out, long_eq_zero_1_out_2, or_1_out, or_2_out, or_3_out,
       or_4_out, or_5_out, or_6_out, or_7_out, or_10_out, or_11_out, or_12_out;

  and and_1 (and_1_out, ~long_eq_zero_1_out_2, ~data_bus_in[31]);  // AND_Gate
  Multiplexer #(.width(32)) multiplexer_1 (.in0(data_bus_in), .in1(from_control_bus), .out(data_out), .sel(or_10_out));
  long_eq_zero long_eq_zero_1 (.in_1(data_bus_in), .out_2(long_eq_zero_1_out_2));
  and and_2 (and_2_out, long_eq_zero_1_out_2, goto_z);
  or or_1 (or_1_out, and_2_out, and_3_out);
  and and_3 (and_3_out, ~long_eq_zero_1_out_2, goto_nz);  // AND_Gate
  and and_4 (and_4_out, goto_z, ~long_eq_zero_1_out_2);  // AND_Gate
  or or_2 (or_2_out, and_4_out, and_5_out);
  and and_5 (and_5_out, long_eq_zero_1_out_2, goto_nz);
  and and_6 (and_6_out, goto_n, data_bus_in[31]);
  or or_3 (or_3_out, and_6_out, and_7_out);
  and and_7 (and_7_out, ~data_bus_in[31], goto_nn);  // AND_Gate
  and and_8 (and_8_out, and_1_out, goto_p);
  or or_4 (or_4_out, and_8_out, and_9_out);
  and and_9 (and_9_out, ~and_1_out, goto_np);  // AND_Gate
  or or_5 (or_5_out, or_2_out, or_12_out);
  and and_10 (and_10_out, goto_n, ~or_3_out);  // AND_Gate
  or or_6 (or_6_out, and_10_out, and_11_out);
  and and_11 (and_11_out, goto_nn, ~or_3_out);  // AND_Gate
  and and_12 (and_12_out, goto_p, ~or_4_out);  // AND_Gate
  or or_7 (or_7_out, and_12_out, and_13_out);
  and and_13 (and_13_out, goto_np, ~or_4_out);  // AND_Gate
  or or_8 (increment, begin_instruction, increment_in, or_5_out);
  or or_9 (write, write_in, or_10_out);
  or or_10 (or_10_out, or_1_out, or_11_out);
  or or_11 (or_11_out, or_3_out, or_4_out);
  or or_12 (or_12_out, or_6_out, or_7_out);
endmodule

module sVPE (
  input  in_1,
  input  in_2,
  input  in_3,
  output out_4,
  output out_5,
  output out_6
);

  VPE_three vpe_three_1 (.in_3({3'b001, in_2}), .in_1(in_1), .in_4(in_3), .out_5(out_6));  // open: in_2

  assign out_4 = in_2;
  assign out_5 = in_3;
endmodule

module sad (
  input  in_1,
  input  in_2,
  output out_3
);

  wire not_1_out;

  S_R_Flip_Flop s_r_ff_1 (.S(1'b0), .R(not_1_out), .clk(in_2), .Q(out_3), .preset(in_1));  // open: reset, Qn
  not not_1 (not_1_out, in_1);
endmodule

module sticky_gate (
  input  enable,
  input  [31:0] data,
  input  clock,
  input  reset,
  output propagate_reset,
  output [31:0] out_put
);

  wire or_1_out, s_r_ff_1_q, s_r_ff_2_q, t_ff_1_q;
  wire [31:0] buffer_1_out, buffer_2_out, buffer_3_out, buffer_4_out, buffer_5_out, buffer_6_out,
       buffer_7_out, buffer_8_out, buffer_9_out, buffer_10_out, buffer_11_out, buffer_12_out, buffer_13_out,
       buffer_14_out, buffer_15_out, gatekeeper_1_out_3, register_1_q;

  S_R_Flip_Flop s_r_ff_1 (.Q(s_r_ff_1_q), .reset(or_1_out), .preset(enable));  // open: S, R, clk, Qn
  S_R_Flip_Flop #(.trigger("falling")) s_r_ff_2 (
    .S(s_r_ff_1_q), .R(1'b0), .clk(enable), .Q(s_r_ff_2_q), .reset(or_1_out));  // open: Qn, preset
  gatekeeper gatekeeper_1 (.in_1(enable), .in_2(data), .out_3(gatekeeper_1_out_3));
  assign buffer_1_out = buffer_6_out;  // Buffer buffer_1, 32 bits wide
  Register #(.trigger("falling"), .width(32)) register_1 (
    .D(data), .en(1'b1), .clk(enable), .Q(register_1_q), .clr(or_1_out));
  T_Flip_Flop t_ff_1 (.T(s_r_ff_2_q), .clk(clock), .Q(t_ff_1_q), .reset(or_1_out));  // open: Qn, preset
  or or_1 (or_1_out, reset, t_ff_1_q);
  assign buffer_2_out = gatekeeper_1_out_3;  // Buffer buffer_2, 32 bits wide
  assign buffer_3_out = buffer_2_out;  // Buffer buffer_3, 32 bits wide
  assign buffer_4_out = buffer_3_out;  // Buffer buffer_4, 32 bits wide
  assign buffer_5_out = buffer_4_out;  // Buffer buffer_5, 32 bits wide
  assign buffer_6_out = buffer_7_out;  // Buffer buffer_6, 32 bits wide
  assign buffer_7_out = buffer_8_out;  // Buffer buffer_7, 32 bits wide
  assign buffer_8_out = buffer_9_out;  // Buffer buffer_8, 32 bits wide
  assign buffer_9_out = buffer_14_out;  // Buffer buffer_9, 32 bits wide
  assign buffer_10_out = buffer_1_out;  // Buffer buffer_10, 32 bits wide
  assign buffer_11_out = buffer_10_out;  // Buffer buffer_11, 32 bits wide
  assign buffer_12_out = buffer_11_out;  // Buffer buffer_12, 32 bits wide
  assign buffer_13_out = buffer_12_out;  // Buffer buffer_13, 32 bits wide
  assign buffer_14_out = buffer_5_out;  // Buffer buffer_14, 32 bits wide
  assign buffer_15_out = buffer_13_out;  // Buffer buffer_15, 32 bits wide
  assign out_put = buffer_15_out | register_1_q;  // OR_Gate or_2, 32 bits wide

  assign propagate_reset = reset;
endmodule
module extra_sticky_gate (
  input  enable,
  input  [31:0] data,
  input  clock,
  input  reset,
  output propagate_reset,
  output [31:0] out_put
);

  wire or_1_out, s_r_ff_1_q, s_r_ff_2_q, t_ff_1_q, t_ff_2_q;
  wire [31:0] buffer_1_out, buffer_2_out, buffer_3_out, buffer_4_out, buffer_5_out, buffer_6_out,
       buffer_7_out, buffer_8_out, buffer_9_out, buffer_10_out, buffer_11_out, buffer_12_out, buffer_13_out,
       buffer_14_out, buffer_15_out, gatekeeper_1_out_3, register_1_q;

  S_R_Flip_Flop s_r_ff_1 (.Q(s_r_ff_1_q), .reset(or_1_out), .preset(enable));  // open: S, R, clk, Qn
  S_R_Flip_Flop #(.trigger("falling")) s_r_ff_2 (
    .S(s_r_ff_1_q), .R(1'b0), .clk(enable), .Q(s_r_ff_2_q), .reset(or_1_out));  // open: Qn, preset
  gatekeeper gatekeeper_1 (.in_1(enable), .in_2(data), .out_3(gatekeeper_1_out_3));
  assign buffer_1_out = buffer_6_out;  // Buffer buffer_1, 32 bits wide
  Register #(.trigger("falling"), .width(32)) register_1 (
    .D(data), .en(1'b1), .clk(enable), .Q(register_1_q), .clr(or_1_out));
  T_Flip_Flop t_ff_1 (.T(s_r_ff_2_q), .clk(clock), .Q(t_ff_1_q), .reset(or_1_out));  // open: Qn, preset
  or or_1 (or_1_out, reset, t_ff_2_q);
  assign buffer_2_out = gatekeeper_1_out_3;  // Buffer buffer_2, 32 bits wide
  assign buffer_3_out = buffer_2_out;  // Buffer buffer_3, 32 bits wide
  assign buffer_4_out = buffer_3_out;  // Buffer buffer_4, 32 bits wide
  assign buffer_5_out = buffer_4_out;  // Buffer buffer_5, 32 bits wide
  assign buffer_6_out = buffer_7_out;  // Buffer buffer_6, 32 bits wide
  assign buffer_7_out = buffer_8_out;  // Buffer buffer_7, 32 bits wide
  assign buffer_8_out = buffer_9_out;  // Buffer buffer_8, 32 bits wide
  assign buffer_9_out = buffer_14_out;  // Buffer buffer_9, 32 bits wide
  assign buffer_10_out = buffer_1_out;  // Buffer buffer_10, 32 bits wide
  assign buffer_11_out = buffer_10_out;  // Buffer buffer_11, 32 bits wide
  assign buffer_12_out = buffer_11_out;  // Buffer buffer_12, 32 bits wide
  assign buffer_13_out = buffer_12_out;  // Buffer buffer_13, 32 bits wide
  T_Flip_Flop t_ff_2 (.T(t_ff_1_q), .clk(clock), .Q(t_ff_2_q), .reset(or_1_out));  // open: Qn, preset
  assign buffer_14_out = buffer_5_out;  // Buffer buffer_14, 32 bits wide
  assign buffer_15_out = buffer_13_out;  // Buffer buffer_15, 32 bits wide
  assign out_put = buffer_15_out | register_1_q;  // OR_Gate or_2, 32 bits wide

  assign propagate_reset = reset;
endmodule

module new_register_unit (
  input  Write,
  input  Data_out,
  input  Addr_out,
  input  ALU_Out,
  input  [3:0] in_5,
  input  [3:0] in_6,
  input  [3:0] in_7,
  input  [3:0] in_8,
  input  [31:0] data_in,
  input  in_10,
  input  in_11,
  output [31:0] out_12,
  output [31:0] out_13,
  output [31:0] out_14,
  output [31:0] out_15
);

  wire [31:0] my_register_1_addr_out, my_register_1_alu1_out, my_register_1_alu2_out, my_register_1_data_out,
       my_register_1_value, my_register_2_addr_out, my_register_2_alu1_out, my_register_2_alu2_out,
       my_register_2_data_out, my_register_2_value, my_register_3_addr_out, my_register_3_alu1_out,
       my_register_3_alu2_out, my_register_3_data_out, my_register_3_value, my_register_4_addr_out,
       my_register_4_alu1_out, my_register_4_alu2_out, my_register_4_data_out, my_register_4_value,
       my_register_5_addr_out, my_register_5_alu1_out, my_register_5_alu2_out, my_register_5_data_out,
       my_register_5_value, my_register_6_addr_out, my_register_6_alu1_out, my_register_6_alu2_out,
       my_register_6_data_out, my_register_6_value, my_register_7_addr_out, my_register_7_alu1_out,
       my_register_7_alu2_out, my_register_7_data_out, my_register_7_value, my_register_8_addr_out,
       my_register_8_alu1_out, my_register_8_alu2_out, my_register_8_data_out, my_register_8_value,
       my_register_9_addr_out, my_register_9_alu1_out, my_register_9_alu2_out, my_register_9_data_out,
       my_register_9_value, my_register_10_addr_out, my_register_10_alu1_out, my_register_10_alu2_out,
       my_register_10_data_out, my_register_10_value, my_register_11_addr_out, my_register_11_alu1_out,
       my_register_11_alu2_out, my_register_11_data_out, my_register_11_value, my_register_12_addr_out,
       my_register_12_alu1_out, my_register_12_alu2_out, my_register_12_data_out, my_register_12_value,
       my_register_13_addr_out, my_register_13_alu1_out, my_register_13_alu2_out, my_register_13_data_out,
       my_register_13_value, my_register_14_addr_out, my_register_14_alu1_out, my_register_14_alu2_out,
       my_register_14_data_out, my_register_14_value, my_register_15_addr_out, my_register_15_alu1_out,
       my_register_15_alu2_out, my_register_15_data_out, my_register_15_value, my_register_16_addr_out,
       my_register_16_alu1_out, my_register_16_alu2_out, my_register_16_data_out, my_register_16_value,
       or_3_out, or_4_out, or_5_out, or_6_out, or_7_out, or_8_out, or_9_out, or_10_out, or_11_out, or_12_out,
       or_13_out, or_14_out, or_15_out, or_16_out, or_17_out, or_18_out, or_19_out, or_20_out, or_21_out,
       or_22_out, or_23_out, or_24_out, or_25_out, or_26_out, or_27_out, or_28_out, or_29_out, or_30_out,
       or_33_out, or_34_out, or_35_out, or_36_out, or_37_out, or_38_out, or_39_out, or_40_out, or_41_out,
       or_42_out, or_43_out, or_44_out, or_45_out, or_46_out, or_47_out, or_48_out, or_49_out, or_50_out,
       or_51_out, or_52_out, or_53_out, or_54_out, or_55_out, or_56_out, or_57_out, or_58_out, or_59_out,
       or_60_out;

  assign out_12 = my_register_1_data_out | or_3_out;  // OR_Gate or_1, 32 bits wide
  assign out_13 = my_register_1_addr_out | or_4_out;  // OR_Gate or_2, 32 bits wide
  // Probe on my_register_1_value
  my_register my_register_1 (
    .clock(in_10), .reset(in_11), .ID(4'b0000), .bus_output(in_5), .ALU_out_1(in_6), .ALU_out_2(in_7),
    .write_target(in_8), .data_in(data_in), .control_in({ALU_Out, Addr_out, Data_out, Write}),
    .data_out(my_register_1_data_out), .addr_out(my_register_1_addr_out), .alu1_out(my_register_1_alu1_out),
    .alu2_out(my_register_1_alu2_out), .value(my_register_1_value));
  assign or_3_out = my_register_2_data_out | or_5_out;  // OR_Gate or_3, 32 bits wide
  assign or_4_out = my_register_2_addr_out | or_6_out;  // OR_Gate or_4, 32 bits wide
  // Probe on my_register_2_value
  my_register my_register_2 (
    .clock(in_10), .reset(in_11), .ID(4'b0001), .bus_output(in_5), .ALU_out_1(in_6), .ALU_out_2(in_7),
    .write_target(in_8), .data_in(data_in), .control_in({ALU_Out, Addr_out, Data_out, Write}),
    .data_out(my_register_2_data_out), .addr_out(my_register_2_addr_out), .alu1_out(my_register_2_alu1_out),
    .alu2_out(my_register_2_alu2_out), .value(my_register_2_value));
  assign or_5_out = my_register_3_data_out | or_7_out;  // OR_Gate or_5, 32 bits wide
  assign or_6_out = my_register_3_addr_out | or_8_out;  // OR_Gate or_6, 32 bits wide
  // Probe on my_register_3_value
  my_register my_register_3 (
    .clock(in_10), .reset(in_11), .ID(4'b0010), .bus_output(in_5), .ALU_out_1(in_6), .ALU_out_2(in_7),
    .write_target(in_8), .data_in(data_in), .control_in({ALU_Out, Addr_out, Data_out, Write}),
    .data_out(my_register_3_data_out), .addr_out(my_register_3_addr_out), .alu1_out(my_register_3_alu1_out),
    .alu2_out(my_register_3_alu2_out), .value(my_register_3_value));
  assign or_7_out = my_register_4_data_out | or_9_out;  // OR_Gate or_7, 32 bits wide
  assign or_8_out = my_register_4_addr_out | or_10_out;  // OR_Gate or_8, 32 bits wide
  // Probe on my_register_4_value
  my_register my_register_4 (
    .clock(in_10), .reset(in_11), .ID(4'b0011), .bus_output(in_5), .ALU_out_1(in_6), .ALU_out_2(in_7),
    .write_target(in_8), .data_in(data_in), .control_in({ALU_Out, Addr_out, Data_out, Write}),
    .data_out(my_register_4_data_out), .addr_out(my_register_4_addr_out), .alu1_out(my_register_4_alu1_out),
    .alu2_out(my_register_4_alu2_out), .value(my_register_4_value));
  assign or_9_out = my_register_5_data_out | or_11_out;  // OR_Gate or_9, 32 bits wide
  assign or_10_out = my_register_5_addr_out | or_12_out;  // OR_Gate or_10, 32 bits wide
  // Probe on my_register_5_value
  my_register my_register_5 (
    .clock(in_10), .reset(in_11), .ID(4'b0100), .bus_output(in_5), .ALU_out_1(in_6), .ALU_out_2(in_7),
    .write_target(in_8), .data_in(data_in), .control_in({ALU_Out, Addr_out, Data_out, Write}),
    .data_out(my_register_5_data_out), .addr_out(my_register_5_addr_out), .alu1_out(my_register_5_alu1_out),
    .alu2_out(my_register_5_alu2_out), .value(my_register_5_value));
  assign or_11_out = my_register_6_data_out | or_13_out;  // OR_Gate or_11, 32 bits wide
  assign or_12_out = my_register_6_addr_out | or_14_out;  // OR_Gate or_12, 32 bits wide
  // Probe on my_register_6_value
  my_register my_register_6 (
    .clock(in_10), .reset(in_11), .ID(4'b0101), .bus_output(in_5), .ALU_out_1(in_6), .ALU_out_2(in_7),
    .write_target(in_8), .data_in(data_in), .control_in({ALU_Out, Addr_out, Data_out, Write}),
    .data_out(my_register_6_data_out), .addr_out(my_register_6_addr_out), .alu1_out(my_register_6_alu1_out),
    .alu2_out(my_register_6_alu2_out), .value(my_register_6_value));
  assign or_13_out = my_register_7_data_out | or_15_out;  // OR_Gate or_13, 32 bits wide
  assign or_14_out = my_register_7_addr_out | or_16_out;  // OR_Gate or_14, 32 bits wide
  // Probe on my_register_7_value
  my_register my_register_7 (
    .clock(in_10), .reset(in_11), .ID(4'b0110), .bus_output(in_5), .ALU_out_1(in_6), .ALU_out_2(in_7),
    .write_target(in_8), .data_in(data_in), .control_in({ALU_Out, Addr_out, Data_out, Write}),
    .data_out(my_register_7_data_out), .addr_out(my_register_7_addr_out), .alu1_out(my_register_7_alu1_out),
    .alu2_out(my_register_7_alu2_out), .value(my_register_7_value));
  assign or_15_out = my_register_8_data_out | or_17_out;  // OR_Gate or_15, 32 bits wide
  assign or_16_out = my_register_8_addr_out | or_18_out;  // OR_Gate or_16, 32 bits wide
  // Probe on my_register_8_value
  my_register my_register_8 (
    .clock(in_10), .reset(in_11), .ID(4'b0111), .bus_output(in_5), .ALU_out_1(in_6), .ALU_out_2(in_7),
    .write_target(in_8), .data_in(data_in), .control_in({ALU_Out, Addr_out, Data_out, Write}),
    .data_out(my_register_8_data_out), .addr_out(my_register_8_addr_out), .alu1_out(my_register_8_alu1_out),
    .alu2_out(my_register_8_alu2_out), .value(my_register_8_value));
  assign or_17_out = my_register_9_data_out | or_19_out;  // OR_Gate or_17, 32 bits wide
  assign or_18_out = my_register_9_addr_out | or_20_out;  // OR_Gate or_18, 32 bits wide
  // Probe on my_register_9_value
  my_register my_register_9 (
    .clock(in_10), .reset(in_11), .ID(4'b1000), .bus_output(in_5), .ALU_out_1(in_6), .ALU_out_2(in_7),
    .write_target(in_8), .data_in(data_in), .control_in({ALU_Out, Addr_out, Data_out, Write}),
    .data_out(my_register_9_data_out), .addr_out(my_register_9_addr_out), .alu1_out(my_register_9_alu1_out),
    .alu2_out(my_register_9_alu2_out), .value(my_register_9_value));
  assign or_19_out = my_register_10_data_out | or_21_out;  // OR_Gate or_19, 32 bits wide
  assign or_20_out = my_register_10_addr_out | or_22_out;  // OR_Gate or_20, 32 bits wide
  // Probe on my_register_10_value
  my_register my_register_10 (
    .clock(in_10), .reset(in_11), .ID(4'b1001), .bus_output(in_5), .ALU_out_1(in_6), .ALU_out_2(in_7),
    .write_target(in_8), .data_in(data_in), .control_in({ALU_Out, Addr_out, Data_out, Write}),
    .data_out(my_register_10_data_out), .addr_out(my_register_10_addr_out),
    .alu1_out(my_register_10_alu1_out), .alu2_out(my_register_10_alu2_out), .value(my_register_10_value));
  assign or_21_out = my_register_11_data_out | or_23_out;  // OR_Gate or_21, 32 bits wide
  assign or_22_out = my_register_11_addr_out | or_24_out;  // OR_Gate or_22, 32 bits wide
  // Probe on my_register_11_value
  my_register my_register_11 (
    .clock(in_10), .reset(in_11), .ID(4'b1010), .bus_output(in_5), .ALU_out_1(in_6), .ALU_out_2(in_7),
    .write_target(in_8), .data_in(data_in), .control_in({ALU_Out, Addr_out, Data_out, Write}),
    .data_out(my_register_11_data_out), .addr_out(my_register_11_addr_out),
    .alu1_out(my_register_11_alu1_out), .alu2_out(my_register_11_alu2_out), .value(my_register_11_value));
  assign or_23_out = my_register_12_data_out | or_25_out;  // OR_Gate or_23, 32 bits wide
  assign or_24_out = my_register_12_addr_out | or_26_out;  // OR_Gate or_24, 32 bits wide
  // Probe on my_register_12_value
  my_register my_register_12 (
    .clock(in_10), .reset(in_11), .ID(4'b1011), .bus_output(in_5), .ALU_out_1(in_6), .ALU_out_2(in_7),
    .write_target(in_8), .data_in(data_in), .control_in({ALU_Out, Addr_out, Data_out, Write}),
    .data_out(my_register_12_data_out), .addr_out(my_register_12_addr_out),
    .alu1_out(my_register_12_alu1_out), .alu2_out(my_register_12_alu2_out), .value(my_register_12_value));
  assign or_25_out = my_register_13_data_out | or_27_out;  // OR_Gate or_25, 32 bits wide
  assign or_26_out = my_register_13_addr_out | or_28_out;  // OR_Gate or_26, 32 bits wide
  // Probe on my_register_13_value
  my_register my_register_13 (
    .clock(in_10), .reset(in_11), .ID(4'b1100), .bus_output(in_5), .ALU_out_1(in_6), .ALU_out_2(in_7),
    .write_target(in_8), .data_in(data_in), .control_in({ALU_Out, Addr_out, Data_out, Write}),
    .data_out(my_register_13_data_out), .addr_out(my_register_13_addr_out),
    .alu1_out(my_register_13_alu1_out), .alu2_out(my_register_13_alu2_out), .value(my_register_13_value));
  assign or_27_out = my_register_14_data_out | or_29_out;  // OR_Gate or_27, 32 bits wide
  assign or_28_out = my_register_14_addr_out | or_30_out;  // OR_Gate or_28, 32 bits wide
  // Probe on my_register_14_value
  my_register my_register_14 (
    .clock(in_10), .reset(in_11), .ID(4'b1101), .bus_output(in_5), .ALU_out_1(in_6), .ALU_out_2(in_7),
    .write_target(in_8), .data_in(data_in), .control_in({ALU_Out, Addr_out, Data_out, Write}),
    .data_out(my_register_14_data_out), .addr_out(my_register_14_addr_out),
    .alu1_out(my_register_14_alu1_out), .alu2_out(my_register_14_alu2_out), .value(my_register_14_value));
  assign or_29_out = my_register_15_data_out | my_register_16_data_out;  // OR_Gate or_29, 32 bits wide
  assign or_30_out = my_register_15_addr_out | my_register_16_addr_out;  // OR_Gate or_30, 32 bits wide
  // Probe on my_register_15_value
  my_register my_register_15 (
    .clock(in_10), .reset(in_11), .ID(4'b1110), .bus_output(in_5), .ALU_out_1(in_6), .ALU_out_2(in_7),
    .write_target(in_8), .data_in(data_in), .control_in({ALU_Out, Addr_out, Data_out, Write}),
    .data_out(my_register_15_data_out), .addr_out(my_register_15_addr_out),
    .alu1_out(my_register_15_alu1_out), .alu2_out(my_register_15_alu2_out), .value(my_register_15_value));
  // Probe on my_register_16_value
  my_register my_register_16 (
    .clock(in_10), .reset(in_11), .ID(4'b1111), .bus_output(in_5), .ALU_out_1(in_6), .ALU_out_2(in_7),
    .write_target(in_8), .data_in(data_in), .control_in({ALU_Out, Addr_out, Data_out, Write}),
    .data_out(my_register_16_data_out), .addr_out(my_register_16_addr_out),
    .alu1_out(my_register_16_alu1_out), .alu2_out(my_register_16_alu2_out), .value(my_register_16_value));
  assign out_14 = my_register_1_alu1_out | or_33_out;  // OR_Gate or_31, 32 bits wide
  assign out_15 = my_register_1_alu2_out | or_34_out;  // OR_Gate or_32, 32 bits wide
  assign or_33_out = my_register_2_alu1_out | or_35_out;  // OR_Gate or_33, 32 bits wide
  assign or_34_out = my_register_2_alu2_out | or_36_out;  // OR_Gate or_34, 32 bits wide
  assign or_35_out = my_register_3_alu1_out | or_37_out;  // OR_Gate or_35, 32 bits wide
  assign or_36_out = my_register_3_alu2_out | or_38_out;  // OR_Gate or_36, 32 bits wide
  assign or_37_out = my_register_4_alu1_out | or_39_out;  // OR_Gate or_37, 32 bits wide
  assign or_38_out = my_register_4_alu2_out | or_40_out;  // OR_Gate or_38, 32 bits wide
  assign or_39_out = my_register_5_alu1_out | or_41_out;  // OR_Gate or_39, 32 bits wide
  assign or_40_out = my_register_5_alu2_out | or_42_out;  // OR_Gate or_40, 32 bits wide
  assign or_41_out = my_register_6_alu1_out | or_43_out;  // OR_Gate or_41, 32 bits wide
  assign or_42_out = my_register_6_alu2_out | or_44_out;  // OR_Gate or_42, 32 bits wide
  assign or_43_out = my_register_7_alu1_out | or_45_out;  // OR_Gate or_43, 32 bits wide
  assign or_44_out = my_register_7_alu2_out | or_46_out;  // OR_Gate or_44, 32 bits wide
  assign or_45_out = my_register_8_alu1_out | or_47_out;  // OR_Gate or_45, 32 bits wide
  assign or_46_out = my_register_8_alu2_out | or_48_out;  // OR_Gate or_46, 32 bits wide
  assign or_47_out = my_register_9_alu1_out | or_49_out;  // OR_Gate or_47, 32 bits wide
  assign or_48_out = my_register_9_alu2_out | or_50_out;  // OR_Gate or_48, 32 bits wide
  assign or_49_out = my_register_10_alu1_out | or_51_out;  // OR_Gate or_49, 32 bits wide
  assign or_50_out = my_register_10_alu2_out | or_52_out;  // OR_Gate or_50, 32 bits wide
  assign or_51_out = my_register_11_alu1_out | or_53_out;  // OR_Gate or_51, 32 bits wide
  assign or_52_out = my_register_11_alu2_out | or_54_out;  // OR_Gate or_52, 32 bits wide
  assign or_53_out = my_register_12_alu1_out | or_55_out;  // OR_Gate or_53, 32 bits wide
  assign or_54_out = my_register_12_alu2_out | or_56_out;  // OR_Gate or_54, 32 bits wide
  assign or_55_out = my_register_13_alu1_out | or_57_out;  // OR_Gate or_55, 32 bits wide
  assign or_56_out = my_register_13_alu2_out | or_58_out;  // OR_Gate or_56, 32 bits wide
  assign or_57_out = my_register_14_alu1_out | or_59_out;  // OR_Gate or_57, 32 bits wide
  assign or_58_out = my_register_14_alu2_out | or_60_out;  // OR_Gate or_58, 32 bits wide
  assign or_59_out = my_register_15_alu1_out | my_register_16_alu1_out;  // OR_Gate or_59, 32 bits wide
  assign or_60_out = my_register_15_alu2_out | my_register_16_alu2_out;  // OR_Gate or_60, 32 bits wide

  // Notes on the sheet:
  //   bus output
  //   ALU out 1
  //   ALU out 2
  //   Write target
  //   Data
  //   Data out
  //   Addr out
  //   ALU out 1
  //   ALU out 2
endmodule

module my_register (
  input  [31:0] data_in,
  input  [3:0] control_in,
  input  [3:0] bus_output,
  input  [3:0] ALU_out_1,
  input  [3:0] ALU_out_2,
  input  [3:0] write_target,
  input  clock,
  input  reset,
  input  [3:0] ID,
  output [31:0] value,
  output [31:0] data_out,
  output [31:0] addr_out,
  output [31:0] alu1_out,
  output [31:0] alu2_out
);

  wire and_1_out, and_2_out, button_1_out, nor_1_out, nor_2_out, nor_3_out, nor_4_out, or_1_out, or_2_out,
       xor_1_out, xor_2_out, xor_3_out, xor_4_out, xor_5_out, xor_6_out, xor_7_out, xor_8_out, xor_9_out,
       xor_10_out, xor_11_out, xor_12_out, xor_13_out, xor_14_out, xor_15_out, xor_16_out, xor_17_out,
       xor_18_out, xor_19_out, xor_20_out;

  or or_1 (or_1_out, control_in[2], control_in[1]);
  xor xor_1 (xor_1_out, bus_output[0], ID[0]);
  xor xor_2 (xor_2_out, bus_output[1], ID[1]);
  xor xor_3 (xor_3_out, bus_output[2], ID[2]);
  xor xor_4 (xor_4_out, bus_output[3], ID[3]);
  xor xor_5 (xor_5_out, or_1_out, 1'b1);
  xor xor_6 (xor_6_out, ALU_out_1[0], ID[0]);
  xor xor_7 (xor_7_out, ALU_out_1[1], ID[1]);
  xor xor_8 (xor_8_out, ALU_out_1[2], ID[2]);
  xor xor_9 (xor_9_out, ALU_out_1[3], ID[3]);
  xor xor_10 (xor_10_out, control_in[3], 1'b1);
  xor xor_11 (xor_11_out, ALU_out_2[0], ID[0]);
  xor xor_12 (xor_12_out, ALU_out_2[1], ID[1]);
  xor xor_13 (xor_13_out, ALU_out_2[2], ID[2]);
  xor xor_14 (xor_14_out, ALU_out_2[3], ID[3]);
  xor xor_15 (xor_15_out, control_in[3], 1'b1);
  xor xor_16 (xor_16_out, write_target[0], ID[0]);
  xor xor_17 (xor_17_out, write_target[1], ID[1]);
  xor xor_18 (xor_18_out, write_target[2], ID[2]);
  xor xor_19 (xor_19_out, write_target[3], ID[3]);
  xor xor_20 (xor_20_out, control_in[0], 1'b1);
  nor nor_1 (nor_1_out, xor_1_out, xor_2_out, xor_3_out, xor_4_out, xor_5_out);
  nor nor_2 (nor_2_out, xor_6_out, xor_7_out, xor_8_out, xor_9_out, xor_10_out);
  nor nor_3 (nor_3_out, xor_11_out, xor_12_out, xor_13_out, xor_14_out, xor_15_out);
  nor nor_4 (nor_4_out, xor_16_out, xor_17_out, xor_18_out, xor_19_out, xor_20_out);
  Register #(.width(32)) register_1 (.D(data_in), .en(nor_4_out), .clk(clock), .Q(value), .clr(reset));
  and and_1 (and_1_out, control_in[2], nor_1_out);
  Button button_1 (.out(button_1_out));
  and and_2 (and_2_out, control_in[1], nor_1_out);
  or or_2 (or_2_out, reset, button_1_out);
  better_sticky_gate better_sticky_gate_1 (
    .enable(and_2_out), .data(value), .clock(clock), .reset(or_2_out), .out_put(data_out));
  better_extra_sticky_gate better_extra_sticky_gate_1 (
    .enable(and_1_out), .data(value), .clock(clock), .reset(or_2_out), .out_put(addr_out));
  better_sticky_gate better_sticky_gate_2 (
    .enable(nor_2_out), .data(value), .clock(clock), .reset(or_2_out), .out_put(alu1_out));
  better_sticky_gate better_sticky_gate_3 (
    .enable(nor_3_out), .data(value), .clock(clock), .reset(or_2_out), .out_put(alu2_out));

  // Notes on the sheet:
  //   Data
  //   output to bus
  //   output to ALU 1
  //   Write
  //   Data out
  //   Addr out
  //   output to ALU 2
endmodule

module GRU (
  input  in_1,
  output out_2
);

  wire s_r_ff_2_q;

  S_R_Flip_Flop s_r_ff_1 (.S(1'b1), .R(1'b0), .clk(in_1), .Q(out_2), .reset(s_r_ff_2_q));  // open: Qn, preset
  S_R_Flip_Flop s_r_ff_2 (.S(out_2), .R(1'b0), .clk(in_1), .Q(s_r_ff_2_q));  // open: reset, Qn, preset
endmodule

module cave (
  input  [15:0] in_1,
  input  [31:0] in_2,
  input  [31:0] in_3,
  input  Clock,
  input  Reset,
  output [31:0] out_6,
  output [31:0] out_7
);

  wire and_1_out, and_2_out, and_3_out, and_4_out, and_5_out, and_6_out, and_7_out, buffer_1_out,
       buffer_2_out, buffer_3_out, buffer_4_out, buffer_5_out, buffer_6_out, buffer_7_out, buffer_8_out,
       buffer_9_out, buffer_10_out, button_1_out, not_1_out, or_1_out, sixt_bit_eq_cmp_1_out_3,
       sixt_bit_eq_cmp_2_out_3, sixt_bit_eq_cmp_3_out_3, sixt_bit_eq_cmp_4_out_3, sixt_bit_eq_cmp_5_out_3,
       sixt_bit_eq_cmp_6_out_3, sixt_bit_eq_cmp_7_out_3;
  wire [31:0] extra_sticky_gate_1_out_put, extra_sticky_gate_2_out_put, extra_sticky_gate_3_out_put,
       extra_sticky_gate_4_out_put, register_1_q, register_2_q, sticky_gate_1_out_put, sticky_gate_2_out_put,
       sticky_gate_3_out_put;

  Button button_1 (.out(button_1_out));
  or or_1 (or_1_out, Reset, button_1_out);
  Register #(.trigger("falling"), .width(32)) register_1 (
    .D(in_2), .en(1'b1), .clk(Clock), .Q(register_1_q), .clr(or_1_out));
  buf buffer_1 (buffer_1_out, Clock);
  buf buffer_2 (buffer_2_out, buffer_1_out);
  buf buffer_3 (buffer_3_out, buffer_2_out);
  buf buffer_4 (buffer_4_out, buffer_5_out);
  buf buffer_5 (buffer_5_out, buffer_6_out);
  buf buffer_6 (buffer_6_out, buffer_7_out);
  buf buffer_7 (buffer_7_out, buffer_10_out);
  not not_1 (not_1_out, Clock);
  and and_1 (and_1_out, not_1_out, sixt_bit_eq_cmp_1_out_3);
  sixt_bit_eq_cmp sixt_bit_eq_cmp_1 (.in_1(in_1), .in_2(16'h20), .out_3(sixt_bit_eq_cmp_1_out_3));
  and and_2 (and_2_out, not_1_out, sixt_bit_eq_cmp_2_out_3);
  sixt_bit_eq_cmp sixt_bit_eq_cmp_2 (.in_1(in_1), .in_2(16'h21), .out_3(sixt_bit_eq_cmp_2_out_3));
  and and_3 (and_3_out, not_1_out, sixt_bit_eq_cmp_3_out_3);
  sixt_bit_eq_cmp sixt_bit_eq_cmp_3 (.in_1(in_1), .in_2(16'h22), .out_3(sixt_bit_eq_cmp_3_out_3));
  and and_4 (and_4_out, not_1_out, sixt_bit_eq_cmp_4_out_3);
  sixt_bit_eq_cmp sixt_bit_eq_cmp_4 (.in_1(in_1), .in_2(16'h23), .out_3(sixt_bit_eq_cmp_4_out_3));
  and and_5 (and_5_out, not_1_out, sixt_bit_eq_cmp_5_out_3);
  sixt_bit_eq_cmp sixt_bit_eq_cmp_5 (.in_1(in_1), .in_2(16'h24), .out_3(sixt_bit_eq_cmp_5_out_3));
  and and_6 (and_6_out, not_1_out, sixt_bit_eq_cmp_6_out_3);
  sixt_bit_eq_cmp sixt_bit_eq_cmp_6 (.in_1(in_1), .in_2(16'h25), .out_3(sixt_bit_eq_cmp_6_out_3));
  and and_7 (and_7_out, not_1_out, sixt_bit_eq_cmp_7_out_3);
  sixt_bit_eq_cmp sixt_bit_eq_cmp_7 (.in_1(in_1), .in_2(16'h26), .out_3(sixt_bit_eq_cmp_7_out_3));
  Register #(.trigger("falling"), .width(32)) register_2 (
    .D(in_3), .en(1'b1), .clk(Clock), .Q(register_2_q), .clr(or_1_out));
  // Probe on register_1_q
  // Probe on register_2_q
  buf buffer_8 (buffer_8_out, buffer_3_out);
  buf buffer_9 (buffer_9_out, buffer_8_out);
  buf buffer_10 (buffer_10_out, buffer_9_out);
  sticky_gate sticky_gate_1 (
    .clock(buffer_4_out), .reset(or_1_out), .enable(and_1_out), .data(register_1_q),
    .out_put(sticky_gate_1_out_put));  // open: propagate_reset
  extra_sticky_gate extra_sticky_gate_1 (
    .clock(buffer_4_out), .reset(or_1_out), .enable(and_2_out), .data(register_1_q),
    .out_put(extra_sticky_gate_1_out_put));  // open: propagate_reset
  sticky_gate sticky_gate_2 (
    .clock(buffer_4_out), .reset(or_1_out), .enable(and_3_out), .data(register_2_q),
    .out_put(sticky_gate_2_out_put));  // open: propagate_reset
  sticky_gate sticky_gate_3 (
    .clock(buffer_4_out), .reset(or_1_out), .enable(and_4_out), .data(register_2_q),
    .out_put(sticky_gate_3_out_put));  // open: propagate_reset
  extra_sticky_gate extra_sticky_gate_2 (
    .clock(buffer_4_out), .reset(or_1_out), .enable(and_5_out), .data(register_2_q),
    .out_put(extra_sticky_gate_2_out_put));  // open: propagate_reset
  extra_sticky_gate extra_sticky_gate_3 (
    .clock(buffer_4_out), .reset(or_1_out), .enable(and_6_out), .data(register_1_q),
    .out_put(extra_sticky_gate_3_out_put));  // open: propagate_reset
  extra_sticky_gate extra_sticky_gate_4 (
    .clock(buffer_4_out), .reset(or_1_out), .enable(and_7_out), .data(register_2_q),
    .out_put(extra_sticky_gate_4_out_put));  // open: propagate_reset
  assign out_6 = sticky_gate_1_out_put | extra_sticky_gate_4_out_put | extra_sticky_gate_3_out_put | sticky_gate_2_out_put;  // OR_Gate or_2, 32 bits wide
  assign out_7 = extra_sticky_gate_1_out_put | extra_sticky_gate_2_out_put | sticky_gate_3_out_put;  // OR_Gate or_3, 32 bits wide

  // Notes on the sheet:
  //   Control
  //   Data
  //   Addr
  //   Data
  //   Addr
endmodule

module falling_edge_PE (
  input  in_1,
  input  in_2,
  input  in_3,
  output out_4,
  output out_5,
  output out_6
);

  wire d_ff_1_q, xor_1_out;

  D_Flip_Flop #(.trigger("falling")) d_ff_1 (
    .D(in_1), .clk(xor_1_out), .Q(d_ff_1_q), .reset(in_3));  // open: Qn, preset
  xor xor_1 (xor_1_out, in_2, d_ff_1_q);
  or or_1 (out_6, in_1, d_ff_1_q);

  assign out_4 = in_3;
  assign out_5 = in_2;
endmodule

module falling_edge_double_PE (
  input  in_1,
  input  in_2,
  input  in_3,
  output out_4,
  output out_5,
  output out_6
);

  wire d_ff_1_q, d_ff_2_q, xor_1_out;

  D_Flip_Flop #(.trigger("falling")) d_ff_1 (
    .D(in_1), .clk(xor_1_out), .Q(d_ff_1_q), .reset(in_3));  // open: Qn, preset
  xor xor_1 (xor_1_out, in_2, d_ff_1_q);
  D_Flip_Flop d_ff_2 (.D(d_ff_1_q), .clk(in_2), .Q(d_ff_2_q), .reset(in_3));  // open: Qn, preset
  or or_1 (out_6, in_1, d_ff_2_q, d_ff_1_q);

  assign out_4 = in_3;
  assign out_5 = in_2;
endmodule

module fun_silly (
  input  in_1,
  input  [15:0] in_2,
  input  [6:0] in_3,
  input  in_4,
  input  in_5,
  output [31:0] out_6,
  output [31:0] out_7,
  output [31:0] out_8,
  output [31:0] out_9,
  output [31:0] out_10,
  output [31:0] out_11,
  output [31:0] out_12,
  output [31:0] out_13,
  output [31:0] out_14,
  output [31:0] out_15,
  output [31:0] out_16,
  output [31:0] out_17,
  output [31:0] out_18,
  output [31:0] out_19,
  output [31:0] out_20,
  output [31:0] out_21,
  output [31:0] out_22,
  output [31:0] out_23,
  output [31:0] out_24,
  output [31:0] out_25,
  output [31:0] out_26,
  output [31:0] out_27,
  output [31:0] out_28,
  output [31:0] out_29,
  output [31:0] out_30,
  output [31:0] out_31,
  output [31:0] out_32,
  output [31:0] out_33,
  output [31:0] out_34,
  output [31:0] out_35,
  output [31:0] out_36,
  output [31:0] out_37,
  output [31:0] out_38,
  output [31:0] out_39,
  output [31:0] out_40,
  output [31:0] out_41,
  output [31:0] out_42,
  output [31:0] out_43,
  output [31:0] out_44,
  output [31:0] out_45,
  output [31:0] out_46,
  output [31:0] out_47,
  output [31:0] out_48,
  output [31:0] out_49,
  output [31:0] out_50,
  output [31:0] out_51,
  output [31:0] out_52,
  output [31:0] out_53,
  output [31:0] out_54,
  output [31:0] out_55,
  output [31:0] out_56,
  output [31:0] out_57,
  output [31:0] out_58,
  output [31:0] out_59,
  output [31:0] out_60,
  output [31:0] out_61,
  output [31:0] out_62,
  output [31:0] out_63,
  output [31:0] out_64,
  output [31:0] out_65,
  output [31:0] out_66,
  output [31:0] out_67,
  output [31:0] out_68,
  output [31:0] out_69
);

  wire buffer_1_out, buffer_2_out, buffer_3_out, buffer_4_out, buffer_5_out, buffer_6_out, buffer_7_out,
       buffer_8_out, buffer_9_out, buffer_10_out, buffer_11_out, buffer_12_out, buffer_13_out, buffer_14_out,
       buffer_15_out, buffer_16_out, buffer_17_out, buffer_18_out, buffer_19_out, buffer_20_out,
       buffer_21_out, buffer_22_out, buffer_23_out, buffer_24_out, buffer_25_out, buffer_26_out,
       buffer_27_out, buffer_28_out, buffer_29_out, buffer_30_out, buffer_31_out, buffer_32_out,
       buffer_33_out, buffer_34_out, buffer_35_out, buffer_36_out, buffer_37_out, buffer_38_out,
       buffer_39_out, sixt_bit_eq_cmp_1_out_3, sixt_bit_eq_cmp_2_out_3, sixt_bit_eq_cmp_3_out_3,
       sixt_bit_eq_cmp_4_out_3, sixt_bit_eq_cmp_5_out_3, sixt_bit_eq_cmp_6_out_3, sixt_bit_eq_cmp_7_out_3,
       sixt_bit_eq_cmp_8_out_3, sixt_bit_eq_cmp_9_out_3, sixt_bit_eq_cmp_10_out_3, sixt_bit_eq_cmp_11_out_3,
       sixt_bit_eq_cmp_12_out_3, sixt_bit_eq_cmp_13_out_3, sixt_bit_eq_cmp_14_out_3,
       sixt_bit_eq_cmp_15_out_3, sixt_bit_eq_cmp_16_out_3, sixt_bit_eq_cmp_17_out_3,
       sixt_bit_eq_cmp_18_out_3, sixt_bit_eq_cmp_19_out_3, sixt_bit_eq_cmp_20_out_3,
       sixt_bit_eq_cmp_21_out_3, sixt_bit_eq_cmp_22_out_3, sixt_bit_eq_cmp_23_out_3,
       sixt_bit_eq_cmp_24_out_3, sixt_bit_eq_cmp_25_out_3, sixt_bit_eq_cmp_26_out_3,
       sixt_bit_eq_cmp_27_out_3, sixt_bit_eq_cmp_28_out_3, sixt_bit_eq_cmp_29_out_3,
       sixt_bit_eq_cmp_30_out_3, sixt_bit_eq_cmp_31_out_3, sixt_bit_eq_cmp_32_out_3,
       sixt_bit_eq_cmp_33_out_3, sixt_bit_eq_cmp_34_out_3, sixt_bit_eq_cmp_35_out_3,
       sixt_bit_eq_cmp_36_out_3, sixt_bit_eq_cmp_37_out_3, sixt_bit_eq_cmp_38_out_3,
       sixt_bit_eq_cmp_39_out_3, sixt_bit_eq_cmp_40_out_3, sixt_bit_eq_cmp_41_out_3,
       sixt_bit_eq_cmp_42_out_3, sixt_bit_eq_cmp_43_out_3, sixt_bit_eq_cmp_44_out_3,
       sixt_bit_eq_cmp_45_out_3, sixt_bit_eq_cmp_46_out_3, sixt_bit_eq_cmp_47_out_3,
       sixt_bit_eq_cmp_48_out_3, sixt_bit_eq_cmp_49_out_3, sixt_bit_eq_cmp_50_out_3,
       sixt_bit_eq_cmp_51_out_3, sixt_bit_eq_cmp_52_out_3, sixt_bit_eq_cmp_53_out_3,
       sixt_bit_eq_cmp_54_out_3, sixt_bit_eq_cmp_55_out_3, sixt_bit_eq_cmp_56_out_3,
       sixt_bit_eq_cmp_57_out_3, sixt_bit_eq_cmp_58_out_3, sixt_bit_eq_cmp_59_out_3,
       sixt_bit_eq_cmp_60_out_3, sixt_bit_eq_cmp_61_out_3, sixt_bit_eq_cmp_62_out_3,
       sixt_bit_eq_cmp_63_out_3, sixt_bit_eq_cmp_64_out_3, sixt_bit_eq_cmp_65_out_3,
       sixt_bit_eq_cmp_66_out_3, sixt_bit_eq_cmp_67_out_3, sixt_bit_eq_cmp_68_out_3,
       sixt_bit_eq_cmp_69_out_3, sixt_bit_eq_cmp_70_out_3, sixt_bit_eq_cmp_71_out_3,
       sixt_bit_eq_cmp_72_out_3, sixt_bit_eq_cmp_73_out_3, sixt_bit_eq_cmp_74_out_3,
       sixt_bit_eq_cmp_75_out_3, sixt_bit_eq_cmp_76_out_3, sixt_bit_eq_cmp_77_out_3,
       sixt_bit_eq_cmp_78_out_3, sixt_bit_eq_cmp_79_out_3, sixt_bit_eq_cmp_80_out_3,
       sixt_bit_eq_cmp_81_out_3, sixt_bit_eq_cmp_82_out_3, sixt_bit_eq_cmp_83_out_3,
       sixt_bit_eq_cmp_84_out_3, sixt_bit_eq_cmp_85_out_3, sixt_bit_eq_cmp_86_out_3,
       sixt_bit_eq_cmp_87_out_3, sixt_bit_eq_cmp_88_out_3, sixt_bit_eq_cmp_89_out_3,
       sixt_bit_eq_cmp_90_out_3, sixt_bit_eq_cmp_91_out_3, sixt_bit_eq_cmp_92_out_3,
       sixt_bit_eq_cmp_93_out_3, sixt_bit_eq_cmp_94_out_3, sixt_bit_eq_cmp_95_out_3,
       sixt_bit_eq_cmp_96_out_3, sixt_bit_eq_cmp_97_out_3, sixt_bit_eq_cmp_98_out_3,
       sixt_bit_eq_cmp_99_out_3, sixt_bit_eq_cmp_100_out_3, sixt_bit_eq_cmp_101_out_3,
       sixt_bit_eq_cmp_102_out_3, sixt_bit_eq_cmp_103_out_3, sixt_bit_eq_cmp_104_out_3,
       sixt_bit_eq_cmp_105_out_3, sixt_bit_eq_cmp_106_out_3, sixt_bit_eq_cmp_107_out_3,
       sixt_bit_eq_cmp_108_out_3, sixt_bit_eq_cmp_109_out_3, sixt_bit_eq_cmp_110_out_3,
       sixt_bit_eq_cmp_111_out_3, sixt_bit_eq_cmp_112_out_3, sixt_bit_eq_cmp_113_out_3,
       sixt_bit_eq_cmp_114_out_3, sixt_bit_eq_cmp_115_out_3, sixt_bit_eq_cmp_116_out_3,
       sixt_bit_eq_cmp_117_out_3, sixt_bit_eq_cmp_118_out_3, sixt_bit_eq_cmp_119_out_3,
       sixt_bit_eq_cmp_120_out_3, sixt_bit_eq_cmp_121_out_3, sixt_bit_eq_cmp_122_out_3,
       sixt_bit_eq_cmp_123_out_3, sixt_bit_eq_cmp_124_out_3, sixt_bit_eq_cmp_125_out_3,
       sixt_bit_eq_cmp_126_out_3, sixt_bit_eq_cmp_127_out_3, sixt_bit_eq_cmp_128_out_3;
  wire [15:0] sixt_bit_incrementer_1_out_2, sixt_bit_incrementer_2_out_2, sixt_bit_incrementer_3_out_2,
       sixt_bit_incrementer_4_out_2, sixt_bit_incrementer_5_out_2, sixt_bit_incrementer_6_out_2,
       sixt_bit_incrementer_7_out_2, sixt_bit_incrementer_8_out_2, sixt_bit_incrementer_9_out_2,
       sixt_bit_incrementer_10_out_2, sixt_bit_incrementer_11_out_2, sixt_bit_incrementer_12_out_2,
       sixt_bit_incrementer_13_out_2, sixt_bit_incrementer_14_out_2, sixt_bit_incrementer_15_out_2,
       sixt_bit_incrementer_16_out_2, sixt_bit_incrementer_17_out_2, sixt_bit_incrementer_18_out_2,
       sixt_bit_incrementer_19_out_2, sixt_bit_incrementer_20_out_2, sixt_bit_incrementer_21_out_2,
       sixt_bit_incrementer_22_out_2, sixt_bit_incrementer_23_out_2, sixt_bit_incrementer_24_out_2,
       sixt_bit_incrementer_25_out_2, sixt_bit_incrementer_26_out_2, sixt_bit_incrementer_27_out_2,
       sixt_bit_incrementer_28_out_2, sixt_bit_incrementer_29_out_2, sixt_bit_incrementer_30_out_2,
       sixt_bit_incrementer_31_out_2, sixt_bit_incrementer_32_out_2, sixt_bit_incrementer_33_out_2,
       sixt_bit_incrementer_34_out_2, sixt_bit_incrementer_35_out_2, sixt_bit_incrementer_36_out_2,
       sixt_bit_incrementer_37_out_2, sixt_bit_incrementer_38_out_2, sixt_bit_incrementer_39_out_2,
       sixt_bit_incrementer_40_out_2, sixt_bit_incrementer_41_out_2, sixt_bit_incrementer_42_out_2,
       sixt_bit_incrementer_43_out_2, sixt_bit_incrementer_44_out_2, sixt_bit_incrementer_45_out_2,
       sixt_bit_incrementer_46_out_2, sixt_bit_incrementer_47_out_2, sixt_bit_incrementer_48_out_2,
       sixt_bit_incrementer_49_out_2, sixt_bit_incrementer_50_out_2, sixt_bit_incrementer_51_out_2,
       sixt_bit_incrementer_52_out_2, sixt_bit_incrementer_53_out_2, sixt_bit_incrementer_54_out_2,
       sixt_bit_incrementer_55_out_2, sixt_bit_incrementer_56_out_2, sixt_bit_incrementer_57_out_2,
       sixt_bit_incrementer_58_out_2, sixt_bit_incrementer_59_out_2, sixt_bit_incrementer_60_out_2,
       sixt_bit_incrementer_61_out_2, sixt_bit_incrementer_62_out_2, sixt_bit_incrementer_63_out_2,
       sixt_bit_incrementer_64_out_2, sixt_bit_incrementer_65_out_2, sixt_bit_incrementer_66_out_2,
       sixt_bit_incrementer_67_out_2, sixt_bit_incrementer_68_out_2, sixt_bit_incrementer_69_out_2,
       sixt_bit_incrementer_70_out_2, sixt_bit_incrementer_71_out_2, sixt_bit_incrementer_72_out_2,
       sixt_bit_incrementer_73_out_2, sixt_bit_incrementer_74_out_2, sixt_bit_incrementer_75_out_2,
       sixt_bit_incrementer_76_out_2, sixt_bit_incrementer_77_out_2, sixt_bit_incrementer_78_out_2,
       sixt_bit_incrementer_79_out_2, sixt_bit_incrementer_80_out_2, sixt_bit_incrementer_81_out_2,
       sixt_bit_incrementer_82_out_2, sixt_bit_incrementer_83_out_2, sixt_bit_incrementer_84_out_2,
       sixt_bit_incrementer_85_out_2, sixt_bit_incrementer_86_out_2, sixt_bit_incrementer_87_out_2,
       sixt_bit_incrementer_88_out_2, sixt_bit_incrementer_89_out_2, sixt_bit_incrementer_90_out_2,
       sixt_bit_incrementer_91_out_2, sixt_bit_incrementer_92_out_2, sixt_bit_incrementer_93_out_2,
       sixt_bit_incrementer_94_out_2, sixt_bit_incrementer_95_out_2, sixt_bit_incrementer_96_out_2,
       sixt_bit_incrementer_97_out_2, sixt_bit_incrementer_98_out_2, sixt_bit_incrementer_99_out_2,
       sixt_bit_incrementer_100_out_2, sixt_bit_incrementer_101_out_2, sixt_bit_incrementer_102_out_2,
       sixt_bit_incrementer_103_out_2, sixt_bit_incrementer_104_out_2, sixt_bit_incrementer_105_out_2,
       sixt_bit_incrementer_106_out_2, sixt_bit_incrementer_107_out_2, sixt_bit_incrementer_108_out_2,
       sixt_bit_incrementer_109_out_2, sixt_bit_incrementer_110_out_2, sixt_bit_incrementer_111_out_2,
       sixt_bit_incrementer_112_out_2, sixt_bit_incrementer_113_out_2, sixt_bit_incrementer_114_out_2,
       sixt_bit_incrementer_115_out_2, sixt_bit_incrementer_116_out_2, sixt_bit_incrementer_117_out_2,
       sixt_bit_incrementer_118_out_2, sixt_bit_incrementer_119_out_2, sixt_bit_incrementer_120_out_2,
       sixt_bit_incrementer_121_out_2, sixt_bit_incrementer_122_out_2, sixt_bit_incrementer_123_out_2,
       sixt_bit_incrementer_124_out_2, sixt_bit_incrementer_125_out_2, sixt_bit_incrementer_126_out_2,
       sixt_bit_incrementer_127_out_2, sixt_bit_incrementer_128_out_2, undriven;

  buf buffer_1 (buffer_1_out, buffer_2_out);
  buf buffer_2 (buffer_2_out, buffer_3_out);
  buf buffer_3 (buffer_3_out, buffer_22_out);
  buf buffer_4 (buffer_4_out, buffer_5_out);
  buf buffer_5 (buffer_5_out, buffer_6_out);
  buf buffer_6 (buffer_6_out, buffer_25_out);
  buf buffer_7 (buffer_7_out, buffer_8_out);
  buf buffer_8 (buffer_8_out, buffer_9_out);
  buf buffer_9 (buffer_9_out, buffer_28_out);
  buf buffer_10 (buffer_10_out, buffer_11_out);
  buf buffer_11 (buffer_11_out, buffer_12_out);
  buf buffer_12 (buffer_12_out, buffer_31_out);
  buf buffer_13 (buffer_13_out, buffer_14_out);
  buf buffer_14 (buffer_14_out, buffer_15_out);
  buf buffer_15 (buffer_15_out, buffer_34_out);
  buf buffer_16 (buffer_16_out, buffer_17_out);
  buf buffer_17 (buffer_17_out, buffer_18_out);
  buf buffer_18 (buffer_18_out, buffer_37_out);
  buf buffer_19 (buffer_19_out, in_5);
  buf buffer_20 (buffer_20_out, buffer_21_out);
  buf buffer_21 (buffer_21_out, buffer_1_out);
  buf buffer_22 (buffer_22_out, buffer_23_out);
  buf buffer_23 (buffer_23_out, buffer_24_out);
  buf buffer_24 (buffer_24_out, buffer_4_out);
  buf buffer_25 (buffer_25_out, buffer_26_out);
  buf buffer_26 (buffer_26_out, buffer_27_out);
  buf buffer_27 (buffer_27_out, buffer_7_out);
  buf buffer_28 (buffer_28_out, buffer_29_out);
  buf buffer_29 (buffer_29_out, buffer_30_out);
  buf buffer_30 (buffer_30_out, buffer_10_out);
  buf buffer_31 (buffer_31_out, buffer_32_out);
  buf buffer_32 (buffer_32_out, buffer_33_out);
  buf buffer_33 (buffer_33_out, buffer_13_out);
  buf buffer_34 (buffer_34_out, buffer_35_out);
  buf buffer_35 (buffer_35_out, buffer_36_out);
  buf buffer_36 (buffer_36_out, buffer_16_out);
  buf buffer_37 (buffer_37_out, buffer_38_out);
  buf buffer_38 (buffer_38_out, buffer_39_out);
  buf buffer_39 (buffer_39_out, buffer_19_out);
  // sixt_bit_selector sixt_bit_selector_1: pin names not known; wires that end beside it: in_1, 16'h80, {{9{1'b0}}, in_3}
  sixt_bit_eq_cmp sixt_bit_eq_cmp_1 (.in_1({16{1'b0}}), .in_2(undriven), .out_3(sixt_bit_eq_cmp_1_out_3));
  sixt_bit_incrementer sixt_bit_incrementer_1 (.in_1({16{1'b0}}), .out_2(sixt_bit_incrementer_1_out_2));
  sixt_bit_eq_cmp sixt_bit_eq_cmp_2 (
    .in_1(sixt_bit_incrementer_1_out_2), .in_2(undriven), .out_3(sixt_bit_eq_cmp_2_out_3));
  sixt_bit_incrementer sixt_bit_incrementer_2 (
    .in_1(sixt_bit_incrementer_1_out_2), .out_2(sixt_bit_incrementer_2_out_2));
  Register #(.width(16)) register_1 (
    .D(in_2), .en(sixt_bit_eq_cmp_1_out_3), .Q(out_6[31:16]), .clk(buffer_20_out), .clr(in_4));
  Register #(.width(16)) register_2 (
    .D(in_2), .en(sixt_bit_eq_cmp_2_out_3), .Q(out_6[15:0]), .clk(buffer_20_out), .clr(in_4));
  sixt_bit_eq_cmp sixt_bit_eq_cmp_3 (
    .in_1(sixt_bit_incrementer_2_out_2), .in_2(undriven), .out_3(sixt_bit_eq_cmp_3_out_3));
  sixt_bit_incrementer sixt_bit_incrementer_3 (
    .in_1(sixt_bit_incrementer_2_out_2), .out_2(sixt_bit_incrementer_3_out_2));
  sixt_bit_eq_cmp sixt_bit_eq_cmp_4 (
    .in_1(sixt_bit_incrementer_3_out_2), .in_2(undriven), .out_3(sixt_bit_eq_cmp_4_out_3));
  sixt_bit_incrementer sixt_bit_incrementer_4 (
    .in_1(sixt_bit_incrementer_3_out_2), .out_2(sixt_bit_incrementer_4_out_2));
  Register #(.width(16)) register_3 (
    .D(in_2), .en(sixt_bit_eq_cmp_3_out_3), .Q(out_7[31:16]), .clk(buffer_20_out), .clr(in_4));
  Register #(.width(16)) register_4 (
    .D(in_2), .en(sixt_bit_eq_cmp_4_out_3), .Q(out_7[15:0]), .clk(buffer_20_out), .clr(in_4));
  sixt_bit_incrementer sixt_bit_incrementer_5 (
    .in_1(sixt_bit_incrementer_4_out_2), .out_2(sixt_bit_incrementer_5_out_2));
  sixt_bit_incrementer sixt_bit_incrementer_6 (
    .in_1(sixt_bit_incrementer_5_out_2), .out_2(sixt_bit_incrementer_6_out_2));
  Register #(.width(16)) register_5 (
    .D(in_2), .en(sixt_bit_eq_cmp_5_out_3), .Q(out_8[31:16]), .clk(buffer_20_out), .clr(in_4));
  sixt_bit_eq_cmp sixt_bit_eq_cmp_5 (
    .in_1(sixt_bit_incrementer_4_out_2), .in_2(undriven), .out_3(sixt_bit_eq_cmp_5_out_3));
  Register #(.width(16)) register_6 (
    .D(in_2), .en(sixt_bit_eq_cmp_6_out_3), .Q(out_8[15:0]), .clk(buffer_20_out), .clr(in_4));
  sixt_bit_eq_cmp sixt_bit_eq_cmp_6 (
    .in_1(sixt_bit_incrementer_5_out_2), .in_2(undriven), .out_3(sixt_bit_eq_cmp_6_out_3));
  sixt_bit_incrementer sixt_bit_incrementer_7 (
    .in_1(sixt_bit_incrementer_6_out_2), .out_2(sixt_bit_incrementer_7_out_2));
  sixt_bit_incrementer sixt_bit_incrementer_8 (
    .in_1(sixt_bit_incrementer_7_out_2), .out_2(sixt_bit_incrementer_8_out_2));
  sixt_bit_eq_cmp sixt_bit_eq_cmp_7 (
    .in_1(sixt_bit_incrementer_6_out_2), .in_2(undriven), .out_3(sixt_bit_eq_cmp_7_out_3));
  sixt_bit_eq_cmp sixt_bit_eq_cmp_8 (
    .in_1(sixt_bit_incrementer_7_out_2), .in_2(undriven), .out_3(sixt_bit_eq_cmp_8_out_3));
  Register #(.width(16)) register_7 (
    .D(in_2), .en(sixt_bit_eq_cmp_7_out_3), .Q(out_9[31:16]), .clk(buffer_20_out), .clr(in_4));
  Register #(.width(16)) register_8 (
    .D(in_2), .en(sixt_bit_eq_cmp_8_out_3), .Q(out_9[15:0]), .clk(buffer_20_out), .clr(in_4));
  sixt_bit_eq_cmp sixt_bit_eq_cmp_9 (
    .in_1(sixt_bit_incrementer_8_out_2), .in_2(undriven), .out_3(sixt_bit_eq_cmp_9_out_3));
  sixt_bit_incrementer sixt_bit_incrementer_9 (
    .in_1(sixt_bit_incrementer_8_out_2), .out_2(sixt_bit_incrementer_9_out_2));
  sixt_bit_eq_cmp sixt_bit_eq_cmp_10 (
    .in_1(sixt_bit_incrementer_9_out_2), .in_2(undriven), .out_3(sixt_bit_eq_cmp_10_out_3));
  sixt_bit_incrementer sixt_bit_incrementer_10 (
    .in_1(sixt_bit_incrementer_9_out_2), .out_2(sixt_bit_incrementer_10_out_2));
  Register #(.width(16)) register_9 (
    .D(in_2), .en(sixt_bit_eq_cmp_9_out_3), .Q(out_10[31:16]), .clk(buffer_20_out), .clr(in_4));
  Register #(.width(16)) register_10 (
    .D(in_2), .en(sixt_bit_eq_cmp_10_out_3), .Q(out_10[15:0]), .clk(buffer_20_out), .clr(in_4));
  sixt_bit_eq_cmp sixt_bit_eq_cmp_11 (
    .in_1(sixt_bit_incrementer_10_out_2), .in_2(undriven), .out_3(sixt_bit_eq_cmp_11_out_3));
  sixt_bit_incrementer sixt_bit_incrementer_11 (
    .in_1(sixt_bit_incrementer_10_out_2), .out_2(sixt_bit_incrementer_11_out_2));
  sixt_bit_eq_cmp sixt_bit_eq_cmp_12 (
    .in_1(sixt_bit_incrementer_11_out_2), .in_2(undriven), .out_3(sixt_bit_eq_cmp_12_out_3));
  sixt_bit_incrementer sixt_bit_incrementer_12 (
    .in_1(sixt_bit_incrementer_11_out_2), .out_2(sixt_bit_incrementer_12_out_2));
  Register #(.width(16)) register_11 (
    .D(in_2), .en(sixt_bit_eq_cmp_11_out_3), .Q(out_11[31:16]), .clk(buffer_20_out), .clr(in_4));
  Register #(.width(16)) register_12 (
    .D(in_2), .en(sixt_bit_eq_cmp_12_out_3), .Q(out_11[15:0]), .clk(buffer_20_out), .clr(in_4));
  sixt_bit_incrementer sixt_bit_incrementer_13 (
    .in_1(sixt_bit_incrementer_12_out_2), .out_2(sixt_bit_incrementer_13_out_2));
  sixt_bit_incrementer sixt_bit_incrementer_14 (
    .in_1(sixt_bit_incrementer_13_out_2), .out_2(sixt_bit_incrementer_14_out_2));
  Register #(.width(16)) register_13 (
    .D(in_2), .en(sixt_bit_eq_cmp_13_out_3), .Q(out_12[31:16]), .clk(buffer_20_out), .clr(in_4));
  sixt_bit_eq_cmp sixt_bit_eq_cmp_13 (
    .in_1(sixt_bit_incrementer_12_out_2), .in_2(undriven), .out_3(sixt_bit_eq_cmp_13_out_3));
  Register #(.width(16)) register_14 (
    .D(in_2), .en(sixt_bit_eq_cmp_14_out_3), .Q(out_12[15:0]), .clk(buffer_20_out), .clr(in_4));
  sixt_bit_eq_cmp sixt_bit_eq_cmp_14 (
    .in_1(sixt_bit_incrementer_13_out_2), .in_2(undriven), .out_3(sixt_bit_eq_cmp_14_out_3));
  sixt_bit_incrementer sixt_bit_incrementer_15 (
    .in_1(sixt_bit_incrementer_14_out_2), .out_2(sixt_bit_incrementer_15_out_2));
  sixt_bit_incrementer sixt_bit_incrementer_16 (
    .in_1(sixt_bit_incrementer_15_out_2), .out_2(sixt_bit_incrementer_16_out_2));
  sixt_bit_eq_cmp sixt_bit_eq_cmp_15 (
    .in_1(sixt_bit_incrementer_14_out_2), .in_2(undriven), .out_3(sixt_bit_eq_cmp_15_out_3));
  sixt_bit_eq_cmp sixt_bit_eq_cmp_16 (
    .in_1(sixt_bit_incrementer_15_out_2), .in_2(undriven), .out_3(sixt_bit_eq_cmp_16_out_3));
  Register #(.width(16)) register_15 (
    .D(in_2), .en(sixt_bit_eq_cmp_15_out_3), .Q(out_13[31:16]), .clk(buffer_20_out), .clr(in_4));
  Register #(.width(16)) register_16 (
    .D(in_2), .en(sixt_bit_eq_cmp_16_out_3), .Q(out_13[15:0]), .clk(buffer_20_out), .clr(in_4));
  sixt_bit_eq_cmp sixt_bit_eq_cmp_17 (
    .in_1(sixt_bit_incrementer_16_out_2), .in_2(undriven), .out_3(sixt_bit_eq_cmp_17_out_3));
  sixt_bit_incrementer sixt_bit_incrementer_17 (
    .in_1(sixt_bit_incrementer_16_out_2), .out_2(sixt_bit_incrementer_17_out_2));
  sixt_bit_eq_cmp sixt_bit_eq_cmp_18 (
    .in_1(sixt_bit_incrementer_17_out_2), .in_2(undriven), .out_3(sixt_bit_eq_cmp_18_out_3));
  sixt_bit_incrementer sixt_bit_incrementer_18 (
    .in_1(sixt_bit_incrementer_17_out_2), .out_2(sixt_bit_incrementer_18_out_2));
  Register #(.width(16)) register_17 (
    .D(in_2), .en(sixt_bit_eq_cmp_17_out_3), .Q(out_14[31:16]), .clk(buffer_20_out), .clr(in_4));
  Register #(.width(16)) register_18 (
    .D(in_2), .en(sixt_bit_eq_cmp_18_out_3), .Q(out_14[15:0]), .clk(buffer_20_out), .clr(in_4));
  sixt_bit_eq_cmp sixt_bit_eq_cmp_19 (
    .in_1(sixt_bit_incrementer_18_out_2), .in_2(undriven), .out_3(sixt_bit_eq_cmp_19_out_3));
  sixt_bit_incrementer sixt_bit_incrementer_19 (
    .in_1(sixt_bit_incrementer_18_out_2), .out_2(sixt_bit_incrementer_19_out_2));
  sixt_bit_eq_cmp sixt_bit_eq_cmp_20 (
    .in_1(sixt_bit_incrementer_19_out_2), .in_2(undriven), .out_3(sixt_bit_eq_cmp_20_out_3));
  sixt_bit_incrementer sixt_bit_incrementer_20 (
    .in_1(sixt_bit_incrementer_19_out_2), .out_2(sixt_bit_incrementer_20_out_2));
  Register #(.width(16)) register_19 (
    .D(in_2), .en(sixt_bit_eq_cmp_19_out_3), .Q(out_15[31:16]), .clk(buffer_20_out), .clr(in_4));
  Register #(.width(16)) register_20 (
    .D(in_2), .en(sixt_bit_eq_cmp_20_out_3), .Q(out_15[15:0]), .clk(buffer_20_out), .clr(in_4));
  sixt_bit_incrementer sixt_bit_incrementer_21 (
    .in_1(sixt_bit_incrementer_20_out_2), .out_2(sixt_bit_incrementer_21_out_2));
  sixt_bit_incrementer sixt_bit_incrementer_22 (
    .in_1(sixt_bit_incrementer_21_out_2), .out_2(sixt_bit_incrementer_22_out_2));
  Register #(.width(16)) register_21 (
    .D(in_2), .en(sixt_bit_eq_cmp_21_out_3), .Q(out_16[31:16]), .clk(buffer_20_out), .clr(in_4));
  sixt_bit_eq_cmp sixt_bit_eq_cmp_21 (
    .in_1(sixt_bit_incrementer_20_out_2), .in_2(undriven), .out_3(sixt_bit_eq_cmp_21_out_3));
  Register #(.width(16)) register_22 (
    .D(in_2), .en(sixt_bit_eq_cmp_22_out_3), .Q(out_16[15:0]), .clk(buffer_20_out), .clr(in_4));
  sixt_bit_eq_cmp sixt_bit_eq_cmp_22 (
    .in_1(sixt_bit_incrementer_21_out_2), .in_2(undriven), .out_3(sixt_bit_eq_cmp_22_out_3));
  sixt_bit_incrementer sixt_bit_incrementer_23 (
    .in_1(sixt_bit_incrementer_22_out_2), .out_2(sixt_bit_incrementer_23_out_2));
  sixt_bit_incrementer sixt_bit_incrementer_24 (
    .in_1(sixt_bit_incrementer_23_out_2), .out_2(sixt_bit_incrementer_24_out_2));
  sixt_bit_eq_cmp sixt_bit_eq_cmp_23 (
    .in_1(sixt_bit_incrementer_22_out_2), .in_2(undriven), .out_3(sixt_bit_eq_cmp_23_out_3));
  sixt_bit_eq_cmp sixt_bit_eq_cmp_24 (
    .in_1(sixt_bit_incrementer_23_out_2), .in_2(undriven), .out_3(sixt_bit_eq_cmp_24_out_3));
  Register #(.width(16)) register_23 (
    .D(in_2), .en(sixt_bit_eq_cmp_23_out_3), .Q(out_17[31:16]), .clk(buffer_20_out), .clr(in_4));
  Register #(.width(16)) register_24 (
    .D(in_2), .en(sixt_bit_eq_cmp_24_out_3), .Q(out_17[15:0]), .clk(buffer_20_out), .clr(in_4));
  sixt_bit_eq_cmp sixt_bit_eq_cmp_25 (
    .in_1(sixt_bit_incrementer_24_out_2), .in_2(undriven), .out_3(sixt_bit_eq_cmp_25_out_3));
  sixt_bit_incrementer sixt_bit_incrementer_25 (
    .in_1(sixt_bit_incrementer_24_out_2), .out_2(sixt_bit_incrementer_25_out_2));
  sixt_bit_eq_cmp sixt_bit_eq_cmp_26 (
    .in_1(sixt_bit_incrementer_25_out_2), .in_2(undriven), .out_3(sixt_bit_eq_cmp_26_out_3));
  sixt_bit_incrementer sixt_bit_incrementer_26 (
    .in_1(sixt_bit_incrementer_25_out_2), .out_2(sixt_bit_incrementer_26_out_2));
  Register #(.width(16)) register_25 (
    .D(in_2), .en(sixt_bit_eq_cmp_25_out_3), .Q(out_18[31:16]), .clk(buffer_20_out), .clr(in_4));
  Register #(.width(16)) register_26 (
    .D(in_2), .en(sixt_bit_eq_cmp_26_out_3), .Q(out_18[15:0]), .clk(buffer_20_out), .clr(in_4));
  sixt_bit_eq_cmp sixt_bit_eq_cmp_27 (
    .in_1(sixt_bit_incrementer_26_out_2), .in_2(undriven), .out_3(sixt_bit_eq_cmp_27_out_3));
  sixt_bit_incrementer sixt_bit_incrementer_27 (
    .in_1(sixt_bit_incrementer_26_out_2), .out_2(sixt_bit_incrementer_27_out_2));
  sixt_bit_eq_cmp sixt_bit_eq_cmp_28 (
    .in_1(sixt_bit_incrementer_27_out_2), .in_2(undriven), .out_3(sixt_bit_eq_cmp_28_out_3));
  sixt_bit_incrementer sixt_bit_incrementer_28 (
    .in_1(sixt_bit_incrementer_27_out_2), .out_2(sixt_bit_incrementer_28_out_2));
  Register #(.width(16)) register_27 (
    .D(in_2), .en(sixt_bit_eq_cmp_27_out_3), .Q(out_19[31:16]), .clk(buffer_20_out), .clr(in_4));
  Register #(.width(16)) register_28 (
    .D(in_2), .en(sixt_bit_eq_cmp_28_out_3), .Q(out_19[15:0]), .clk(buffer_20_out), .clr(in_4));
  sixt_bit_incrementer sixt_bit_incrementer_29 (
    .in_1(sixt_bit_incrementer_28_out_2), .out_2(sixt_bit_incrementer_29_out_2));
  sixt_bit_incrementer sixt_bit_incrementer_30 (
    .in_1(sixt_bit_incrementer_29_out_2), .out_2(sixt_bit_incrementer_30_out_2));
  Register #(.width(16)) register_29 (
    .D(in_2), .en(sixt_bit_eq_cmp_29_out_3), .Q(out_20[31:16]), .clk(buffer_20_out), .clr(in_4));
  sixt_bit_eq_cmp sixt_bit_eq_cmp_29 (
    .in_1(sixt_bit_incrementer_28_out_2), .in_2(undriven), .out_3(sixt_bit_eq_cmp_29_out_3));
  Register #(.width(16)) register_30 (
    .D(in_2), .en(sixt_bit_eq_cmp_30_out_3), .Q(out_20[15:0]), .clk(buffer_20_out), .clr(in_4));
  sixt_bit_eq_cmp sixt_bit_eq_cmp_30 (
    .in_1(sixt_bit_incrementer_29_out_2), .in_2(undriven), .out_3(sixt_bit_eq_cmp_30_out_3));
  sixt_bit_incrementer sixt_bit_incrementer_31 (
    .in_1(sixt_bit_incrementer_30_out_2), .out_2(sixt_bit_incrementer_31_out_2));
  sixt_bit_incrementer sixt_bit_incrementer_32 (
    .in_1(sixt_bit_incrementer_31_out_2), .out_2(sixt_bit_incrementer_32_out_2));
  sixt_bit_eq_cmp sixt_bit_eq_cmp_31 (
    .in_1(sixt_bit_incrementer_30_out_2), .in_2(undriven), .out_3(sixt_bit_eq_cmp_31_out_3));
  sixt_bit_eq_cmp sixt_bit_eq_cmp_32 (
    .in_1(sixt_bit_incrementer_31_out_2), .in_2(undriven), .out_3(sixt_bit_eq_cmp_32_out_3));
  Register #(.width(16)) register_31 (
    .D(in_2), .en(sixt_bit_eq_cmp_31_out_3), .Q(out_21[31:16]), .clk(buffer_20_out), .clr(in_4));
  Register #(.width(16)) register_32 (
    .D(in_2), .en(sixt_bit_eq_cmp_32_out_3), .Q(out_21[15:0]), .clk(buffer_20_out), .clr(in_4));
  sixt_bit_eq_cmp sixt_bit_eq_cmp_33 (
    .in_1(sixt_bit_incrementer_32_out_2), .in_2(undriven), .out_3(sixt_bit_eq_cmp_33_out_3));
  sixt_bit_incrementer sixt_bit_incrementer_33 (
    .in_1(sixt_bit_incrementer_32_out_2), .out_2(sixt_bit_incrementer_33_out_2));
  sixt_bit_eq_cmp sixt_bit_eq_cmp_34 (
    .in_1(sixt_bit_incrementer_33_out_2), .in_2(undriven), .out_3(sixt_bit_eq_cmp_34_out_3));
  sixt_bit_incrementer sixt_bit_incrementer_34 (
    .in_1(sixt_bit_incrementer_33_out_2), .out_2(sixt_bit_incrementer_34_out_2));
  Register #(.width(16)) register_33 (
    .D(in_2), .en(sixt_bit_eq_cmp_33_out_3), .Q(out_22[31:16]), .clk(buffer_20_out), .clr(in_4));
  Register #(.width(16)) register_34 (
    .D(in_2), .en(sixt_bit_eq_cmp_34_out_3), .Q(out_22[15:0]), .clk(buffer_20_out), .clr(in_4));
  sixt_bit_eq_cmp sixt_bit_eq_cmp_35 (
    .in_1(sixt_bit_incrementer_34_out_2), .in_2(undriven), .out_3(sixt_bit_eq_cmp_35_out_3));
  sixt_bit_incrementer sixt_bit_incrementer_35 (
    .in_1(sixt_bit_incrementer_34_out_2), .out_2(sixt_bit_incrementer_35_out_2));
  sixt_bit_eq_cmp sixt_bit_eq_cmp_36 (
    .in_1(sixt_bit_incrementer_35_out_2), .in_2(undriven), .out_3(sixt_bit_eq_cmp_36_out_3));
  sixt_bit_incrementer sixt_bit_incrementer_36 (
    .in_1(sixt_bit_incrementer_35_out_2), .out_2(sixt_bit_incrementer_36_out_2));
  Register #(.width(16)) register_35 (
    .D(in_2), .en(sixt_bit_eq_cmp_35_out_3), .Q(out_23[31:16]), .clk(buffer_20_out), .clr(in_4));
  Register #(.width(16)) register_36 (
    .D(in_2), .en(sixt_bit_eq_cmp_36_out_3), .Q(out_23[15:0]), .clk(buffer_20_out), .clr(in_4));
  sixt_bit_incrementer sixt_bit_incrementer_37 (
    .in_1(sixt_bit_incrementer_36_out_2), .out_2(sixt_bit_incrementer_37_out_2));
  sixt_bit_incrementer sixt_bit_incrementer_38 (
    .in_1(sixt_bit_incrementer_37_out_2), .out_2(sixt_bit_incrementer_38_out_2));
  Register #(.width(16)) register_37 (
    .D(in_2), .en(sixt_bit_eq_cmp_37_out_3), .Q(out_24[31:16]), .clk(buffer_20_out), .clr(in_4));
  sixt_bit_eq_cmp sixt_bit_eq_cmp_37 (
    .in_1(sixt_bit_incrementer_36_out_2), .in_2(undriven), .out_3(sixt_bit_eq_cmp_37_out_3));
  Register #(.width(16)) register_38 (
    .D(in_2), .en(sixt_bit_eq_cmp_38_out_3), .Q(out_24[15:0]), .clk(buffer_20_out), .clr(in_4));
  sixt_bit_eq_cmp sixt_bit_eq_cmp_38 (
    .in_1(sixt_bit_incrementer_37_out_2), .in_2(undriven), .out_3(sixt_bit_eq_cmp_38_out_3));
  sixt_bit_incrementer sixt_bit_incrementer_39 (
    .in_1(sixt_bit_incrementer_38_out_2), .out_2(sixt_bit_incrementer_39_out_2));
  sixt_bit_incrementer sixt_bit_incrementer_40 (
    .in_1(sixt_bit_incrementer_39_out_2), .out_2(sixt_bit_incrementer_40_out_2));
  sixt_bit_eq_cmp sixt_bit_eq_cmp_39 (
    .in_1(sixt_bit_incrementer_38_out_2), .in_2(undriven), .out_3(sixt_bit_eq_cmp_39_out_3));
  sixt_bit_eq_cmp sixt_bit_eq_cmp_40 (
    .in_1(sixt_bit_incrementer_39_out_2), .in_2(undriven), .out_3(sixt_bit_eq_cmp_40_out_3));
  Register #(.width(16)) register_39 (
    .D(in_2), .en(sixt_bit_eq_cmp_39_out_3), .Q(out_25[31:16]), .clk(buffer_20_out), .clr(in_4));
  Register #(.width(16)) register_40 (
    .D(in_2), .en(sixt_bit_eq_cmp_40_out_3), .Q(out_25[15:0]), .clk(buffer_20_out), .clr(in_4));
  sixt_bit_eq_cmp sixt_bit_eq_cmp_41 (
    .in_1(sixt_bit_incrementer_40_out_2), .in_2(undriven), .out_3(sixt_bit_eq_cmp_41_out_3));
  sixt_bit_incrementer sixt_bit_incrementer_41 (
    .in_1(sixt_bit_incrementer_40_out_2), .out_2(sixt_bit_incrementer_41_out_2));
  sixt_bit_eq_cmp sixt_bit_eq_cmp_42 (
    .in_1(sixt_bit_incrementer_41_out_2), .in_2(undriven), .out_3(sixt_bit_eq_cmp_42_out_3));
  sixt_bit_incrementer sixt_bit_incrementer_42 (
    .in_1(sixt_bit_incrementer_41_out_2), .out_2(sixt_bit_incrementer_42_out_2));
  Register #(.width(16)) register_41 (
    .D(in_2), .en(sixt_bit_eq_cmp_41_out_3), .Q(out_26[31:16]), .clk(buffer_20_out), .clr(in_4));
  Register #(.width(16)) register_42 (
    .D(in_2), .en(sixt_bit_eq_cmp_42_out_3), .Q(out_26[15:0]), .clk(buffer_20_out), .clr(in_4));
  sixt_bit_eq_cmp sixt_bit_eq_cmp_43 (
    .in_1(sixt_bit_incrementer_42_out_2), .in_2(undriven), .out_3(sixt_bit_eq_cmp_43_out_3));
  sixt_bit_incrementer sixt_bit_incrementer_43 (
    .in_1(sixt_bit_incrementer_42_out_2), .out_2(sixt_bit_incrementer_43_out_2));
  sixt_bit_eq_cmp sixt_bit_eq_cmp_44 (
    .in_1(sixt_bit_incrementer_43_out_2), .in_2(undriven), .out_3(sixt_bit_eq_cmp_44_out_3));
  sixt_bit_incrementer sixt_bit_incrementer_44 (
    .in_1(sixt_bit_incrementer_43_out_2), .out_2(sixt_bit_incrementer_44_out_2));
  Register #(.width(16)) register_43 (
    .D(in_2), .en(sixt_bit_eq_cmp_43_out_3), .Q(out_27[31:16]), .clk(buffer_20_out), .clr(in_4));
  Register #(.width(16)) register_44 (
    .D(in_2), .en(sixt_bit_eq_cmp_44_out_3), .Q(out_27[15:0]), .clk(buffer_20_out), .clr(in_4));
  sixt_bit_incrementer sixt_bit_incrementer_45 (
    .in_1(sixt_bit_incrementer_44_out_2), .out_2(sixt_bit_incrementer_45_out_2));
  sixt_bit_incrementer sixt_bit_incrementer_46 (
    .in_1(sixt_bit_incrementer_45_out_2), .out_2(sixt_bit_incrementer_46_out_2));
  Register #(.width(16)) register_45 (
    .D(in_2), .en(sixt_bit_eq_cmp_45_out_3), .Q(out_28[31:16]), .clk(buffer_20_out), .clr(in_4));
  sixt_bit_eq_cmp sixt_bit_eq_cmp_45 (
    .in_1(sixt_bit_incrementer_44_out_2), .in_2(undriven), .out_3(sixt_bit_eq_cmp_45_out_3));
  Register #(.width(16)) register_46 (
    .D(in_2), .en(sixt_bit_eq_cmp_46_out_3), .Q(out_28[15:0]), .clk(buffer_20_out), .clr(in_4));
  sixt_bit_eq_cmp sixt_bit_eq_cmp_46 (
    .in_1(sixt_bit_incrementer_45_out_2), .in_2(undriven), .out_3(sixt_bit_eq_cmp_46_out_3));
  sixt_bit_incrementer sixt_bit_incrementer_47 (
    .in_1(sixt_bit_incrementer_46_out_2), .out_2(sixt_bit_incrementer_47_out_2));
  sixt_bit_incrementer sixt_bit_incrementer_48 (
    .in_1(sixt_bit_incrementer_47_out_2), .out_2(sixt_bit_incrementer_48_out_2));
  sixt_bit_eq_cmp sixt_bit_eq_cmp_47 (
    .in_1(sixt_bit_incrementer_46_out_2), .in_2(undriven), .out_3(sixt_bit_eq_cmp_47_out_3));
  sixt_bit_eq_cmp sixt_bit_eq_cmp_48 (
    .in_1(sixt_bit_incrementer_47_out_2), .in_2(undriven), .out_3(sixt_bit_eq_cmp_48_out_3));
  Register #(.width(16)) register_47 (
    .D(in_2), .en(sixt_bit_eq_cmp_47_out_3), .Q(out_29[31:16]), .clk(buffer_20_out), .clr(in_4));
  Register #(.width(16)) register_48 (
    .D(in_2), .en(sixt_bit_eq_cmp_48_out_3), .Q(out_29[15:0]), .clk(buffer_20_out), .clr(in_4));
  sixt_bit_eq_cmp sixt_bit_eq_cmp_49 (
    .in_1(sixt_bit_incrementer_48_out_2), .in_2(undriven), .out_3(sixt_bit_eq_cmp_49_out_3));
  sixt_bit_incrementer sixt_bit_incrementer_49 (
    .in_1(sixt_bit_incrementer_48_out_2), .out_2(sixt_bit_incrementer_49_out_2));
  sixt_bit_eq_cmp sixt_bit_eq_cmp_50 (
    .in_1(sixt_bit_incrementer_49_out_2), .in_2(undriven), .out_3(sixt_bit_eq_cmp_50_out_3));
  sixt_bit_incrementer sixt_bit_incrementer_50 (
    .in_1(sixt_bit_incrementer_49_out_2), .out_2(sixt_bit_incrementer_50_out_2));
  Register #(.width(16)) register_49 (
    .D(in_2), .en(sixt_bit_eq_cmp_49_out_3), .Q(out_30[31:16]), .clk(buffer_20_out), .clr(in_4));
  Register #(.width(16)) register_50 (
    .D(in_2), .en(sixt_bit_eq_cmp_50_out_3), .Q(out_30[15:0]), .clk(buffer_20_out), .clr(in_4));
  sixt_bit_eq_cmp sixt_bit_eq_cmp_51 (
    .in_1(sixt_bit_incrementer_50_out_2), .in_2(undriven), .out_3(sixt_bit_eq_cmp_51_out_3));
  sixt_bit_incrementer sixt_bit_incrementer_51 (
    .in_1(sixt_bit_incrementer_50_out_2), .out_2(sixt_bit_incrementer_51_out_2));
  sixt_bit_eq_cmp sixt_bit_eq_cmp_52 (
    .in_1(sixt_bit_incrementer_51_out_2), .in_2(undriven), .out_3(sixt_bit_eq_cmp_52_out_3));
  sixt_bit_incrementer sixt_bit_incrementer_52 (
    .in_1(sixt_bit_incrementer_51_out_2), .out_2(sixt_bit_incrementer_52_out_2));
  Register #(.width(16)) register_51 (
    .D(in_2), .en(sixt_bit_eq_cmp_51_out_3), .Q(out_31[31:16]), .clk(buffer_20_out), .clr(in_4));
  Register #(.width(16)) register_52 (
    .D(in_2), .en(sixt_bit_eq_cmp_52_out_3), .Q(out_31[15:0]), .clk(buffer_20_out), .clr(in_4));
  sixt_bit_incrementer sixt_bit_incrementer_53 (
    .in_1(sixt_bit_incrementer_52_out_2), .out_2(sixt_bit_incrementer_53_out_2));
  sixt_bit_incrementer sixt_bit_incrementer_54 (
    .in_1(sixt_bit_incrementer_53_out_2), .out_2(sixt_bit_incrementer_54_out_2));
  Register #(.width(16)) register_53 (
    .D(in_2), .en(sixt_bit_eq_cmp_53_out_3), .Q(out_32[31:16]), .clk(buffer_20_out), .clr(in_4));
  sixt_bit_eq_cmp sixt_bit_eq_cmp_53 (
    .in_1(sixt_bit_incrementer_52_out_2), .in_2(undriven), .out_3(sixt_bit_eq_cmp_53_out_3));
  Register #(.width(16)) register_54 (
    .D(in_2), .en(sixt_bit_eq_cmp_54_out_3), .Q(out_32[15:0]), .clk(buffer_20_out), .clr(in_4));
  sixt_bit_eq_cmp sixt_bit_eq_cmp_54 (
    .in_1(sixt_bit_incrementer_53_out_2), .in_2(undriven), .out_3(sixt_bit_eq_cmp_54_out_3));
  sixt_bit_incrementer sixt_bit_incrementer_55 (
    .in_1(sixt_bit_incrementer_54_out_2), .out_2(sixt_bit_incrementer_55_out_2));
  sixt_bit_incrementer sixt_bit_incrementer_56 (
    .in_1(sixt_bit_incrementer_55_out_2), .out_2(sixt_bit_incrementer_56_out_2));
  sixt_bit_eq_cmp sixt_bit_eq_cmp_55 (
    .in_1(sixt_bit_incrementer_54_out_2), .in_2(undriven), .out_3(sixt_bit_eq_cmp_55_out_3));
  sixt_bit_eq_cmp sixt_bit_eq_cmp_56 (
    .in_1(sixt_bit_incrementer_55_out_2), .in_2(undriven), .out_3(sixt_bit_eq_cmp_56_out_3));
  Register #(.width(16)) register_55 (
    .D(in_2), .en(sixt_bit_eq_cmp_55_out_3), .Q(out_33[31:16]), .clk(buffer_20_out), .clr(in_4));
  Register #(.width(16)) register_56 (
    .D(in_2), .en(sixt_bit_eq_cmp_56_out_3), .Q(out_33[15:0]), .clk(buffer_20_out), .clr(in_4));
  sixt_bit_eq_cmp sixt_bit_eq_cmp_57 (
    .in_1(sixt_bit_incrementer_56_out_2), .in_2(undriven), .out_3(sixt_bit_eq_cmp_57_out_3));
  sixt_bit_incrementer sixt_bit_incrementer_57 (
    .in_1(sixt_bit_incrementer_56_out_2), .out_2(sixt_bit_incrementer_57_out_2));
  sixt_bit_eq_cmp sixt_bit_eq_cmp_58 (
    .in_1(sixt_bit_incrementer_57_out_2), .in_2(undriven), .out_3(sixt_bit_eq_cmp_58_out_3));
  sixt_bit_incrementer sixt_bit_incrementer_58 (
    .in_1(sixt_bit_incrementer_57_out_2), .out_2(sixt_bit_incrementer_58_out_2));
  Register #(.width(16)) register_57 (
    .D(in_2), .en(sixt_bit_eq_cmp_57_out_3), .Q(out_34[31:16]), .clk(buffer_20_out), .clr(in_4));
  Register #(.width(16)) register_58 (
    .D(in_2), .en(sixt_bit_eq_cmp_58_out_3), .Q(out_34[15:0]), .clk(buffer_20_out), .clr(in_4));
  sixt_bit_eq_cmp sixt_bit_eq_cmp_59 (
    .in_1(sixt_bit_incrementer_58_out_2), .in_2(undriven), .out_3(sixt_bit_eq_cmp_59_out_3));
  sixt_bit_incrementer sixt_bit_incrementer_59 (
    .in_1(sixt_bit_incrementer_58_out_2), .out_2(sixt_bit_incrementer_59_out_2));
  sixt_bit_eq_cmp sixt_bit_eq_cmp_60 (
    .in_1(sixt_bit_incrementer_59_out_2), .in_2(undriven), .out_3(sixt_bit_eq_cmp_60_out_3));
  sixt_bit_incrementer sixt_bit_incrementer_60 (
    .in_1(sixt_bit_incrementer_59_out_2), .out_2(sixt_bit_incrementer_60_out_2));
  Register #(.width(16)) register_59 (
    .D(in_2), .en(sixt_bit_eq_cmp_59_out_3), .Q(out_35[31:16]), .clk(buffer_20_out), .clr(in_4));
  Register #(.width(16)) register_60 (
    .D(in_2), .en(sixt_bit_eq_cmp_60_out_3), .Q(out_35[15:0]), .clk(buffer_20_out), .clr(in_4));
  sixt_bit_incrementer sixt_bit_incrementer_61 (
    .in_1(sixt_bit_incrementer_60_out_2), .out_2(sixt_bit_incrementer_61_out_2));
  sixt_bit_incrementer sixt_bit_incrementer_62 (
    .in_1(sixt_bit_incrementer_61_out_2), .out_2(sixt_bit_incrementer_62_out_2));
  Register #(.width(16)) register_61 (
    .D(in_2), .en(sixt_bit_eq_cmp_61_out_3), .Q(out_36[31:16]), .clk(buffer_20_out), .clr(in_4));
  sixt_bit_eq_cmp sixt_bit_eq_cmp_61 (
    .in_1(sixt_bit_incrementer_60_out_2), .in_2(undriven), .out_3(sixt_bit_eq_cmp_61_out_3));
  Register #(.width(16)) register_62 (
    .D(in_2), .en(sixt_bit_eq_cmp_62_out_3), .Q(out_36[15:0]), .clk(buffer_20_out), .clr(in_4));
  sixt_bit_eq_cmp sixt_bit_eq_cmp_62 (
    .in_1(sixt_bit_incrementer_61_out_2), .in_2(undriven), .out_3(sixt_bit_eq_cmp_62_out_3));
  sixt_bit_incrementer sixt_bit_incrementer_63 (
    .in_1(sixt_bit_incrementer_62_out_2), .out_2(sixt_bit_incrementer_63_out_2));
  sixt_bit_incrementer sixt_bit_incrementer_64 (
    .in_1(sixt_bit_incrementer_63_out_2), .out_2(sixt_bit_incrementer_64_out_2));
  sixt_bit_eq_cmp sixt_bit_eq_cmp_63 (
    .in_1(sixt_bit_incrementer_62_out_2), .in_2(undriven), .out_3(sixt_bit_eq_cmp_63_out_3));
  sixt_bit_eq_cmp sixt_bit_eq_cmp_64 (
    .in_1(sixt_bit_incrementer_63_out_2), .in_2(undriven), .out_3(sixt_bit_eq_cmp_64_out_3));
  Register #(.width(16)) register_63 (
    .D(in_2), .en(sixt_bit_eq_cmp_63_out_3), .Q(out_37[31:16]), .clk(buffer_20_out), .clr(in_4));
  Register #(.width(16)) register_64 (
    .D(in_2), .en(sixt_bit_eq_cmp_64_out_3), .Q(out_37[15:0]), .clk(buffer_20_out), .clr(in_4));
  sixt_bit_eq_cmp sixt_bit_eq_cmp_65 (
    .in_1(sixt_bit_incrementer_64_out_2), .in_2(undriven), .out_3(sixt_bit_eq_cmp_65_out_3));
  sixt_bit_incrementer sixt_bit_incrementer_65 (
    .in_1(sixt_bit_incrementer_64_out_2), .out_2(sixt_bit_incrementer_65_out_2));
  sixt_bit_eq_cmp sixt_bit_eq_cmp_66 (
    .in_1(sixt_bit_incrementer_65_out_2), .in_2(undriven), .out_3(sixt_bit_eq_cmp_66_out_3));
  sixt_bit_incrementer sixt_bit_incrementer_66 (
    .in_1(sixt_bit_incrementer_65_out_2), .out_2(sixt_bit_incrementer_66_out_2));
  Register #(.width(16)) register_65 (
    .D(in_2), .en(sixt_bit_eq_cmp_65_out_3), .Q(out_38[31:16]), .clk(buffer_20_out), .clr(in_4));
  Register #(.width(16)) register_66 (
    .D(in_2), .en(sixt_bit_eq_cmp_66_out_3), .Q(out_38[15:0]), .clk(buffer_20_out), .clr(in_4));
  sixt_bit_eq_cmp sixt_bit_eq_cmp_67 (
    .in_1(sixt_bit_incrementer_66_out_2), .in_2(undriven), .out_3(sixt_bit_eq_cmp_67_out_3));
  sixt_bit_incrementer sixt_bit_incrementer_67 (
    .in_1(sixt_bit_incrementer_66_out_2), .out_2(sixt_bit_incrementer_67_out_2));
  sixt_bit_eq_cmp sixt_bit_eq_cmp_68 (
    .in_1(sixt_bit_incrementer_67_out_2), .in_2(undriven), .out_3(sixt_bit_eq_cmp_68_out_3));
  sixt_bit_incrementer sixt_bit_incrementer_68 (
    .in_1(sixt_bit_incrementer_67_out_2), .out_2(sixt_bit_incrementer_68_out_2));
  Register #(.width(16)) register_67 (
    .D(in_2), .en(sixt_bit_eq_cmp_67_out_3), .Q(out_39[31:16]), .clk(buffer_20_out), .clr(in_4));
  Register #(.width(16)) register_68 (
    .D(in_2), .en(sixt_bit_eq_cmp_68_out_3), .Q(out_39[15:0]), .clk(buffer_20_out), .clr(in_4));
  sixt_bit_incrementer sixt_bit_incrementer_69 (
    .in_1(sixt_bit_incrementer_68_out_2), .out_2(sixt_bit_incrementer_69_out_2));
  sixt_bit_incrementer sixt_bit_incrementer_70 (
    .in_1(sixt_bit_incrementer_69_out_2), .out_2(sixt_bit_incrementer_70_out_2));
  Register #(.width(16)) register_69 (
    .D(in_2), .en(sixt_bit_eq_cmp_69_out_3), .Q(out_40[31:16]), .clk(buffer_20_out), .clr(in_4));
  sixt_bit_eq_cmp sixt_bit_eq_cmp_69 (
    .in_1(sixt_bit_incrementer_68_out_2), .in_2(undriven), .out_3(sixt_bit_eq_cmp_69_out_3));
  Register #(.width(16)) register_70 (
    .D(in_2), .en(sixt_bit_eq_cmp_70_out_3), .Q(out_40[15:0]), .clk(buffer_20_out), .clr(in_4));
  sixt_bit_eq_cmp sixt_bit_eq_cmp_70 (
    .in_1(sixt_bit_incrementer_69_out_2), .in_2(undriven), .out_3(sixt_bit_eq_cmp_70_out_3));
  sixt_bit_incrementer sixt_bit_incrementer_71 (
    .in_1(sixt_bit_incrementer_70_out_2), .out_2(sixt_bit_incrementer_71_out_2));
  sixt_bit_incrementer sixt_bit_incrementer_72 (
    .in_1(sixt_bit_incrementer_71_out_2), .out_2(sixt_bit_incrementer_72_out_2));
  sixt_bit_eq_cmp sixt_bit_eq_cmp_71 (
    .in_1(sixt_bit_incrementer_70_out_2), .in_2(undriven), .out_3(sixt_bit_eq_cmp_71_out_3));
  sixt_bit_eq_cmp sixt_bit_eq_cmp_72 (
    .in_1(sixt_bit_incrementer_71_out_2), .in_2(undriven), .out_3(sixt_bit_eq_cmp_72_out_3));
  Register #(.width(16)) register_71 (
    .D(in_2), .en(sixt_bit_eq_cmp_71_out_3), .Q(out_41[31:16]), .clk(buffer_20_out), .clr(in_4));
  Register #(.width(16)) register_72 (
    .D(in_2), .en(sixt_bit_eq_cmp_72_out_3), .Q(out_41[15:0]), .clk(buffer_20_out), .clr(in_4));
  sixt_bit_eq_cmp sixt_bit_eq_cmp_73 (
    .in_1(sixt_bit_incrementer_72_out_2), .in_2(undriven), .out_3(sixt_bit_eq_cmp_73_out_3));
  sixt_bit_incrementer sixt_bit_incrementer_73 (
    .in_1(sixt_bit_incrementer_72_out_2), .out_2(sixt_bit_incrementer_73_out_2));
  sixt_bit_eq_cmp sixt_bit_eq_cmp_74 (
    .in_1(sixt_bit_incrementer_73_out_2), .in_2(undriven), .out_3(sixt_bit_eq_cmp_74_out_3));
  sixt_bit_incrementer sixt_bit_incrementer_74 (
    .in_1(sixt_bit_incrementer_73_out_2), .out_2(sixt_bit_incrementer_74_out_2));
  Register #(.width(16)) register_73 (
    .D(in_2), .en(sixt_bit_eq_cmp_73_out_3), .Q(out_42[31:16]), .clk(buffer_20_out), .clr(in_4));
  Register #(.width(16)) register_74 (
    .D(in_2), .en(sixt_bit_eq_cmp_74_out_3), .Q(out_42[15:0]), .clk(buffer_20_out), .clr(in_4));
  sixt_bit_eq_cmp sixt_bit_eq_cmp_75 (
    .in_1(sixt_bit_incrementer_74_out_2), .in_2(undriven), .out_3(sixt_bit_eq_cmp_75_out_3));
  sixt_bit_incrementer sixt_bit_incrementer_75 (
    .in_1(sixt_bit_incrementer_74_out_2), .out_2(sixt_bit_incrementer_75_out_2));
  sixt_bit_eq_cmp sixt_bit_eq_cmp_76 (
    .in_1(sixt_bit_incrementer_75_out_2), .in_2(undriven), .out_3(sixt_bit_eq_cmp_76_out_3));
  sixt_bit_incrementer sixt_bit_incrementer_76 (
    .in_1(sixt_bit_incrementer_75_out_2), .out_2(sixt_bit_incrementer_76_out_2));
  Register #(.width(16)) register_75 (
    .D(in_2), .en(sixt_bit_eq_cmp_75_out_3), .Q(out_43[31:16]), .clk(buffer_20_out), .clr(in_4));
  Register #(.width(16)) register_76 (
    .D(in_2), .en(sixt_bit_eq_cmp_76_out_3), .Q(out_43[15:0]), .clk(buffer_20_out), .clr(in_4));
  sixt_bit_incrementer sixt_bit_incrementer_77 (
    .in_1(sixt_bit_incrementer_76_out_2), .out_2(sixt_bit_incrementer_77_out_2));
  sixt_bit_incrementer sixt_bit_incrementer_78 (
    .in_1(sixt_bit_incrementer_77_out_2), .out_2(sixt_bit_incrementer_78_out_2));
  Register #(.width(16)) register_77 (
    .D(in_2), .en(sixt_bit_eq_cmp_77_out_3), .Q(out_44[31:16]), .clk(buffer_20_out), .clr(in_4));
  sixt_bit_eq_cmp sixt_bit_eq_cmp_77 (
    .in_1(sixt_bit_incrementer_76_out_2), .in_2(undriven), .out_3(sixt_bit_eq_cmp_77_out_3));
  Register #(.width(16)) register_78 (
    .D(in_2), .en(sixt_bit_eq_cmp_78_out_3), .Q(out_44[15:0]), .clk(buffer_20_out), .clr(in_4));
  sixt_bit_eq_cmp sixt_bit_eq_cmp_78 (
    .in_1(sixt_bit_incrementer_77_out_2), .in_2(undriven), .out_3(sixt_bit_eq_cmp_78_out_3));
  sixt_bit_incrementer sixt_bit_incrementer_79 (
    .in_1(sixt_bit_incrementer_78_out_2), .out_2(sixt_bit_incrementer_79_out_2));
  sixt_bit_incrementer sixt_bit_incrementer_80 (
    .in_1(sixt_bit_incrementer_79_out_2), .out_2(sixt_bit_incrementer_80_out_2));
  sixt_bit_eq_cmp sixt_bit_eq_cmp_79 (
    .in_1(sixt_bit_incrementer_78_out_2), .in_2(undriven), .out_3(sixt_bit_eq_cmp_79_out_3));
  sixt_bit_eq_cmp sixt_bit_eq_cmp_80 (
    .in_1(sixt_bit_incrementer_79_out_2), .in_2(undriven), .out_3(sixt_bit_eq_cmp_80_out_3));
  Register #(.width(16)) register_79 (
    .D(in_2), .en(sixt_bit_eq_cmp_79_out_3), .Q(out_45[31:16]), .clk(buffer_20_out), .clr(in_4));
  Register #(.width(16)) register_80 (
    .D(in_2), .en(sixt_bit_eq_cmp_80_out_3), .Q(out_45[15:0]), .clk(buffer_20_out), .clr(in_4));
  sixt_bit_eq_cmp sixt_bit_eq_cmp_81 (
    .in_1(sixt_bit_incrementer_80_out_2), .in_2(undriven), .out_3(sixt_bit_eq_cmp_81_out_3));
  sixt_bit_incrementer sixt_bit_incrementer_81 (
    .in_1(sixt_bit_incrementer_80_out_2), .out_2(sixt_bit_incrementer_81_out_2));
  sixt_bit_eq_cmp sixt_bit_eq_cmp_82 (
    .in_1(sixt_bit_incrementer_81_out_2), .in_2(undriven), .out_3(sixt_bit_eq_cmp_82_out_3));
  sixt_bit_incrementer sixt_bit_incrementer_82 (
    .in_1(sixt_bit_incrementer_81_out_2), .out_2(sixt_bit_incrementer_82_out_2));
  Register #(.width(16)) register_81 (
    .D(in_2), .en(sixt_bit_eq_cmp_81_out_3), .Q(out_46[31:16]), .clk(buffer_20_out), .clr(in_4));
  Register #(.width(16)) register_82 (
    .D(in_2), .en(sixt_bit_eq_cmp_82_out_3), .Q(out_46[15:0]), .clk(buffer_20_out), .clr(in_4));
  sixt_bit_eq_cmp sixt_bit_eq_cmp_83 (
    .in_1(sixt_bit_incrementer_82_out_2), .in_2(undriven), .out_3(sixt_bit_eq_cmp_83_out_3));
  sixt_bit_incrementer sixt_bit_incrementer_83 (
    .in_1(sixt_bit_incrementer_82_out_2), .out_2(sixt_bit_incrementer_83_out_2));
  sixt_bit_eq_cmp sixt_bit_eq_cmp_84 (
    .in_1(sixt_bit_incrementer_83_out_2), .in_2(undriven), .out_3(sixt_bit_eq_cmp_84_out_3));
  sixt_bit_incrementer sixt_bit_incrementer_84 (
    .in_1(sixt_bit_incrementer_83_out_2), .out_2(sixt_bit_incrementer_84_out_2));
  Register #(.width(16)) register_83 (
    .D(in_2), .en(sixt_bit_eq_cmp_83_out_3), .Q(out_47[31:16]), .clk(buffer_20_out), .clr(in_4));
  Register #(.width(16)) register_84 (
    .D(in_2), .en(sixt_bit_eq_cmp_84_out_3), .Q(out_47[15:0]), .clk(buffer_20_out), .clr(in_4));
  sixt_bit_incrementer sixt_bit_incrementer_85 (
    .in_1(sixt_bit_incrementer_84_out_2), .out_2(sixt_bit_incrementer_85_out_2));
  sixt_bit_incrementer sixt_bit_incrementer_86 (
    .in_1(sixt_bit_incrementer_85_out_2), .out_2(sixt_bit_incrementer_86_out_2));
  Register #(.width(16)) register_85 (
    .D(in_2), .en(sixt_bit_eq_cmp_85_out_3), .Q(out_48[31:16]), .clk(buffer_20_out), .clr(in_4));
  sixt_bit_eq_cmp sixt_bit_eq_cmp_85 (
    .in_1(sixt_bit_incrementer_84_out_2), .in_2(undriven), .out_3(sixt_bit_eq_cmp_85_out_3));
  Register #(.width(16)) register_86 (
    .D(in_2), .en(sixt_bit_eq_cmp_86_out_3), .Q(out_48[15:0]), .clk(buffer_20_out), .clr(in_4));
  sixt_bit_eq_cmp sixt_bit_eq_cmp_86 (
    .in_1(sixt_bit_incrementer_85_out_2), .in_2(undriven), .out_3(sixt_bit_eq_cmp_86_out_3));
  sixt_bit_incrementer sixt_bit_incrementer_87 (
    .in_1(sixt_bit_incrementer_86_out_2), .out_2(sixt_bit_incrementer_87_out_2));
  sixt_bit_incrementer sixt_bit_incrementer_88 (
    .in_1(sixt_bit_incrementer_87_out_2), .out_2(sixt_bit_incrementer_88_out_2));
  sixt_bit_eq_cmp sixt_bit_eq_cmp_87 (
    .in_1(sixt_bit_incrementer_86_out_2), .in_2(undriven), .out_3(sixt_bit_eq_cmp_87_out_3));
  sixt_bit_eq_cmp sixt_bit_eq_cmp_88 (
    .in_1(sixt_bit_incrementer_87_out_2), .in_2(undriven), .out_3(sixt_bit_eq_cmp_88_out_3));
  Register #(.width(16)) register_87 (
    .D(in_2), .en(sixt_bit_eq_cmp_87_out_3), .Q(out_49[31:16]), .clk(buffer_20_out), .clr(in_4));
  Register #(.width(16)) register_88 (
    .D(in_2), .en(sixt_bit_eq_cmp_88_out_3), .Q(out_49[15:0]), .clk(buffer_20_out), .clr(in_4));
  sixt_bit_eq_cmp sixt_bit_eq_cmp_89 (
    .in_1(sixt_bit_incrementer_88_out_2), .in_2(undriven), .out_3(sixt_bit_eq_cmp_89_out_3));
  sixt_bit_incrementer sixt_bit_incrementer_89 (
    .in_1(sixt_bit_incrementer_88_out_2), .out_2(sixt_bit_incrementer_89_out_2));
  sixt_bit_eq_cmp sixt_bit_eq_cmp_90 (
    .in_1(sixt_bit_incrementer_89_out_2), .in_2(undriven), .out_3(sixt_bit_eq_cmp_90_out_3));
  sixt_bit_incrementer sixt_bit_incrementer_90 (
    .in_1(sixt_bit_incrementer_89_out_2), .out_2(sixt_bit_incrementer_90_out_2));
  Register #(.width(16)) register_89 (
    .D(in_2), .en(sixt_bit_eq_cmp_89_out_3), .Q(out_50[31:16]), .clk(buffer_20_out), .clr(in_4));
  Register #(.width(16)) register_90 (
    .D(in_2), .en(sixt_bit_eq_cmp_90_out_3), .Q(out_50[15:0]), .clk(buffer_20_out), .clr(in_4));
  sixt_bit_eq_cmp sixt_bit_eq_cmp_91 (
    .in_1(sixt_bit_incrementer_90_out_2), .in_2(undriven), .out_3(sixt_bit_eq_cmp_91_out_3));
  sixt_bit_incrementer sixt_bit_incrementer_91 (
    .in_1(sixt_bit_incrementer_90_out_2), .out_2(sixt_bit_incrementer_91_out_2));
  sixt_bit_eq_cmp sixt_bit_eq_cmp_92 (
    .in_1(sixt_bit_incrementer_91_out_2), .in_2(undriven), .out_3(sixt_bit_eq_cmp_92_out_3));
  sixt_bit_incrementer sixt_bit_incrementer_92 (
    .in_1(sixt_bit_incrementer_91_out_2), .out_2(sixt_bit_incrementer_92_out_2));
  Register #(.width(16)) register_91 (
    .D(in_2), .en(sixt_bit_eq_cmp_91_out_3), .Q(out_51[31:16]), .clk(buffer_20_out), .clr(in_4));
  Register #(.width(16)) register_92 (
    .D(in_2), .en(sixt_bit_eq_cmp_92_out_3), .Q(out_51[15:0]), .clk(buffer_20_out), .clr(in_4));
  sixt_bit_incrementer sixt_bit_incrementer_93 (
    .in_1(sixt_bit_incrementer_92_out_2), .out_2(sixt_bit_incrementer_93_out_2));
  sixt_bit_incrementer sixt_bit_incrementer_94 (
    .in_1(sixt_bit_incrementer_93_out_2), .out_2(sixt_bit_incrementer_94_out_2));
  Register #(.width(16)) register_93 (
    .D(in_2), .en(sixt_bit_eq_cmp_93_out_3), .Q(out_52[31:16]), .clk(buffer_20_out), .clr(in_4));
  sixt_bit_eq_cmp sixt_bit_eq_cmp_93 (
    .in_1(sixt_bit_incrementer_92_out_2), .in_2(undriven), .out_3(sixt_bit_eq_cmp_93_out_3));
  Register #(.width(16)) register_94 (
    .D(in_2), .en(sixt_bit_eq_cmp_94_out_3), .Q(out_52[15:0]), .clk(buffer_20_out), .clr(in_4));
  sixt_bit_eq_cmp sixt_bit_eq_cmp_94 (
    .in_1(sixt_bit_incrementer_93_out_2), .in_2(undriven), .out_3(sixt_bit_eq_cmp_94_out_3));
  sixt_bit_incrementer sixt_bit_incrementer_95 (
    .in_1(sixt_bit_incrementer_94_out_2), .out_2(sixt_bit_incrementer_95_out_2));
  sixt_bit_incrementer sixt_bit_incrementer_96 (
    .in_1(sixt_bit_incrementer_95_out_2), .out_2(sixt_bit_incrementer_96_out_2));
  sixt_bit_eq_cmp sixt_bit_eq_cmp_95 (
    .in_1(sixt_bit_incrementer_94_out_2), .in_2(undriven), .out_3(sixt_bit_eq_cmp_95_out_3));
  sixt_bit_eq_cmp sixt_bit_eq_cmp_96 (
    .in_1(sixt_bit_incrementer_95_out_2), .in_2(undriven), .out_3(sixt_bit_eq_cmp_96_out_3));
  Register #(.width(16)) register_95 (
    .D(in_2), .en(sixt_bit_eq_cmp_95_out_3), .Q(out_53[31:16]), .clk(buffer_20_out), .clr(in_4));
  Register #(.width(16)) register_96 (
    .D(in_2), .en(sixt_bit_eq_cmp_96_out_3), .Q(out_53[15:0]), .clk(buffer_20_out), .clr(in_4));
  sixt_bit_eq_cmp sixt_bit_eq_cmp_97 (
    .in_1(sixt_bit_incrementer_96_out_2), .in_2(undriven), .out_3(sixt_bit_eq_cmp_97_out_3));
  sixt_bit_incrementer sixt_bit_incrementer_97 (
    .in_1(sixt_bit_incrementer_96_out_2), .out_2(sixt_bit_incrementer_97_out_2));
  sixt_bit_eq_cmp sixt_bit_eq_cmp_98 (
    .in_1(sixt_bit_incrementer_97_out_2), .in_2(undriven), .out_3(sixt_bit_eq_cmp_98_out_3));
  sixt_bit_incrementer sixt_bit_incrementer_98 (
    .in_1(sixt_bit_incrementer_97_out_2), .out_2(sixt_bit_incrementer_98_out_2));
  Register #(.width(16)) register_97 (
    .D(in_2), .en(sixt_bit_eq_cmp_97_out_3), .Q(out_54[31:16]), .clk(buffer_20_out), .clr(in_4));
  Register #(.width(16)) register_98 (
    .D(in_2), .en(sixt_bit_eq_cmp_98_out_3), .Q(out_54[15:0]), .clk(buffer_20_out), .clr(in_4));
  sixt_bit_eq_cmp sixt_bit_eq_cmp_99 (
    .in_1(sixt_bit_incrementer_98_out_2), .in_2(undriven), .out_3(sixt_bit_eq_cmp_99_out_3));
  sixt_bit_incrementer sixt_bit_incrementer_99 (
    .in_1(sixt_bit_incrementer_98_out_2), .out_2(sixt_bit_incrementer_99_out_2));
  sixt_bit_eq_cmp sixt_bit_eq_cmp_100 (
    .in_1(sixt_bit_incrementer_99_out_2), .in_2(undriven), .out_3(sixt_bit_eq_cmp_100_out_3));
  sixt_bit_incrementer sixt_bit_incrementer_100 (
    .in_1(sixt_bit_incrementer_99_out_2), .out_2(sixt_bit_incrementer_100_out_2));
  Register #(.width(16)) register_99 (
    .D(in_2), .en(sixt_bit_eq_cmp_99_out_3), .Q(out_55[31:16]), .clk(buffer_20_out), .clr(in_4));
  Register #(.width(16)) register_100 (
    .D(in_2), .en(sixt_bit_eq_cmp_100_out_3), .Q(out_55[15:0]), .clk(buffer_20_out), .clr(in_4));
  sixt_bit_incrementer sixt_bit_incrementer_101 (
    .in_1(sixt_bit_incrementer_100_out_2), .out_2(sixt_bit_incrementer_101_out_2));
  sixt_bit_incrementer sixt_bit_incrementer_102 (
    .in_1(sixt_bit_incrementer_101_out_2), .out_2(sixt_bit_incrementer_102_out_2));
  Register #(.width(16)) register_101 (
    .D(in_2), .en(sixt_bit_eq_cmp_101_out_3), .Q(out_56[31:16]), .clk(buffer_20_out), .clr(in_4));
  sixt_bit_eq_cmp sixt_bit_eq_cmp_101 (
    .in_1(sixt_bit_incrementer_100_out_2), .in_2(undriven), .out_3(sixt_bit_eq_cmp_101_out_3));
  Register #(.width(16)) register_102 (
    .D(in_2), .en(sixt_bit_eq_cmp_102_out_3), .Q(out_56[15:0]), .clk(buffer_20_out), .clr(in_4));
  sixt_bit_eq_cmp sixt_bit_eq_cmp_102 (
    .in_1(sixt_bit_incrementer_101_out_2), .in_2(undriven), .out_3(sixt_bit_eq_cmp_102_out_3));
  sixt_bit_incrementer sixt_bit_incrementer_103 (
    .in_1(sixt_bit_incrementer_102_out_2), .out_2(sixt_bit_incrementer_103_out_2));
  sixt_bit_incrementer sixt_bit_incrementer_104 (
    .in_1(sixt_bit_incrementer_103_out_2), .out_2(sixt_bit_incrementer_104_out_2));
  sixt_bit_eq_cmp sixt_bit_eq_cmp_103 (
    .in_1(sixt_bit_incrementer_102_out_2), .in_2(undriven), .out_3(sixt_bit_eq_cmp_103_out_3));
  sixt_bit_eq_cmp sixt_bit_eq_cmp_104 (
    .in_1(sixt_bit_incrementer_103_out_2), .in_2(undriven), .out_3(sixt_bit_eq_cmp_104_out_3));
  Register #(.width(16)) register_103 (
    .D(in_2), .en(sixt_bit_eq_cmp_103_out_3), .Q(out_57[31:16]), .clk(buffer_20_out), .clr(in_4));
  Register #(.width(16)) register_104 (
    .D(in_2), .en(sixt_bit_eq_cmp_104_out_3), .Q(out_57[15:0]), .clk(buffer_20_out), .clr(in_4));
  sixt_bit_eq_cmp sixt_bit_eq_cmp_105 (
    .in_1(sixt_bit_incrementer_104_out_2), .in_2(undriven), .out_3(sixt_bit_eq_cmp_105_out_3));
  sixt_bit_incrementer sixt_bit_incrementer_105 (
    .in_1(sixt_bit_incrementer_104_out_2), .out_2(sixt_bit_incrementer_105_out_2));
  sixt_bit_eq_cmp sixt_bit_eq_cmp_106 (
    .in_1(sixt_bit_incrementer_105_out_2), .in_2(undriven), .out_3(sixt_bit_eq_cmp_106_out_3));
  sixt_bit_incrementer sixt_bit_incrementer_106 (
    .in_1(sixt_bit_incrementer_105_out_2), .out_2(sixt_bit_incrementer_106_out_2));
  Register #(.width(16)) register_105 (
    .D(in_2), .en(sixt_bit_eq_cmp_105_out_3), .Q(out_58[31:16]), .clk(buffer_20_out), .clr(in_4));
  Register #(.width(16)) register_106 (
    .D(in_2), .en(sixt_bit_eq_cmp_106_out_3), .Q(out_58[15:0]), .clk(buffer_20_out), .clr(in_4));
  sixt_bit_eq_cmp sixt_bit_eq_cmp_107 (
    .in_1(sixt_bit_incrementer_106_out_2), .in_2(undriven), .out_3(sixt_bit_eq_cmp_107_out_3));
  sixt_bit_incrementer sixt_bit_incrementer_107 (
    .in_1(sixt_bit_incrementer_106_out_2), .out_2(sixt_bit_incrementer_107_out_2));
  sixt_bit_eq_cmp sixt_bit_eq_cmp_108 (
    .in_1(sixt_bit_incrementer_107_out_2), .in_2(undriven), .out_3(sixt_bit_eq_cmp_108_out_3));
  sixt_bit_incrementer sixt_bit_incrementer_108 (
    .in_1(sixt_bit_incrementer_107_out_2), .out_2(sixt_bit_incrementer_108_out_2));
  Register #(.width(16)) register_107 (
    .D(in_2), .en(sixt_bit_eq_cmp_107_out_3), .Q(out_59[31:16]), .clk(buffer_20_out), .clr(in_4));
  Register #(.width(16)) register_108 (
    .D(in_2), .en(sixt_bit_eq_cmp_108_out_3), .Q(out_59[15:0]), .clk(buffer_20_out), .clr(in_4));
  sixt_bit_incrementer sixt_bit_incrementer_109 (
    .in_1(sixt_bit_incrementer_108_out_2), .out_2(sixt_bit_incrementer_109_out_2));
  sixt_bit_incrementer sixt_bit_incrementer_110 (
    .in_1(sixt_bit_incrementer_109_out_2), .out_2(sixt_bit_incrementer_110_out_2));
  Register #(.width(16)) register_109 (
    .D(in_2), .en(sixt_bit_eq_cmp_109_out_3), .Q(out_60[31:16]), .clk(buffer_20_out), .clr(in_4));
  sixt_bit_eq_cmp sixt_bit_eq_cmp_109 (
    .in_1(sixt_bit_incrementer_108_out_2), .in_2(undriven), .out_3(sixt_bit_eq_cmp_109_out_3));
  Register #(.width(16)) register_110 (
    .D(in_2), .en(sixt_bit_eq_cmp_110_out_3), .Q(out_60[15:0]), .clk(buffer_20_out), .clr(in_4));
  sixt_bit_eq_cmp sixt_bit_eq_cmp_110 (
    .in_1(sixt_bit_incrementer_109_out_2), .in_2(undriven), .out_3(sixt_bit_eq_cmp_110_out_3));
  sixt_bit_incrementer sixt_bit_incrementer_111 (
    .in_1(sixt_bit_incrementer_110_out_2), .out_2(sixt_bit_incrementer_111_out_2));
  sixt_bit_incrementer sixt_bit_incrementer_112 (
    .in_1(sixt_bit_incrementer_111_out_2), .out_2(sixt_bit_incrementer_112_out_2));
  sixt_bit_eq_cmp sixt_bit_eq_cmp_111 (
    .in_1(sixt_bit_incrementer_110_out_2), .in_2(undriven), .out_3(sixt_bit_eq_cmp_111_out_3));
  sixt_bit_eq_cmp sixt_bit_eq_cmp_112 (
    .in_1(sixt_bit_incrementer_111_out_2), .in_2(undriven), .out_3(sixt_bit_eq_cmp_112_out_3));
  Register #(.width(16)) register_111 (
    .D(in_2), .en(sixt_bit_eq_cmp_111_out_3), .Q(out_61[31:16]), .clk(buffer_20_out), .clr(in_4));
  Register #(.width(16)) register_112 (
    .D(in_2), .en(sixt_bit_eq_cmp_112_out_3), .Q(out_61[15:0]), .clk(buffer_20_out), .clr(in_4));
  sixt_bit_eq_cmp sixt_bit_eq_cmp_113 (
    .in_1(sixt_bit_incrementer_112_out_2), .in_2(undriven), .out_3(sixt_bit_eq_cmp_113_out_3));
  sixt_bit_incrementer sixt_bit_incrementer_113 (
    .in_1(sixt_bit_incrementer_112_out_2), .out_2(sixt_bit_incrementer_113_out_2));
  sixt_bit_eq_cmp sixt_bit_eq_cmp_114 (
    .in_1(sixt_bit_incrementer_113_out_2), .in_2(undriven), .out_3(sixt_bit_eq_cmp_114_out_3));
  sixt_bit_incrementer sixt_bit_incrementer_114 (
    .in_1(sixt_bit_incrementer_113_out_2), .out_2(sixt_bit_incrementer_114_out_2));
  Register #(.width(16)) register_113 (
    .D(in_2), .en(sixt_bit_eq_cmp_113_out_3), .Q(out_62[31:16]), .clk(buffer_20_out), .clr(in_4));
  Register #(.width(16)) register_114 (
    .D(in_2), .en(sixt_bit_eq_cmp_114_out_3), .Q(out_62[15:0]), .clk(buffer_20_out), .clr(in_4));
  sixt_bit_eq_cmp sixt_bit_eq_cmp_115 (
    .in_1(sixt_bit_incrementer_114_out_2), .in_2(undriven), .out_3(sixt_bit_eq_cmp_115_out_3));
  sixt_bit_incrementer sixt_bit_incrementer_115 (
    .in_1(sixt_bit_incrementer_114_out_2), .out_2(sixt_bit_incrementer_115_out_2));
  sixt_bit_eq_cmp sixt_bit_eq_cmp_116 (
    .in_1(sixt_bit_incrementer_115_out_2), .in_2(undriven), .out_3(sixt_bit_eq_cmp_116_out_3));
  sixt_bit_incrementer sixt_bit_incrementer_116 (
    .in_1(sixt_bit_incrementer_115_out_2), .out_2(sixt_bit_incrementer_116_out_2));
  Register #(.width(16)) register_115 (
    .D(in_2), .en(sixt_bit_eq_cmp_115_out_3), .Q(out_63[31:16]), .clk(buffer_20_out), .clr(in_4));
  Register #(.width(16)) register_116 (
    .D(in_2), .en(sixt_bit_eq_cmp_116_out_3), .Q(out_63[15:0]), .clk(buffer_20_out), .clr(in_4));
  sixt_bit_incrementer sixt_bit_incrementer_117 (
    .in_1(sixt_bit_incrementer_116_out_2), .out_2(sixt_bit_incrementer_117_out_2));
  sixt_bit_incrementer sixt_bit_incrementer_118 (
    .in_1(sixt_bit_incrementer_117_out_2), .out_2(sixt_bit_incrementer_118_out_2));
  Register #(.width(16)) register_117 (
    .D(in_2), .en(sixt_bit_eq_cmp_117_out_3), .Q(out_64[31:16]), .clk(buffer_20_out), .clr(in_4));
  sixt_bit_eq_cmp sixt_bit_eq_cmp_117 (
    .in_1(sixt_bit_incrementer_116_out_2), .in_2(undriven), .out_3(sixt_bit_eq_cmp_117_out_3));
  Register #(.width(16)) register_118 (
    .D(in_2), .en(sixt_bit_eq_cmp_118_out_3), .Q(out_64[15:0]), .clk(buffer_20_out), .clr(in_4));
  sixt_bit_eq_cmp sixt_bit_eq_cmp_118 (
    .in_1(sixt_bit_incrementer_117_out_2), .in_2(undriven), .out_3(sixt_bit_eq_cmp_118_out_3));
  sixt_bit_incrementer sixt_bit_incrementer_119 (
    .in_1(sixt_bit_incrementer_118_out_2), .out_2(sixt_bit_incrementer_119_out_2));
  sixt_bit_incrementer sixt_bit_incrementer_120 (
    .in_1(sixt_bit_incrementer_119_out_2), .out_2(sixt_bit_incrementer_120_out_2));
  sixt_bit_eq_cmp sixt_bit_eq_cmp_119 (
    .in_1(sixt_bit_incrementer_118_out_2), .in_2(undriven), .out_3(sixt_bit_eq_cmp_119_out_3));
  sixt_bit_eq_cmp sixt_bit_eq_cmp_120 (
    .in_1(sixt_bit_incrementer_119_out_2), .in_2(undriven), .out_3(sixt_bit_eq_cmp_120_out_3));
  Register #(.width(16)) register_119 (
    .D(in_2), .en(sixt_bit_eq_cmp_119_out_3), .Q(out_65[31:16]), .clk(buffer_20_out), .clr(in_4));
  Register #(.width(16)) register_120 (
    .D(in_2), .en(sixt_bit_eq_cmp_120_out_3), .Q(out_65[15:0]), .clk(buffer_20_out), .clr(in_4));
  sixt_bit_eq_cmp sixt_bit_eq_cmp_121 (
    .in_1(sixt_bit_incrementer_120_out_2), .in_2(undriven), .out_3(sixt_bit_eq_cmp_121_out_3));
  sixt_bit_incrementer sixt_bit_incrementer_121 (
    .in_1(sixt_bit_incrementer_120_out_2), .out_2(sixt_bit_incrementer_121_out_2));
  sixt_bit_eq_cmp sixt_bit_eq_cmp_122 (
    .in_1(sixt_bit_incrementer_121_out_2), .in_2(undriven), .out_3(sixt_bit_eq_cmp_122_out_3));
  sixt_bit_incrementer sixt_bit_incrementer_122 (
    .in_1(sixt_bit_incrementer_121_out_2), .out_2(sixt_bit_incrementer_122_out_2));
  Register #(.width(16)) register_121 (
    .D(in_2), .en(sixt_bit_eq_cmp_121_out_3), .Q(out_66[31:16]), .clk(buffer_20_out), .clr(in_4));
  Register #(.width(16)) register_122 (
    .D(in_2), .en(sixt_bit_eq_cmp_122_out_3), .Q(out_66[15:0]), .clk(buffer_20_out), .clr(in_4));
  sixt_bit_eq_cmp sixt_bit_eq_cmp_123 (
    .in_1(sixt_bit_incrementer_122_out_2), .in_2(undriven), .out_3(sixt_bit_eq_cmp_123_out_3));
  sixt_bit_incrementer sixt_bit_incrementer_123 (
    .in_1(sixt_bit_incrementer_122_out_2), .out_2(sixt_bit_incrementer_123_out_2));
  sixt_bit_eq_cmp sixt_bit_eq_cmp_124 (
    .in_1(sixt_bit_incrementer_123_out_2), .in_2(undriven), .out_3(sixt_bit_eq_cmp_124_out_3));
  sixt_bit_incrementer sixt_bit_incrementer_124 (
    .in_1(sixt_bit_incrementer_123_out_2), .out_2(sixt_bit_incrementer_124_out_2));
  Register #(.width(16)) register_123 (
    .D(in_2), .en(sixt_bit_eq_cmp_123_out_3), .Q(out_67[31:16]), .clk(buffer_20_out), .clr(in_4));
  Register #(.width(16)) register_124 (
    .D(in_2), .en(sixt_bit_eq_cmp_124_out_3), .Q(out_67[15:0]), .clk(buffer_20_out), .clr(in_4));
  sixt_bit_incrementer sixt_bit_incrementer_125 (
    .in_1(sixt_bit_incrementer_124_out_2), .out_2(sixt_bit_incrementer_125_out_2));
  sixt_bit_incrementer sixt_bit_incrementer_126 (
    .in_1(sixt_bit_incrementer_125_out_2), .out_2(sixt_bit_incrementer_126_out_2));
  Register #(.width(16)) register_125 (
    .D(in_2), .en(sixt_bit_eq_cmp_125_out_3), .Q(out_68[31:16]), .clk(buffer_20_out), .clr(in_4));
  sixt_bit_eq_cmp sixt_bit_eq_cmp_125 (
    .in_1(sixt_bit_incrementer_124_out_2), .in_2(undriven), .out_3(sixt_bit_eq_cmp_125_out_3));
  Register #(.width(16)) register_126 (
    .D(in_2), .en(sixt_bit_eq_cmp_126_out_3), .Q(out_68[15:0]), .clk(buffer_20_out), .clr(in_4));
  sixt_bit_eq_cmp sixt_bit_eq_cmp_126 (
    .in_1(sixt_bit_incrementer_125_out_2), .in_2(undriven), .out_3(sixt_bit_eq_cmp_126_out_3));
  sixt_bit_incrementer sixt_bit_incrementer_127 (
    .in_1(sixt_bit_incrementer_126_out_2), .out_2(sixt_bit_incrementer_127_out_2));
  sixt_bit_incrementer sixt_bit_incrementer_128 (
    .in_1(sixt_bit_incrementer_127_out_2), .out_2(sixt_bit_incrementer_128_out_2));
  sixt_bit_eq_cmp sixt_bit_eq_cmp_127 (
    .in_1(sixt_bit_incrementer_126_out_2), .in_2(undriven), .out_3(sixt_bit_eq_cmp_127_out_3));
  sixt_bit_eq_cmp sixt_bit_eq_cmp_128 (
    .in_1(sixt_bit_incrementer_127_out_2), .in_2(undriven), .out_3(sixt_bit_eq_cmp_128_out_3));
  Register #(.width(16)) register_127 (
    .D(in_2), .en(sixt_bit_eq_cmp_127_out_3), .Q(out_69[31:16]), .clk(buffer_20_out), .clr(in_4));
  Register #(.width(16)) register_128 (
    .D(in_2), .en(sixt_bit_eq_cmp_128_out_3), .Q(out_69[15:0]), .clk(buffer_20_out), .clr(in_4));
endmodule

module fun_silly_controller (
  input  [15:0] in_1,
  input  [15:0] in_2,
  input  [15:0] in_3,
  input  Clock,
  input  Reset,
  output out_6,
  output out_7,
  output [15:0] out_8,
  output [6:0] out_9,
  output out_10,
  output out_11
);

  wire sixt_bit_eq_cmp_3_out_3;

  sixt_bit_eq_cmp sixt_bit_eq_cmp_1 (.in_1(in_1), .in_2(16'hc2), .out_3(out_6));
  sixt_bit_eq_cmp sixt_bit_eq_cmp_2 (.in_1(16'hc1), .in_2(in_1), .out_3(out_7));
  sixt_bit_eq_cmp sixt_bit_eq_cmp_3 (.in_1(in_1), .in_2(16'hc0), .out_3(sixt_bit_eq_cmp_3_out_3));
  or or_1 (out_11, sixt_bit_eq_cmp_3_out_3, Reset);

  assign out_8 = in_2;
  assign out_9 = in_3[6:0];
  assign out_10 = Clock;

  // Notes on the sheet:
  //   Control
  //   Data
  //   Address
endmodule
module fun_silly_2 (
  input  in_1,
  input  in_2,
  input  [15:0] in_3,
  input  [6:0] in_4,
  input  in_5,
  input  in_6,
  output [31:0] out_7,
  output [31:0] out_8,
  output [31:0] out_9,
  output [31:0] out_10,
  output [31:0] out_11,
  output [31:0] out_12,
  output [31:0] out_13,
  output [31:0] out_14,
  output [31:0] out_15,
  output [31:0] out_16,
  output [31:0] out_17,
  output [31:0] out_18,
  output [31:0] out_19,
  output [31:0] out_20,
  output [31:0] out_21,
  output [31:0] out_22,
  output [31:0] out_23,
  output [31:0] out_24,
  output [31:0] out_25,
  output [31:0] out_26,
  output [31:0] out_27,
  output [31:0] out_28,
  output [31:0] out_29,
  output [31:0] out_30,
  output [31:0] out_31,
  output [31:0] out_32,
  output [31:0] out_33,
  output [31:0] out_34,
  output [31:0] out_35,
  output [31:0] out_36,
  output [31:0] out_37,
  output [31:0] out_38,
  output [31:0] out_39,
  output [31:0] out_40,
  output [31:0] out_41,
  output [31:0] out_42,
  output [31:0] out_43,
  output [31:0] out_44,
  output [31:0] out_45,
  output [31:0] out_46,
  output [31:0] out_47,
  output [31:0] out_48,
  output [31:0] out_49,
  output [31:0] out_50,
  output [31:0] out_51,
  output [31:0] out_52,
  output [31:0] out_53,
  output [31:0] out_54,
  output [31:0] out_55,
  output [31:0] out_56,
  output [31:0] out_57,
  output [31:0] out_58,
  output [31:0] out_59,
  output [31:0] out_60,
  output [31:0] out_61,
  output [31:0] out_62,
  output [31:0] out_63,
  output [31:0] out_64,
  output [31:0] out_65,
  output [31:0] out_66,
  output [31:0] out_67,
  output [31:0] out_68,
  output [31:0] out_69,
  output [31:0] out_70
);

  wire and_1_out, and_2_out, and_3_out, and_4_out, and_5_out, and_6_out, buffer_1_out, buffer_2_out,
       buffer_3_out, buffer_4_out, buffer_5_out, buffer_6_out, buffer_7_out, buffer_8_out, buffer_9_out,
       or_1_out, or_2_out, s_r_ff_1_q, s_r_ff_2_q, s_r_ff_3_q, t_ff_1_q;
  wire [31:0] fun_silly_1_out_6, fun_silly_1_out_7, fun_silly_1_out_8, fun_silly_1_out_9, fun_silly_1_out_10,
       fun_silly_1_out_11, fun_silly_1_out_12, fun_silly_1_out_13, fun_silly_1_out_14, fun_silly_1_out_15,
       fun_silly_1_out_16, fun_silly_1_out_17, fun_silly_1_out_18, fun_silly_1_out_19, fun_silly_1_out_20,
       fun_silly_1_out_21, fun_silly_1_out_22, fun_silly_1_out_23, fun_silly_1_out_24, fun_silly_1_out_25,
       fun_silly_1_out_26, fun_silly_1_out_27, fun_silly_1_out_28, fun_silly_1_out_29, fun_silly_1_out_30,
       fun_silly_1_out_31, fun_silly_1_out_32, fun_silly_1_out_33, fun_silly_1_out_34, fun_silly_1_out_35,
       fun_silly_1_out_36, fun_silly_1_out_37, fun_silly_1_out_38, fun_silly_1_out_39, fun_silly_1_out_40,
       fun_silly_1_out_41, fun_silly_1_out_42, fun_silly_1_out_43, fun_silly_1_out_44, fun_silly_1_out_45,
       fun_silly_1_out_46, fun_silly_1_out_47, fun_silly_1_out_48, fun_silly_1_out_49, fun_silly_1_out_50,
       fun_silly_1_out_51, fun_silly_1_out_52, fun_silly_1_out_53, fun_silly_1_out_54, fun_silly_1_out_55,
       fun_silly_1_out_56, fun_silly_1_out_57, fun_silly_1_out_58, fun_silly_1_out_59, fun_silly_1_out_60,
       fun_silly_1_out_61, fun_silly_1_out_62, fun_silly_1_out_63, fun_silly_1_out_64, fun_silly_1_out_65,
       fun_silly_1_out_66, fun_silly_1_out_67, fun_silly_1_out_68, fun_silly_1_out_69, fun_silly_2_out_6,
       fun_silly_2_out_7, fun_silly_2_out_8, fun_silly_2_out_9, fun_silly_2_out_10, fun_silly_2_out_11,
       fun_silly_2_out_12, fun_silly_2_out_13, fun_silly_2_out_14, fun_silly_2_out_15, fun_silly_2_out_16,
       fun_silly_2_out_17, fun_silly_2_out_18, fun_silly_2_out_19, fun_silly_2_out_20, fun_silly_2_out_21,
       fun_silly_2_out_22, fun_silly_2_out_23, fun_silly_2_out_24, fun_silly_2_out_25, fun_silly_2_out_26,
       fun_silly_2_out_27, fun_silly_2_out_28, fun_silly_2_out_29, fun_silly_2_out_30, fun_silly_2_out_31,
       fun_silly_2_out_32, fun_silly_2_out_33, fun_silly_2_out_34, fun_silly_2_out_35, fun_silly_2_out_36,
       fun_silly_2_out_37, fun_silly_2_out_38, fun_silly_2_out_39, fun_silly_2_out_40, fun_silly_2_out_41,
       fun_silly_2_out_42, fun_silly_2_out_43, fun_silly_2_out_44, fun_silly_2_out_45, fun_silly_2_out_46,
       fun_silly_2_out_47, fun_silly_2_out_48, fun_silly_2_out_49, fun_silly_2_out_50, fun_silly_2_out_51,
       fun_silly_2_out_52, fun_silly_2_out_53, fun_silly_2_out_54, fun_silly_2_out_55, fun_silly_2_out_56,
       fun_silly_2_out_57, fun_silly_2_out_58, fun_silly_2_out_59, fun_silly_2_out_60, fun_silly_2_out_61,
       fun_silly_2_out_62, fun_silly_2_out_63, fun_silly_2_out_64, fun_silly_2_out_65, fun_silly_2_out_66,
       fun_silly_2_out_67, fun_silly_2_out_68, fun_silly_2_out_69;

  T_Flip_Flop t_ff_1 (.T(1'b1), .clk(in_2), .Q(t_ff_1_q));  // open: Qn, reset, preset
  buf buffer_1 (buffer_1_out, buffer_3_out);
  buf buffer_2 (buffer_2_out, buffer_1_out);
  buf buffer_3 (buffer_3_out, buffer_4_out);
  buf buffer_4 (buffer_4_out, buffer_5_out);
  buf buffer_5 (buffer_5_out, buffer_9_out);
  buf buffer_6 (buffer_6_out, in_5);
  buf buffer_7 (buffer_7_out, buffer_6_out);
  S_R_Flip_Flop #(.trigger("falling")) s_r_ff_1 (
    .S(in_2), .R(1'b0), .clk(in_5), .Q(s_r_ff_1_q), .reset(s_r_ff_3_q));  // open: Qn, preset
  S_R_Flip_Flop s_r_ff_2 (
    .S(s_r_ff_1_q), .R(1'b0), .clk(in_5), .Q(s_r_ff_2_q), .reset(s_r_ff_3_q));  // open: Qn, preset
  S_R_Flip_Flop #(.trigger("falling")) s_r_ff_3 (
    .S(s_r_ff_2_q), .R(1'b0), .clk(in_5), .Q(s_r_ff_3_q), .reset(s_r_ff_3_q));  // open: Qn, preset
  buf buffer_8 (buffer_8_out, buffer_2_out);
  buf buffer_9 (buffer_9_out, buffer_7_out);
  and and_1 (and_1_out, s_r_ff_2_q, ~t_ff_1_q);  // AND_Gate
  and and_2 (and_2_out, t_ff_1_q, s_r_ff_2_q);
  or or_1 (or_1_out, and_2_out, in_6, and_3_out);
  and and_3 (and_3_out, ~t_ff_1_q, in_6);  // AND_Gate
  and and_4 (and_4_out, in_1, t_ff_1_q);
  and and_5 (and_5_out, ~t_ff_1_q, in_1);  // AND_Gate
  and and_6 (and_6_out, ~t_ff_1_q, in_6);  // AND_Gate
  or or_2 (or_2_out, and_6_out, and_1_out);
  fun_silly fun_silly_1 (
    .in_4(or_1_out), .in_5(buffer_8_out), .in_1(and_4_out), .in_2(in_3), .in_3(in_4),
    .out_10(fun_silly_1_out_10), .out_60(fun_silly_1_out_60), .out_61(fun_silly_1_out_61),
    .out_62(fun_silly_1_out_62), .out_63(fun_silly_1_out_63), .out_64(fun_silly_1_out_64),
    .out_65(fun_silly_1_out_65), .out_66(fun_silly_1_out_66), .out_67(fun_silly_1_out_67),
    .out_68(fun_silly_1_out_68), .out_69(fun_silly_1_out_69), .out_11(fun_silly_1_out_11),
    .out_12(fun_silly_1_out_12), .out_13(fun_silly_1_out_13), .out_14(fun_silly_1_out_14),
    .out_15(fun_silly_1_out_15), .out_16(fun_silly_1_out_16), .out_17(fun_silly_1_out_17),
    .out_18(fun_silly_1_out_18), .out_19(fun_silly_1_out_19), .out_6(fun_silly_1_out_6),
    .out_20(fun_silly_1_out_20), .out_21(fun_silly_1_out_21), .out_22(fun_silly_1_out_22),
    .out_23(fun_silly_1_out_23), .out_24(fun_silly_1_out_24), .out_25(fun_silly_1_out_25),
    .out_26(fun_silly_1_out_26), .out_27(fun_silly_1_out_27), .out_28(fun_silly_1_out_28),
    .out_29(fun_silly_1_out_29), .out_7(fun_silly_1_out_7), .out_30(fun_silly_1_out_30),
    .out_31(fun_silly_1_out_31), .out_32(fun_silly_1_out_32), .out_33(fun_silly_1_out_33),
    .out_34(fun_silly_1_out_34), .out_35(fun_silly_1_out_35), .out_36(fun_silly_1_out_36),
    .out_37(fun_silly_1_out_37), .out_38(fun_silly_1_out_38), .out_39(fun_silly_1_out_39),
    .out_8(fun_silly_1_out_8), .out_40(fun_silly_1_out_40), .out_41(fun_silly_1_out_41),
    .out_42(fun_silly_1_out_42), .out_43(fun_silly_1_out_43), .out_44(fun_silly_1_out_44),
    .out_45(fun_silly_1_out_45), .out_46(fun_silly_1_out_46), .out_47(fun_silly_1_out_47),
    .out_48(fun_silly_1_out_48), .out_49(fun_silly_1_out_49), .out_9(fun_silly_1_out_9),
    .out_50(fun_silly_1_out_50), .out_51(fun_silly_1_out_51), .out_52(fun_silly_1_out_52),
    .out_53(fun_silly_1_out_53), .out_54(fun_silly_1_out_54), .out_55(fun_silly_1_out_55),
    .out_56(fun_silly_1_out_56), .out_57(fun_silly_1_out_57), .out_58(fun_silly_1_out_58),
    .out_59(fun_silly_1_out_59));
  fun_silly fun_silly_2 (
    .in_4(or_2_out), .in_5(buffer_8_out), .in_1(and_5_out), .in_2(in_3), .in_3(in_4),
    .out_10(fun_silly_2_out_10), .out_60(fun_silly_2_out_60), .out_61(fun_silly_2_out_61),
    .out_62(fun_silly_2_out_62), .out_63(fun_silly_2_out_63), .out_64(fun_silly_2_out_64),
    .out_65(fun_silly_2_out_65), .out_66(fun_silly_2_out_66), .out_67(fun_silly_2_out_67),
    .out_68(fun_silly_2_out_68), .out_69(fun_silly_2_out_69), .out_11(fun_silly_2_out_11),
    .out_12(fun_silly_2_out_12), .out_13(fun_silly_2_out_13), .out_14(fun_silly_2_out_14),
    .out_15(fun_silly_2_out_15), .out_16(fun_silly_2_out_16), .out_17(fun_silly_2_out_17),
    .out_18(fun_silly_2_out_18), .out_19(fun_silly_2_out_19), .out_6(fun_silly_2_out_6),
    .out_20(fun_silly_2_out_20), .out_21(fun_silly_2_out_21), .out_22(fun_silly_2_out_22),
    .out_23(fun_silly_2_out_23), .out_24(fun_silly_2_out_24), .out_25(fun_silly_2_out_25),
    .out_26(fun_silly_2_out_26), .out_27(fun_silly_2_out_27), .out_28(fun_silly_2_out_28),
    .out_29(fun_silly_2_out_29), .out_7(fun_silly_2_out_7), .out_30(fun_silly_2_out_30),
    .out_31(fun_silly_2_out_31), .out_32(fun_silly_2_out_32), .out_33(fun_silly_2_out_33),
    .out_34(fun_silly_2_out_34), .out_35(fun_silly_2_out_35), .out_36(fun_silly_2_out_36),
    .out_37(fun_silly_2_out_37), .out_38(fun_silly_2_out_38), .out_39(fun_silly_2_out_39),
    .out_8(fun_silly_2_out_8), .out_40(fun_silly_2_out_40), .out_41(fun_silly_2_out_41),
    .out_42(fun_silly_2_out_42), .out_43(fun_silly_2_out_43), .out_44(fun_silly_2_out_44),
    .out_45(fun_silly_2_out_45), .out_46(fun_silly_2_out_46), .out_47(fun_silly_2_out_47),
    .out_48(fun_silly_2_out_48), .out_49(fun_silly_2_out_49), .out_9(fun_silly_2_out_9),
    .out_50(fun_silly_2_out_50), .out_51(fun_silly_2_out_51), .out_52(fun_silly_2_out_52),
    .out_53(fun_silly_2_out_53), .out_54(fun_silly_2_out_54), .out_55(fun_silly_2_out_55),
    .out_56(fun_silly_2_out_56), .out_57(fun_silly_2_out_57), .out_58(fun_silly_2_out_58),
    .out_59(fun_silly_2_out_59));
  Multiplexer #(.width(32)) multiplexer_1 (.in0(fun_silly_1_out_6), .in1(fun_silly_2_out_6), .out(out_7));  // open: sel
  Multiplexer #(.width(32)) multiplexer_2 (.in0(fun_silly_1_out_7), .in1(fun_silly_2_out_7), .out(out_8));  // open: sel
  Multiplexer #(.width(32)) multiplexer_3 (.in0(fun_silly_1_out_8), .in1(fun_silly_2_out_8), .out(out_9));  // open: sel
  Multiplexer #(.width(32)) multiplexer_4 (
    .in0(fun_silly_1_out_9), .in1(fun_silly_2_out_9), .out(out_10));  // open: sel
  Multiplexer #(.width(32)) multiplexer_5 (
    .in0(fun_silly_1_out_10), .in1(fun_silly_2_out_10), .out(out_11));  // open: sel
  Multiplexer #(.width(32)) multiplexer_6 (
    .in0(fun_silly_1_out_11), .in1(fun_silly_2_out_11), .out(out_12));  // open: sel
  Multiplexer #(.width(32)) multiplexer_7 (
    .in0(fun_silly_1_out_12), .in1(fun_silly_2_out_12), .out(out_13));  // open: sel
  Multiplexer #(.width(32)) multiplexer_8 (
    .in0(fun_silly_1_out_13), .in1(fun_silly_2_out_13), .out(out_14));  // open: sel
  Multiplexer #(.width(32)) multiplexer_9 (
    .in0(fun_silly_1_out_14), .in1(fun_silly_2_out_14), .out(out_15));  // open: sel
  Multiplexer #(.width(32)) multiplexer_10 (
    .in0(fun_silly_1_out_15), .in1(fun_silly_2_out_15), .out(out_16));  // open: sel
  Multiplexer #(.width(32)) multiplexer_11 (
    .in0(fun_silly_1_out_16), .in1(fun_silly_2_out_16), .out(out_17));  // open: sel
  Multiplexer #(.width(32)) multiplexer_12 (
    .in0(fun_silly_1_out_17), .in1(fun_silly_2_out_17), .out(out_18));  // open: sel
  Multiplexer #(.width(32)) multiplexer_13 (
    .in0(fun_silly_1_out_18), .in1(fun_silly_2_out_18), .out(out_19));  // open: sel
  Multiplexer #(.width(32)) multiplexer_14 (
    .in0(fun_silly_1_out_19), .in1(fun_silly_2_out_19), .out(out_20));  // open: sel
  Multiplexer #(.width(32)) multiplexer_15 (
    .in0(fun_silly_1_out_20), .in1(fun_silly_2_out_20), .out(out_21));  // open: sel
  Multiplexer #(.width(32)) multiplexer_16 (
    .in0(fun_silly_1_out_21), .in1(fun_silly_2_out_21), .out(out_22));  // open: sel
  Multiplexer #(.width(32)) multiplexer_17 (
    .in0(fun_silly_1_out_22), .in1(fun_silly_2_out_22), .out(out_23));  // open: sel
  Multiplexer #(.width(32)) multiplexer_18 (
    .in0(fun_silly_1_out_23), .in1(fun_silly_2_out_23), .out(out_24));  // open: sel
  Multiplexer #(.width(32)) multiplexer_19 (
    .in0(fun_silly_1_out_24), .in1(fun_silly_2_out_24), .out(out_25));  // open: sel
  Multiplexer #(.width(32)) multiplexer_20 (
    .in0(fun_silly_1_out_25), .in1(fun_silly_2_out_25), .out(out_26));  // open: sel
  Multiplexer #(.width(32)) multiplexer_21 (
    .in0(fun_silly_1_out_26), .in1(fun_silly_2_out_26), .out(out_27));  // open: sel
  Multiplexer #(.width(32)) multiplexer_22 (
    .in0(fun_silly_1_out_27), .in1(fun_silly_2_out_27), .out(out_28));  // open: sel
  Multiplexer #(.width(32)) multiplexer_23 (
    .in0(fun_silly_1_out_28), .in1(fun_silly_2_out_28), .out(out_29));  // open: sel
  Multiplexer #(.width(32)) multiplexer_24 (
    .in0(fun_silly_1_out_29), .in1(fun_silly_2_out_29), .out(out_30));  // open: sel
  Multiplexer #(.width(32)) multiplexer_25 (
    .in0(fun_silly_1_out_30), .in1(fun_silly_2_out_30), .out(out_31));  // open: sel
  Multiplexer #(.width(32)) multiplexer_26 (
    .in0(fun_silly_1_out_31), .in1(fun_silly_2_out_31), .out(out_32));  // open: sel
  Multiplexer #(.width(32)) multiplexer_27 (
    .in0(fun_silly_1_out_32), .in1(fun_silly_2_out_32), .out(out_33));  // open: sel
  Multiplexer #(.width(32)) multiplexer_28 (
    .in0(fun_silly_1_out_33), .in1(fun_silly_2_out_33), .out(out_34));  // open: sel
  Multiplexer #(.width(32)) multiplexer_29 (
    .in0(fun_silly_1_out_34), .in1(fun_silly_2_out_34), .out(out_35));  // open: sel
  Multiplexer #(.width(32)) multiplexer_30 (
    .in0(fun_silly_1_out_35), .in1(fun_silly_2_out_35), .out(out_36));  // open: sel
  Multiplexer #(.width(32)) multiplexer_31 (
    .in0(fun_silly_1_out_36), .in1(fun_silly_2_out_36), .out(out_37));  // open: sel
  Multiplexer #(.width(32)) multiplexer_32 (
    .in0(fun_silly_1_out_37), .in1(fun_silly_2_out_37), .out(out_38));  // open: sel
  Multiplexer #(.width(32)) multiplexer_33 (
    .in0(fun_silly_1_out_38), .in1(fun_silly_2_out_38), .out(out_39));  // open: sel
  Multiplexer #(.width(32)) multiplexer_34 (
    .in0(fun_silly_1_out_39), .in1(fun_silly_2_out_39), .out(out_40));  // open: sel
  Multiplexer #(.width(32)) multiplexer_35 (
    .in0(fun_silly_1_out_40), .in1(fun_silly_2_out_40), .out(out_41));  // open: sel
  Multiplexer #(.width(32)) multiplexer_36 (
    .in0(fun_silly_1_out_41), .in1(fun_silly_2_out_41), .out(out_42));  // open: sel
  Multiplexer #(.width(32)) multiplexer_37 (
    .in0(fun_silly_1_out_42), .in1(fun_silly_2_out_42), .out(out_43));  // open: sel
  Multiplexer #(.width(32)) multiplexer_38 (
    .in0(fun_silly_1_out_43), .in1(fun_silly_2_out_43), .out(out_44));  // open: sel
  Multiplexer #(.width(32)) multiplexer_39 (
    .in0(fun_silly_1_out_44), .in1(fun_silly_2_out_44), .out(out_45));  // open: sel
  Multiplexer #(.width(32)) multiplexer_40 (
    .in0(fun_silly_1_out_45), .in1(fun_silly_2_out_45), .out(out_46));  // open: sel
  Multiplexer #(.width(32)) multiplexer_41 (
    .in0(fun_silly_1_out_46), .in1(fun_silly_2_out_46), .out(out_47));  // open: sel
  Multiplexer #(.width(32)) multiplexer_42 (
    .in0(fun_silly_1_out_47), .in1(fun_silly_2_out_47), .out(out_48));  // open: sel
  Multiplexer #(.width(32)) multiplexer_43 (
    .in0(fun_silly_1_out_48), .in1(fun_silly_2_out_48), .out(out_49));  // open: sel
  Multiplexer #(.width(32)) multiplexer_44 (
    .in0(fun_silly_1_out_49), .in1(fun_silly_2_out_49), .out(out_50));  // open: sel
  Multiplexer #(.width(32)) multiplexer_45 (
    .in0(fun_silly_1_out_50), .in1(fun_silly_2_out_50), .out(out_51));  // open: sel
  Multiplexer #(.width(32)) multiplexer_46 (
    .in0(fun_silly_1_out_51), .in1(fun_silly_2_out_51), .out(out_52));  // open: sel
  Multiplexer #(.width(32)) multiplexer_47 (
    .in0(fun_silly_1_out_52), .in1(fun_silly_2_out_52), .out(out_53));  // open: sel
  Multiplexer #(.width(32)) multiplexer_48 (
    .in0(fun_silly_1_out_53), .in1(fun_silly_2_out_53), .out(out_54));  // open: sel
  Multiplexer #(.width(32)) multiplexer_49 (
    .in0(fun_silly_1_out_54), .in1(fun_silly_2_out_54), .out(out_55));  // open: sel
  Multiplexer #(.width(32)) multiplexer_50 (
    .in0(fun_silly_1_out_55), .in1(fun_silly_2_out_55), .out(out_56));  // open: sel
  Multiplexer #(.width(32)) multiplexer_51 (
    .in0(fun_silly_1_out_56), .in1(fun_silly_2_out_56), .out(out_57));  // open: sel
  Multiplexer #(.width(32)) multiplexer_52 (
    .in0(fun_silly_1_out_57), .in1(fun_silly_2_out_57), .out(out_58));  // open: sel
  Multiplexer #(.width(32)) multiplexer_53 (
    .in0(fun_silly_1_out_58), .in1(fun_silly_2_out_58), .out(out_59));  // open: sel
  Multiplexer #(.width(32)) multiplexer_54 (
    .in0(fun_silly_1_out_59), .in1(fun_silly_2_out_59), .out(out_60));  // open: sel
  Multiplexer #(.width(32)) multiplexer_55 (
    .in0(fun_silly_1_out_60), .in1(fun_silly_2_out_60), .out(out_61));  // open: sel
  Multiplexer #(.width(32)) multiplexer_56 (
    .in0(fun_silly_1_out_61), .in1(fun_silly_2_out_61), .out(out_62));  // open: sel
  Multiplexer #(.width(32)) multiplexer_57 (
    .in0(fun_silly_1_out_62), .in1(fun_silly_2_out_62), .out(out_63));  // open: sel
  Multiplexer #(.width(32)) multiplexer_58 (
    .in0(fun_silly_1_out_63), .in1(fun_silly_2_out_63), .out(out_64));  // open: sel
  Multiplexer #(.width(32)) multiplexer_59 (
    .in0(fun_silly_1_out_64), .in1(fun_silly_2_out_64), .out(out_65));  // open: sel
  Multiplexer #(.width(32)) multiplexer_60 (
    .in0(fun_silly_1_out_65), .in1(fun_silly_2_out_65), .out(out_66));  // open: sel
  Multiplexer #(.width(32)) multiplexer_61 (
    .in0(fun_silly_1_out_66), .in1(fun_silly_2_out_66), .out(out_67));  // open: sel
  Multiplexer #(.width(32)) multiplexer_62 (
    .in0(fun_silly_1_out_67), .in1(fun_silly_2_out_67), .out(out_68));  // open: sel
  Multiplexer #(.width(32)) multiplexer_63 (
    .in0(fun_silly_1_out_68), .in1(fun_silly_2_out_68), .out(out_69));  // open: sel
  Multiplexer #(.width(32)) multiplexer_64 (
    .in0(fun_silly_1_out_69), .in1(fun_silly_2_out_69), .out(out_70));  // open: sel
endmodule

module keyboard_receiver (
  input  [6:0] in_1,
  input  Thanks,
  input  Incoming,
  input  Clock,
  input  Reset,
  output [15:0] out_6
);

  wire and_1_out, and_2_out, and_3_out, cpg_1_out_6, or_1_out;
  wire [6:0] multiplexer_1_out, multiplexer_2_out, multiplexer_3_out, multiplexer_4_out, multiplexer_5_out,
       multiplexer_6_out, multiplexer_7_out, multiplexer_8_out, multiplexer_9_out, multiplexer_10_out,
       multiplexer_11_out, multiplexer_12_out, multiplexer_13_out, multiplexer_14_out, multiplexer_15_out,
       multiplexer_16_out, register_2_q, register_3_q, register_4_q, register_5_q, register_6_q,
       register_7_q, register_8_q, register_9_q, register_10_q, register_11_q, register_12_q, register_13_q,
       register_14_q, register_15_q, register_16_q;

  or or_1 (or_1_out, Incoming, Thanks);
  and and_1 (and_1_out, Thanks, ~Incoming);  // AND_Gate
  and and_2 (and_2_out, or_1_out, ~Thanks);  // AND_Gate
  and and_3 (and_3_out, ~Incoming, and_1_out);  // AND_Gate
  Register #(.width(7)) register_1 (
    .D(multiplexer_1_out), .en(or_1_out), .clk(cpg_1_out_6), .Q(out_6[6:0]), .clr(Reset));
  Multiplexer #(.width(7)) multiplexer_1 (.in0(register_2_q), .in1(in_1), .out(multiplexer_1_out));  // open: sel
  CPG cpg_1 (.in_1(and_2_out), .in_2(and_3_out), .in_5(Clock), .out_6(cpg_1_out_6));  // open: in_3, in_4
  // Probe on out_6[6:0]
  Multiplexer #(.width(7)) multiplexer_2 (.in0(register_3_q), .in1(out_6[6:0]), .out(multiplexer_2_out));  // open: sel
  Register #(.width(7)) register_2 (
    .D(multiplexer_2_out), .en(or_1_out), .clk(cpg_1_out_6), .Q(register_2_q), .clr(Reset));
  // Probe on register_2_q
  Register #(.width(7)) register_3 (
    .D(multiplexer_3_out), .en(or_1_out), .clk(cpg_1_out_6), .Q(register_3_q), .clr(Reset));
  Multiplexer #(.width(7)) multiplexer_3 (
    .in0(register_4_q), .in1(register_2_q), .out(multiplexer_3_out));  // open: sel
  T_Flip_Flop t_ff_1 (.T(1'b1), .clk(cpg_1_out_6));  // open: Q, Qn, reset, preset
  // Probe on register_3_q
  Multiplexer #(.width(7)) multiplexer_4 (
    .in0(register_5_q), .in1(register_3_q), .out(multiplexer_4_out));  // open: sel
  Register #(.width(7)) register_4 (
    .D(multiplexer_4_out), .en(or_1_out), .clk(cpg_1_out_6), .Q(register_4_q), .clr(Reset));
  // Probe on register_4_q
  Register #(.width(7)) register_5 (
    .D(multiplexer_5_out), .en(or_1_out), .clk(cpg_1_out_6), .Q(register_5_q), .clr(Reset));
  Multiplexer #(.width(7)) multiplexer_5 (
    .in0(register_6_q), .in1(register_4_q), .out(multiplexer_5_out));  // open: sel
  // Probe on register_5_q
  Multiplexer #(.width(7)) multiplexer_6 (
    .in0(register_7_q), .in1(register_5_q), .out(multiplexer_6_out));  // open: sel
  Register #(.width(7)) register_6 (
    .D(multiplexer_6_out), .en(or_1_out), .clk(cpg_1_out_6), .Q(register_6_q), .clr(Reset));
  // Probe on register_6_q
  Register #(.width(7)) register_7 (
    .D(multiplexer_7_out), .en(or_1_out), .clk(cpg_1_out_6), .Q(register_7_q), .clr(Reset));
  Multiplexer #(.width(7)) multiplexer_7 (
    .in0(register_8_q), .in1(register_6_q), .out(multiplexer_7_out));  // open: sel
  // Probe on register_7_q
  Multiplexer #(.width(7)) multiplexer_8 (
    .in0(register_9_q), .in1(register_7_q), .out(multiplexer_8_out));  // open: sel
  Register #(.width(7)) register_8 (
    .D(multiplexer_8_out), .en(or_1_out), .clk(cpg_1_out_6), .Q(register_8_q), .clr(Reset));
  // Probe on register_8_q
  Register #(.width(7)) register_9 (
    .D(multiplexer_9_out), .en(or_1_out), .clk(cpg_1_out_6), .Q(register_9_q), .clr(Reset));
  Multiplexer #(.width(7)) multiplexer_9 (
    .in0(register_10_q), .in1(register_8_q), .out(multiplexer_9_out));  // open: sel
  // Probe on register_9_q
  Multiplexer #(.width(7)) multiplexer_10 (
    .in0(register_11_q), .in1(register_9_q), .out(multiplexer_10_out));  // open: sel
  Register #(.width(7)) register_10 (
    .D(multiplexer_10_out), .en(or_1_out), .clk(cpg_1_out_6), .Q(register_10_q), .clr(Reset));
  Register #(.width(7)) register_11 (
    .D(multiplexer_11_out), .en(or_1_out), .clk(cpg_1_out_6), .Q(register_11_q), .clr(Reset));
  Multiplexer #(.width(7)) multiplexer_11 (
    .in0(register_12_q), .in1(register_10_q), .out(multiplexer_11_out));  // open: sel
  Multiplexer #(.width(7)) multiplexer_12 (
    .in0(register_13_q), .in1(register_11_q), .out(multiplexer_12_out));  // open: sel
  Register #(.width(7)) register_12 (
    .D(multiplexer_12_out), .en(or_1_out), .clk(cpg_1_out_6), .Q(register_12_q), .clr(Reset));
  Register #(.width(7)) register_13 (
    .D(multiplexer_13_out), .en(or_1_out), .clk(cpg_1_out_6), .Q(register_13_q), .clr(Reset));
  Multiplexer #(.width(7)) multiplexer_13 (
    .in0(register_14_q), .in1(register_12_q), .out(multiplexer_13_out));  // open: sel
  Multiplexer #(.width(7)) multiplexer_14 (
    .in0(register_15_q), .in1(register_13_q), .out(multiplexer_14_out));  // open: sel
  Register #(.width(7)) register_14 (
    .D(multiplexer_14_out), .en(or_1_out), .clk(cpg_1_out_6), .Q(register_14_q), .clr(Reset));
  Register #(.width(7)) register_15 (
    .D(multiplexer_15_out), .en(or_1_out), .clk(cpg_1_out_6), .Q(register_15_q), .clr(Reset));
  Multiplexer #(.width(7)) multiplexer_15 (
    .in0(register_16_q), .in1(register_14_q), .out(multiplexer_15_out));  // open: sel
  Multiplexer #(.width(7)) multiplexer_16 (
    .in0({7{1'b0}}), .in1(register_15_q), .out(multiplexer_16_out));  // open: sel
  Register #(.width(7)) register_16 (
    .D(multiplexer_16_out), .en(or_1_out), .clk(cpg_1_out_6), .Q(register_16_q), .clr(Reset));

  assign out_6[15:7] = {9{1'b0}};
endmodule

module CPG (
  input  in_1,
  input  in_2,
  input  in_3,
  input  in_4,
  input  in_5,
  output out_6
);

  wire and_1_out, and_2_out, and_3_out, and_4_out, and_5_out, and_6_out, d_ff_1_q, d_ff_2_q, or_1_out,
       or_2_out;

  D_Flip_Flop d_ff_1 (.D(1'b1), .clk(in_5), .Q(d_ff_1_q), .reset(d_ff_1_q));  // open: Qn, preset
  D_Flip_Flop #(.trigger("falling")) d_ff_2 (.D(1'b1), .clk(in_5), .Q(d_ff_2_q), .reset(d_ff_2_q));  // open: Qn, preset
  and and_1 (and_1_out, d_ff_1_q, in_5);
  and and_2 (and_2_out, ~in_5, d_ff_2_q);  // AND_Gate
  and and_3 (and_3_out, in_3, in_5);
  and and_4 (and_4_out, ~in_5, in_4);  // AND_Gate
  and and_5 (and_5_out, in_1, and_1_out);
  and and_6 (and_6_out, in_2, and_2_out);
  or or_1 (or_1_out, and_3_out, and_4_out);
  or or_2 (or_2_out, and_5_out, and_6_out);
  or or_3 (out_6, or_1_out, or_2_out);
endmodule

module CE_DFF (
  input  in_1,
  input  in_2,
  input  in_3,
  input  in_4,
  input  in_5,
  input  in_6,
  output out_7
);

  wire and_1_out, and_2_out, and_3_out, and_4_out, d_ff_1_q, d_ff_2_q, or_1_out;

  D_Flip_Flop d_ff_1 (.D(1'b1), .clk(in_6), .Q(d_ff_1_q), .reset(d_ff_1_q));  // open: Qn, preset
  D_Flip_Flop #(.trigger("falling")) d_ff_2 (.D(1'b1), .clk(in_6), .Q(d_ff_2_q), .reset(d_ff_2_q));  // open: Qn, preset
  and and_1 (and_1_out, in_4, in_6);
  and and_2 (and_2_out, in_5, ~in_6);  // AND_Gate
  and and_3 (and_3_out, d_ff_1_q, in_2, in_6);
  and and_4 (and_4_out, ~in_6, in_3, d_ff_2_q);  // AND_Gate
  D_Flip_Flop #(.trigger("high")) d_ff_3 (.D(in_1), .clk(or_1_out), .Q(out_7));  // open: Qn, preset, reset
  or or_1 (or_1_out, and_1_out, and_2_out, and_3_out, and_4_out);
endmodule

module edger (
  input  in_1,
  output out_2
);

  wire d_ff_1_q, d_ff_2_q;

  D_Flip_Flop d_ff_1 (.D(1'b1), .clk(in_1), .Q(d_ff_1_q), .reset(d_ff_1_q));  // open: Qn, preset
  D_Flip_Flop #(.trigger("falling")) d_ff_2 (.D(1'b1), .clk(in_1), .Q(d_ff_2_q), .reset(d_ff_2_q));  // open: Qn, preset
  or or_1 (out_2, d_ff_1_q, d_ff_2_q);
endmodule

module playing (
);

  wire button_1_out, button_2_out, clock_1_out, keyboard_1_avail;
  wire [6:0] keyboard_1_data;
  wire [15:0] keyboard_receiver_1_out_6;

  Clock clock_1 (.out(clock_1_out));
  TTY tty_1 (.data(keyboard_receiver_1_out_6[6:0]), .clk(clock_1_out), .we(button_1_out));  // open: clr
  Keyboard keyboard_1 (.clk(clock_1_out), .avail(keyboard_1_avail), .data(keyboard_1_data));  // open: re, clr
  Button button_1 (.out(button_1_out));
  Button button_2 (.out(button_2_out));
  keyboard_receiver keyboard_receiver_1 (
    .Thanks(button_1_out), .Incoming(keyboard_1_avail), .Clock(clock_1_out), .Reset(button_2_out),
    .in_1(keyboard_1_data), .out_6(keyboard_receiver_1_out_6));
endmodule

module ports (
  input  [15:0] in_1,
  input  [31:0] in_2,
  input  [31:0] in_3,
  input  in_4,
  input  [15:0] in_5,
  input  [15:0] in_6,
  input  [15:0] in_7,
  input  [15:0] in_8,
  input  in_9,
  input  in_10,
  input  in_11,
  input  in_12,
  output [15:0] out_13,
  output out_14,
  output out_15,
  output out_16,
  output out_17,
  output [15:0] out_18,
  output [15:0] out_19,
  output [15:0] out_20,
  output [15:0] out_21
);

  wire and_1_out, and_2_out, and_3_out, and_4_out, and_5_out, and_6_out, and_7_out, and_8_out, and_9_out,
       and_10_out, and_11_out, and_12_out, and_13_out, and_14_out, and_15_out, and_16_out, and_17_out,
       and_18_out, and_19_out, and_20_out, and_21_out, and_22_out, and_23_out, and_24_out, buffer_1_out,
       buffer_2_out, buffer_3_out, buffer_4_out, buffer_5_out, buffer_6_out, buffer_7_out, buffer_8_out,
       buffer_9_out, buffer_10_out, buffer_11_out, buffer_12_out, buffer_13_out, buffer_14_out,
       buffer_15_out, buffer_16_out, buffer_17_out, buffer_18_out, buffer_19_out, buffer_20_out,
       buffer_21_out, buffer_22_out, buffer_23_out, buffer_24_out, buffer_25_out, buffer_26_out,
       buffer_27_out, or_4_out, sixt_bit_eq_cmp_1_out_3, sixt_bit_eq_cmp_2_out_3, sixt_bit_eq_cmp_3_out_3,
       sixt_bit_eq_cmp_4_out_3, sixt_bit_eq_cmp_5_out_3, sixt_bit_eq_cmp_6_out_3, sixt_bit_eq_zero_1_out_2,
       sixt_bit_eq_zero_2_out_2, sixt_bit_eq_zero_3_out_2, sixt_bit_eq_zero_4_out_2,
       sixt_bit_eq_zero_5_out_2, sixt_bit_eq_zero_6_out_2, sixt_bit_eq_zero_7_out_2, sixt_bit_eq_zero_8_out_2;
  wire [3:0] or_8_out;
  wire [15:0] or_10_out, or_11_out, or_12_out, sixt_bit_decrementer_1_out_2, sixt_bit_decrementer_2_out_2,
       sixt_bit_decrementer_3_out_2, sixt_bit_decrementer_5_out_2, sixt_bit_decrementer_6_out_2,
       sixt_bit_decrementer_7_out_2, sixt_bit_decrementer_8_out_2, sticky_gate_1_p4, sticky_gate_2_p4,
       sticky_gate_3_p4, sticky_gate_4_p4, sticky_gate_5_p4, sticky_gate_6_p4;

  and and_1 (and_1_out, or_4_out, sixt_bit_eq_cmp_4_out_3, in_3[3]);
  and and_2 (and_2_out, or_4_out, sixt_bit_eq_cmp_2_out_3, sixt_bit_eq_zero_1_out_2);
  or or_1 (out_14, and_1_out, and_2_out);
  sixt_bit_decrementer sixt_bit_decrementer_1 (.in_1(in_3[15:0]), .out_2(sixt_bit_decrementer_1_out_2));
  sixt_bit_eq_zero sixt_bit_eq_zero_1 (.in_1(in_3[15:0]), .out_2(sixt_bit_eq_zero_1_out_2));
  or or_2 (or_8_out[3], and_5_out, and_3_out);
  and and_3 (and_3_out, sixt_bit_eq_cmp_1_out_3, sixt_bit_eq_zero_1_out_2);
  and and_4 (and_4_out, or_4_out, sixt_bit_eq_cmp_4_out_3, in_3[2]);
  and and_5 (and_5_out, in_3[3], sixt_bit_eq_cmp_3_out_3, in_9);
  or or_3 (out_15, and_4_out, and_8_out);
  sixt_bit_decrementer sixt_bit_decrementer_2 (
    .in_1(sixt_bit_decrementer_1_out_2), .out_2(sixt_bit_decrementer_2_out_2));
  sixt_bit_eq_zero sixt_bit_eq_zero_2 (.in_1(sixt_bit_decrementer_1_out_2), .out_2(sixt_bit_eq_zero_2_out_2));
  or or_4 (or_4_out, in_2[15], in_2[14], in_2[13], in_2[12], in_2[11], in_2[10], in_2[9], in_2[8], in_2[7], in_2[6], in_2[5], in_2[4], in_2[3], in_2[2], in_2[1], in_2[0]);
  or or_5 (or_8_out[2], and_7_out, and_6_out);
  and and_6 (and_6_out, sixt_bit_eq_cmp_1_out_3, sixt_bit_eq_zero_2_out_2);
  and and_7 (and_7_out, in_3[2], sixt_bit_eq_cmp_3_out_3, in_10);
  and and_8 (and_8_out, or_4_out, sixt_bit_eq_cmp_2_out_3, sixt_bit_eq_zero_2_out_2);
  sixt_bit_decrementer sixt_bit_decrementer_3 (
    .in_1(sixt_bit_decrementer_2_out_2), .out_2(sixt_bit_decrementer_3_out_2));
  sixt_bit_eq_zero sixt_bit_eq_zero_3 (.in_1(sixt_bit_decrementer_2_out_2), .out_2(sixt_bit_eq_zero_3_out_2));
  or or_6 (or_8_out[1], and_11_out, and_9_out);
  and and_9 (and_9_out, sixt_bit_eq_cmp_1_out_3, sixt_bit_eq_zero_3_out_2);
  and and_10 (and_10_out, or_4_out, sixt_bit_eq_cmp_4_out_3, in_3[1]);
  and and_11 (and_11_out, in_3[1], sixt_bit_eq_cmp_3_out_3, in_11);
  and and_12 (and_12_out, or_4_out, sixt_bit_eq_cmp_2_out_3, sixt_bit_eq_zero_3_out_2);
  or or_7 (out_16, and_10_out, and_12_out);
  or or_8 (or_8_out[0], and_15_out, and_13_out);
  and and_13 (and_13_out, sixt_bit_eq_cmp_1_out_3, sixt_bit_eq_zero_4_out_2);
  and and_14 (and_14_out, or_4_out, sixt_bit_eq_cmp_4_out_3, in_3[0]);
  and and_15 (and_15_out, in_3[0], sixt_bit_eq_cmp_3_out_3, in_12);
  and and_16 (and_16_out, or_4_out, sixt_bit_eq_cmp_2_out_3, sixt_bit_eq_zero_4_out_2);
  or or_9 (out_17, and_14_out, and_16_out);
  sixt_bit_decrementer sixt_bit_decrementer_4 (.in_1(sixt_bit_decrementer_3_out_2));  // open: out_2
  sixt_bit_eq_zero sixt_bit_eq_zero_4 (.in_1(sixt_bit_decrementer_3_out_2), .out_2(sixt_bit_eq_zero_4_out_2));
  sixt_bit_eq_cmp sixt_bit_eq_cmp_1 (.in_1(in_1), .in_2(16'ha0), .out_3(sixt_bit_eq_cmp_1_out_3));
  sixt_bit_eq_cmp sixt_bit_eq_cmp_2 (.in_1(in_1), .in_2(16'ha1), .out_3(sixt_bit_eq_cmp_2_out_3));
  sixt_bit_eq_cmp sixt_bit_eq_cmp_3 (.in_1(in_1), .in_2(16'ha2), .out_3(sixt_bit_eq_cmp_3_out_3));
  sixt_bit_eq_cmp sixt_bit_eq_cmp_4 (.in_1(in_1), .in_2(16'ha3), .out_3(sixt_bit_eq_cmp_4_out_3));
  sixt_bit_eq_cmp sixt_bit_eq_cmp_5 (.in_1(in_1), .in_2(16'ha4), .out_3(sixt_bit_eq_cmp_5_out_3));
  sixt_bit_eq_cmp sixt_bit_eq_cmp_6 (.in_1(in_1), .in_2(16'ha5), .out_3(sixt_bit_eq_cmp_6_out_3));
  buf buffer_1 (buffer_1_out, buffer_8_out);
  buf buffer_2 (buffer_2_out, buffer_13_out);
  buf buffer_3 (buffer_3_out, buffer_18_out);
  buf buffer_4 (buffer_4_out, buffer_23_out);
  sixt_bit_eq_zero sixt_bit_eq_zero_5 (.in_1(in_3[15:0]), .out_2(sixt_bit_eq_zero_5_out_2));
  sixt_bit_decrementer sixt_bit_decrementer_5 (.in_1(in_3[15:0]), .out_2(sixt_bit_decrementer_5_out_2));
  buf buffer_5 (buffer_5_out, in_4);
  buf buffer_6 (buffer_6_out, buffer_5_out);
  buf buffer_7 (buffer_7_out, buffer_6_out);
  buf buffer_8 (buffer_8_out, buffer_9_out);
  buf buffer_9 (buffer_9_out, buffer_7_out);
  buf buffer_10 (buffer_10_out, buffer_1_out);
  buf buffer_11 (buffer_11_out, buffer_10_out);
  buf buffer_12 (buffer_12_out, buffer_11_out);
  buf buffer_13 (buffer_13_out, buffer_14_out);
  buf buffer_14 (buffer_14_out, buffer_12_out);
  buf buffer_15 (buffer_15_out, buffer_2_out);
  buf buffer_16 (buffer_16_out, buffer_15_out);
  buf buffer_17 (buffer_17_out, buffer_16_out);
  buf buffer_18 (buffer_18_out, buffer_19_out);
  buf buffer_19 (buffer_19_out, buffer_17_out);
  buf buffer_20 (buffer_20_out, buffer_3_out);
  buf buffer_21 (buffer_21_out, buffer_20_out);
  buf buffer_22 (buffer_22_out, buffer_21_out);
  buf buffer_23 (buffer_23_out, buffer_24_out);
  buf buffer_24 (buffer_24_out, buffer_22_out);
  buf buffer_25 (buffer_25_out, buffer_4_out);
  buf buffer_26 (buffer_26_out, buffer_25_out);
  buf buffer_27 (buffer_27_out, buffer_26_out);
  // sticky_gate sticky_gate_1: pin names not known; wires that end beside it: {{12{1'b0}}, or_8_out}, sixt_bit_eq_cmp_3_out_3, in_4, sticky_gate_1_p4
  // sticky_gate sticky_gate_2: pin names not known; wires that end beside it: {{12{1'b0}}, or_8_out}, sixt_bit_eq_cmp_1_out_3, in_4, sticky_gate_2_p4
  and and_17 (and_17_out, sixt_bit_eq_cmp_5_out_3, sixt_bit_eq_zero_5_out_2);
  and and_18 (and_18_out, sixt_bit_eq_cmp_6_out_3, sixt_bit_eq_zero_5_out_2);
  assign or_10_out = sticky_gate_2_p4 | sticky_gate_1_p4 | sticky_gate_3_p4;  // OR_Gate or_10, 16 bits wide
  // sticky_gate sticky_gate_3: pin names not known; wires that end beside it: in_5, and_17_out, in_4, sticky_gate_3_p4
  sixt_bit_eq_zero sixt_bit_eq_zero_6 (.in_1(sixt_bit_decrementer_5_out_2), .out_2(sixt_bit_eq_zero_6_out_2));
  sixt_bit_decrementer sixt_bit_decrementer_6 (
    .in_1(sixt_bit_decrementer_5_out_2), .out_2(sixt_bit_decrementer_6_out_2));
  Register #(.width(16)) register_1 (.D(in_2[15:0]), .en(and_18_out), .clk(buffer_27_out), .Q(out_18));  // open: clr
  and and_19 (and_19_out, sixt_bit_eq_cmp_5_out_3, sixt_bit_eq_zero_6_out_2);
  and and_20 (and_20_out, sixt_bit_eq_cmp_6_out_3, sixt_bit_eq_zero_6_out_2);
  assign or_11_out = or_10_out | sticky_gate_4_p4;  // OR_Gate or_11, 16 bits wide
  // sticky_gate sticky_gate_4: pin names not known; wires that end beside it: in_6, and_19_out, in_4, sticky_gate_4_p4
  sixt_bit_eq_zero sixt_bit_eq_zero_7 (.in_1(sixt_bit_decrementer_6_out_2), .out_2(sixt_bit_eq_zero_7_out_2));
  sixt_bit_decrementer sixt_bit_decrementer_7 (
    .in_1(sixt_bit_decrementer_6_out_2), .out_2(sixt_bit_decrementer_7_out_2));
  Register #(.width(16)) register_2 (.D(in_2[15:0]), .en(and_20_out), .clk(buffer_27_out), .Q(out_19));  // open: clr
  and and_21 (and_21_out, sixt_bit_eq_cmp_5_out_3, sixt_bit_eq_zero_7_out_2);
  and and_22 (and_22_out, sixt_bit_eq_cmp_6_out_3, sixt_bit_eq_zero_7_out_2);
  assign or_12_out = or_11_out | sticky_gate_5_p4;  // OR_Gate or_12, 16 bits wide
  // sticky_gate sticky_gate_5: pin names not known; wires that end beside it: in_7, and_21_out, in_4, sticky_gate_5_p4
  sixt_bit_eq_zero sixt_bit_eq_zero_8 (.in_1(sixt_bit_decrementer_7_out_2), .out_2(sixt_bit_eq_zero_8_out_2));
  sixt_bit_decrementer sixt_bit_decrementer_8 (
    .in_1(sixt_bit_decrementer_7_out_2), .out_2(sixt_bit_decrementer_8_out_2));
  Register #(.width(16)) register_3 (.D(in_2[15:0]), .en(and_22_out), .clk(buffer_27_out), .Q(out_20));  // open: clr
  and and_23 (and_23_out, sixt_bit_eq_cmp_5_out_3, sixt_bit_eq_zero_8_out_2);
  and and_24 (and_24_out, sixt_bit_eq_cmp_6_out_3, sixt_bit_eq_zero_8_out_2);
  Register #(.width(16)) register_4 (.D(in_2[15:0]), .en(and_24_out), .clk(buffer_27_out), .Q(out_21));  // open: clr
  // Probe on out_13
  assign out_13 = or_12_out | sticky_gate_6_p4;  // OR_Gate or_13, 16 bits wide
  // sticky_gate sticky_gate_6: pin names not known; wires that end beside it: in_8, and_23_out, in_4, sticky_gate_6_p4
  // Pins of 16 and 32 bits meet at in_2
  // Pins of 16 and 32 bits meet at in_3

  // Notes on the sheet:
  //   Control
  //   Data
  //   Address
endmodule

module microcode_address_register (
  input  [15:0] control_bus_in,
  input  [31:0] dbus,
  input  [15:0] instr_decoder,
  input  running_bit,
  input  clock,
  input  restart_instr,
  input  reload_bios,
  output set_run_bit_high,
  output [15:0] mcar_out
);

  wire and_1_out, and_2_out, and_3_out, and_4_out, and_5_out, and_6_out, and_7_out, and_8_out, and_9_out,
       and_10_out, and_11_out, and_12_out, and_13_out, and_14_out, and_15_out, and_16_out, and_17_out,
       and_18_out, and_19_out, and_20_out, and_21_out, and_22_out, and_23_out, and_24_out, and_25_out,
       and_26_out, and_27_out, and_28_out, and_29_out, and_30_out, and_31_out, and_32_out, and_33_out,
       and_34_out, and_35_out, and_36_out, bios_rom_out_out_3, buffer_1_out, buffer_2_out, buffer_3_out,
       buffer_4_out, buffer_5_out, buffer_6_out, buffer_7_out, buffer_8_out, buffer_9_out, buffer_10_out,
       buffer_11_out, buffer_12_out, buffer_13_out, buffer_14_out, buffer_15_out, buffer_16_out,
       buffer_17_out, buffer_18_out, buffer_19_out, buffer_20_out, buffer_21_out, buffer_22_out,
       buffer_23_out, buffer_24_out, buffer_25_out, buffer_26_out, buffer_27_out, buffer_28_out,
       buffer_29_out, finish_instruction_out_3, long_eq_zero_1_out_2, multiplexer_2_out, multiplexer_3_out,
       multiplexer_4_out, multiplexer_5_out, multiplexer_6_out, multiplexer_7_out, multiplexer_8_out,
       multiplexer_9_out, multiplexer_10_out, multiplexer_11_out, multiplexer_12_out, multiplexer_13_out,
       multiplexer_14_out, multiplexer_15_out, multiplexer_16_out, multiplexer_17_out, nor_1_out, not_1_out,
       not_2_out, not_3_out, not_4_out, not_5_out, not_6_out, not_7_out, not_8_out, not_9_out, not_10_out,
       not_11_out, not_12_out, not_13_out, not_14_out, not_15_out, not_16_out, not_17_out, or_1_out,
       or_4_out, or_5_out, or_6_out, or_7_out, start_instruction_out_3;
  wire [1:0] or_3_out;
  wire [7:0] eight_bit_adder_1_out_4, multiplexer_18_out, register_2_q;
  wire [15:0] multiplexer_1_out, register_1_q, sixt_bit_incrementer_1_out_2;

  // Probe on control_bus_in
  or or_1 (or_1_out, running_bit, set_run_bit_high);
  or or_2 (or_3_out[1], reload_bios, restart_instr, or_1_out);
  sixt_bit_eq_cmp start_instruction (.in_1(control_bus_in), .in_2(16'h1), .out_3(start_instruction_out_3));
  Multiplexer #(.select(2), .width(16)) multiplexer_1 (
    .in0({16{1'b0}}), .in1(16'h3), .in2(16'h9), .in3({16{1'b0}}), .out(multiplexer_1_out), .sel(or_3_out));
  or or_3 (or_3_out[0], reload_bios, and_1_out, and_2_out);
  and and_1 (and_1_out, nor_1_out, start_instruction_out_3);
  nor nor_1 (nor_1_out, reload_bios, or_1_out, restart_instr);
  and and_2 (and_2_out, ~or_1_out, finish_instruction_out_3);  // AND_Gate
  Register #(.width(16)) register_1 (
    .D(multiplexer_1_out), .en(1'b1), .clk(buffer_1_out), .Q(register_1_q));  // open: clr
  buf buffer_1 (buffer_1_out, buffer_2_out);
  buf buffer_2 (buffer_2_out, buffer_4_out);
  buf buffer_3 (buffer_3_out, buffer_1_out);
  or or_4 (or_4_out, start_instruction_out_3, finish_instruction_out_3);
  sixt_bit_eq_cmp finish_instruction (.in_1(control_bus_in), .in_2(16'hfffe), .out_3(finish_instruction_out_3));
  buf or_5 (or_5_out, finish_instruction_out_3);  // OR_Gate
  or or_6 (or_6_out, reload_bios, buffer_17_out, restart_instr);
  buf buffer_4 (buffer_4_out, buffer_5_out);
  buf buffer_5 (buffer_5_out, buffer_6_out);
  buf buffer_6 (buffer_6_out, buffer_7_out);
  buf buffer_7 (buffer_7_out, buffer_23_out);
  buf buffer_8 (buffer_8_out, buffer_3_out);
  buf buffer_9 (buffer_9_out, buffer_8_out);
  buf buffer_10 (buffer_10_out, buffer_9_out);
  buf buffer_11 (buffer_11_out, buffer_10_out);
  buf buffer_12 (buffer_12_out, buffer_28_out);
  not not_1 (not_1_out, or_4_out);
  not not_2 (not_2_out, register_1_q[0]);
  Multiplexer multiplexer_2 (
    .in0(instr_decoder[0]), .in1(sixt_bit_incrementer_1_out_2[0]), .out(multiplexer_2_out));  // open: sel
  not not_3 (not_3_out, register_1_q[1]);
  Multiplexer multiplexer_3 (
    .in0(instr_decoder[1]), .in1(sixt_bit_incrementer_1_out_2[1]), .out(multiplexer_3_out));  // open: sel
  not not_4 (not_4_out, register_1_q[2]);
  Multiplexer multiplexer_4 (
    .in0(instr_decoder[2]), .in1(sixt_bit_incrementer_1_out_2[2]), .out(multiplexer_4_out));  // open: sel
  not not_5 (not_5_out, register_1_q[3]);
  Multiplexer multiplexer_5 (
    .in0(instr_decoder[3]), .in1(sixt_bit_incrementer_1_out_2[3]), .out(multiplexer_5_out));  // open: sel
  not not_6 (not_6_out, register_1_q[4]);
  Multiplexer multiplexer_6 (
    .in0(instr_decoder[4]), .in1(sixt_bit_incrementer_1_out_2[4]), .out(multiplexer_6_out));  // open: sel
  not not_7 (not_7_out, register_1_q[5]);
  Multiplexer multiplexer_7 (
    .in0(instr_decoder[5]), .in1(sixt_bit_incrementer_1_out_2[5]), .out(multiplexer_7_out));  // open: sel
  not not_8 (not_8_out, register_1_q[6]);
  Multiplexer multiplexer_8 (
    .in0(instr_decoder[6]), .in1(sixt_bit_incrementer_1_out_2[6]), .out(multiplexer_8_out));  // open: sel
  not not_9 (not_9_out, register_1_q[7]);
  Multiplexer multiplexer_9 (
    .in0(instr_decoder[7]), .in1(sixt_bit_incrementer_1_out_2[7]), .out(multiplexer_9_out));  // open: sel
  not not_10 (not_10_out, register_1_q[8]);
  Multiplexer multiplexer_10 (
    .in0(instr_decoder[8]), .in1(sixt_bit_incrementer_1_out_2[8]), .out(multiplexer_10_out));  // open: sel
  not not_11 (not_11_out, register_1_q[9]);
  Multiplexer multiplexer_11 (
    .in0(instr_decoder[9]), .in1(sixt_bit_incrementer_1_out_2[9]), .out(multiplexer_11_out));  // open: sel
  not not_12 (not_12_out, register_1_q[10]);
  Multiplexer multiplexer_12 (
    .in0(instr_decoder[10]), .in1(sixt_bit_incrementer_1_out_2[10]), .out(multiplexer_12_out));  // open: sel
  not not_13 (not_13_out, register_1_q[11]);
  Multiplexer multiplexer_13 (
    .in0(instr_decoder[11]), .in1(sixt_bit_incrementer_1_out_2[11]), .out(multiplexer_13_out));  // open: sel
  not not_14 (not_14_out, register_1_q[12]);
  Multiplexer multiplexer_14 (
    .in0(instr_decoder[12]), .in1(sixt_bit_incrementer_1_out_2[12]), .out(multiplexer_14_out));  // open: sel
  not not_15 (not_15_out, register_1_q[13]);
  Multiplexer multiplexer_15 (
    .in0(instr_decoder[13]), .in1(sixt_bit_incrementer_1_out_2[13]), .out(multiplexer_15_out));  // open: sel
  not not_16 (not_16_out, register_1_q[14]);
  Multiplexer multiplexer_16 (
    .in0(instr_decoder[14]), .in1(sixt_bit_incrementer_1_out_2[14]), .out(multiplexer_16_out));  // open: sel
  not not_17 (not_17_out, register_1_q[15]);
  Multiplexer multiplexer_17 (
    .in0(instr_decoder[15]), .in1(sixt_bit_incrementer_1_out_2[15]), .out(multiplexer_17_out));  // open: sel
  buf buffer_13 (buffer_13_out, or_5_out);
  buf buffer_14 (buffer_14_out, buffer_13_out);
  buf buffer_15 (buffer_15_out, buffer_14_out);
  buf buffer_16 (buffer_16_out, buffer_15_out);
  buf buffer_17 (buffer_17_out, buffer_18_out);
  buf buffer_18 (buffer_18_out, buffer_19_out);
  buf buffer_19 (buffer_19_out, buffer_16_out);
  buf buffer_20 (buffer_20_out, or_6_out);
  buf buffer_21 (buffer_21_out, buffer_20_out);
  buf buffer_22 (buffer_22_out, buffer_21_out);
  buf buffer_23 (buffer_23_out, buffer_24_out);
  buf buffer_24 (buffer_24_out, buffer_22_out);
  buf buffer_25 (buffer_25_out, buffer_11_out);
  buf buffer_26 (buffer_26_out, buffer_25_out);
  buf buffer_27 (buffer_27_out, buffer_26_out);
  buf buffer_28 (buffer_28_out, buffer_29_out);
  buf buffer_29 (buffer_29_out, buffer_27_out);
  and and_3 (and_3_out, buffer_12_out, register_1_q[0]);
  and and_4 (and_4_out, not_2_out, buffer_12_out);
  and and_5 (and_5_out, buffer_12_out, register_1_q[1]);
  and and_6 (and_6_out, not_3_out, buffer_12_out);
  and and_7 (and_7_out, buffer_12_out, register_1_q[2]);
  and and_8 (and_8_out, not_4_out, buffer_12_out);
  and and_9 (and_9_out, buffer_12_out, register_1_q[3]);
  and and_10 (and_10_out, not_5_out, buffer_12_out);
  and and_11 (and_11_out, buffer_12_out, register_1_q[4]);
  and and_12 (and_12_out, not_6_out, buffer_12_out);
  and and_13 (and_13_out, buffer_12_out, register_1_q[5]);
  and and_14 (and_14_out, not_7_out, buffer_12_out);
  and and_15 (and_15_out, buffer_12_out, register_1_q[6]);
  and and_16 (and_16_out, not_8_out, buffer_12_out);
  and and_17 (and_17_out, buffer_12_out, register_1_q[7]);
  and and_18 (and_18_out, not_9_out, buffer_12_out);
  and and_19 (and_19_out, buffer_12_out, register_1_q[8]);
  and and_20 (and_20_out, not_10_out, buffer_12_out);
  and and_21 (and_21_out, buffer_12_out, register_1_q[9]);
  and and_22 (and_22_out, not_11_out, buffer_12_out);
  and and_23 (and_23_out, buffer_12_out, register_1_q[10]);
  and and_24 (and_24_out, not_12_out, buffer_12_out);
  and and_25 (and_25_out, buffer_12_out, register_1_q[11]);
  and and_26 (and_26_out, not_13_out, buffer_12_out);
  and and_27 (and_27_out, buffer_12_out, register_1_q[12]);
  and and_28 (and_28_out, not_14_out, buffer_12_out);
  and and_29 (and_29_out, buffer_12_out, register_1_q[13]);
  and and_30 (and_30_out, not_15_out, buffer_12_out);
  and and_31 (and_31_out, buffer_12_out, register_1_q[14]);
  and and_32 (and_32_out, not_16_out, buffer_12_out);
  and and_33 (and_33_out, buffer_12_out, register_1_q[15]);
  and and_34 (and_34_out, not_17_out, buffer_12_out);
  long_eq_zero long_eq_zero_1 (.in_1(dbus), .out_2(long_eq_zero_1_out_2));
  D_Flip_Flop d_ff_1 (
    .D(multiplexer_2_out), .clk(clock), .Q(mcar_out[0]), .preset(and_3_out), .reset(and_4_out));  // open: Qn
  D_Flip_Flop d_ff_2 (
    .D(multiplexer_3_out), .clk(clock), .Q(mcar_out[1]), .preset(and_5_out), .reset(and_6_out));  // open: Qn
  D_Flip_Flop d_ff_3 (
    .D(multiplexer_4_out), .clk(clock), .Q(mcar_out[2]), .preset(and_7_out), .reset(and_8_out));  // open: Qn
  D_Flip_Flop d_ff_4 (
    .D(multiplexer_5_out), .clk(clock), .Q(mcar_out[3]), .preset(and_9_out), .reset(and_10_out));  // open: Qn
  D_Flip_Flop d_ff_5 (
    .D(multiplexer_6_out), .clk(clock), .Q(mcar_out[4]), .preset(and_11_out), .reset(and_12_out));  // open: Qn
  D_Flip_Flop d_ff_6 (
    .D(multiplexer_7_out), .clk(clock), .Q(mcar_out[5]), .preset(and_13_out), .reset(and_14_out));  // open: Qn
  D_Flip_Flop d_ff_7 (
    .D(multiplexer_8_out), .clk(clock), .Q(mcar_out[6]), .preset(and_15_out), .reset(and_16_out));  // open: Qn
  D_Flip_Flop d_ff_8 (
    .D(multiplexer_9_out), .clk(clock), .Q(mcar_out[7]), .preset(and_17_out), .reset(and_18_out));  // open: Qn
  D_Flip_Flop d_ff_9 (
    .D(multiplexer_10_out), .clk(clock), .Q(mcar_out[8]), .preset(and_19_out), .reset(and_20_out));  // open: Qn
  D_Flip_Flop d_ff_10 (
    .D(multiplexer_11_out), .clk(clock), .Q(mcar_out[9]), .preset(and_21_out), .reset(and_22_out));  // open: Qn
  D_Flip_Flop d_ff_11 (
    .D(multiplexer_12_out), .clk(clock), .Q(mcar_out[10]), .preset(and_23_out), .reset(and_24_out));  // open: Qn
  D_Flip_Flop d_ff_12 (
    .D(multiplexer_13_out), .clk(clock), .Q(mcar_out[11]), .preset(and_25_out), .reset(and_26_out));  // open: Qn
  D_Flip_Flop d_ff_13 (
    .D(multiplexer_14_out), .clk(clock), .Q(mcar_out[12]), .preset(and_27_out), .reset(and_28_out));  // open: Qn
  D_Flip_Flop d_ff_14 (
    .D(multiplexer_15_out), .clk(clock), .Q(mcar_out[13]), .preset(and_29_out), .reset(and_30_out));  // open: Qn
  D_Flip_Flop d_ff_15 (
    .D(multiplexer_16_out), .clk(clock), .Q(mcar_out[14]), .preset(and_31_out), .reset(and_32_out));  // open: Qn
  D_Flip_Flop d_ff_16 (
    .D(multiplexer_17_out), .clk(clock), .Q(mcar_out[15]), .preset(and_33_out), .reset(and_34_out));  // open: Qn
  sixt_bit_eq_cmp bios_rom_out (.in_1(control_bus_in), .in_2(16'hb0), .out_3(bios_rom_out_out_3));
  and and_35 (and_35_out, long_eq_zero_1_out_2, ~set_run_bit_high);  // AND_Gate
  Multiplexer #(.width(8)) multiplexer_18 (
    .in0({8{1'b0}}), .in1(eight_bit_adder_1_out_4), .out(multiplexer_18_out));  // open: sel
  sixt_bit_incrementer sixt_bit_incrementer_1 (.in_1(mcar_out), .out_2(sixt_bit_incrementer_1_out_2));
  and and_36 (and_36_out, bios_rom_out_out_3, ~running_bit);  // AND_Gate
  Register register_2 (.D(multiplexer_18_out), .en(or_7_out), .clk(clock), .Q(register_2_q));  // open: clr
  buf or_7 (or_7_out, and_36_out);  // OR_Gate
  eight_bit_adder eight_bit_adder_1 (
    .in_2(8'h1), .in_3(register_2_q), .out_4(eight_bit_adder_1_out_4));  // open: in_1, out_5
  eight_bit_eq_cmp eight_bit_eq_cmp_1 (.in_1(register_2_q), .in_2(8'h5), .out_3(set_run_bit_high));

  // Notes on the sheet:
  //   BIOS_load loop
  //   Running loop
  //   BIOS_load start
endmodule

module new_one_ticker (
  input  signal_in,
  input  clock_in,
  input  reset,
  output signal_out
);

  wire and_1_out, not_1_out, or_1_out, s_r_ff_1_q;

  not not_1 (not_1_out, signal_in);
  and and_1 (and_1_out, signal_in, ~s_r_ff_1_q);  // AND_Gate
  D_Flip_Flop d_ff_1 (.D(1'b0), .clk(clock_in), .Q(signal_out), .preset(and_1_out), .reset(reset));  // open: Qn
  S_R_Flip_Flop s_r_ff_1 (.Q(s_r_ff_1_q), .reset(or_1_out), .preset(signal_out));  // open: S, R, clk, Qn
  or or_1 (or_1_out, not_1_out, reset);
endmodule

module better_sticky_gate (
  input  enable,
  input  [31:0] data,
  input  clock,
  input  reset,
  output [31:0] out_put
);

  wire or_1_out, s_r_ff_1_q, s_r_ff_2_q, t_ff_1_q, t_ff_2_q;
  wire [31:0] buffer_1_out, buffer_2_out, buffer_3_out, buffer_4_out, buffer_5_out, buffer_6_out,
       buffer_7_out, buffer_8_out, buffer_9_out, buffer_10_out, buffer_11_out, buffer_12_out, buffer_13_out,
       buffer_14_out, buffer_15_out, gatekeeper_1_out_3, register_1_q;

  S_R_Flip_Flop s_r_ff_1 (.Q(s_r_ff_1_q), .reset(or_1_out), .preset(enable));  // open: S, R, clk, Qn
  S_R_Flip_Flop #(.trigger("falling")) s_r_ff_2 (
    .S(s_r_ff_1_q), .R(1'b0), .clk(enable), .Q(s_r_ff_2_q), .reset(or_1_out));  // open: Qn, preset
  gatekeeper gatekeeper_1 (.in_1(enable), .in_2(data), .out_3(gatekeeper_1_out_3));
  assign buffer_1_out = buffer_6_out;  // Buffer buffer_1, 32 bits wide
  Register #(.trigger("falling"), .width(32)) register_1 (
    .D(data), .en(1'b1), .clk(enable), .Q(register_1_q), .clr(or_1_out));
  T_Flip_Flop #(.trigger("falling")) t_ff_1 (
    .T(s_r_ff_2_q), .clk(clock), .Q(t_ff_1_q), .reset(or_1_out));  // open: Qn, preset
  or or_1 (or_1_out, reset, t_ff_2_q);
  assign buffer_2_out = gatekeeper_1_out_3;  // Buffer buffer_2, 32 bits wide
  assign buffer_3_out = buffer_2_out;  // Buffer buffer_3, 32 bits wide
  assign buffer_4_out = buffer_3_out;  // Buffer buffer_4, 32 bits wide
  assign buffer_5_out = buffer_4_out;  // Buffer buffer_5, 32 bits wide
  assign buffer_6_out = buffer_7_out;  // Buffer buffer_6, 32 bits wide
  assign buffer_7_out = buffer_8_out;  // Buffer buffer_7, 32 bits wide
  assign buffer_8_out = buffer_9_out;  // Buffer buffer_8, 32 bits wide
  assign buffer_9_out = buffer_14_out;  // Buffer buffer_9, 32 bits wide
  assign buffer_10_out = buffer_1_out;  // Buffer buffer_10, 32 bits wide
  assign buffer_11_out = buffer_10_out;  // Buffer buffer_11, 32 bits wide
  assign buffer_12_out = buffer_11_out;  // Buffer buffer_12, 32 bits wide
  assign buffer_13_out = buffer_12_out;  // Buffer buffer_13, 32 bits wide
  T_Flip_Flop t_ff_2 (.T(t_ff_1_q), .clk(clock), .Q(t_ff_2_q), .reset(or_1_out));  // open: Qn, preset
  assign buffer_14_out = buffer_5_out;  // Buffer buffer_14, 32 bits wide
  assign buffer_15_out = buffer_13_out;  // Buffer buffer_15, 32 bits wide
  assign out_put = buffer_15_out | register_1_q;  // OR_Gate or_2, 32 bits wide
endmodule

module better_extra_sticky_gate (
  input  enable,
  input  [31:0] data,
  input  clock,
  input  reset,
  output [31:0] out_put
);

  wire or_1_out, s_r_ff_1_q, s_r_ff_2_q, t_ff_1_q, t_ff_2_q, t_ff_3_q;
  wire [31:0] buffer_1_out, buffer_2_out, buffer_3_out, buffer_4_out, buffer_5_out, buffer_6_out,
       buffer_7_out, buffer_8_out, buffer_9_out, buffer_10_out, buffer_11_out, buffer_12_out, buffer_13_out,
       buffer_14_out, buffer_15_out, gatekeeper_1_out_3, register_1_q;

  S_R_Flip_Flop s_r_ff_1 (.Q(s_r_ff_1_q), .reset(or_1_out), .preset(enable));  // open: S, R, clk, Qn
  S_R_Flip_Flop #(.trigger("falling")) s_r_ff_2 (
    .S(s_r_ff_1_q), .R(1'b0), .clk(enable), .Q(s_r_ff_2_q), .reset(or_1_out));  // open: Qn, preset
  gatekeeper gatekeeper_1 (.in_1(enable), .in_2(data), .out_3(gatekeeper_1_out_3));
  assign buffer_1_out = buffer_6_out;  // Buffer buffer_1, 32 bits wide
  Register #(.trigger("falling"), .width(32)) register_1 (
    .D(data), .en(1'b1), .clk(enable), .Q(register_1_q), .clr(or_1_out));
  T_Flip_Flop #(.trigger("falling")) t_ff_1 (
    .T(s_r_ff_2_q), .clk(clock), .Q(t_ff_1_q), .reset(or_1_out));  // open: Qn, preset
  or or_1 (or_1_out, reset, t_ff_3_q);
  assign buffer_2_out = gatekeeper_1_out_3;  // Buffer buffer_2, 32 bits wide
  assign buffer_3_out = buffer_2_out;  // Buffer buffer_3, 32 bits wide
  assign buffer_4_out = buffer_3_out;  // Buffer buffer_4, 32 bits wide
  assign buffer_5_out = buffer_4_out;  // Buffer buffer_5, 32 bits wide
  assign buffer_6_out = buffer_7_out;  // Buffer buffer_6, 32 bits wide
  assign buffer_7_out = buffer_8_out;  // Buffer buffer_7, 32 bits wide
  assign buffer_8_out = buffer_9_out;  // Buffer buffer_8, 32 bits wide
  assign buffer_9_out = buffer_14_out;  // Buffer buffer_9, 32 bits wide
  assign buffer_10_out = buffer_1_out;  // Buffer buffer_10, 32 bits wide
  assign buffer_11_out = buffer_10_out;  // Buffer buffer_11, 32 bits wide
  assign buffer_12_out = buffer_11_out;  // Buffer buffer_12, 32 bits wide
  assign buffer_13_out = buffer_12_out;  // Buffer buffer_13, 32 bits wide
  T_Flip_Flop #(.trigger("falling")) t_ff_2 (
    .T(t_ff_1_q), .clk(clock), .Q(t_ff_2_q), .reset(or_1_out));  // open: Qn, preset
  assign buffer_14_out = buffer_5_out;  // Buffer buffer_14, 32 bits wide
  assign buffer_15_out = buffer_13_out;  // Buffer buffer_15, 32 bits wide
  assign out_put = buffer_15_out | register_1_q;  // OR_Gate or_2, 32 bits wide
  T_Flip_Flop t_ff_3 (.T(t_ff_2_q), .clk(clock), .Q(t_ff_3_q), .reset(or_1_out));  // open: Qn, preset
endmodule

module wait_inducer (
  input  [15:0] opcode,
  output start_waiting
);

  wire and_1_out, and_2_out, and_3_out, comparator_1_eq, comparator_2_eq, comparator_3_eq, comparator_4_eq,
       comparator_5_eq, comparator_6_eq, comparator_7_eq, comparator_8_eq, comparator_9_eq, comparator_10_eq,
       or_1_out, or_2_out;

  Comparator #(.width(16)) comparator_1 (.a(16'hff0f), .b(opcode), .eq(comparator_1_eq));  // open: gt, lt
  Comparator #(.width(4)) comparator_2 (.a(opcode[3:0]), .b(4'b0100), .eq(comparator_2_eq));  // open: gt, lt
  Comparator #(.width(4)) comparator_3 (.a(opcode[7:4]), .b(4'b0000), .eq(comparator_3_eq));  // open: gt, lt
  Comparator #(.width(4)) comparator_4 (.a(opcode[11:8]), .b(4'b0000), .eq(comparator_4_eq));  // open: gt, lt
  Comparator #(.width(4)) comparator_5 (.a(opcode[3:0]), .b(4'b0101), .eq(comparator_5_eq));  // open: gt, lt
  Comparator #(.width(4)) comparator_6 (.a(opcode[7:4]), .b(4'b0000), .eq(comparator_6_eq));  // open: gt, lt
  Comparator #(.width(4)) comparator_7 (.a(opcode[11:8]), .b(4'b0000), .eq(comparator_7_eq));  // open: gt, lt
  or or_1 (or_1_out, opcode[12], opcode[13], opcode[14], opcode[15]);
  Comparator #(.width(4)) comparator_8 (.a(opcode[3:0]), .b(4'b0101), .eq(comparator_8_eq));  // open: gt, lt
  Comparator #(.width(4)) comparator_9 (.a(opcode[7:4]), .b(4'b0000), .eq(comparator_9_eq));  // open: gt, lt
  Comparator #(.width(4)) comparator_10 (.a(opcode[11:8]), .b(4'b0000), .eq(comparator_10_eq));  // open: gt, lt
  or or_2 (or_2_out, opcode[12], opcode[13], opcode[14], opcode[15]);
  or or_3 (start_waiting, and_1_out, comparator_1_eq, and_2_out);
  and and_1 (and_1_out, comparator_2_eq, comparator_3_eq, comparator_4_eq, or_1_out);
  and and_2 (and_2_out, comparator_5_eq, comparator_6_eq, comparator_7_eq, or_1_out);
  and and_3 (and_3_out, comparator_8_eq, comparator_9_eq, comparator_10_eq, or_2_out);
endmodule

module continuous_byte_reader (
  input  [7:0] byte_in,
  input  [31:0] address_in,
  input  read,
  input  [31:0] offs,
  input  use_offset,
  input  output_enable,
  input  remember_between_reads,
  input  clock,
  input  reset,
  output [7:0] byte1,
  output [7:0] byte2,
  output [7:0] byte3,
  output [7:0] byte4,
  output [31:0] data_out,
  output [31:0] bytes_read,
  output [31:0] address_out
);

  wire and_1_out, and_2_out, and_3_out, and_4_out, and_6_out, button_1_out, comparator_1_eq, comparator_2_eq,
       comparator_3_eq, comparator_4_eq, comparator_4_lt, new_one_ticker_1_signal_out, or_1_out, or_2_out,
       or_3_out, or_4_out, or_5_out, or_6_out, s_r_ff_1_q, variable_pulse_divider_1_out_5;
  wire [7:0] multiplexer_1_out, multiplexer_2_out, multiplexer_4_out;
  wire [31:0] adder_1_out, adder_2_out, multiplexer_3_out, negator_1_out, register_1_q, saved_address_q;

  or or_1 (or_1_out, reset, button_1_out);
  Button button_1 (.out(button_1_out));
  or or_2 (or_2_out, ~read, or_3_out);  // OR_Gate
  Comparator #(.width(32)) comparator_1 (.a({32{1'b0}}), .b(register_1_q), .eq(comparator_1_eq));  // open: gt, lt
  Register #(.trigger("falling"), .width(32)) register_1 (
    .D(adder_2_out), .en(read), .clk(clock), .Q(register_1_q), .clr(or_3_out));
  Register #(.width(32)) saved_address (.D(address_in), .en(1'b1), .clk(read), .Q(saved_address_q), .clr(or_3_out));
  or or_3 (or_3_out, or_1_out, and_6_out);
  Multiplexer #(.width(8)) multiplexer_1 (.in0(byte_in), .in1(byte2), .out(multiplexer_1_out), .sel(comparator_4_lt));
  Register #(.trigger("falling")) register_2 (
    .D(multiplexer_1_out), .en(or_4_out), .clk(variable_pulse_divider_1_out_5), .Q(byte1), .clr(or_3_out));
  or or_4 (or_4_out, and_1_out, comparator_4_lt);
  and and_1 (and_1_out, comparator_1_eq, ~or_3_out);  // AND_Gate
  Multiplexer #(.width(8)) multiplexer_2 (.in0(byte_in), .in1(byte3), .out(multiplexer_2_out), .sel(comparator_4_lt));
  and and_2 (and_2_out, comparator_2_eq, ~or_3_out);  // AND_Gate
  Comparator #(.width(32)) comparator_2 (.a(32'h1), .b(register_1_q), .eq(comparator_2_eq));  // open: gt, lt
  Register #(.width(32)) register_3 (.D(register_1_q), .en(read), .clk(clock), .Q(bytes_read), .clr(or_3_out));
  Adder #(.width(32)) adder_1 (.a(register_1_q), .b(saved_address_q), .out(adder_1_out));  // open: cin, cout
  variable_pulse_divider variable_pulse_divider_1 (
    .period(8'h1), .activate(read), .clock(clock), .reset(or_2_out), .out_5(variable_pulse_divider_1_out_5));
  Register #(.trigger("falling")) register_4 (
    .D(multiplexer_2_out), .en(or_5_out), .clk(variable_pulse_divider_1_out_5), .Q(byte2), .clr(or_3_out));
  or or_5 (or_5_out, and_2_out, comparator_4_lt);
  Comparator #(.width(32)) comparator_3 (.a(32'h2), .b(register_1_q), .eq(comparator_3_eq));  // open: gt, lt
  Adder #(.width(32)) adder_2 (.a(register_1_q), .b(32'h1), .out(adder_2_out));  // open: cin, cout
  Negator #(.width(32)) negator_1 (.in(adder_1_out), .out(negator_1_out));
  Multiplexer #(.select(2), .width(32)) multiplexer_3 (
    .in0(negator_1_out), .in1(negator_1_out), .in2({32{1'b0}}), .in3(offs), .out(multiplexer_3_out),
    .sel({output_enable, use_offset}));
  Multiplexer #(.width(8)) multiplexer_4 (.in0(byte_in), .in1(byte4), .out(multiplexer_4_out), .sel(comparator_4_lt));
  and and_3 (and_3_out, comparator_3_eq, ~or_3_out);  // AND_Gate
  Adder #(.width(32)) adder_3 (.a(adder_1_out), .b(multiplexer_3_out), .out(address_out));  // open: cin, cout
  Register #(.trigger("falling")) register_5 (
    .D(multiplexer_4_out), .en(or_6_out), .clk(variable_pulse_divider_1_out_5), .Q(byte3), .clr(or_3_out));
  or or_6 (or_6_out, and_3_out, comparator_4_lt);
  S_R_Flip_Flop s_r_ff_1 (.Q(s_r_ff_1_q), .preset(output_enable));  // open: S, R, clk, reset, Qn
  Register #(.trigger("falling")) register_6 (
    .D(byte_in), .en(comparator_4_eq), .clk(variable_pulse_divider_1_out_5), .Q(byte4), .clr(or_3_out));
  Comparator #(.width(32)) comparator_4 (
    .a(32'h3), .b(register_1_q), .eq(comparator_4_eq), .lt(comparator_4_lt));  // open: gt
  and and_4 (and_4_out, ~output_enable, s_r_ff_1_q);  // AND_Gate
  new_one_ticker new_one_ticker_1 (
    .clock_in(clock), .reset(or_1_out), .signal_in(and_4_out), .signal_out(new_one_ticker_1_signal_out));
  assign data_out = {byte4, byte3, byte2, byte1} & {32{output_enable}};  // AND_Gate and_5, 32 bits wide
  and and_6 (and_6_out, ~remember_between_reads, new_one_ticker_1_signal_out);  // AND_Gate
endmodule

module variable_pulse_divider (
  input  [7:0] period,
  input  activate,
  input  clock,
  input  reset,
  output out_5
);

  wire and_1_out, comparator_1_eq, comparator_2_eq, or_1_out;
  wire [7:0] multiplexer_1_out, register_1_q, subtractor_1_out;

  Multiplexer #(.width(8)) multiplexer_1 (.in0(register_1_q), .in1(period), .out(multiplexer_1_out));  // open: sel
  Comparator comparator_1 (.a(period), .b({8{1'b0}}), .eq(comparator_1_eq));  // open: gt, lt
  Register #(.trigger("falling")) register_1 (
    .D(subtractor_1_out), .en(and_1_out), .clk(clock), .Q(register_1_q), .clr(reset));
  Subtractor subtractor_1 (.a(multiplexer_1_out), .b(8'h1), .out(subtractor_1_out));  // open: bin, bout
  and and_1 (and_1_out, activate, ~comparator_1_eq);  // AND_Gate
  Comparator comparator_2 (.a(register_1_q), .b({8{1'b0}}), .eq(comparator_2_eq));  // open: gt, lt
  or or_1 (or_1_out, comparator_2_eq, comparator_1_eq);
  and and_2 (out_5, or_1_out, activate, ~reset, clock);  // AND_Gate
endmodule

module is_long_instruction (
  input  [7:0] first_byte,
  output out_2
);

  ROM #(.dataWidth(1)) rom_1 (.addr(first_byte));  // open: data

  assign out_2 = 1'b1;

  // Notes on the sheet:
  //   contents of rom_1 (hex, n*v repeats v):
  //   16*0 16*1
endmodule
